// Logisim project Prob_Cap3.circ as structural Verilog: 6 circuits, main circuit p3.2-nand
module p3_2_nand (
  input  A,
  input  B,
  output NAND,
  output f
);

  nand nand_1 (NAND, A, B);
  or or_1 (f, ~B, ~A);  // OR_Gate
  p3_2_nor p3_2_nor_1 ();  // open: A, B, NOR, g
endmodule

module p3_2_nor (
  input  A,
  input  B,
  output NOR,
  output g
);

  nor nor_1 (NOR, A, B);
  and and_1 (g, ~B, ~A);  // AND_Gate
endmodule

module p3_5 (
  input  A,
  input  B,
  output XOR,
  output f,
  output g
);

  wire and_1_out, and_2_out, or_1_out, or_2_out;

  xor xor_1 (XOR, A, B);
  and and_1 (and_1_out, B, ~A);  // AND_Gate
  and and_2 (and_2_out, ~B, A);  // AND_Gate
  or or_1 (or_1_out, B, A);
  or or_2 (or_2_out, ~B, ~A);  // OR_Gate
  or or_3 (f, and_1_out, and_2_out);
  and and_3 (g, or_1_out, or_2_out);
endmodule

module p3_6_a (
  input  A,
  input  B,
  input  C,
  output f,
  output g
);

  wire and_1_out, and_2_out, or_1_out;

  or or_1 (or_1_out, B, C);
  and and_1 (and_1_out, B, A);
  and and_2 (and_2_out, C, A);
  and and_3 (f, A, or_1_out);
  or or_2 (g, and_1_out, and_2_out);
endmodule

module p3_6_b (
  input  A,
  input  B,
  input  C,
  output f,
  output g
);

  wire and_1_out, or_1_out, or_2_out;

  and and_1 (and_1_out, B, C);
  or or_1 (or_1_out, B, A);
  or or_2 (or_2_out, C, A);
  or or_3 (f, A, and_1_out);
  and and_2 (g, or_1_out, or_2_out);
endmodule

module p3_8 (
  input  A,
  input  B,
  input  C,
  output f,
  output g
);

  wire xnor_1_out, xor_1_out;

  xor xor_1 (xor_1_out, A, B);
  xor xor_2 (f, xor_1_out, C);
  xnor xnor_1 (xnor_1_out, A, B);
  xnor xnor_2 (g, xnor_1_out, C);
endmodule
