// Logisim project Prob_Cap4.circ as structural Verilog: 24 circuits, main circuit p4.22
module p4_1 (
  input  A,
  input  B,
  input  C,
  output f,
  output g
);

  wire nor_1_out, nor_2_out, nor_3_out, not_1_out, not_2_out;

  not not_1 (not_1_out, A);
  not not_2 (not_2_out, B);
  nor nor_1 (nor_1_out, not_1_out, not_2_out, C);
  nor nor_2 (nor_2_out, A, not_2_out);
  or or_1 (g, ~C, not_1_out, not_2_out);  // OR_Gate
  nor nor_3 (nor_3_out, nor_1_out, nor_2_out, not_2_out);
  nor nor_4 (f, nor_3_out, nor_3_out);
endmodule

module p4_2 (
  input  A,
  input  B,
  input  C,
  input  D,
  input  E,
  input  F,
  output f_2
);

  wire nand_1_out, nand_2_out, nand_3_out, nand_4_out, not_1_out, not_2_out, not_3_out;

  not not_1 (not_1_out, B);
  nand nand_1 (nand_1_out, not_1_out, C);
  not not_2 (not_2_out, D);
  nand nand_2 (nand_2_out, E, not_3_out);
  not not_3 (not_3_out, F);
  nand nand_3 (nand_3_out, not_2_out, nand_2_out);
  nand nand_4 (nand_4_out, nand_1_out, nand_3_out);
  nand nand_5 (f_2, A, nand_4_out);
endmodule

module p4_3 (
  input  A,
  input  B,
  input  C,
  input  D,
  output S
);

  wire nand_1_out, nand_2_out, nand_3_out, not_1_out, not_2_out, not_3_out;

  not not_1 (not_1_out, B);
  not not_2 (not_2_out, D);
  not not_3 (not_3_out, C);
  nand nand_1 (nand_1_out, not_2_out, not_3_out);
  nand nand_2 (nand_2_out, D, C, not_1_out);
  nand nand_3 (nand_3_out, D, not_1_out, A);
  nand nand_4 (S, nand_1_out, nand_2_out, nand_3_out);
endmodule

module p4_4 (
  input  A,
  input  B,
  input  C,
  output f
);

  wire and_1_out, and_2_out, nand_1_out, nand_2_out, or_1_out, undriven;

  and and_1 (and_1_out, undriven, C);
  or or_1 (or_1_out, undriven, C);
  nand nand_1 (nand_1_out, A, B, undriven);
  and and_2 (and_2_out, nand_1_out, and_1_out);
  nand nand_2 (nand_2_out, and_1_out, or_1_out);
  nor nor_1 (f, and_2_out, nand_2_out);
endmodule

module p4_5 (
  input  A,
  input  B,
  input  C,
  output f,
  output g
);

  wire nand_1_out, nor_1_out, or_1_out, xnor_1_out;

  or or_1 (or_1_out, A, B);
  nor nor_1 (nor_1_out, B, C);
  or or_2 (g, C, B, ~A);  // OR_Gate
  nand nand_1 (nand_1_out, or_1_out, nor_1_out);
  xnor xnor_1 (xnor_1_out, nor_1_out, C);
  or or_3 (f, nand_1_out, xnor_1_out);
endmodule

module p4_6 (
  input  A,
  input  B,
  output f
);

  wire nand_1_out, nand_2_out, nand_3_out, nand_4_out;

  nand nand_1 (nand_1_out, A, A);
  nand nand_2 (nand_2_out, B, B);
  nand nand_3 (nand_3_out, nand_1_out, B);
  nand nand_4 (nand_4_out, A, nand_2_out);
  nand nand_5 (f, nand_3_out, nand_4_out);
endmodule

module p4_7 (
  input  A,
  input  B,
  input  C,
  input  A_2,
  input  B_2,
  input  C_2,
  input  A_3,
  input  B_3,
  input  C_3,
  input  A_4,
  input  B_4,
  input  C_4,
  output f,
  output f_2,
  output f_3,
  output f_4
);

  wire nand_1_out, nand_2_out, nand_3_out, nand_4_out, nand_6_out, nand_7_out, nor_1_out, nor_2_out, or_1_out;

  and and_1 (f, A, or_1_out);
  or or_1 (or_1_out, B, C);
  nand nand_1 (nand_1_out, A_2, B_2);
  nand nand_2 (nand_2_out, A_2, C_2);
  nor nor_1 (nor_1_out, A_3, A_3);
  nor nor_2 (nor_2_out, B_3, C_3);
  nand nand_3 (nand_3_out, B_4, B_4);
  nand nand_4 (nand_4_out, C_4, C_4);
  nand nand_5 (f_2, nand_1_out, nand_2_out);
  nor nor_3 (f_3, nor_1_out, nor_2_out);
  nand nand_6 (nand_6_out, A_4, nand_7_out);
  nand nand_7 (nand_7_out, nand_3_out, nand_4_out);
  nand nand_8 (f_4, nand_6_out, nand_6_out);
endmodule

module p4_8 (
  input  A,
  input  B,
  input  C,
  output f
);

  wire nor_1_out, nor_2_out, nor_3_out, nor_4_out, nor_5_out;

  nor nor_1 (nor_1_out, A, A);
  nor nor_2 (nor_2_out, B, B);
  nor nor_3 (nor_3_out, C, C);
  nor nor_4 (nor_4_out, nor_1_out, nor_3_out);
  nor nor_5 (nor_5_out, nor_1_out, nor_2_out);
  nor nor_6 (f, nor_4_out, nor_5_out);
endmodule

module p4_9 (
  input  A,
  input  B,
  input  C,
  output f,
  output h,
  output g
);

  wire A_prime_B_prime_out, AB_prime_out, AC_out, not_1_out, not_2_out, xor_1_out;

  not not_1 (not_1_out, A);
  not not_2 (not_2_out, B);
  and A_prime_B_prime (A_prime_B_prime_out, not_2_out, not_1_out);
  or or_1 (f, A_prime_B_prime_out, AC_out);
  and AC (AC_out, C, A);
  and AB_prime (AB_prime_out, not_2_out, A);
  or or_2 (g, AB_prime_out, xor_1_out);
  xor xor_1 (xor_1_out, C, A);
  xor xor_2 (h, f, g);
endmodule

module p4_10 (
  input  A,
  input  B,
  input  C,
  input  A_2,
  input  B_2,
  input  C_2,
  output f,
  output f_2
);

  wire and_1_out, and_2_out, and_3_out, and_4_out, undriven;

  and and_1 (and_1_out, A, undriven, B);
  and and_2 (and_2_out, ~A, C);  // AND_Gate
  and and_3 (and_3_out, A_2, B_2);
  and and_4 (and_4_out, A_2, ~C_2);  // AND_Gate
  or or_1 (f, and_1_out, and_2_out);
  or or_2 (f_2, and_3_out, and_4_out);
endmodule

module p4_11 (
  input  A,
  input  B,
  input  C,
  input  A_2,
  input  B_2,
  input  C_2,
  output f,
  output f_2,
  output g
);

  or or_1 (f, A, B);
  xor xor_1 (f, A, C);
  or or_2 (f_2, A_2, B_2);
  xor xor_2 (g, A_2, C_2);
endmodule

module p4_12 (
  input  A,
  input  B,
  input  A_2,
  input  B_2,
  input  A_3,
  input  B_3,
  input  A_4,
  input  B_4,
  input  A_5,
  input  B_5,
  output f,
  output f_2,
  output f_3,
  output f_4,
  output f_5
);

  wire transistor_1_out, transistor_2_out, transistor_3_out;

  Transistor #(.\type ("n")) transistor_1 (.in(1'b1), .out(transistor_1_out), .gate(A));
  Transistor #(.\type ("n")) transistor_2 (.in(1'b1), .out(transistor_2_out), .gate(A_2));
  Transistor #(.\type ("n")) transistor_3 (.in(1'b1), .out(transistor_3_out), .gate(A_4));
  Transistor #(.\type ("n")) transistor_4 (.in(transistor_1_out), .out(f), .gate(B));
  Transistor #(.\type ("n")) transistor_5 (.in(transistor_2_out), .out(f_2), .gate(B_2));
  Pull_Resistor pull_resistor_1 (.node(f_2));
  Transistor #(.\type ("n")) transistor_6 (.in(transistor_3_out), .out(f_5), .gate(B_4));
  Pull_Resistor pull_resistor_2 (.node(f_5));
  and and_1 (f_3, A_3, B_3);
  and and_2 (f_4, A_5, B_5);
endmodule

module p4_13_NAND (
  input  A,
  input  B,
  input  C,
  input  D,
  output f
);

  wire nand_1_out, nand_2_out, nand_3_out, nand_4_out, not_1_out, not_2_out, not_3_out, not_4_out;

  not not_1 (not_1_out, A);
  not not_2 (not_2_out, B);
  not not_3 (not_3_out, D);
  not not_4 (not_4_out, C);
  nand nand_1 (nand_1_out, not_3_out, C, not_2_out, A);
  nand nand_2 (nand_2_out, not_3_out, C, B, not_1_out);
  nand nand_3 (nand_3_out, D, not_4_out, not_2_out, A);
  nand nand_4 (nand_4_out, D, not_4_out, B, not_1_out);
  nand nand_5 (f, nand_1_out, nand_2_out, nand_3_out, nand_4_out);
endmodule

module p4_13_NOR (
  input  A,
  input  B,
  input  C,
  input  D,
  output f
);

  wire nor_1_out, nor_2_out, nor_3_out, nor_4_out, not_1_out, not_2_out, not_3_out, not_4_out;

  not not_1 (not_1_out, B);
  not not_2 (not_2_out, A);
  not not_3 (not_3_out, D);
  not not_4 (not_4_out, C);
  nor nor_1 (nor_1_out, B, A);
  nor nor_2 (nor_2_out, D, C);
  nor nor_3 (nor_3_out, not_3_out, not_4_out);
  nor nor_4 (nor_4_out, not_1_out, not_2_out);
  nor nor_5 (f, nor_1_out, nor_2_out, nor_3_out, nor_4_out);
endmodule

module p4_14_NAND (
  input  A,
  input  B,
  input  C,
  input  D,
  output f
);

  wire nand_1_out, nand_2_out;

  nand nand_1 (nand_1_out, B, C);
  nand nand_2 (nand_2_out, ~B, ~D);  // NAND_Gate
  nand nand_3 (f, nand_1_out, nand_2_out);
endmodule

module p4_14_NOR (
  input  A,
  input  B,
  input  C,
  input  D,
  output f
);

  wire nor_1_out, nor_2_out;

  nor nor_1 (nor_1_out, ~B, C);  // NOR_Gate
  nor nor_2 (nor_2_out, B, ~D);  // NOR_Gate
  nor nor_3 (f, nor_1_out, nor_2_out);
endmodule

module p4_15_NAND (
  input  A,
  input  B,
  input  C,
  input  D,
  output f
);

  wire nand_1_out, nand_3_out;

  nand nand_1 (nand_1_out, A, B);
  nand nand_2 (f, nand_1_out, nand_3_out, D);
  nand nand_3 (nand_3_out, ~A, ~B);  // NAND_Gate
endmodule

module p4_15_NOR (
  input  A,
  input  B,
  input  C,
  input  D,
  output f
);

  wire nor_1_out, nor_2_out;

  nor nor_1 (nor_1_out, A, ~B, ~D);  // NOR_Gate
  nor nor_2 (nor_2_out, B, ~A, ~D);  // NOR_Gate
  nor nor_3 (f, nor_1_out, nor_2_out);
endmodule

module p4_17 (
  input  A,
  input  B,
  input  C,
  output f
);

  wire not_1_out;

  not not_1 (not_1_out, C);
  or or_1 (f, A, not_1_out);
endmodule

module p4_18 (
  input  A,
  input  B,
  input  C,
  output f
);

  wire and_1_out;

  and and_1 (and_1_out, B, C);
  or or_1 (f, A, and_1_out);
endmodule

module p4_19 (
  input  A,
  input  B,
  input  C,
  output f,
  output g,
  output h
);

  wire not_1_out, not_2_out, not_3_out, not_4_out, not_5_out, not_6_out, or_1_out, or_2_out, or_3_out,
       or_4_out, or_5_out, or_6_out, or_7_out;

  or or_1 (or_1_out, A, B);
  or or_2 (or_2_out, A, C);
  or or_3 (or_3_out, B, C);
  not not_1 (not_1_out, B);
  not not_2 (not_2_out, C);
  not not_3 (not_3_out, A);
  not not_4 (not_4_out, C);
  not not_5 (not_5_out, A);
  not not_6 (not_6_out, B);
  not not_7 (h, C);
  and and_1 (f, or_1_out, or_2_out, or_3_out);
  or or_4 (or_4_out, A, B, C);
  or or_5 (or_5_out, A, not_1_out, not_2_out);
  or or_6 (or_6_out, not_3_out, B, not_4_out);
  or or_7 (or_7_out, not_5_out, not_6_out, C);
  and and_2 (g, or_4_out, or_5_out, or_6_out, or_7_out);
endmodule

module p4_20 (
  input  A,
  input  B,
  input  C,
  output f
);

  wire and_1_out, and_2_out, and_3_out;

  and and_1 (and_1_out, A, B);
  and and_2 (and_2_out, B, C);
  and and_3 (and_3_out, C, A);
  LED Alarma (.in(f));
  or or_1 (f, and_1_out, and_2_out, and_3_out);
endmodule

module p4_21 (
  input  D1,
  input  D0,
  input  R1,
  input  R0,
  output f
);

  wire not_1_out, not_2_out, not_3_out, not_4_out, not_5_out, not_6_out, not_7_out, or_1_out, or_2_out,
       or_3_out, or_4_out;

  not not_1 (not_1_out, D0);
  not not_2 (not_2_out, D0);
  not not_3 (not_3_out, R1);
  not not_4 (not_4_out, D1);
  not not_5 (not_5_out, D1);
  not not_6 (not_6_out, R1);
  not not_7 (not_7_out, R0);
  or or_1 (or_1_out, D1, not_1_out, R0);
  or or_2 (or_2_out, D1, not_2_out, not_3_out);
  or or_3 (or_3_out, not_4_out, R1, R0);
  or or_4 (or_4_out, not_5_out, D0, not_6_out, not_7_out);
  and and_1 (f, or_1_out, or_2_out, or_3_out, or_4_out);
endmodule

module p4_22 (
  input  M1,
  input  M1_2,
  input  M0,
  input  M0_2,
  input  P1,
  input  P1_2,
  input  M1_3,
  input  M0_3,
  input  P0,
  input  P1_3,
  input  M1_4,
  input  M0_4,
  input  P1_4,
  input  M1_5,
  input  M0_5,
  input  P1_5,
  output d1,
  output s,
  output d1_2,
  output d1_3,
  output d1_4,
  output d1_5,
  output d0
);

  wire and_1_out, and_2_out, and_3_out, and_4_out, and_5_out, and_6_out, and_7_out, and_8_out, and_9_out,
       and_10_out, and_11_out, nand_1_out, nand_2_out, nor_1_out, nor_2_out, not_1_out, not_2_out, not_3_out,
       not_4_out, not_5_out, not_6_out, not_7_out, not_8_out, not_9_out, not_10_out, not_11_out, not_12_out,
       or_4_out, or_5_out;

  not not_1 (not_1_out, M1);
  not not_2 (not_2_out, P1_2);
  not not_3 (not_3_out, P0);
  not not_4 (not_4_out, M0_2);
  not not_5 (not_5_out, P1_2);
  not not_6 (not_6_out, P1_2);
  not not_7 (not_7_out, M0_2);
  and and_1 (and_1_out, M1, not_7_out, P1_2);
  and and_2 (and_2_out, M1, M0_2, not_8_out);
  not not_8 (not_8_out, P1_2);
  not not_9 (not_9_out, M1);
  and and_3 (and_3_out, not_9_out, M0_2, P0);
  and and_4 (and_4_out, M0_2, P1_2, not_10_out);
  not not_10 (not_10_out, P0);
  and and_5 (and_5_out, M1, not_11_out, not_12_out);
  not not_11 (not_11_out, P1_2);
  not not_12 (not_12_out, P0);
  and and_6 (and_6_out, not_1_out, M0_2, not_2_out, not_3_out);
  and and_7 (and_7_out, M1, not_4_out, not_5_out);
  and and_8 (and_8_out, M1, not_6_out, P0);
  and and_9 (and_9_out, M1, M0_2, P1_2);
  or or_1 (d1_4, and_1_out, and_2_out);
  or or_2 (d0, and_3_out, and_4_out, and_5_out);
  or or_3 (s, and_6_out, and_7_out, and_8_out, and_9_out);
  and and_10 (and_10_out, M1_2, ~M0, P1);  // AND_Gate
  and and_11 (and_11_out, M1_2, M0, ~P1);  // AND_Gate
  nand nand_1 (nand_1_out, M1_3, ~M0_3, P1_3);  // NAND_Gate
  nand nand_2 (nand_2_out, M1_3, M0_3, ~P1_3);  // NAND_Gate
  or or_4 (or_4_out, M0_4, P1_4);
  or or_5 (or_5_out, ~M0_4, ~P1_4);  // OR_Gate
  nor nor_1 (nor_1_out, M0_5, P1_5);
  nor nor_2 (nor_2_out, ~M0_5, ~P1_5);  // NOR_Gate
  or or_6 (d1, and_10_out, and_11_out);
  nand nand_3 (d1_2, nand_1_out, nand_2_out);
  and and_12 (d1_3, M1_4, or_4_out, or_5_out);
  nor nor_3 (d1_5, M1_5, nor_1_out, nor_2_out);
endmodule
