// Logisim project Prob_Cap5.circ as structural Verilog: 40 circuits, main circuit p5.24
module p5_1 (
  input  [2:0] A_B_C,
  input  [2:0] A_B_C_2,
  input  [2:0] A_B_C_3,
  input  [2:0] A_B_C_4,
  output f1,
  output f3,
  output f2,
  output f4
);

  wire decoder_1_out3, decoder_1_out4, decoder_1_out6, decoder_2_out3, decoder_2_out4, decoder_2_out6,
       decoder_3_out3, decoder_3_out4, decoder_3_out6, decoder_4_out3, decoder_4_out4, decoder_4_out6;

  Decoder #(.select(3), .disabled(0), .enable("false")) decoder_1 (
    .out3(decoder_1_out3), .out4(decoder_1_out4), .out6(decoder_1_out6), .sel(A_B_C));  // open: out0, out1, out2, out5, out7
  Decoder #(.select(3), .disabled(0), .enable("false")) decoder_2 (
    .out3(decoder_2_out3), .out4(decoder_2_out4), .out6(decoder_2_out6), .sel(A_B_C_3));  // open: out0, out1, out2, out5, out7
  or or_1 (f1, decoder_1_out3, decoder_1_out4, decoder_1_out6);
  nor nor_1 (f2, decoder_2_out3, decoder_2_out4, decoder_2_out6);
  Decoder #(.select(3), .disabled(0), .enable("false")) decoder_3 (
    .out3(decoder_3_out3), .out4(decoder_3_out4), .out6(decoder_3_out6), .sel(A_B_C_2));  // open: out0, out1, out2, out5, out7
  Decoder #(.select(3), .disabled(0), .enable("false")) decoder_4 (
    .out3(decoder_4_out3), .out4(decoder_4_out4), .out6(decoder_4_out6), .sel(A_B_C_4));  // open: out0, out1, out2, out5, out7
  and and_1 (f3, decoder_3_out3, decoder_3_out4, decoder_3_out6);
  nand nand_1 (f4, decoder_4_out3, decoder_4_out4, decoder_4_out6);
endmodule

module p5_2 (
  input  [2:0] A_B_C,
  input  [2:0] A_B_C_2,
  input  [2:0] A_B_C_3,
  input  [2:0] A_B_C_4,
  output g1,
  output g3,
  output g2,
  output g4
);

  wire decoder_1_out0, decoder_1_out1, decoder_1_out2, decoder_1_out3, decoder_1_out4, decoder_1_out5,
       decoder_1_out6, decoder_1_out7, decoder_2_out0, decoder_2_out1, decoder_2_out2, decoder_2_out3,
       decoder_2_out4, decoder_2_out5, decoder_2_out6, decoder_2_out7, decoder_3_out0, decoder_3_out1,
       decoder_3_out2, decoder_3_out3, decoder_3_out4, decoder_3_out5, decoder_3_out6, decoder_3_out7,
       decoder_4_out0, decoder_4_out1, decoder_4_out2, decoder_4_out3, decoder_4_out4, decoder_4_out5,
       decoder_4_out6, decoder_4_out7, not_4_out, not_5_out, not_7_out, not_12_out, not_13_out, not_15_out,
       not_20_out, not_21_out, not_23_out, not_28_out, not_29_out, not_31_out;

  // NOT_Gate not_1 has open pins: in=decoder_1_out0, out=open
  // NOT_Gate not_2 has open pins: in=decoder_1_out1, out=open
  // NOT_Gate not_3 has open pins: in=decoder_1_out2, out=open
  not not_4 (not_4_out, decoder_1_out3);
  not not_5 (not_5_out, decoder_1_out4);
  // NOT_Gate not_6 has open pins: in=decoder_1_out5, out=open
  not not_7 (not_7_out, decoder_1_out6);
  // NOT_Gate not_8 has open pins: in=decoder_1_out7, out=open
  Decoder #(.select(3), .disabled(0), .enable("false")) decoder_1 (
    .out0(decoder_1_out0), .out1(decoder_1_out1), .out2(decoder_1_out2), .out3(decoder_1_out3),
    .out4(decoder_1_out4), .out5(decoder_1_out5), .out6(decoder_1_out6), .out7(decoder_1_out7), .sel(A_B_C));
  // NOT_Gate not_9 has open pins: in=decoder_2_out0, out=open
  // NOT_Gate not_10 has open pins: in=decoder_2_out1, out=open
  // NOT_Gate not_11 has open pins: in=decoder_2_out2, out=open
  not not_12 (not_12_out, decoder_2_out3);
  not not_13 (not_13_out, decoder_2_out4);
  // NOT_Gate not_14 has open pins: in=decoder_2_out5, out=open
  not not_15 (not_15_out, decoder_2_out6);
  // NOT_Gate not_16 has open pins: in=decoder_2_out7, out=open
  Decoder #(.select(3), .disabled(0), .enable("false")) decoder_2 (
    .out0(decoder_2_out0), .out1(decoder_2_out1), .out2(decoder_2_out2), .out3(decoder_2_out3),
    .out4(decoder_2_out4), .out5(decoder_2_out5), .out6(decoder_2_out6), .out7(decoder_2_out7), .sel(A_B_C_3));
  or or_1 (g1, not_4_out, not_5_out, not_7_out);
  nor nor_1 (g2, not_12_out, not_13_out, not_15_out);
  Decoder #(.select(3), .disabled(0), .enable("false")) decoder_3 (
    .out0(decoder_3_out0), .out1(decoder_3_out1), .out2(decoder_3_out2), .out3(decoder_3_out3),
    .out4(decoder_3_out4), .out5(decoder_3_out5), .out6(decoder_3_out6), .out7(decoder_3_out7), .sel(A_B_C_2));
  Decoder #(.select(3), .disabled(0), .enable("false")) decoder_4 (
    .out0(decoder_4_out0), .out1(decoder_4_out1), .out2(decoder_4_out2), .out3(decoder_4_out3),
    .out4(decoder_4_out4), .out5(decoder_4_out5), .out6(decoder_4_out6), .out7(decoder_4_out7), .sel(A_B_C_4));
  // NOT_Gate not_17 has open pins: in=decoder_3_out0, out=open
  // NOT_Gate not_18 has open pins: in=decoder_3_out1, out=open
  // NOT_Gate not_19 has open pins: in=decoder_3_out2, out=open
  not not_20 (not_20_out, decoder_3_out3);
  and and_1 (g3, not_20_out, not_21_out, not_23_out);
  not not_21 (not_21_out, decoder_3_out4);
  // NOT_Gate not_22 has open pins: in=decoder_3_out5, out=open
  not not_23 (not_23_out, decoder_3_out6);
  // NOT_Gate not_24 has open pins: in=decoder_3_out7, out=open
  // NOT_Gate not_25 has open pins: in=decoder_4_out0, out=open
  // NOT_Gate not_26 has open pins: in=decoder_4_out1, out=open
  // NOT_Gate not_27 has open pins: in=decoder_4_out2, out=open
  not not_28 (not_28_out, decoder_4_out3);
  not not_29 (not_29_out, decoder_4_out4);
  nand nand_1 (g4, not_28_out, not_29_out, not_31_out);
  // NOT_Gate not_30 has open pins: in=decoder_4_out5, out=open
  not not_31 (not_31_out, decoder_4_out6);
  // NOT_Gate not_32 has open pins: in=decoder_4_out7, out=open
endmodule

module p5_3 (
  input  A,
  input  B,
  input  C,
  input  D,
  output f
);

  wire decoder_1_out1, decoder_1_out2, decoder_2_out0, decoder_2_out1, decoder_2_out2, decoder_2_out3,
       decoder_3_out1, decoder_4_out0, decoder_5_out2;

  Decoder #(.select(2), .disabled(0)) decoder_1 (
    .out1(decoder_1_out1), .out2(decoder_1_out2), .sel({C, D}), .en(decoder_2_out0));  // open: out0, out3
  Decoder #(.select(2), .disabled(0)) decoder_2 (
    .out0(decoder_2_out0), .out1(decoder_2_out1), .out2(decoder_2_out2), .out3(decoder_2_out3), .sel({A, B}),
    .en(1'b1));
  Decoder #(.select(2), .disabled(0)) decoder_3 (
    .out1(decoder_3_out1), .sel({C, D}), .en(decoder_2_out1));  // open: out0, out2, out3
  or or_1 (f, decoder_1_out1, decoder_1_out2, decoder_3_out1, decoder_5_out2, decoder_4_out0);
  Decoder #(.select(2), .disabled(0)) decoder_4 (
    .out0(decoder_4_out0), .sel({C, D}), .en(decoder_2_out3));  // open: out1, out2, out3
  Decoder #(.select(2), .disabled(0)) decoder_5 (
    .out2(decoder_5_out2), .sel({C, D}), .en(decoder_2_out2));  // open: out0, out1, out3
endmodule

module p5_4 (
  input  A,
  input  B,
  input  C,
  output f
);

  wire decoder_1_out0, decoder_1_out1, decoder_1_out2, decoder_1_out3, decoder_1_out4, decoder_1_out5,
       decoder_1_out6, decoder_1_out7, not_1_out, not_2_out, not_6_out, not_8_out;

  not not_1 (not_1_out, decoder_1_out0);
  not not_2 (not_2_out, decoder_1_out1);
  // NOT_Gate not_3 has open pins: in=decoder_1_out2, out=open
  // NOT_Gate not_4 has open pins: in=decoder_1_out3, out=open
  // NOT_Gate not_5 has open pins: in=decoder_1_out4, out=open
  not not_6 (not_6_out, decoder_1_out5);
  // NOT_Gate not_7 has open pins: in=decoder_1_out6, out=open
  not not_8 (not_8_out, decoder_1_out7);
  Decoder #(.select(3), .disabled(0)) decoder_1 (
    .out0(decoder_1_out0), .out1(decoder_1_out1), .out2(decoder_1_out2), .out3(decoder_1_out3),
    .out4(decoder_1_out4), .out5(decoder_1_out5), .out6(decoder_1_out6), .out7(decoder_1_out7),
    .sel({A, B, C}), .en(1'b1));
  and and_1 (f, not_1_out, not_2_out, not_6_out, not_8_out);
endmodule

module p5_5 (
  input  A,
  input  B,
  input  C,
  output f
);

  wire and_1_out, and_2_out, decoder_1_out0, decoder_1_out1, decoder_1_out2, decoder_1_out3, decoder_1_out4,
       decoder_1_out5, decoder_1_out6, decoder_1_out7, not_1_out, not_3_out, not_5_out, not_7_out;

  not not_1 (not_1_out, decoder_1_out0);
  // NOT_Gate not_2 has open pins: in=decoder_1_out1, out=open
  not not_3 (not_3_out, decoder_1_out2);
  // NOT_Gate not_4 has open pins: in=decoder_1_out3, out=open
  not not_5 (not_5_out, decoder_1_out4);
  // NOT_Gate not_6 has open pins: in=decoder_1_out5, out=open
  not not_7 (not_7_out, decoder_1_out6);
  // NOT_Gate not_8 has open pins: in=decoder_1_out7, out=open
  Decoder #(.select(3), .enable("false")) decoder_1 (
    .out0(decoder_1_out0), .out1(decoder_1_out1), .out2(decoder_1_out2), .out3(decoder_1_out3),
    .out4(decoder_1_out4), .out5(decoder_1_out5), .out6(decoder_1_out6), .out7(decoder_1_out7),
    .sel({A, B, C}));
  and and_1 (and_1_out, not_1_out, not_3_out);
  and and_2 (and_2_out, not_5_out, not_7_out);
  and and_3 (f, and_1_out, and_2_out);
endmodule

module p5_6 (
  input  A,
  input  B,
  input  C,
  output f
);

  wire decoder_1_out3, decoder_1_out4, decoder_1_out6, nor_1_out, or_1_out;

  or or_1 (or_1_out, B, ~C);  // OR_Gate
  Decoder #(.select(3), .disabled(0)) decoder_1 (
    .out3(decoder_1_out3), .out4(decoder_1_out4), .out6(decoder_1_out6), .sel({A, B, C}), .en(or_1_out));  // open: out0, out1, out2, out5, out7
  nor nor_1 (nor_1_out, decoder_1_out3, decoder_1_out4);
  and and_1 (f, nor_1_out, ~decoder_1_out6);  // AND_Gate
endmodule

module p5_7 (
  input  A,
  input  B,
  input  C,
  output f
);

  wire decoder_1_out1, decoder_1_out4, decoder_1_out6, not_1_out, not_2_out, not_3_out;

  Decoder #(.select(3), .enable("false")) decoder_1 (
    .out1(decoder_1_out1), .out4(decoder_1_out4), .out6(decoder_1_out6), .sel({A, B, C}));  // open: out0, out2, out3, out5, out7
  not not_1 (not_1_out, decoder_1_out1);
  nand nand_1 (f, not_1_out, not_2_out, not_3_out);
  not not_2 (not_2_out, decoder_1_out4);
  not not_3 (not_3_out, decoder_1_out6);
endmodule

module p5_8 (
  input  A,
  input  B,
  input  C,
  input  D,
  output f
);

  wire and_1_out, and_2_out, decoder_1_out0, decoder_1_out2, decoder_2_out1, decoder_2_out3;

  Decoder #(.select(2), .enable("false")) decoder_1 (
    .out0(decoder_1_out0), .out2(decoder_1_out2), .sel({A, B}));  // open: out1, out3
  Decoder #(.select(2), .enable("false")) decoder_2 (
    .out1(decoder_2_out1), .out3(decoder_2_out3), .sel({C, D}));  // open: out0, out2
  and and_1 (and_1_out, decoder_1_out0, decoder_2_out3);
  and and_2 (and_2_out, decoder_1_out2, decoder_2_out1);
  or or_1 (f, and_1_out, and_2_out);
endmodule

module p5_9 (
  input  A,
  input  B,
  input  C,
  output f,
  output f_2
);

  wire decoder_1_out2, decoder_1_out3, decoder_2_out0, decoder_2_out1, decoder_3_out0, decoder_3_out1,
       nor_1_out, not_1_out, not_2_out, or_1_out;

  not not_1 (not_1_out, A);
  not not_2 (not_2_out, A);
  Decoder #(.select(2), .disabled(0)) decoder_1 (
    .out2(decoder_1_out2), .out3(decoder_1_out3), .sel({B, C}), .en(A));  // open: out0, out1
  Decoder #(.select(2), .disabled(0)) decoder_2 (
    .out0(decoder_2_out0), .out1(decoder_2_out1), .sel({B, C}), .en(not_1_out));  // open: out2, out3
  Decoder #(.select(2), .disabled(0)) decoder_3 (
    .out0(decoder_3_out0), .out1(decoder_3_out1), .sel({B, C}), .en(A));  // open: out2, out3
  or or_1 (or_1_out, decoder_2_out0, decoder_2_out1);
  nor nor_1 (nor_1_out, decoder_3_out0, decoder_3_out1);
  or or_2 (f_2, not_2_out, decoder_1_out2, decoder_1_out3);
  or or_3 (f, or_1_out, nor_1_out);
endmodule

module p5_10 (
  input  A,
  input  B,
  input  C,
  output f_SOP,
  output f_POS,
  output f,
  output f_2,
  output f_3
);

  wire and_1_out, and_3_out, decoder_1_out1, decoder_1_out3, decoder_1_out5, decoder_1_out6, decoder_1_out7,
       decoder_2_out0, decoder_2_out2, decoder_2_out4, decoder_3_out0, decoder_3_out2, decoder_3_out4,
       or_1_out, or_2_out, or_4_out, or_5_out, or_6_out, or_8_out;

  or or_1 (or_1_out, A, C);
  or or_2 (or_2_out, C, B);
  Decoder #(.select(3), .enable("false")) decoder_1 (
    .out1(decoder_1_out1), .out3(decoder_1_out3), .out5(decoder_1_out5), .out6(decoder_1_out6),
    .out7(decoder_1_out7), .sel({A, B, C}));  // open: out0, out2, out4
  Decoder #(.select(3), .enable("false")) decoder_2 (
    .out0(decoder_2_out0), .out2(decoder_2_out2), .out4(decoder_2_out4), .sel({A, B, C}));  // open: out1, out3, out5, out6, out7
  Decoder #(.select(3), .enable("false")) decoder_3 (
    .out0(decoder_3_out0), .out2(decoder_3_out2), .out4(decoder_3_out4), .sel({A, B, C}));  // open: out1, out3, out5, out6, out7
  and and_1 (and_1_out, A, B);
  or or_3 (f_SOP, and_1_out, C);
  and and_2 (f_POS, or_1_out, or_2_out);
  or or_4 (or_4_out, decoder_1_out1, decoder_1_out3);
  or or_5 (or_5_out, decoder_1_out6, decoder_1_out7);
  and and_3 (and_3_out, ~decoder_2_out2, ~decoder_2_out4);  // AND_Gate
  or or_6 (or_6_out, decoder_3_out2, decoder_3_out4);
  or or_7 (f, or_4_out, or_8_out);
  or or_8 (or_8_out, decoder_1_out5, or_5_out);
  and and_4 (f_2, ~decoder_2_out0, and_3_out);  // AND_Gate
  nor nor_1 (f_3, decoder_3_out0, or_6_out);
endmodule

// C
module p5_11 (
  input  A,
  input  B,
  input  C,
  input  D,
  output f,
  output f_2,
  output f_3,
  output f_4
);

  wire decoder_1_out0, decoder_1_out2, decoder_1_out4, decoder_1_out5, decoder_2_out0, decoder_2_out4,
       decoder_3_out0, decoder_3_out2, decoder_4_out0, decoder_5_out0, decoder_6_out0, decoder_7_out0,
       decoder_8_out0, decoder_8_out1, decoder_8_out2, decoder_9_out0, decoder_9_out1, decoder_10_out0,
       decoder_10_out1, decoder_11_out0, decoder_12_out0, decoder_13_out0, decoder_14_out0, decoder_14_out2,
       decoder_15_out0, decoder_16_out0, decoder_17_out0, decoder_17_out1, decoder_18_out0, decoder_19_out0,
       decoder_20_out0, decoder_21_out0, not_1_out, or_1_out, or_2_out, or_3_out, or_4_out, or_5_out,
       or_6_out, or_7_out, or_8_out;

  not not_1 (not_1_out, A);
  Decoder #(.select(3), .disabled(0), .enable("false")) decoder_1 (
    .out0(decoder_1_out0), .out2(decoder_1_out2), .out4(decoder_1_out4), .out5(decoder_1_out5),
    .sel({A, B, C}));  // open: out1, out3, out6, out7
  Decoder #(.select(3), .disabled(0)) decoder_2 (
    .out0(decoder_2_out0), .out4(decoder_2_out4), .sel({B, C, D}), .en(not_1_out));  // open: out1, out2, out3, out5, out6, out7
  Decoder #(.select(3), .disabled(0)) decoder_3 (
    .out0(decoder_3_out0), .out2(decoder_3_out2), .sel({B, C, D}), .en(A));  // open: out1, out3, out4, out5, out6, out7
  Decoder #(.disabled(0)) decoder_4 (.out0(decoder_4_out0), .sel(D), .en(decoder_1_out0));  // open: out1
  Decoder #(.disabled(0)) decoder_5 (.out0(decoder_5_out0), .sel(D), .en(decoder_1_out2));  // open: out1
  Decoder #(.disabled(0)) decoder_6 (.out0(decoder_6_out0), .sel(D), .en(decoder_1_out4));  // open: out1
  Decoder #(.disabled(0)) decoder_7 (.out0(decoder_7_out0), .sel(D), .en(decoder_1_out5));  // open: out1
  or or_1 (or_1_out, decoder_2_out0, decoder_2_out4);
  or or_2 (or_2_out, decoder_3_out0, decoder_3_out2);
  or or_3 (or_3_out, decoder_4_out0, decoder_5_out0);
  or or_4 (or_4_out, decoder_6_out0, decoder_7_out0);
  nor nor_1 (f, or_1_out, or_2_out);
  nor nor_2 (f_3, or_3_out, or_4_out);
  Decoder #(.select(2), .enable("false")) decoder_8 (
    .out0(decoder_8_out0), .out1(decoder_8_out1), .out2(decoder_8_out2), .sel({A, B}));  // open: out3
  Decoder #(.disabled(0)) decoder_9 (.out0(decoder_9_out0), .out1(decoder_9_out1), .sel(B), .en(decoder_10_out0));
  Decoder #(.disabled(0), .enable("false")) decoder_10 (.out0(decoder_10_out0), .out1(decoder_10_out1), .sel(A));
  Decoder #(.disabled(0)) decoder_11 (.out0(decoder_11_out0), .sel(B), .en(decoder_10_out1));  // open: out1
  Decoder #(.select(2), .disabled(0)) decoder_12 (
    .out0(decoder_12_out0), .sel({C, D}), .en(decoder_8_out0));  // open: out1, out2, out3
  Decoder #(.select(2), .disabled(0)) decoder_13 (
    .out0(decoder_13_out0), .sel({C, D}), .en(decoder_8_out1));  // open: out1, out2, out3
  Decoder #(.select(2), .disabled(0)) decoder_14 (
    .out0(decoder_14_out0), .out2(decoder_14_out2), .sel({C, D}), .en(decoder_8_out2));  // open: out1, out3
  Decoder #(.disabled(0)) decoder_15 (.out0(decoder_15_out0), .sel(C), .en(decoder_9_out0));  // open: out1
  Decoder #(.disabled(0)) decoder_16 (.out0(decoder_16_out0), .sel(C), .en(decoder_9_out1));  // open: out1
  Decoder #(.disabled(0)) decoder_17 (.out0(decoder_17_out0), .out1(decoder_17_out1), .sel(C), .en(decoder_11_out0));
  or or_5 (or_5_out, decoder_12_out0, decoder_13_out0);
  or or_6 (or_6_out, decoder_14_out0, decoder_14_out2);
  Decoder #(.disabled(0)) decoder_18 (.out0(decoder_18_out0), .sel(D), .en(decoder_15_out0));  // open: out1
  or or_7 (or_7_out, decoder_18_out0, decoder_19_out0);
  Decoder #(.disabled(0)) decoder_19 (.out0(decoder_19_out0), .sel(D), .en(decoder_16_out0));  // open: out1
  or or_8 (or_8_out, decoder_20_out0, decoder_21_out0);
  Decoder #(.disabled(0)) decoder_20 (.out0(decoder_20_out0), .sel(D), .en(decoder_17_out0));  // open: out1
  Decoder #(.disabled(0)) decoder_21 (.out0(decoder_21_out0), .sel(D), .en(decoder_17_out1));  // open: out1
  nor nor_3 (f_2, or_5_out, or_6_out);
  nor nor_4 (f_4, or_7_out, or_8_out);
endmodule

module p5_12 (
  input  [2:0] ABC,
  output f
);

  wire [2:0] not_1_out;

  Multiplexer #(.select(3), .enable("false")) multiplexer_1 (
    .in0(1'b0), .in1(1'b0), .in2(1'b0), .in3(1'b1), .in4(1'b0), .in5(1'b0), .in6(1'b1), .in7(1'b1), .out(f),
    .sel(not_1_out));
  assign not_1_out = ~ABC;  // NOT_Gate not_1, 3 bits wide
endmodule

module p5_13 (
  input  C,
  input  B,
  input  A,
  output f
);

  wire multiplexer_1_out, not_1_out, not_2_out;

  Multiplexer #(.enable("false")) multiplexer_1 (.in0(C), .in1(not_1_out), .out(multiplexer_1_out), .sel(B));
  not not_1 (not_1_out, C);
  Multiplexer #(.enable("false")) multiplexer_2 (.in0(multiplexer_1_out), .in1(not_2_out), .out(f), .sel(A));
  not not_2 (not_2_out, multiplexer_1_out);
endmodule

module p5_14 (
  input  A,
  input  B,
  input  C,
  output f
);

  wire multiplexer_1_out, multiplexer_2_out, not_1_out;

  Multiplexer #(.select(2), .disabled(0)) multiplexer_1 (
    .in0(1'b1), .in1(1'b1), .in2(1'b1), .in3(1'b1), .out(multiplexer_1_out), .sel({B, C}), .en(not_1_out));
  Multiplexer #(.select(2), .disabled(0)) multiplexer_2 (
    .in0(1'b0), .in1(1'b1), .in2(1'b1), .in3(1'b0), .out(multiplexer_2_out), .sel({B, C}), .en(A));
  not not_1 (not_1_out, A);
  or or_1 (f, multiplexer_1_out, multiplexer_2_out);
endmodule

module p5_15 (
  input  A,
  input  B,
  input  C,
  input  D,
  input  E,
  output f
);

  wire multiplexer_1_out, multiplexer_3_out;

  Multiplexer #(.select(2), .enable("false")) multiplexer_1 (
    .in0(1'b0), .in1(1'b1), .in2(1'b1), .in3(1'b0), .out(multiplexer_1_out), .sel({A, B}));
  Multiplexer #(.enable("false")) multiplexer_2 (.in0(multiplexer_1_out), .in1(multiplexer_3_out), .out(f), .sel(E));
  Multiplexer #(.select(2), .enable("false")) multiplexer_3 (
    .in0(1'b1), .in1(1'b1), .in2(1'b0), .in3(1'b1), .out(multiplexer_3_out), .sel({C, D}));
endmodule

module p5_16 (
  input  C,
  input  A,
  input  B,
  output f
);

  wire decoder_1_out0, decoder_1_out1, decoder_1_out2, decoder_1_out3, multiplexer_1_out, nor_1_out;

  Decoder #(.select(2), .disabled(0), .enable("false")) decoder_1 (
    .out0(decoder_1_out0), .out1(decoder_1_out1), .out2(decoder_1_out2), .out3(decoder_1_out3), .sel({A, B}));
  Multiplexer #(.disabled(0), .enable("false")) multiplexer_1 (
    .in0(decoder_1_out0), .in1(decoder_1_out1), .out(multiplexer_1_out), .sel(C));
  nor nor_1 (nor_1_out, decoder_1_out2, decoder_1_out3);
  or or_1 (f, multiplexer_1_out, nor_1_out);
endmodule

module p5_17 (
  input  B,
  input  A,
  input  C,
  output f
);

  wire decoder_1_out0, decoder_1_out1, decoder_1_out2, multiplexer_1_out, or_1_out;

  Decoder #(.select(2), .enable("false")) decoder_1 (
    .out0(decoder_1_out0), .out1(decoder_1_out1), .out2(decoder_1_out2), .sel({A, B}));  // open: out3
  or or_1 (or_1_out, decoder_1_out0, decoder_1_out1);
  and and_1 (f, B, multiplexer_1_out);
  Multiplexer #(.select(2), .enable("false")) multiplexer_1 (
    .in0(1'b1), .in1(1'b0), .in2(decoder_1_out2), .in3(or_1_out), .out(multiplexer_1_out), .sel({A, C}));
endmodule

module p5_18 (
  input  A,
  input  B,
  input  C,
  input  D,
  output f
);

  wire decoder_1_out1, not_2_out;
  wire [1:1] multiplexer_1_out, not_1_out;

  Multiplexer #(.select(2), .enable("false")) multiplexer_1 (
    .in0(A), .in1(1'b0), .in2(B), .in3(1'b1), .out(multiplexer_1_out[1]), .sel({not_1_out[1], D}));
  not not_1 (not_1_out[1], C);
  not not_2 (not_2_out, decoder_1_out1);
  Decoder #(.select(2), .enable("false")) decoder_1 (
    .out1(decoder_1_out1), .sel({multiplexer_1_out[1], D}));  // open: out0, out2, out3
  nor nor_1 (f, multiplexer_1_out[1], not_2_out);
endmodule

module p5_19 (
  input  A,
  input  B,
  input  C,
  input  D,
  output f
);

  wire decoder_1_out2, decoder_1_out3, multiplexer_1_out;

  Decoder #(.select(2), .disabled(0)) decoder_1 (
    .out2(decoder_1_out2), .out3(decoder_1_out3), .sel({A, B}), .en(1'b1));  // open: out0, out1
  Multiplexer #(.select(2), .disabled(0)) multiplexer_1 (
    .in0(1'b1), .in1(1'b1), .in2(1'b0), .in3(1'b0), .out(multiplexer_1_out), .sel({C, D}), .en(decoder_1_out2));
  or or_1 (f, multiplexer_1_out, decoder_1_out3);
endmodule

module p5_20 (
  input  B,
  input  B_2,
  input  A,
  input  A_2,
  input  B_3,
  input  B_4,
  input  A_3,
  input  A_4,
  input  B_5,
  input  B_6,
  input  A_5,
  input  A_6,
  input  A_7,
  input  A_8,
  input  B_7,
  input  B_8,
  input  A_9,
  input  A_10,
  input  B_9,
  input  B_10,
  input  A_11,
  input  A_12,
  input  B_11,
  input  B_12,
  output AB,
  output AB__prime,
  output A_B,
  output A_B__prime,
  output A_xor_B,
  output A_xnor_B,
  output AB_2,
  output AB__prime_2,
  output A_B_2,
  output A_B__prime_2,
  output A_xor_B_2,
  output A_xnor_B_2
);

  wire not_1_out, not_2_out, not_3_out, not_4_out;

  Multiplexer #(.enable("false")) multiplexer_1 (.in0(1'b0), .in1(B), .out(AB), .sel(A));
  Multiplexer #(.enable("false")) multiplexer_2 (.in0(B_3), .in1(1'b1), .out(A_B), .sel(A_3));
  Multiplexer #(.enable("false")) multiplexer_3 (.in0(B_5), .in1(not_1_out), .out(A_xor_B), .sel(A_5));
  not not_1 (not_1_out, B_5);
  and and_1 (AB_2, A_7, B_7);
  or or_1 (A_B_2, A_9, B_9);
  xor xor_1 (A_xor_B_2, A_11, B_11);
  Multiplexer #(.enable("false")) multiplexer_4 (.in0(1'b1), .in1(not_2_out), .out(AB__prime), .sel(A_2));
  not not_2 (not_2_out, B_2);
  not not_3 (not_3_out, B_4);
  Multiplexer #(.enable("false")) multiplexer_5 (.in0(not_3_out), .in1(1'b0), .out(A_B__prime), .sel(A_4));
  not not_4 (not_4_out, B_6);
  Multiplexer #(.enable("false")) multiplexer_6 (.in0(not_4_out), .in1(B_6), .out(A_xnor_B), .sel(A_6));
  nand nand_1 (AB__prime_2, A_8, B_8);
  nor nor_1 (A_B__prime_2, A_10, B_10);
  xnor xnor_1 (A_xnor_B_2, A_12, B_12);
endmodule

module p5_21 (
  input  A,
  input  A_2,
  input  B,
  input  C,
  input  B_2,
  input  C_2,
  input  A_3,
  input  B_3,
  input  C_3,
  output f,
  output f_2,
  output f_3
);

  wire multiplexer_2_out;

  Multiplexer #(.enable("false")) multiplexer_1 (.in0(1'b0), .in1(multiplexer_2_out), .out(f), .sel(C));
  Multiplexer #(.enable("false")) multiplexer_2 (.in0(1'b0), .in1(A_2), .out(multiplexer_2_out), .sel(B));
  Multiplexer #(.select(2), .enable("false")) multiplexer_3 (
    .in0(1'b0), .in1(1'b0), .in2(1'b0), .in3(A), .out(f_2), .sel({B_2, C_2}));
  Multiplexer #(.select(3), .enable("false")) multiplexer_4 (
    .in0(1'b0), .in1(1'b0), .in2(1'b0), .in3(1'b0), .in4(1'b0), .in5(1'b0), .in6(1'b0), .in7(1'b1),
    .out(f_3), .sel({C_3, B_3, A_3}));
endmodule

module p5_22 (
  input  A,
  input  B,
  input  C,
  output f,
  output f_2,
  output f_3
);

  wire multiplexer_1_out, nand_1_out, not_1_out, not_2_out;

  nand nand_1 (nand_1_out, A, C);
  not not_1 (not_1_out, C);
  Multiplexer #(.enable("false")) multiplexer_1 (.in0(1'b1), .in1(not_2_out), .out(multiplexer_1_out), .sel(C));
  not not_2 (not_2_out, A);
  Multiplexer #(.enable("false")) multiplexer_2 (.in0(nand_1_out), .in1(C), .out(f), .sel(B));
  Multiplexer #(.select(2), .enable("false")) multiplexer_3 (
    .in0(1'b1), .in1(C), .in2(not_1_out), .in3(C), .out(f_2), .sel({A, B}));
  Multiplexer #(.enable("false")) multiplexer_4 (.in0(multiplexer_1_out), .in1(C), .out(f_3), .sel(B));
endmodule

module p5_23 (
  input  A,
  input  B,
  input  C,
  input  D,
  output f,
  output f_2,
  output f_3,
  output f_4,
  output f_5,
  output f_6
);

  wire and_1_out, and_2_out, and_3_out, and_4_out, multiplexer_7_out, or_1_out, or_2_out;

  Multiplexer #(.select(3), .disabled(0), .enable("false")) multiplexer_1 (
    .in0(D), .in1(1'b0), .in2(D), .in3(1'b0), .in4(D), .in5(1'b1), .in6(D), .in7(1'b0), .out(f),
    .sel({A, B, C}));
  Multiplexer #(.select(2), .disabled(0), .enable("false")) multiplexer_2 (
    .in0(D), .in1(A), .in2(D), .in3(1'b0), .out(f_4), .sel({B, C}));
  and and_1 (and_1_out, ~C, D);  // AND_Gate
  or or_1 (or_1_out, and_1_out, and_2_out);
  and and_2 (and_2_out, C, ~B);  // AND_Gate
  and and_3 (and_3_out, ~C, D);  // AND_Gate
  or or_2 (or_2_out, C, D);
  Multiplexer #(.disabled(0), .enable("false")) multiplexer_3 (.in0(and_1_out), .in1(or_1_out), .out(f_3), .sel(A));
  Multiplexer #(.disabled(0), .enable("false")) multiplexer_4 (.in0(D), .in1(and_4_out), .out(f_5), .sel(C));
  and and_4 (and_4_out, A, ~B);  // AND_Gate
  Multiplexer #(.select(2), .disabled(0), .enable("false")) multiplexer_5 (
    .in0(and_3_out), .in1(and_3_out), .in2(or_2_out), .in3(and_3_out), .out(f_2), .sel({A, B}));
  Multiplexer #(.disabled(0), .enable("false")) multiplexer_6 (.in0(D), .in1(multiplexer_7_out), .out(f_6), .sel(C));
  Multiplexer #(.disabled(0), .enable("false")) multiplexer_7 (.in0(A), .in1(1'b0), .out(multiplexer_7_out), .sel(B));
endmodule

module p5_23_netMUX (
  input  A,
  input  B,
  input  C,
  input  D,
  output f,
  output f_2,
  output f_3,
  output f_4,
  output f_5,
  output f_6,
  output f_7,
  output f_8
);

  wire multiplexer_2_out, multiplexer_3_out, multiplexer_4_out, multiplexer_5_out, multiplexer_6_out,
       multiplexer_7_out, multiplexer_8_out, multiplexer_9_out, multiplexer_11_out, multiplexer_13_out,
       multiplexer_14_out, multiplexer_15_out, multiplexer_16_out, multiplexer_17_out, multiplexer_18_out,
       multiplexer_19_out, multiplexer_20_out, multiplexer_21_out, multiplexer_22_out, multiplexer_23_out,
       multiplexer_24_out, multiplexer_25_out, multiplexer_26_out, multiplexer_27_out, multiplexer_30_out,
       multiplexer_31_out, multiplexer_32_out, multiplexer_33_out, multiplexer_34_out, multiplexer_35_out,
       multiplexer_36_out, multiplexer_37_out, multiplexer_38_out, multiplexer_39_out, multiplexer_41_out,
       multiplexer_42_out, multiplexer_43_out, multiplexer_44_out, multiplexer_45_out, multiplexer_46_out,
       multiplexer_47_out, multiplexer_48_out, multiplexer_50_out, multiplexer_51_out, multiplexer_52_out,
       multiplexer_53_out, multiplexer_54_out, multiplexer_55_out, multiplexer_56_out, multiplexer_57_out,
       multiplexer_58_out, multiplexer_59_out, multiplexer_60_out, multiplexer_61_out, multiplexer_62_out,
       multiplexer_63_out;

  Multiplexer #(.select(4), .enable("false")) multiplexer_1 (
    .in0(1'b0), .in1(1'b1), .in2(1'b0), .in3(1'b0), .in4(1'b0), .in5(1'b1), .in6(1'b0), .in7(1'b0),
    .in8(1'b0), .in9(1'b1), .in10(1'b1), .in11(1'b1), .in12(1'b0), .in13(1'b1), .in14(1'b0), .in15(1'b0),
    .out(f), .sel({A, B, C, D}));
  Multiplexer #(.enable("false")) multiplexer_2 (.in0(1'b0), .in1(1'b1), .out(multiplexer_2_out), .sel(D));
  Multiplexer #(.enable("false")) multiplexer_3 (.in0(1'b0), .in1(1'b0), .out(multiplexer_3_out), .sel(D));
  Multiplexer #(.enable("false")) multiplexer_4 (.in0(1'b0), .in1(1'b1), .out(multiplexer_4_out), .sel(D));
  Multiplexer #(.enable("false")) multiplexer_5 (.in0(1'b0), .in1(1'b0), .out(multiplexer_5_out), .sel(D));
  Multiplexer #(.enable("false")) multiplexer_6 (.in0(1'b0), .in1(1'b1), .out(multiplexer_6_out), .sel(D));
  Multiplexer #(.enable("false")) multiplexer_7 (.in0(1'b1), .in1(1'b1), .out(multiplexer_7_out), .sel(D));
  Multiplexer #(.enable("false")) multiplexer_8 (.in0(1'b0), .in1(1'b1), .out(multiplexer_8_out), .sel(D));
  Multiplexer #(.enable("false")) multiplexer_9 (.in0(1'b0), .in1(1'b0), .out(multiplexer_9_out), .sel(D));
  Multiplexer #(.select(3), .enable("false")) multiplexer_10 (
    .in0(multiplexer_2_out), .in1(multiplexer_3_out), .in2(multiplexer_4_out), .in3(multiplexer_5_out),
    .in4(multiplexer_6_out), .in5(multiplexer_7_out), .in6(multiplexer_8_out), .in7(multiplexer_9_out),
    .out(f_5), .sel({A, B, C}));
  Multiplexer #(.select(3), .enable("false")) multiplexer_11 (
    .in0(1'b0), .in1(1'b1), .in2(1'b0), .in3(1'b0), .in4(1'b0), .in5(1'b1), .in6(1'b0), .in7(1'b0),
    .out(multiplexer_11_out), .sel({B, C, D}));
  Multiplexer #(.enable("false")) multiplexer_12 (
    .in0(multiplexer_11_out), .in1(multiplexer_13_out), .out(f_2), .sel(A));
  Multiplexer #(.select(3), .enable("false")) multiplexer_13 (
    .in0(1'b0), .in1(1'b1), .in2(1'b1), .in3(1'b1), .in4(1'b0), .in5(1'b1), .in6(1'b0), .in7(1'b0),
    .out(multiplexer_13_out), .sel({B, C, D}));
  Multiplexer #(.enable("false")) multiplexer_14 (.in0(1'b0), .in1(1'b1), .out(multiplexer_14_out), .sel(D));
  Multiplexer #(.enable("false")) multiplexer_15 (.in0(1'b0), .in1(1'b0), .out(multiplexer_15_out), .sel(D));
  Multiplexer #(.enable("false")) multiplexer_16 (.in0(1'b0), .in1(1'b1), .out(multiplexer_16_out), .sel(D));
  Multiplexer #(.enable("false")) multiplexer_17 (.in0(1'b0), .in1(1'b0), .out(multiplexer_17_out), .sel(D));
  Multiplexer #(.enable("false")) multiplexer_18 (.in0(1'b0), .in1(1'b1), .out(multiplexer_18_out), .sel(D));
  Multiplexer #(.enable("false")) multiplexer_19 (.in0(1'b1), .in1(1'b1), .out(multiplexer_19_out), .sel(D));
  Multiplexer #(.enable("false")) multiplexer_20 (.in0(1'b0), .in1(1'b1), .out(multiplexer_20_out), .sel(D));
  Multiplexer #(.enable("false")) multiplexer_21 (.in0(1'b0), .in1(1'b0), .out(multiplexer_21_out), .sel(D));
  Multiplexer #(.select(2), .enable("false")) multiplexer_22 (
    .in0(multiplexer_14_out), .in1(multiplexer_15_out), .in2(multiplexer_16_out), .in3(multiplexer_17_out),
    .out(multiplexer_22_out), .sel({B, C}));
  Multiplexer #(.select(2), .enable("false")) multiplexer_23 (
    .in0(multiplexer_18_out), .in1(multiplexer_19_out), .in2(multiplexer_20_out), .in3(multiplexer_21_out),
    .out(multiplexer_23_out), .sel({B, C}));
  Multiplexer #(.select(2), .enable("false")) multiplexer_24 (
    .in0(1'b0), .in1(1'b1), .in2(1'b0), .in3(1'b0), .out(multiplexer_24_out), .sel({C, D}));
  Multiplexer #(.select(2), .enable("false")) multiplexer_25 (
    .in0(1'b0), .in1(1'b1), .in2(1'b0), .in3(1'b0), .out(multiplexer_25_out), .sel({C, D}));
  Multiplexer #(.select(2), .enable("false")) multiplexer_26 (
    .in0(1'b0), .in1(1'b1), .in2(1'b1), .in3(1'b1), .out(multiplexer_26_out), .sel({C, D}));
  Multiplexer #(.select(2), .enable("false")) multiplexer_27 (
    .in0(1'b0), .in1(1'b1), .in2(1'b0), .in3(1'b0), .out(multiplexer_27_out), .sel({C, D}));
  Multiplexer #(.enable("false")) multiplexer_28 (
    .in0(multiplexer_22_out), .in1(multiplexer_23_out), .out(f_6), .sel(A));
  Multiplexer #(.select(2), .enable("false")) multiplexer_29 (
    .in0(multiplexer_24_out), .in1(multiplexer_25_out), .in2(multiplexer_26_out), .in3(multiplexer_27_out),
    .out(f_3), .sel({A, B}));
  Multiplexer #(.enable("false")) multiplexer_30 (.in0(1'b0), .in1(1'b1), .out(multiplexer_30_out), .sel(D));
  Multiplexer #(.enable("false")) multiplexer_31 (.in0(1'b0), .in1(1'b0), .out(multiplexer_31_out), .sel(D));
  Multiplexer #(.enable("false")) multiplexer_32 (.in0(1'b0), .in1(1'b1), .out(multiplexer_32_out), .sel(D));
  Multiplexer #(.enable("false")) multiplexer_33 (.in0(1'b0), .in1(1'b0), .out(multiplexer_33_out), .sel(D));
  Multiplexer #(.enable("false")) multiplexer_34 (.in0(1'b0), .in1(1'b1), .out(multiplexer_34_out), .sel(D));
  Multiplexer #(.enable("false")) multiplexer_35 (.in0(1'b1), .in1(1'b1), .out(multiplexer_35_out), .sel(D));
  Multiplexer #(.enable("false")) multiplexer_36 (.in0(1'b0), .in1(1'b1), .out(multiplexer_36_out), .sel(D));
  Multiplexer #(.enable("false")) multiplexer_37 (.in0(1'b0), .in1(1'b0), .out(multiplexer_37_out), .sel(D));
  Multiplexer #(.enable("false")) multiplexer_38 (
    .in0(multiplexer_30_out), .in1(multiplexer_31_out), .out(multiplexer_38_out), .sel(C));
  Multiplexer #(.enable("false")) multiplexer_39 (
    .in0(multiplexer_32_out), .in1(multiplexer_33_out), .out(multiplexer_39_out), .sel(C));
  Multiplexer #(.select(2), .enable("false")) multiplexer_40 (
    .in0(multiplexer_38_out), .in1(multiplexer_39_out), .in2(multiplexer_41_out), .in3(multiplexer_42_out),
    .out(f_7), .sel({A, B}));
  Multiplexer #(.enable("false")) multiplexer_41 (
    .in0(multiplexer_34_out), .in1(multiplexer_35_out), .out(multiplexer_41_out), .sel(C));
  Multiplexer #(.enable("false")) multiplexer_42 (
    .in0(multiplexer_36_out), .in1(multiplexer_37_out), .out(multiplexer_42_out), .sel(C));
  Multiplexer #(.select(2), .enable("false")) multiplexer_43 (
    .in0(1'b0), .in1(1'b1), .in2(1'b0), .in3(1'b0), .out(multiplexer_43_out), .sel({C, D}));
  Multiplexer #(.enable("false")) multiplexer_44 (
    .in0(multiplexer_43_out), .in1(multiplexer_45_out), .out(multiplexer_44_out), .sel(B));
  Multiplexer #(.select(2), .enable("false")) multiplexer_45 (
    .in0(1'b0), .in1(1'b1), .in2(1'b0), .in3(1'b0), .out(multiplexer_45_out), .sel({C, D}));
  Multiplexer #(.select(2), .enable("false")) multiplexer_46 (
    .in0(1'b0), .in1(1'b1), .in2(1'b1), .in3(1'b1), .out(multiplexer_46_out), .sel({C, D}));
  Multiplexer #(.enable("false")) multiplexer_47 (
    .in0(multiplexer_46_out), .in1(multiplexer_48_out), .out(multiplexer_47_out), .sel(B));
  Multiplexer #(.select(2), .enable("false")) multiplexer_48 (
    .in0(1'b0), .in1(1'b1), .in2(1'b0), .in3(1'b0), .out(multiplexer_48_out), .sel({C, D}));
  Multiplexer #(.enable("false")) multiplexer_49 (
    .in0(multiplexer_44_out), .in1(multiplexer_47_out), .out(f_4), .sel(A));
  Multiplexer #(.enable("false")) multiplexer_50 (.in0(1'b0), .in1(1'b1), .out(multiplexer_50_out), .sel(D));
  Multiplexer #(.enable("false")) multiplexer_51 (
    .in0(multiplexer_50_out), .in1(multiplexer_52_out), .out(multiplexer_51_out), .sel(C));
  Multiplexer #(.enable("false")) multiplexer_52 (.in0(1'b0), .in1(1'b0), .out(multiplexer_52_out), .sel(D));
  Multiplexer #(.enable("false")) multiplexer_53 (.in0(1'b0), .in1(1'b1), .out(multiplexer_53_out), .sel(D));
  Multiplexer #(.enable("false")) multiplexer_54 (
    .in0(multiplexer_53_out), .in1(multiplexer_55_out), .out(multiplexer_54_out), .sel(C));
  Multiplexer #(.enable("false")) multiplexer_55 (.in0(1'b0), .in1(1'b0), .out(multiplexer_55_out), .sel(D));
  Multiplexer #(.enable("false")) multiplexer_56 (.in0(1'b0), .in1(1'b1), .out(multiplexer_56_out), .sel(D));
  Multiplexer #(.enable("false")) multiplexer_57 (
    .in0(multiplexer_56_out), .in1(multiplexer_58_out), .out(multiplexer_57_out), .sel(C));
  Multiplexer #(.enable("false")) multiplexer_58 (.in0(1'b1), .in1(1'b1), .out(multiplexer_58_out), .sel(D));
  Multiplexer #(.enable("false")) multiplexer_59 (.in0(1'b0), .in1(1'b1), .out(multiplexer_59_out), .sel(D));
  Multiplexer #(.enable("false")) multiplexer_60 (
    .in0(multiplexer_59_out), .in1(multiplexer_61_out), .out(multiplexer_60_out), .sel(C));
  Multiplexer #(.enable("false")) multiplexer_61 (.in0(1'b0), .in1(1'b0), .out(multiplexer_61_out), .sel(D));
  Multiplexer #(.enable("false")) multiplexer_62 (
    .in0(multiplexer_51_out), .in1(multiplexer_54_out), .out(multiplexer_62_out), .sel(B));
  Multiplexer #(.enable("false")) multiplexer_63 (
    .in0(multiplexer_57_out), .in1(multiplexer_60_out), .out(multiplexer_63_out), .sel(B));
  Multiplexer #(.enable("false")) multiplexer_64 (
    .in0(multiplexer_62_out), .in1(multiplexer_63_out), .out(f_8), .sel(A));
endmodule

module p5_24 (
  input  A,
  input  B,
  input  C,
  input  D,
  output f,
  output f_2,
  output f_3
);

  wire and_1_out, multiplexer_3_out, multiplexer_5_out, not_1_out, or_1_out;

  not not_1 (not_1_out, D);
  Multiplexer #(.select(2), .enable("false")) multiplexer_1 (
    .in0(1'b1), .in1(1'b0), .in2(A), .in3(not_1_out), .out(f), .sel({B, C}));
  or or_1 (or_1_out, A, ~B);  // OR_Gate
  Multiplexer #(.enable("false")) multiplexer_2 (.in0(or_1_out), .in1(and_1_out), .out(f_2), .sel(C));
  and and_1 (and_1_out, B, ~D);  // AND_Gate
  Multiplexer #(.enable("false")) multiplexer_3 (.in0(1'b1), .in1(A), .out(multiplexer_3_out), .sel(B));
  Multiplexer #(.enable("false")) multiplexer_4 (.in0(multiplexer_3_out), .in1(multiplexer_5_out), .out(f_3), .sel(C));
  Multiplexer #(.enable("false")) multiplexer_5 (.in0(B), .in1(1'b0), .out(multiplexer_5_out), .sel(D));
endmodule

module p5_25 (
  input  D,
  input  A,
  input  B,
  input  C,
  input  C_2,
  input  D_2,
  input  D_3,
  input  A_2,
  input  B_2,
  input  C_3,
  input  B_3,
  input  A_3,
  output f,
  output f_2,
  output f_3
);

  wire or_1_out, or_2_out;

  or or_1 (or_1_out, C_2, D_3);
  Multiplexer #(.select(3), .enable("false")) multiplexer_1 (
    .in0(D), .in1(1'b1), .in2(D), .in3(1'b1), .in4(D), .in5(1'b1), .in6(D), .in7(D), .out(f), .sel({A, B, C}));
  Multiplexer #(.select(2), .enable("false")) multiplexer_2 (
    .in0(or_1_out), .in1(or_1_out), .in2(or_1_out), .in3(D_3), .out(f_3), .sel({A_3, B_3}));
  Multiplexer #(.enable("false")) multiplexer_3 (.in0(D_2), .in1(or_2_out), .out(f_2), .sel(C_3));
  or or_2 (or_2_out, D_2, ~A_2, ~B_2);  // OR_Gate
endmodule

module p5_26 (
  input  A,
  input  B,
  input  C,
  output f,
  output f_2,
  output f_3,
  output f_4
);

  wire and_1_out, multiplexer_4_out, multiplexer_5_out, multiplexer_6_out, not_1_out, not_2_out, or_1_out,
       xor_1_out;

  or or_1 (or_1_out, B, C);
  and and_1 (and_1_out, ~B, ~C);  // AND_Gate
  not not_1 (not_1_out, C);
  Multiplexer #(.disabled(0), .enable("false")) multiplexer_1 (.in0(or_1_out), .in1(and_1_out), .out(f_2), .sel(A));
  Multiplexer #(.select(2), .enable("false")) multiplexer_2 (
    .in0(C), .in1(1'b1), .in2(not_1_out), .in3(1'b0), .out(f), .sel({A, B}));
  xor xor_1 (xor_1_out, C, A);
  Multiplexer #(.disabled(0), .enable("false")) multiplexer_3 (.in0(xor_1_out), .in1(not_2_out), .out(f_3), .sel(B));
  not not_2 (not_2_out, A);
  Multiplexer #(.disabled(0), .enable("false")) multiplexer_4 (
    .in0(1'b1), .in1(1'b0), .out(multiplexer_4_out), .sel(C));
  Multiplexer #(.disabled(0), .enable("false")) multiplexer_5 (
    .in0(C), .in1(multiplexer_4_out), .out(multiplexer_5_out), .sel(A));
  Multiplexer #(.disabled(0), .enable("false")) multiplexer_6 (
    .in0(1'b1), .in1(1'b0), .out(multiplexer_6_out), .sel(A));
  Multiplexer #(.disabled(0), .enable("false")) multiplexer_7 (
    .in0(multiplexer_5_out), .in1(multiplexer_6_out), .out(f_4), .sel(B));
endmodule

module p5_27 (
  input  A,
  input  B,
  input  C,
  output f,
  output f_2,
  output f_3,
  output f_4
);

  wire multiplexer_2_out, multiplexer_3_out, multiplexer_5_out, multiplexer_6_out, multiplexer_7_out,
       multiplexer_8_out, multiplexer_10_out, multiplexer_11_out, multiplexer_12_out, multiplexer_13_out,
       multiplexer_14_out, multiplexer_16_out;

  Multiplexer #(.select(3), .enable("false")) multiplexer_1 (
    .in0(1'b1), .in1(1'b1), .in2(1'b0), .in3(1'b1), .in4(1'b1), .in5(1'b0), .in6(1'b0), .in7(1'b1), .out(f),
    .sel({A, B, C}));
  Multiplexer #(.select(2), .enable("false")) multiplexer_2 (
    .in0(1'b1), .in1(1'b1), .in2(1'b0), .in3(1'b1), .out(multiplexer_2_out), .sel({B, C}));
  Multiplexer #(.select(2), .enable("false")) multiplexer_3 (
    .in0(1'b1), .in1(1'b0), .in2(1'b0), .in3(1'b1), .out(multiplexer_3_out), .sel({B, C}));
  Multiplexer #(.enable("false")) multiplexer_4 (.in0(multiplexer_2_out), .in1(multiplexer_3_out), .out(f_2), .sel(A));
  Multiplexer #(.enable("false")) multiplexer_5 (.in0(1'b1), .in1(1'b1), .out(multiplexer_5_out), .sel(C));
  Multiplexer #(.enable("false")) multiplexer_6 (.in0(1'b0), .in1(1'b1), .out(multiplexer_6_out), .sel(C));
  Multiplexer #(.enable("false")) multiplexer_7 (.in0(1'b1), .in1(1'b0), .out(multiplexer_7_out), .sel(C));
  Multiplexer #(.enable("false")) multiplexer_8 (.in0(1'b0), .in1(1'b1), .out(multiplexer_8_out), .sel(C));
  Multiplexer #(.select(2), .enable("false")) multiplexer_9 (
    .in0(multiplexer_5_out), .in1(multiplexer_6_out), .in2(multiplexer_7_out), .in3(multiplexer_8_out),
    .out(f_3), .sel({A, B}));
  Multiplexer #(.enable("false")) multiplexer_10 (.in0(1'b1), .in1(1'b1), .out(multiplexer_10_out), .sel(C));
  Multiplexer #(.enable("false")) multiplexer_11 (.in0(1'b0), .in1(1'b1), .out(multiplexer_11_out), .sel(C));
  Multiplexer #(.enable("false")) multiplexer_12 (.in0(1'b1), .in1(1'b0), .out(multiplexer_12_out), .sel(C));
  Multiplexer #(.enable("false")) multiplexer_13 (.in0(1'b0), .in1(1'b1), .out(multiplexer_13_out), .sel(C));
  Multiplexer #(.enable("false")) multiplexer_14 (
    .in0(multiplexer_10_out), .in1(multiplexer_11_out), .out(multiplexer_14_out), .sel(B));
  Multiplexer #(.enable("false")) multiplexer_15 (
    .in0(multiplexer_14_out), .in1(multiplexer_16_out), .out(f_4), .sel(A));
  Multiplexer #(.enable("false")) multiplexer_16 (
    .in0(multiplexer_12_out), .in1(multiplexer_13_out), .out(multiplexer_16_out), .sel(B));
endmodule

module p5_28 (
  input  A,
  input  B,
  input  C,
  input  D,
  output f,
  output f_2,
  output f_3
);

  wire and_1_out, and_2_out, multiplexer_1_out, multiplexer_2_out, or_1_out, xnor_1_out, xor_1_out;

  and and_1 (and_1_out, D, A);
  xor xor_1 (xor_1_out, A, C);
  Multiplexer #(.select(2), .disabled(0), .enable("false")) multiplexer_1 (
    .in0(1'b0), .in1(1'b0), .in2(1'b1), .in3(1'b0), .out(multiplexer_1_out), .sel({C, D}));
  Multiplexer #(.select(2), .disabled(0), .enable("false")) multiplexer_2 (
    .in0(1'b1), .in1(1'b1), .in2(1'b0), .in3(1'b1), .out(multiplexer_2_out), .sel({C, D}));
  and and_2 (and_2_out, ~and_1_out, C);  // AND_Gate
  Multiplexer #(.disabled(0), .enable("false")) multiplexer_3 (.in0(and_2_out), .in1(or_1_out), .out(f_3), .sel(B));
  or or_1 (or_1_out, and_1_out, xor_1_out);
  Multiplexer #(.select(2), .disabled(0), .enable("false")) multiplexer_4 (
    .in0(C), .in1(C), .in2(multiplexer_1_out), .in3(multiplexer_2_out), .out(f), .sel({A, B}));
  xnor xnor_1 (xnor_1_out, B, D);
  Multiplexer #(.select(2), .disabled(0), .enable("false")) multiplexer_5 (
    .in0(1'b0), .in1(1'b1), .in2(B), .in3(xnor_1_out), .out(f_2), .sel({A, C}));
endmodule

module p5_29 (
  input  A,
  input  B,
  input  C,
  input  D,
  output f,
  output f_2,
  output f_3,
  output f_4,
  output f_5
);

  wire and_1_out, and_2_out, decoder_1_out0, decoder_1_out1, decoder_1_out2, decoder_1_out3,
       multiplexer_1_out, multiplexer_3_out, multiplexer_4_out, multiplexer_5_out, multiplexer_6_out,
       multiplexer_7_out, multiplexer_8_out, multiplexer_9_out, multiplexer_10_out, multiplexer_11_out,
       nand_1_out, not_1_out, not_2_out, not_3_out, not_4_out, not_5_out, not_6_out, not_7_out, or_2_out;

  Decoder #(.select(2), .enable("false")) decoder_1 (
    .out0(decoder_1_out0), .out1(decoder_1_out1), .out2(decoder_1_out2), .out3(decoder_1_out3), .sel({A, B}));
  not not_1 (not_1_out, C);
  not not_2 (not_2_out, A);
  not not_3 (not_3_out, B);
  Multiplexer #(.disabled(0), .enable("false")) multiplexer_1 (
    .in0(not_1_out), .in1(B), .out(multiplexer_1_out), .sel(A));
  Multiplexer #(.disabled(0), .enable("false")) multiplexer_2 (
    .in0(multiplexer_1_out), .in1(multiplexer_3_out), .out(f_5), .sel(D));
  Multiplexer #(.disabled(0), .enable("false")) multiplexer_3 (
    .in0(not_2_out), .in1(not_3_out), .out(multiplexer_3_out), .sel(C));
  Multiplexer #(.select(2), .disabled(0)) multiplexer_4 (
    .in0(1'b1), .in1(1'b1), .in2(1'b0), .in3(1'b1), .out(multiplexer_4_out), .sel({C, D}), .en(decoder_1_out0));
  Multiplexer #(.select(2), .disabled(0)) multiplexer_5 (
    .in0(1'b1), .in1(1'b1), .in2(1'b0), .in3(1'b0), .out(multiplexer_5_out), .sel({C, D}), .en(decoder_1_out1));
  or or_1 (f, multiplexer_4_out, multiplexer_5_out, multiplexer_6_out, multiplexer_7_out);
  Multiplexer #(.select(2), .disabled(0)) multiplexer_6 (
    .in0(1'b0), .in1(1'b0), .in2(1'b0), .in3(1'b1), .out(multiplexer_6_out), .sel({C, D}), .en(decoder_1_out2));
  Multiplexer #(.select(2), .disabled(0)) multiplexer_7 (
    .in0(1'b1), .in1(1'b0), .in2(1'b1), .in3(1'b0), .out(multiplexer_7_out), .sel({C, D}), .en(decoder_1_out3));
  Multiplexer #(.select(2), .disabled(0), .enable("false")) multiplexer_8 (
    .in0(1'b1), .in1(1'b1), .in2(1'b0), .in3(1'b1), .out(multiplexer_8_out), .sel({C, D}));
  Multiplexer #(.select(2), .disabled(0), .enable("false")) multiplexer_9 (
    .in0(1'b1), .in1(1'b1), .in2(1'b0), .in3(1'b0), .out(multiplexer_9_out), .sel({C, D}));
  Multiplexer #(.select(2), .disabled(0), .enable("false")) multiplexer_10 (
    .in0(1'b0), .in1(1'b0), .in2(1'b0), .in3(1'b1), .out(multiplexer_10_out), .sel({C, D}));
  Multiplexer #(.select(2), .disabled(0), .enable("false")) multiplexer_11 (
    .in0(1'b1), .in1(1'b0), .in2(1'b1), .in3(1'b0), .out(multiplexer_11_out), .sel({C, D}));
  Multiplexer #(.select(2), .disabled(0), .enable("false")) multiplexer_12 (
    .in0(multiplexer_8_out), .in1(multiplexer_9_out), .in2(multiplexer_10_out), .in3(multiplexer_11_out),
    .out(f_2), .sel({A, B}));
  not not_4 (not_4_out, C);
  or or_2 (or_2_out, not_4_out, D);
  and and_1 (and_1_out, C, D);
  not not_5 (not_5_out, D);
  Multiplexer #(.select(2), .enable("false")) multiplexer_13 (
    .in0(or_2_out), .in1(not_4_out), .in2(and_1_out), .in3(not_5_out), .out(f_3), .sel({A, B}));
  not not_6 (not_6_out, D);
  and and_2 (and_2_out, A, not_6_out);
  not not_7 (not_7_out, A);
  Multiplexer #(.select(2), .enable("false")) multiplexer_14 (
    .in0(not_7_out), .in1(D), .in2(nand_1_out), .in3(and_2_out), .out(f_4), .sel({B, C}));
  nand nand_1 (nand_1_out, A, D);
endmodule

module p5_30 (
  input  A3,
  input  A2,
  input  A1,
  input  A0,
  output a3_2,
  output a2_2,
  output a1_2,
  output a0_2
);

  wire not_1_out, not_2_out, not_3_out;

  not not_1 (not_1_out, A3);
  not not_2 (not_2_out, A2);
  not not_3 (not_3_out, A1);
  and and_1 (a2_2, not_1_out, A2);
  and and_2 (a1_2, not_1_out, not_2_out, A1);
  and and_3 (a0_2, not_1_out, not_2_out, not_3_out, A0);

  assign a3_2 = A3;
endmodule

module p5_31 (
  input  C,
  input  B,
  input  A,
  output f,
  output g,
  output h
);

  wire decoder_1_out0, decoder_1_out1, decoder_1_out2, decoder_1_out3;

  Decoder #(.select(3), .disabled(0)) decoder_1 (
    .out0(decoder_1_out0), .out1(decoder_1_out1), .out2(decoder_1_out2), .out3(decoder_1_out3),
    .sel({C, B, A}), .en(C));  // open: out4, out5, out6, out7
  Priority_Encoder #(.disabled(0)) priority_encoder_1 (
    .in2(decoder_1_out0), .in3(decoder_1_out1), .in4(decoder_1_out2), .in5(decoder_1_out3), .out({h, g, f}),
    .en_in(decoder_1_out0));  // open: in0, in1, in6, in7, gs, en_out

  // Notes on the sheet:
  //   Ei
endmodule

module p5_32 (
  input  A,
  input  B,
  input  C,
  output f,
  output g,
  output h,
  output f_2,
  output g_2,
  output h_2
);

  wire decoder_1_out0, decoder_1_out1, decoder_1_out2, decoder_1_out3, decoder_1_out4, decoder_1_out5,
       decoder_1_out6, decoder_1_out7;
  wire [7:0] decoder_2_out0;

  Decoder #(.select(3), .disabled(0)) decoder_1 (
    .out0(decoder_1_out0), .out1(decoder_1_out1), .out2(decoder_1_out2), .out3(decoder_1_out3),
    .out4(decoder_1_out4), .out5(decoder_1_out5), .out6(decoder_1_out6), .out7(decoder_1_out7),
    .sel({C, B, A}), .en(1'b1));
  Decoder #(.select(3), .disabled(0)) decoder_2 (
    .out0(decoder_2_out0[0]), .out1(decoder_2_out0[1]), .out2(decoder_2_out0[2]), .out3(decoder_2_out0[3]),
    .out4(decoder_2_out0[4]), .out5(decoder_2_out0[5]), .out6(decoder_2_out0[6]), .out7(decoder_2_out0[7]),
    .sel({C, B, A}), .en(1'b1));
  Priority_Encoder #(.disabled(0)) priority_encoder_1 (
    .in0(decoder_1_out0), .in1(decoder_1_out3), .in2(decoder_1_out1), .in3(decoder_1_out4),
    .in4(decoder_1_out7), .in5(decoder_1_out5), .in6(decoder_1_out6), .in7(decoder_1_out2), .out({h, g, f}),
    .en_in(1'b1));  // open: gs, en_out
  Priority_Encoder #(.disabled(0)) priority_encoder_2 (
    .in0(decoder_2_out0[0]), .in1(decoder_2_out0[3]), .in2(decoder_2_out0[1]), .in3(decoder_2_out0[4]),
    .in4(decoder_2_out0[7]), .in5(decoder_2_out0[5]), .in6(decoder_2_out0[6]), .in7(decoder_2_out0[2]),
    .out({h_2, g_2, f_2}), .en_in(1'b1));  // open: gs, en_out
endmodule

module p5_33 (
  input  A,
  input  B,
  input  C,
  output f,
  output f_2
);

  wire demultiplexer_1_out0, demultiplexer_1_out3, xnor_1_out;

  Demultiplexer #(.select(2), .disabled(0), .enable("false")) demultiplexer_1 (
    .out0(demultiplexer_1_out0), .out3(demultiplexer_1_out3), .in(A), .sel({B, C}));  // open: out1, out2
  xnor xnor_1 (xnor_1_out, B, C);
  or or_1 (f, demultiplexer_1_out0, demultiplexer_1_out3);
  and and_1 (f_2, A, xnor_1_out);
endmodule

module p5_34 (
  input  A,
  input  B,
  input  C,
  input  D,
  output m,
  output m_2,
  output m_3,
  output vx,
  output vx_2,
  output vx_3,
  output vx_4,
  output vy,
  output vy_2,
  output vy_3
);

  wire and_1_out, decoder_1_out0, decoder_1_out1, decoder_1_out2, not_1_out;

  Decoder #(.select(3), .disabled(0), .enable("false")) decoder_1 (
    .out0(decoder_1_out0), .out1(decoder_1_out1), .out2(decoder_1_out2), .sel({A, B, D}));  // open: out3, out4, out5, out6, out7
  Decoder #(.select(2), .disabled(0), .enable("false")) decoder_2 (
    .out3(vy_3), .sel({B, D}));  // open: out0, out1, out2
  Decoder #(.select(2), .disabled(0), .enable("false")) decoder_3 (.out0(m), .sel({C, D}));  // open: out1, out2, out3
  nor nor_1 (vx, decoder_1_out0, decoder_1_out1, decoder_1_out2);
  Multiplexer #(.select(2), .disabled(0), .enable("false")) multiplexer_1 (
    .in0(1'b0), .in1(1'b0), .in2(1'b0), .in3(1'b1), .out(vy), .sel({B, D}));
  Multiplexer #(.select(2), .disabled(0), .enable("false")) multiplexer_2 (
    .in0(1'b1), .in1(1'b0), .in2(1'b0), .in3(1'b0), .out(m_2), .sel({C, D}));
  Multiplexer #(.select(3), .disabled(0), .enable("false")) multiplexer_3 (
    .in0(1'b0), .in1(1'b0), .in2(1'b0), .in3(1'b1), .in4(1'b1), .in5(1'b1), .in6(1'b1), .in7(1'b1),
    .out(vx_3), .sel({A, B, D}));
  not not_1 (not_1_out, D);
  Multiplexer #(.disabled(0), .enable("false")) multiplexer_4 (.in0(not_1_out), .in1(1'b0), .out(m_3), .sel(C));
  Multiplexer #(.select(2), .disabled(0), .enable("false")) multiplexer_5 (
    .in0(1'b0), .in1(D), .in2(1'b1), .in3(1'b1), .out(vx_2), .sel({A, B}));
  Multiplexer #(.disabled(0), .enable("false")) multiplexer_6 (.in0(1'b0), .in1(D), .out(vy_2), .sel(B));
  and and_1 (and_1_out, D, B);
  Multiplexer #(.disabled(0), .enable("false")) multiplexer_7 (.in0(and_1_out), .in1(1'b1), .out(vx_4), .sel(A));
endmodule

module p5_35_f (
  input  A,
  input  B,
  input  C,
  output f,
  output f_2,
  output f_3,
  output f_4,
  output f_5
);

  wire and_1_out, and_2_out, and_3_out, and_4_out, and_5_out, nand_1_out, nand_3_out, nor_1_out, nor_2_out,
       or_3_out, or_4_out;

  and and_1 (and_1_out, A, B);
  and and_2 (and_2_out, A, ~B, C);  // AND_Gate
  or or_1 (f, and_1_out, and_2_out, and_3_out);
  and and_3 (and_3_out, ~A, B, ~C);  // AND_Gate
  and and_4 (and_4_out, B, ~C);  // AND_Gate
  or or_2 (f_2, and_4_out, and_5_out);
  and and_5 (and_5_out, C, A);
  nand nand_1 (nand_1_out, B, ~C);  // NAND_Gate
  nand nand_2 (f_4, nand_1_out, nand_3_out);
  nand nand_3 (nand_3_out, C, A);
  or or_3 (or_3_out, B, C);
  or or_4 (or_4_out, ~C, A);  // OR_Gate
  nor nor_1 (nor_1_out, B, C);
  nor nor_2 (nor_2_out, ~C, A);  // NOR_Gate
  and and_6 (f_3, or_3_out, or_4_out);
  nor nor_3 (f_5, nor_1_out, nor_2_out);
endmodule

module p5_35_g (
  input  A,
  input  B,
  input  C,
  input  D,
  output g,
  output g_2,
  output g_3,
  output g_4
);

  wire and_1_out, and_2_out, and_3_out, or_2_out;

  and and_1 (and_1_out, A, B);
  and and_2 (and_2_out, ~B, A, C);  // AND_Gate
  and and_3 (and_3_out, ~A, D);  // AND_Gate
  Multiplexer #(.select(3), .disabled(0), .enable("false")) multiplexer_1 (
    .in0(D), .in1(D), .in2(D), .in3(D), .in4(1'b0), .in5(1'b1), .in6(1'b1), .in7(1'b1), .out(g_3),
    .sel({A, B, C}));
  or or_1 (g, and_1_out, and_2_out, and_3_out);
  Multiplexer #(.select(2), .disabled(0), .enable("false")) multiplexer_2 (
    .in0(D), .in1(D), .in2(C), .in3(1'b1), .out(g_4), .sel({A, B}));
  or or_2 (or_2_out, B, C);
  Multiplexer #(.disabled(0), .enable("false")) multiplexer_3 (.in0(D), .in1(or_2_out), .out(g_2), .sel(A));
endmodule

module p5_36 (
  input  A,
  input  B,
  input  C,
  input  D,
  output f,
  output m,
  output g,
  output h,
  output h_2,
  output h_3
);

  wire decoder_1_out1, decoder_1_out4, decoder_1_out5, decoder_2_out1, decoder_2_out2, decoder_3_out1,
       decoder_3_out2, decoder_3_out3, nand_1_out, not_1_out, not_2_out, not_3_out, not_4_out, not_5_out;

  nand nand_1 (nand_1_out, A, B);
  Multiplexer #(.enable("false")) multiplexer_1 (.in0(nand_1_out), .in1(1'b0), .out(m), .sel(C));
  not not_1 (not_1_out, decoder_1_out1);
  not not_2 (not_2_out, decoder_1_out4);
  not not_3 (not_3_out, decoder_1_out5);
  Decoder #(.select(3), .enable("false")) decoder_1 (
    .out1(decoder_1_out1), .out4(decoder_1_out4), .out5(decoder_1_out5), .sel({A, B, D}));  // open: out0, out2, out3, out6, out7
  Decoder #(.select(2), .enable("false")) decoder_2 (
    .out1(decoder_2_out1), .out2(decoder_2_out2), .sel({B, A}));  // open: out0, out3
  nand nand_2 (g, not_1_out, not_2_out, not_3_out);
  or or_1 (h, decoder_2_out1, decoder_2_out2);
  Decoder #(.select(3), .enable("false")) decoder_3 (
    .out1(decoder_3_out1), .out2(decoder_3_out2), .out3(decoder_3_out3), .sel({A, B, D}));  // open: out0, out4, out5, out6, out7
  Multiplexer #(.enable("false")) multiplexer_2 (.in0(B), .in1(not_4_out), .out(h_2), .sel(A));
  not not_4 (not_4_out, B);
  or or_2 (f, decoder_3_out1, decoder_3_out2, decoder_3_out3);
  Multiplexer #(.enable("false")) multiplexer_3 (.in0(A), .in1(not_5_out), .out(h_3), .sel(B));
  not not_5 (not_5_out, A);
endmodule

module p5_37_MUX (
  input  P,
  input  S,
  input  V1,
  input  V2,
  output f,
  output f_2,
  output f_3,
  output r,
  output r_2,
  output r_3,
  output f_4,
  output f_5,
  output r_4,
  output r_5
);

  wire and_1_out, and_2_out, and_3_out, nand_1_out, nand_2_out, nand_3_out, nand_5_out, nand_6_out,
       nor_1_out, nor_2_out, nor_3_out, nor_4_out, nor_5_out, nor_6_out, nor_7_out, nor_8_out, nor_10_out,
       not_1_out, not_2_out, or_1_out, undriven, undriven_2;

  not not_1 (not_1_out, V2);
  nand nand_1 (nand_1_out, undriven, undriven);
  Multiplexer #(.select(3), .disabled(0), .enable("false")) multiplexer_1 (
    .in0(1'b0), .in1(1'b0), .in2(1'b0), .in3(V2), .in4(1'b0), .in5(V2), .in6(1'b1), .in7(1'b1), .out(f_2),
    .sel({P, S, V1}));
  Multiplexer #(.select(3), .disabled(0), .enable("false")) multiplexer_2 (
    .in0(1'b1), .in1(1'b1), .in2(1'b1), .in3(1'b1), .in4(not_1_out), .in5(1'b0), .in6(not_1_out), .in7(1'b0),
    .out(r_2), .sel({P, S, V1}));
  nand nand_2 (nand_2_out, S, V1, V2);
  nand nand_3 (nand_3_out, V2, V1, P);
  nand nand_4 (f_4, nand_2_out, nand_3_out, nand_5_out);
  nand nand_5 (nand_5_out, P, S);
  nand nand_6 (nand_6_out, ~V1, ~V2);  // NAND_Gate
  nand nand_7 (r_5, nand_6_out, P);
  and and_1 (and_1_out, V1, V2);
  not not_2 (not_2_out, V2);
  nor nor_1 (nor_1_out, undriven_2, undriven_2);
  Multiplexer #(.select(2), .disabled(0), .enable("false")) multiplexer_3 (
    .in0(1'b0), .in1(and_1_out), .in2(and_1_out), .in3(1'b1), .out(f), .sel({P, S}));
  Multiplexer #(.select(2), .disabled(0), .enable("false")) multiplexer_4 (
    .in0(1'b1), .in1(1'b1), .in2(not_2_out), .in3(1'b0), .out(r_3), .sel({P, V1}));
  nor nor_2 (nor_2_out, ~V1, ~P);  // NOR_Gate
  nor nor_3 (nor_3_out, ~P, ~V2);  // NOR_Gate
  nor nor_4 (nor_4_out, V1, S);
  nor nor_5 (nor_5_out, V2, S);
  nor nor_6 (nor_6_out, S, P);
  nor nor_7 (nor_7_out, V1, P);
  nor nor_8 (nor_8_out, P, V2);
  nor nor_9 (r_4, nor_2_out, nor_3_out);
  and and_2 (and_2_out, V1, V2);
  and and_3 (and_3_out, and_2_out, S);
  or or_1 (or_1_out, S, and_2_out);
  nor nor_10 (nor_10_out, V1, V2);
  nor nor_11 (f_5, nor_4_out, nor_5_out, nor_6_out, nor_7_out, nor_8_out);
  Multiplexer #(.disabled(0), .enable("false")) multiplexer_5 (.in0(and_3_out), .in1(or_1_out), .out(f_3), .sel(P));
  Multiplexer #(.disabled(0), .enable("false")) multiplexer_6 (.in0(1'b1), .in1(nor_10_out), .out(r), .sel(P));

  // Notes on the sheet:
  //   A
  //   A'
  //   A
  //   A'
endmodule

module p5_37_DEC (
  input  P,
  input  S,
  input  V1,
  input  V2,
  output f,
  output f_2,
  output f_3,
  output r,
  output r_2
);

  wire and_1_out, decoder_1_out7, decoder_2_out3, decoder_2_out4, decoder_2_out5, decoder_2_out6,
       decoder_2_out7, decoder_3_out0, decoder_3_out4, decoder_4_out0, decoder_4_out1, decoder_4_out2,
       decoder_4_out3, decoder_5_out7, decoder_6_out0, decoder_6_out1, decoder_6_out2, decoder_7_out0,
       decoder_8_out0, decoder_9_out1, decoder_9_out2, decoder_9_out3, decoder_10_out3, decoder_11_out3,
       nor_1_out, not_1_out, not_2_out, not_3_out, or_1_out;

  Decoder #(.select(3), .disabled(0)) decoder_1 (
    .out7(decoder_1_out7), .sel({S, V1, V2}), .en(not_1_out));  // open: out0, out1, out2, out3, out4, out5, out6
  not not_1 (not_1_out, P);
  Decoder #(.select(3), .disabled(0)) decoder_2 (
    .out3(decoder_2_out3), .out4(decoder_2_out4), .out5(decoder_2_out5), .out6(decoder_2_out6),
    .out7(decoder_2_out7), .sel({S, V1, V2}), .en(P));  // open: out0, out1, out2
  not not_2 (not_2_out, P);
  Decoder #(.select(3), .disabled(0)) decoder_3 (
    .out0(decoder_3_out0), .out4(decoder_3_out4), .sel({S, V1, V2}), .en(P));  // open: out1, out2, out3, out5, out6, out7
  or or_1 (or_1_out, decoder_2_out3, decoder_2_out4, decoder_2_out5, decoder_2_out6, decoder_2_out7);
  or or_2 (r, not_2_out, decoder_3_out0, decoder_3_out4);
  or or_3 (f_3, decoder_1_out7, or_1_out);
  not not_3 (not_3_out, P);
  Decoder #(.select(2), .disabled(0), .enable("false")) decoder_4 (
    .out0(decoder_4_out0), .out1(decoder_4_out1), .out2(decoder_4_out2), .out3(decoder_4_out3), .sel({P, S}));
  Decoder #(.select(3), .disabled(0)) decoder_5 (
    .out7(decoder_5_out7), .sel({S, V1, V2}), .en(not_3_out));  // open: out0, out1, out2, out3, out4, out5, out6
  Decoder #(.select(3), .disabled(0)) decoder_6 (
    .out0(decoder_6_out0), .out1(decoder_6_out1), .out2(decoder_6_out2), .sel({S, V1, V2}), .en(P));  // open: out3, out4, out5, out6, out7
  or or_4 (r_2, decoder_4_out0, decoder_4_out1, decoder_7_out0, decoder_8_out0);
  Decoder #(.select(2), .disabled(0)) decoder_7 (
    .out0(decoder_7_out0), .sel({V1, V2}), .en(decoder_4_out2));  // open: out1, out2, out3
  Decoder #(.select(2), .disabled(0)) decoder_8 (
    .out0(decoder_8_out0), .sel({V1, V2}), .en(decoder_4_out3));  // open: out1, out2, out3
  and and_1 (and_1_out, P, nor_1_out);
  nor nor_1 (nor_1_out, decoder_6_out0, decoder_6_out1, decoder_6_out2);
  or or_5 (f, decoder_5_out7, and_1_out);
  Decoder #(.select(2), .disabled(0), .enable("false")) decoder_9 (
    .out1(decoder_9_out1), .out2(decoder_9_out2), .out3(decoder_9_out3), .sel({P, S}));  // open: out0
  Decoder #(.select(2), .disabled(0)) decoder_10 (
    .out3(decoder_10_out3), .sel({V1, V2}), .en(decoder_9_out1));  // open: out0, out1, out2
  Decoder #(.select(2), .disabled(0)) decoder_11 (
    .out3(decoder_11_out3), .sel({V1, V2}), .en(decoder_9_out2));  // open: out0, out1, out2
  or or_6 (f_2, decoder_10_out3, decoder_11_out3, decoder_9_out3);
endmodule
