// Logisim project Prob_Cap6.circ as structural Verilog: 22 circuits, main circuit p6.11
module p6_1 (
  input  [3:0] A,
  input  [3:0] B,
  input  [3:0] A_2,
  input  [3:0] B_2
);

  wire comparator_1_gt, comparator_2_eq, comparator_2_gt, comparator_2_lt, not_1_out;
  wire [3:0] multiplexer_1_out, multiplexer_2_out, multiplexer_3_out;

  // Probe on A
  // Probe on B
  // Probe on A_2
  // Probe on B_2
  Comparator #(.width(4), .mode("unsigned")) comparator_1 (.a(A), .b(B), .gt(comparator_1_gt));  // open: eq, lt
  Comparator #(.width(4), .mode("unsigned")) comparator_2 (
    .a(A_2), .b(B_2), .gt(comparator_2_gt), .eq(comparator_2_eq), .lt(comparator_2_lt));
  not not_1 (not_1_out, comparator_2_eq);
  Hex_Digit_Display hex_digit_display_1 (.value(multiplexer_1_out));  // open: dp
  Multiplexer #(.width(4), .enable("false")) multiplexer_1 (
    .in0(A), .in1(B), .out(multiplexer_1_out), .sel(comparator_1_gt));
  Hex_Digit_Display hex_digit_display_2 (.value(multiplexer_2_out));  // open: dp
  Multiplexer #(.width(4)) multiplexer_2 (
    .in0(A_2), .in1(B_2), .out(multiplexer_2_out), .sel(comparator_2_gt), .en(not_1_out));
  Multiplexer #(.width(4)) multiplexer_3 (
    .in0(A_2), .in1(B_2), .out(multiplexer_3_out), .sel(comparator_2_lt), .en(not_1_out));
  Hex_Digit_Display hex_digit_display_3 (.value(multiplexer_3_out));  // open: dp

  // Notes on the sheet:
  //   (menor)
  //   (menor)
  //   (mayor)
endmodule

module p6_2 (
  input  [3:0] A,
  input  [3:0] B,
  input  [3:0] C,
  input  [3:0] A_2,
  input  [3:0] B_2,
  input  [3:0] C_2
);

  wire comparator_1_lt, comparator_2_eq, comparator_2_lt, comparator_3_lt, comparator_4_eq, comparator_4_lt,
       nand_1_out;
  wire [3:0] multiplexer_1_out, multiplexer_2_out, multiplexer_3_out, multiplexer_4_out;

  // Probe on A
  // Probe on B
  // Probe on C
  // Probe on A_2
  // Probe on B_2
  // Probe on C_2
  Multiplexer #(.width(4), .enable("false")) multiplexer_1 (
    .in0(A), .in1(B), .out(multiplexer_1_out), .sel(comparator_1_lt));
  Comparator #(.width(4), .mode("unsigned")) comparator_1 (.a(A), .b(B), .lt(comparator_1_lt));  // open: gt, eq
  Multiplexer #(.width(4), .enable("false")) multiplexer_2 (
    .in0(A_2), .in1(B_2), .out(multiplexer_2_out), .sel(comparator_2_lt));
  Comparator #(.width(4), .mode("unsigned")) comparator_2 (
    .a(A_2), .b(B_2), .eq(comparator_2_eq), .lt(comparator_2_lt));  // open: gt
  Comparator #(.width(4), .mode("unsigned")) comparator_3 (
    .a(multiplexer_1_out), .b(C), .lt(comparator_3_lt));  // open: gt, eq
  Comparator #(.width(4), .mode("unsigned")) comparator_4 (
    .a(multiplexer_2_out), .b(C_2), .eq(comparator_4_eq), .lt(comparator_4_lt));  // open: gt
  Hex_Digit_Display hex_digit_display_1 (.value(multiplexer_3_out));  // open: dp
  Multiplexer #(.width(4), .enable("false")) multiplexer_3 (
    .in0(multiplexer_1_out), .in1(C), .out(multiplexer_3_out), .sel(comparator_3_lt));
  Hex_Digit_Display hex_digit_display_2 (.value(multiplexer_4_out));  // open: dp
  Multiplexer #(.width(4)) multiplexer_4 (
    .in0(multiplexer_2_out), .in1(C_2), .out(multiplexer_4_out), .sel(comparator_4_lt), .en(nand_1_out));
  nand nand_1 (nand_1_out, comparator_4_eq, comparator_2_eq);

  // Notes on the sheet:
  //   (mayor)
  //   (mayor)
endmodule

module p6_3 (
  input  [3:0] T,
  input  [3:0] T_2
);

  wire and_1_out, comparator_1_gt, comparator_2_lt, comparator_3_gt, comparator_4_lt, or_1_out;

  // Probe on T
  // Probe on T_2
  Comparator #(.width(4)) comparator_1 (.a(T), .b(4'b0101), .gt(comparator_1_gt));  // open: eq, lt
  Comparator #(.width(4)) comparator_2 (.a(T), .b(4'b1101), .lt(comparator_2_lt));  // open: gt, eq
  // Probe on 4'b1101
  Comparator #(.width(4), .mode("unsigned")) comparator_3 (.a(T_2), .b(4'b0101), .gt(comparator_3_gt));  // open: eq, lt
  Comparator #(.width(4), .mode("unsigned")) comparator_4 (.a(T_2), .b(4'b1101), .lt(comparator_4_lt));  // open: gt, eq
  // Probe on 4'b1101
  LED Alarma (.in(or_1_out));
  or or_1 (or_1_out, comparator_1_gt, comparator_2_lt);
  LED Alarma_2 (.in(and_1_out));
  and and_1 (and_1_out, comparator_3_gt, comparator_4_lt);

  // Notes on the sheet:
  //   (C2)
  //   (sin signo)
  //   T > (+5)
  //   T< (-3)
  //   T > 0101 (+5)
  //   T < 1101 (-3)
endmodule

module p6_4 (
  input  [3:0] A,
  input  [3:0] B,
  input  [3:0] A_2,
  input  [3:0] B_2,
  input  [3:0] A_3,
  input  [3:0] B_3,
  output [3:0] f,
  output [3:0] f_2,
  output [3:0] f_3
);

  wire comparator_1_lt, comparator_2_lt, comparator_3_lt;
  wire [3:0] bit_extender_1_out, multiplexer_2_out, not_1_out, not_2_out, not_3_out;

  // Probe on B_3
  // Probe on A
  assign not_1_out = ~B;  // NOT_Gate not_1, 4 bits wide
  Comparator #(.width(4), .mode("unsigned")) comparator_1 (.a(A), .b(B), .lt(comparator_1_lt));  // open: gt, eq
  // Probe on B
  // Probe on A_2
  assign not_2_out = ~B_2;  // NOT_Gate not_2, 4 bits wide
  Comparator #(.width(4), .mode("unsigned")) comparator_2 (.a(A_2), .b(B_2), .lt(comparator_2_lt));  // open: gt, eq
  // Probe on B_2
  // Probe on A_3
  assign not_3_out = ~B_3;  // NOT_Gate not_3, 4 bits wide
  Comparator #(.width(4), .mode("unsigned")) comparator_3 (.a(A_3), .b(B_3), .lt(comparator_3_lt));  // open: gt, eq
  // Probe on B_3
  Multiplexer #(.width(4), .enable("false")) multiplexer_1 (
    .in0(4'b0000), .in1(not_1_out), .out(f), .sel(comparator_1_lt));
  assign bit_extender_1_out = {{3{comparator_2_lt}}, comparator_2_lt};  // Bit_Extender bit_extender_1
  Multiplexer #(.width(4), .enable("false")) multiplexer_2 (
    .in0(4'b0000), .in1(not_3_out), .out(multiplexer_2_out), .sel(comparator_3_lt));
  assign f_2 = not_2_out & bit_extender_1_out;  // AND_Gate and_1, 4 bits wide
  Adder #(.width(4)) adder_1 (.a(multiplexer_2_out), .b(4'b0001), .out(f_3));  // open: cin, cout
  // Probe on f_3

  // Notes on the sheet:
  //   decimal con signo
  //   decimal con signo
endmodule

module p6_5 (
  input  [3:0] V1,
  input  [3:0] V0
);

  wire and_1_out, and_2_out, and_3_out, comparator_1_eq, comparator_1_gt, comparator_1_lt, comparator_2_gt,
       comparator_2_lt, or_1_out;

  Hex_Digit_Display hex_digit_display_1 (.value(V0));  // open: dp
  Hex_Digit_Display hex_digit_display_2 (.value(V1));  // open: dp
  Comparator #(.width(4)) comparator_1 (
    .a(V1), .b(4'b0001), .gt(comparator_1_gt), .eq(comparator_1_eq), .lt(comparator_1_lt));
  Comparator #(.width(4)) comparator_2 (.a(V0), .b(4'b0101), .gt(comparator_2_gt), .lt(comparator_2_lt));  // open: eq
  or or_1 (or_1_out, comparator_1_gt, and_1_out);
  and and_1 (and_1_out, comparator_1_eq, comparator_2_gt);
  and and_2 (and_2_out, comparator_1_lt, comparator_2_lt);
  LED \Demasiado_rápido  (.in(or_1_out));
  and and_3 (and_3_out, ~or_1_out, ~and_2_out);  // AND_Gate
  LED led_1 (.in(and_3_out));
  LED Demasiado_lento (.in(and_2_out));

  // Notes on the sheet:
  //   Vel. Km/h
  //   V1>1
  //   V1=1 AND V0>5
  //   V1<1 AND V0<5
endmodule

module p6_6 (
  input  A,
  input  B,
  input  C,
  input  D,
  output p,
  output q,
  output r,
  output s
);

  wire and_1_out, and_2_out, and_3_out, and_4_out, and_5_out, and_6_out, and_7_out, not_1_out, not_2_out,
       not_3_out, not_4_out, not_5_out, not_6_out;

  and and_1 (and_1_out, B, D);
  and and_2 (and_2_out, B, C);
  not not_1 (not_1_out, B);
  and and_3 (and_3_out, not_1_out, D);
  not not_2 (not_2_out, B);
  and and_4 (and_4_out, not_2_out, C);
  not not_3 (not_3_out, C);
  and and_5 (and_5_out, B, not_3_out, not_4_out);
  not not_4 (not_4_out, D);
  not not_5 (not_5_out, C);
  and and_6 (and_6_out, not_5_out, not_6_out);
  not not_6 (not_6_out, D);
  and and_7 (and_7_out, C, D);
  not not_7 (s, D);
  or or_1 (p, and_1_out, and_2_out, A);
  or or_2 (q, and_3_out, and_4_out, and_5_out);
  or or_3 (r, and_6_out, and_7_out);
endmodule

module p6_7 (
  input  A,
  input  B,
  input  C,
  input  D,
  output p,
  output q,
  output r,
  output s
);

  xor xor_1 (q, A, B);
  xor xor_2 (r, q, C);
  xor xor_3 (s, r, D);

  assign p = A;
endmodule

module p6_8 (
  input  A,
  input  B,
  input  C,
  input  D,
  output p,
  output q,
  output r,
  output s,
  output p_2,
  output q_2,
  output r_2,
  output s_2
);

  wire decoder_1_out0, decoder_1_out1, decoder_1_out8, decoder_1_out9, decoder_1_out10, decoder_1_out11,
       decoder_1_out12, decoder_1_out13, decoder_1_out14, decoder_1_out15;

  Decoder #(.select(4), .enable("false")) decoder_1 (
    .out0(decoder_1_out0), .out1(decoder_1_out1), .out8(decoder_1_out8), .out9(decoder_1_out9),
    .out10(decoder_1_out10), .out11(decoder_1_out11), .out12(decoder_1_out12), .out13(decoder_1_out13),
    .out14(decoder_1_out14), .out15(decoder_1_out15), .sel({A, B, C, D}));  // open: out2, out3, out4, out5, out6, out7
  and and_1 (p, A, ~B, ~C);  // AND_Gate
  xor xor_1 (q, B, C);
  Priority_Encoder #(.select(4)) priority_encoder_1 (
    .in0(decoder_1_out0), .in1(decoder_1_out1), .in2(decoder_1_out14), .in3(decoder_1_out15),
    .in4(decoder_1_out12), .in5(decoder_1_out13), .in6(decoder_1_out10), .in7(decoder_1_out11),
    .in8(decoder_1_out8), .in9(decoder_1_out9), .out({p_2, q_2, r_2, s_2}));  // open: in10, in11, in12, in13, in14, in15, gs, en_out, en_in

  assign r = C;
  assign s = D;
endmodule

module p6_9_mems (
  input  [3:0] ABCD,
  input  [3:0] ABCD_2
);

  wire [2:0] p6_9_adap_1_edc, p6_9_adap_2_edc;
  wire [3:0] p6_9_adap_1_gfab, p6_9_adap_2_gfab;
  wire [6:0] p6_9_gates_1_g;
  wire [7:0] rom_1_data;

  p6_9_gates p6_9_gates_1 (
    .A(ABCD[3]), .B(ABCD[2]), .C(ABCD[1]), .D(ABCD[0]), .a_2(p6_9_gates_1_g[6]), .b_2(p6_9_gates_1_g[5]),
    .c_2(p6_9_gates_1_g[4]), .d_2(p6_9_gates_1_g[3]), .e(p6_9_gates_1_g[2]), .f(p6_9_gates_1_g[1]),
    .g(p6_9_gates_1_g[0]));
  _7_Segment_Display u_7_segment_display_1 (
    .g(p6_9_adap_1_gfab[3]), .f(p6_9_adap_1_gfab[2]), .a(p6_9_adap_1_gfab[1]), .b(p6_9_adap_1_gfab[0]),
    .e(p6_9_adap_1_edc[2]), .d(p6_9_adap_1_edc[1]), .c(p6_9_adap_1_edc[0]));  // open: dp
  p6_9_adap p6_9_adap_1 (.abcdefg(p6_9_gates_1_g), .gfab(p6_9_adap_1_gfab), .edc(p6_9_adap_1_edc));
  ROM #(.addrWidth(4)) rom_1 (.addr(ABCD_2), .data(rom_1_data));  // open: sel
  p6_9_adap p6_9_adap_2 (.abcdefg(rom_1_data[7:1]), .gfab(p6_9_adap_2_gfab), .edc(p6_9_adap_2_edc));
  _7_Segment_Display u_7_segment_display_2 (
    .g(p6_9_adap_2_gfab[3]), .f(p6_9_adap_2_gfab[2]), .a(p6_9_adap_2_gfab[1]), .b(p6_9_adap_2_gfab[0]),
    .e(p6_9_adap_2_edc[2]), .d(p6_9_adap_2_edc[1]), .c(p6_9_adap_2_edc[0]), .dp(rom_1_data[0]));

  // Notes on the sheet:
  //   contents of rom_1 (hex, n*v repeats v):
  //   fc 60 da f2 66 b6 be e0 fe f6
endmodule

module p6_9_gates (
  input  A,
  input  B,
  input  C,
  input  D,
  output a_2,
  output b_2,
  output c_2,
  output d_2,
  output e,
  output f,
  output g
);

  wire and_1_out, and_2_out, and_3_out, and_4_out, and_5_out, and_6_out, and_7_out, and_8_out, and_9_out,
       and_10_out, and_11_out, and_12_out, and_13_out, and_14_out, and_15_out, and_16_out, not_1_out,
       not_2_out, not_3_out, not_4_out, not_5_out, not_6_out, not_7_out, not_8_out, not_9_out, not_10_out,
       not_11_out, not_12_out, not_13_out, not_14_out, not_15_out, not_16_out, not_17_out, not_18_out,
       not_19_out, not_20_out, not_21_out;

  not not_1 (not_1_out, B);
  and and_1 (and_1_out, not_1_out, not_2_out);
  not not_2 (not_2_out, D);
  and and_2 (and_2_out, B, D);
  not not_3 (not_3_out, B);
  not not_4 (not_4_out, C);
  and and_3 (and_3_out, not_4_out, not_5_out);
  not not_5 (not_5_out, D);
  and and_4 (and_4_out, C, D);
  not not_6 (not_6_out, C);
  or or_1 (c_2, not_6_out, D, B);
  not not_7 (not_7_out, B);
  and and_5 (and_5_out, not_7_out, not_8_out);
  not not_8 (not_8_out, D);
  not not_9 (not_9_out, B);
  and and_6 (and_6_out, not_9_out, C);
  and and_7 (and_7_out, C, not_10_out);
  not not_10 (not_10_out, D);
  and and_8 (and_8_out, B, not_11_out, D);
  not not_11 (not_11_out, C);
  not not_12 (not_12_out, B);
  and and_9 (and_9_out, not_12_out, not_13_out);
  not not_13 (not_13_out, D);
  and and_10 (and_10_out, C, not_14_out);
  not not_14 (not_14_out, D);
  not not_15 (not_15_out, C);
  and and_11 (and_11_out, not_15_out, not_16_out);
  not not_16 (not_16_out, D);
  and and_12 (and_12_out, B, not_17_out);
  not not_17 (not_17_out, C);
  and and_13 (and_13_out, B, not_18_out);
  not not_18 (not_18_out, D);
  not not_19 (not_19_out, B);
  and and_14 (and_14_out, not_19_out, C);
  and and_15 (and_15_out, B, not_20_out);
  not not_20 (not_20_out, C);
  and and_16 (and_16_out, B, not_21_out);
  not not_21 (not_21_out, D);
  or or_2 (a_2, and_1_out, C, and_2_out, A);
  or or_3 (b_2, not_3_out, and_3_out, and_4_out);
  or or_4 (d_2, and_5_out, and_6_out, and_7_out, and_8_out, A);
  or or_5 (e, and_9_out, and_10_out);
  or or_6 (f, and_11_out, and_12_out, and_13_out, A);
  or or_7 (g, and_14_out, and_15_out, and_16_out, A);
endmodule

module p6_9_adap (
  input  [6:0] abcdefg,
  output [3:0] gfab,
  output [2:0] edc
);


  assign edc = {abcdefg[2], abcdefg[3], abcdefg[4]};
  assign gfab = {abcdefg[0], abcdefg[1], abcdefg[6:5]};
endmodule

module p6_10 (
  input  A,
  input  B,
  input  C,
  input  D,
  output p,
  output q,
  output r,
  output s
);

  wire [15:0] decoder_1_out0;

  Decoder #(.select(4), .enable("false")) decoder_1 (
    .out0(decoder_1_out0[0]), .out1(decoder_1_out0[1]), .out2(decoder_1_out0[2]), .out3(decoder_1_out0[3]),
    .out4(decoder_1_out0[4]), .out5(decoder_1_out0[5]), .out6(decoder_1_out0[6]), .out7(decoder_1_out0[7]),
    .out8(decoder_1_out0[8]), .out9(decoder_1_out0[9]), .out10(decoder_1_out0[10]),
    .out11(decoder_1_out0[11]), .out12(decoder_1_out0[12]), .out13(decoder_1_out0[13]),
    .out14(decoder_1_out0[14]), .out15(decoder_1_out0[15]), .sel({A, B, C, D}));
  Priority_Encoder #(.select(4)) priority_encoder_1 (
    .in0(decoder_1_out0[0]), .in1(decoder_1_out0[1]), .in2(decoder_1_out0[2]), .in3(decoder_1_out0[3]),
    .in4(decoder_1_out0[4]), .in5(decoder_1_out0[5]), .in6(decoder_1_out0[6]), .in7(decoder_1_out0[7]),
    .in8(decoder_1_out0[8]), .in9(decoder_1_out0[15]), .in10(decoder_1_out0[14]), .in11(decoder_1_out0[13]),
    .in12(decoder_1_out0[12]), .in13(decoder_1_out0[11]), .in14(decoder_1_out0[10]),
    .in15(decoder_1_out0[9]), .out({p, q, r, s}));  // open: gs, en_out, en_in
endmodule

module p6_11 (
  input  A0,
  input  A1,
  input  A2,
  input  [2:0] A,
  output Cout
);

  wire and_1_out, and_2_out, and_3_out, and_4_out, and_5_out, and_6_out, or_1_out, or_2_out, s0, s1, s2,
       xor_1_out, xor_3_out, xor_5_out;
  wire [2:0] adder_1_out;
  wire [3:3] or_3_out;

  xor xor_1 (xor_1_out, A0, 1'b1);
  Adder #(.width(3)) adder_1 (.a(A), .b(3'b111), .out(adder_1_out), .cin(1'b1), .cout(Cout));
  xor xor_2 (s0, xor_1_out, 1'b1);
  and and_1 (and_1_out, xor_1_out, 1'b1);
  and and_2 (and_2_out, A0, 1'b1);
  // Probe on {Cout, adder_1_out}
  // Probe on {Cout, adder_1_out}
  or or_1 (or_1_out, and_1_out, and_2_out);
  xor xor_3 (xor_3_out, A1, 1'b1);
  xor xor_4 (s1, xor_3_out, or_1_out);
  and and_3 (and_3_out, xor_3_out, or_1_out);
  and and_4 (and_4_out, A1, 1'b1);
  or or_2 (or_2_out, and_3_out, and_4_out);
  xor xor_5 (xor_5_out, A2, 1'b1);
  xor xor_6 (s2, xor_5_out, or_2_out);
  and and_5 (and_5_out, xor_5_out, or_2_out);
  or or_3 (or_3_out[3], and_5_out, and_6_out);
  and and_6 (and_6_out, A2, 1'b1);
  // Probe on {A0, A1, A2}
  // Probe on 3'b111
  // Probe on {A0, A1, A2}
  // Probe on 3'b111
  // Probe on {or_3_out[3], s2, s1, s0}
  // Probe on {or_3_out[3], s2, s1, s0}
endmodule

module p6_12 (
  input  Cin,
  input  A,
  input  B,
  input  Cin_2,
  input  A_2,
  input  B_2,
  output Cout,
  output s,
  output s_2,
  output Cout_2
);

  wire decoder_1_out1, decoder_1_out2, decoder_1_out3, decoder_1_out4, decoder_1_out5, decoder_1_out6,
       decoder_1_out7, decoder_2_out1, decoder_2_out2, decoder_2_out3, decoder_2_out4, decoder_2_out5,
       decoder_2_out6, decoder_2_out7, or_1_out, or_2_out, or_3_out, or_7_out;

  Decoder #(.select(3), .enable("false")) decoder_1 (
    .out1(decoder_1_out1), .out2(decoder_1_out2), .out3(decoder_1_out3), .out4(decoder_1_out4),
    .out5(decoder_1_out5), .out6(decoder_1_out6), .out7(decoder_1_out7), .sel({Cin, A, B}));  // open: out0
  Decoder #(.select(3), .enable("false")) decoder_2 (
    .out1(decoder_2_out1), .out2(decoder_2_out2), .out3(decoder_2_out3), .out4(decoder_2_out4),
    .out5(decoder_2_out5), .out6(decoder_2_out6), .out7(decoder_2_out7), .sel({Cin_2, A_2, B_2}));  // open: out0
  or or_1 (or_1_out, decoder_1_out1, decoder_1_out2);
  or or_2 (or_2_out, decoder_1_out3, decoder_1_out5);
  or or_3 (or_3_out, decoder_1_out4, decoder_1_out7);
  or or_4 (s_2, decoder_2_out1, decoder_2_out2, decoder_2_out4, decoder_2_out7);
  or or_5 (Cout_2, decoder_2_out7, decoder_2_out3, decoder_2_out5, decoder_2_out6);
  or or_6 (Cout, or_2_out, or_7_out);
  or or_7 (or_7_out, decoder_1_out6, decoder_1_out7);
  or or_8 (s, or_1_out, or_3_out);
  // Probe on {Cout_2, s_2}
  // Probe on {Cout_2, s_2}
  // Probe on {Cout, s}
  // Probe on {Cout, s}
endmodule

module p6_13 (
  input  [3:0] A,
  input  [3:0] B,
  input  C0,
  output [3:0] S,
  output C4,
  output PG,
  output GG
);

  wire and_1_out, and_2_out, and_3_out, and_4_out, and_5_out, and_6_out, and_7_out, and_8_out, and_9_out, G0,
       G1, G2, G3, LA0_pi, LA1_pi, LA2_pi, LA3_pi, or_2_out, or_3_out, or_4_out;

  // Probe on A
  or or_1 (C4, G3, and_1_out);
  and and_1 (and_1_out, LA3_pi, or_2_out);
  p6_13_aux LA3 (.Ai(A[3]), .Bi(B[3]), .Ci(or_2_out), .Pi(LA3_pi), .Si(S[3]), .Gi(G3));
  or or_2 (or_2_out, G2, and_2_out);
  // Probe on B
  and and_2 (and_2_out, LA2_pi, or_3_out);
  p6_13_aux LA2 (.Ai(A[2]), .Bi(B[2]), .Ci(or_3_out), .Pi(LA2_pi), .Si(S[2]), .Gi(G2));
  or or_3 (or_3_out, G1, and_5_out);
  and and_3 (and_3_out, LA2_pi, LA3_pi);
  and and_4 (and_4_out, LA3_pi, G2);
  p6_13_aux LA1 (.Ai(A[1]), .Bi(B[1]), .Ci(or_4_out), .Pi(LA1_pi), .Si(S[1]), .Gi(G1));
  and and_5 (and_5_out, LA1_pi, or_4_out);
  and and_6 (and_6_out, and_3_out, G1);
  // Probe on S
  or or_4 (or_4_out, G0, and_7_out);
  and and_7 (and_7_out, LA0_pi, C0);
  and and_8 (and_8_out, LA1_pi, and_3_out);
  and and_9 (and_9_out, and_8_out, G0);
  p6_13_aux LA0 (.Ai(A[0]), .Bi(B[0]), .Ci(C0), .Pi(LA0_pi), .Si(S[0]), .Gi(G0));
  and and_10 (PG, LA0_pi, and_8_out);
  or or_5 (GG, and_9_out, and_6_out, and_4_out, G3);
endmodule

// LAi
module p6_13_aux (
  input  Ai,
  input  Bi,
  input  Ci,
  output Pi,
  output Si,
  output Gi
);

  xor xor_1 (Pi, Ai, Bi);
  xor xor_2 (Si, Pi, Ci);
  and and_1 (Gi, Ai, Bi);
endmodule

module p6_14 (
  input  [1:0] A,
  input  [1:0] A_2,
  output [2:0] f,
  output [2:0] f_2
);

  // Probe on A
  // Probe on A_2
  or or_1 (f[2], A[1], A[0]);
  not not_1 (f[0], A[0]);
  Adder #(.width(2)) adder_1 (.a(A_2), .b(2'b11), .out(f_2[1:0]), .cout(f_2[2]));  // open: cin
  // Probe on f
  xnor xnor_1 (f[1], A[1], A[0]);
  // Probe on f_2
endmodule

module p6_15 (
  input  [3:0] A,
  input  [3:0] A_2
);

  wire bitselector_1_out;
  wire [3:0] adder_1_out, multiplexer_1_out, multiplexer_2_out, negator_1_out, not_1_out;

  // Probe on A
  assign not_1_out = ~A;  // NOT_Gate not_1, 4 bits wide
  // Probe on A_2
  Negator #(.width(4)) negator_1 (.in(A_2), .out(negator_1_out));
  BitSelector #(.width(4)) bitselector_1 (.in(A_2), .out(bitselector_1_out), .sel(2'b11));
  Adder #(.width(4)) adder_1 (.a(not_1_out), .b(4'b0001), .out(adder_1_out));  // open: cin, cout
  Hex_Digit_Display hex_digit_display_1 (.value(multiplexer_1_out), .dp(bitselector_1_out));
  Multiplexer #(.width(4), .enable("false")) multiplexer_1 (
    .in0(A_2), .in1(negator_1_out), .out(multiplexer_1_out), .sel(bitselector_1_out));
  Hex_Digit_Display hex_digit_display_2 (.value(multiplexer_2_out), .dp(A[3]));
  Multiplexer #(.width(4), .enable("false")) multiplexer_2 (
    .in0(A), .in1(adder_1_out), .out(multiplexer_2_out), .sel(A[3]));
endmodule

module p6_16 (
  input  [3:0] A,
  input  [3:0] B,
  input  [3:0] A_2,
  input  [3:0] B_2
);

  wire not_1_out;
  wire [3:0] adder_1_out, adder_2_out, controlled_buffer_1_out, multiplexer_1_out, negator_1_out,
       negator_2_out, negator_3_out;

  // Probe on A
  Negator #(.width(4)) negator_1 (.in(B), .out(negator_1_out));
  // Probe on B
  // Probe on A_2
  Negator #(.width(4)) negator_2 (.in(B_2), .out(negator_2_out));
  // Probe on B_2
  // Probe on adder_1_out
  Adder #(.width(4)) adder_1 (.a(A), .b(negator_1_out), .out(adder_1_out));  // open: cin, cout
  // Probe on adder_2_out
  Adder #(.width(4)) adder_2 (.a(A_2), .b(negator_2_out), .out(adder_2_out));  // open: cin, cout
  Hex_Digit_Display hex_digit_display_1 (.value(controlled_buffer_1_out));  // open: dp
  assign controlled_buffer_1_out = not_1_out ? adder_1_out : 4'bz;  // Controlled_Buffer controlled_buffer_1
  not not_1 (not_1_out, adder_1_out[3]);
  Multiplexer #(.width(4), .enable("false")) multiplexer_1 (
    .in0(adder_2_out), .in1(negator_3_out), .out(multiplexer_1_out), .sel(adder_2_out[3]));
  Negator #(.width(4)) negator_3 (.in(adder_2_out), .out(negator_3_out));
  Hex_Digit_Display hex_digit_display_2 (.value(multiplexer_1_out), .dp(adder_2_out[3]));
endmodule

module p6_17 (
  input  Juez,
  input  A,
  input  B,
  input  C,
  input  D,
  input  Juez_2,
  input  A_2,
  input  B_2,
  input  C_2,
  input  D_2,
  input  Juez_3,
  input  A_3,
  input  B_3,
  input  C_3,
  input  D_3
);

  wire adder_1_cout, adder_1_out, adder_2_cout, adder_2_out, adder_3_cout, and_1_out, and_2_out, and_3_out,
       and_4_out, comparator_1_eq, comparator_1_gt, comparator_2_eq, comparator_2_gt, multiplexer_1_out,
       multiplexer_2_out, or_1_out, xor_1_out, xor_2_out, xor_3_out;
  wire [2:0] adder_3_out, bitadder_1_out;

  Adder #(.width(1)) adder_1 (.a(A), .b(B), .out(adder_1_out), .cout(adder_1_cout));  // open: cin
  Adder #(.width(1)) adder_2 (.a(C), .b(D), .out(adder_2_out), .cout(adder_2_cout));  // open: cin
  BitAdder #(.width(4)) bitadder_1 (.in0({D_2, C_2, B_2, A_2}), .out(bitadder_1_out));
  and and_1 (and_1_out, A_3, B_3);
  and and_2 (and_2_out, A_3, C_3);
  and and_3 (and_3_out, A_3, D_3);
  and and_4 (and_4_out, B_3, C_3, D_3);
  Adder #(.width(1)) adder_3 (
    .a(adder_1_out), .b(adder_2_out), .out(adder_3_out[0]), .cout(adder_3_cout));  // open: cin
  Adder #(.width(1)) adder_4 (
    .a(adder_1_cout), .b(adder_2_cout), .out(adder_3_out[1]), .cin(adder_3_cout), .cout(adder_3_out[2]));
  Comparator #(.width(3), .mode("unsigned")) comparator_1 (
    .a(bitadder_1_out), .b(3'b010), .gt(comparator_1_gt), .eq(comparator_1_eq));  // open: lt
  or or_1 (or_1_out, and_1_out, and_2_out, and_3_out, and_4_out);
  Comparator #(.width(3), .mode("unsigned")) comparator_2 (
    .a(adder_3_out), .b(3'b010), .gt(comparator_2_gt), .eq(comparator_2_eq));  // open: lt
  Multiplexer #(.enable("false")) multiplexer_1 (
    .in0(comparator_1_gt), .in1(A_2), .out(multiplexer_1_out), .sel(comparator_1_eq));
  // Probe on xor_1_out
  xor xor_1 (xor_1_out, Juez_3, or_1_out);
  Multiplexer #(.enable("false")) multiplexer_2 (
    .in0(comparator_2_gt), .in1(A), .out(multiplexer_2_out), .sel(comparator_2_eq));
  // Probe on xor_2_out
  xor xor_2 (xor_2_out, Juez_2, multiplexer_1_out);
  // Probe on xor_3_out
  xor xor_3 (xor_3_out, Juez, multiplexer_2_out);

  // Notes on the sheet:
  //   Jurado
  //   Jurado
  //   Jurado
  //   Votos culpabilidad
  //   Empate
  //   Culpable
  //   Empate
endmodule

module p6_18 (
  input  [3:0] L,
  input  [2:0] C
);

  wire C1C0_out, C2C0_out, C2C1_out, comparator_1_eq, comparator_1_gt, multiplexer_1_out, or_1_out;
  wire [2:0] bitadder_1_out;

  BitAdder #(.width(4)) bitadder_1 (.in0(L), .out(bitadder_1_out));
  Comparator #(.width(3)) comparator_1 (
    .a(bitadder_1_out), .b(3'b010), .gt(comparator_1_gt), .eq(comparator_1_eq));  // open: lt
  and C2C1 (C2C1_out, C[2], C[1]);
  and C2C0 (C2C0_out, C[2], C[0]);
  or or_1 (or_1_out, C2C1_out, C2C0_out, C1C0_out);
  and C1C0 (C1C0_out, C[1], C[0]);
  Multiplexer #(.enable("false")) multiplexer_1 (
    .in0(comparator_1_gt), .in1(or_1_out), .out(multiplexer_1_out), .sel(comparator_1_eq));
  // Probe on multiplexer_1_out

  // Notes on the sheet:
  //   Mayoría en C
endmodule

module p6_19 (
  input  [3:0] N1,
  input  [3:0] N2,
  input  [1:0] C1C0
);

  wire comparator_1_gt;
  wire [3:0] adder_1_out, adder_2_out, multiplexer_1_out, multiplexer_2_out, multiplexer_3_out;
  wire [3:3] adder_1_cout;

  // Probe on N1
  // Probe on N2
  Multiplexer #(.width(4), .disabled(0), .enable("false")) multiplexer_1 (
    .in0(N1), .in1(N2), .out(multiplexer_1_out), .sel(comparator_1_gt));
  Comparator #(.width(4), .mode("unsigned")) comparator_1 (.a(N2), .b(N1), .gt(comparator_1_gt));  // open: eq, lt
  Multiplexer #(.width(4), .disabled(0), .enable("false")) multiplexer_2 (
    .in0(N2), .in1(N1), .out(multiplexer_2_out), .sel(comparator_1_gt));
  Adder #(.width(4)) adder_1 (.a(N2), .b(N1), .out(adder_1_out), .cout(adder_1_cout[3]));  // open: cin
  // Probe on multiplexer_1_out
  // Probe on multiplexer_2_out
  Adder #(.width(4)) adder_2 (
    .a({adder_1_cout[3], adder_1_out[3:1]}), .b(4'b0000), .out(adder_2_out), .cin(adder_1_out[0]));  // open: cout
  // Probe on multiplexer_3_out
  Multiplexer #(.select(2), .width(4), .enable("false")) multiplexer_3 (
    .in0(multiplexer_2_out), .in1({adder_1_cout[3], adder_1_out[3:1]}), .in2(adder_2_out),
    .in3(multiplexer_1_out), .out(multiplexer_3_out), .sel(C1C0));

  // Notes on the sheet:
  //   crossbar switch
  //   N2>N1
  //   División/2
  //   mayor
  //   menor
  //   Calif. final
endmodule
