// Logisim project Prob_Cap7.circ as structural Verilog: 10 circuits, main circuit p7.2
module p7_2 (
  input  A,
  input  B
);

  wire and_1_out, and_2_out, CLK_out, or_1_out, t_ff_1_q, t_ff_1_qn;

  and and_1 (and_1_out, t_ff_1_qn, A);
  and and_2 (and_2_out, B, t_ff_1_q);
  Clock CLK (.out(CLK_out));
  T_Flip_Flop t_ff_1 (.clk(CLK_out), .T(or_1_out), .Q(t_ff_1_q), .Qn(t_ff_1_qn));  // open: preset, reset, en
  or or_1 (or_1_out, and_1_out, and_2_out);
endmodule

module p7_3 (
  input  A
);

  wire CLK_out, d_ff_1_q, nand_1_out;

  Clock CLK (.out(CLK_out));
  D_Flip_Flop d_ff_1 (.clk(CLK_out), .D(nand_1_out), .Q(d_ff_1_q));  // open: Qn, preset, en, reset
  nand nand_1 (nand_1_out, A, d_ff_1_q);
endmodule

module p7_5 (
  input  T,
  output out_2
);

  wire CLK_out;

  J_K_Flip_Flop j_k_ff_1 (.J(T), .clk(CLK_out), .K(T), .Q(out_2));  // open: Qn, preset, en, reset
  Clock CLK (.out(CLK_out));
endmodule

module p7_6 (
  input  T
);

  wire CLK_out, d_ff_1_q, xor_1_out;

  Clock CLK (.out(CLK_out));
  xor xor_1 (xor_1_out, T, d_ff_1_q);
  D_Flip_Flop d_ff_1 (.clk(CLK_out), .D(xor_1_out), .Q(d_ff_1_q));  // open: Qn, preset, en, reset
endmodule

module p7_8 (
  input  A
);

  wire CLK_out, nand_1_out, not_1_out, t_ff_1_qn;

  Clock CLK (.out(CLK_out));
  not not_1 (not_1_out, CLK_out);
  nand nand_1 (nand_1_out, A, t_ff_1_qn);
  T_Flip_Flop #(.trigger("falling")) t_ff_1 (
    .clk(not_1_out), .T(nand_1_out), .Qn(t_ff_1_qn));  // open: Q, preset, reset, en
endmodule

module p7_9 (
  input  J,
  input  K
);

  wire and_1_out, and_2_out, CLK_out, d_ff_1_q, d_ff_1_qn, or_1_out;

  and and_1 (and_1_out, d_ff_1_qn, J);
  and and_2 (and_2_out, ~K, d_ff_1_q);  // AND_Gate
  Clock CLK (.out(CLK_out));
  D_Flip_Flop d_ff_1 (.clk(CLK_out), .D(or_1_out), .Q(d_ff_1_q), .Qn(d_ff_1_qn));  // open: preset, en, reset
  or or_1 (or_1_out, and_1_out, and_2_out);
endmodule

module p7_10 (
  input  A,
  input  B
);

  wire and_1_out, and_2_out, CLK_out, or_1_out, t_ff_1_q, t_ff_1_qn;

  Clock CLK (.out(CLK_out));
  and and_1 (and_1_out, t_ff_1_q, ~A);  // AND_Gate
  or or_1 (or_1_out, and_1_out, and_2_out);
  and and_2 (and_2_out, B, t_ff_1_qn);
  T_Flip_Flop t_ff_1 (.clk(CLK_out), .T(or_1_out), .Q(t_ff_1_q), .Qn(t_ff_1_qn));  // open: preset, reset, en
endmodule

module p7_11 (
);

  wire CLK_2_out, CLK_3_out, CLK_4_out, CLK_out, d_ff_1_q, d_ff_2_qn, d_ff_3_q, d_ff_4_qn;

  Clock CLK (.out(CLK_out));
  D_Flip_Flop d_ff_1 (.clk(CLK_out), .D(d_ff_1_q), .Q(d_ff_1_q));  // open: Qn, preset, en, reset
  Clock CLK_2 (.out(CLK_2_out));
  D_Flip_Flop d_ff_2 (.clk(CLK_2_out), .D(d_ff_2_qn), .Qn(d_ff_2_qn));  // open: Q, preset, en, reset
  Clock CLK_3 (.out(CLK_3_out));
  D_Flip_Flop d_ff_3 (.clk(d_ff_3_q), .D(CLK_3_out), .Q(d_ff_3_q));  // open: Qn, preset, en, reset
  Clock CLK_4 (.out(CLK_4_out));
  D_Flip_Flop d_ff_4 (.clk(d_ff_4_qn), .D(CLK_4_out), .Qn(d_ff_4_qn));  // open: Q, preset, en, reset
endmodule

module p7_12 (
);

  wire CLK_out, j_k_ff_1_q, j_k_ff_1_qn;

  Clock CLK (.out(CLK_out));
  J_K_Flip_Flop j_k_ff_1 (
    .J(j_k_ff_1_qn), .clk(CLK_out), .K(j_k_ff_1_q), .Q(j_k_ff_1_q), .Qn(j_k_ff_1_qn));  // open: preset, en, reset
endmodule

module p7_13_Pres_Clr (
  input  PRE_star,
  input  CLR_star,
  input  PRE_star_2,
  input  PRE_star_3,
  input  CLR_star_2,
  input  CLR_star_3
);

  wire and_1_out, and_2_out, CLK_2_out, CLK_3_out, CLK_out, not_1_out, not_2_out, not_3_out, not_4_out,
       or_1_out;

  Clock CLK (.out(CLK_out));
  and and_1 (and_1_out, ~PRE_star, CLR_star);  // AND_Gate
  Clock CLK_2 (.out(CLK_2_out));
  not not_1 (not_1_out, PRE_star_2);
  and and_2 (and_2_out, ~not_1_out, not_2_out);  // AND_Gate
  not not_2 (not_2_out, CLR_star_2);
  J_K_Flip_Flop j_k_ff_1 (.J(1'b1), .clk(CLK_out), .K(1'b1), .preset(PRE_star), .reset(and_1_out));  // open: Q, Qn, en
  J_K_Flip_Flop j_k_ff_2 (
    .J(1'b1), .clk(CLK_2_out), .K(1'b1), .preset(not_1_out), .reset(and_2_out));  // open: Q, Qn, en
  Clock CLK_3 (.out(CLK_3_out));
  not not_3 (not_3_out, or_1_out);
  not not_4 (not_4_out, PRE_star_3);
  or or_1 (or_1_out, ~PRE_star_3, CLR_star_3);  // OR_Gate
  J_K_Flip_Flop j_k_ff_3 (
    .J(1'b1), .clk(CLK_3_out), .K(1'b1), .preset(not_4_out), .reset(not_3_out));  // open: Q, Qn, en
endmodule
