// Logisim project Prob_Cap8.circ as structural Verilog: 11 circuits, main circuit p8.2
module p8_1 (
);

  wire CLK_out, q0_qn;

  Clock CLK (.out(CLK_out));
  J_K_Flip_Flop #(.trigger("falling")) q0 (
    .J(1'b1), .clk(CLK_out), .K(1'b1), .Qn(q0_qn));  // open: Q, preset, en, reset
  J_K_Flip_Flop #(.trigger("falling")) q1 (.J(1'b1), .clk(q0_qn), .K(1'b1));  // open: Q, Qn, preset, en, reset
endmodule

module p8_2 (
);

  wire CLK_2_out, CLK_out, INIT_CLR_2_out, INIT_CLR_out, or_1_out, or_2_out, q0_2_qn, q0_qn, q1_2_qn, q1_qn,
       q2_2_q, q2_2_qn, q2_q, q2_qn, q3_2_q, q3_2_qn, q3_q, q3q2_2_out, q3q2_out;

  Clock CLK (.out(CLK_out));
  Button INIT_CLR (.out(INIT_CLR_out));
  or or_1 (or_1_out, INIT_CLR_out, q3q2_2_out);
  Clock CLK_2 (.out(CLK_2_out));
  Button INIT_CLR_2 (.out(INIT_CLR_2_out));
  or or_2 (or_2_out, INIT_CLR_2_out, q3q2_out);
  and q3q2 (q3q2_out, q2_2_q, q3_2_q);
  T_Flip_Flop q0 (.clk(CLK_out), .T(1'b1), .Qn(q0_qn), .reset(or_1_out));  // open: Q, preset, en
  and q3q2_2 (q3q2_2_out, q2_q, q3_q);
  D_Flip_Flop q0_2 (.clk(CLK_2_out), .D(q0_2_qn), .Qn(q0_2_qn), .reset(or_2_out));  // open: Q, preset, en
  T_Flip_Flop q1 (.clk(q0_qn), .T(1'b1), .Qn(q1_qn), .reset(or_1_out));  // open: Q, preset, en
  D_Flip_Flop q1_2 (.clk(q0_2_qn), .D(q1_2_qn), .Qn(q1_2_qn), .reset(or_2_out));  // open: Q, preset, en
  T_Flip_Flop q2 (.clk(q1_qn), .T(1'b1), .Q(q2_q), .Qn(q2_qn), .reset(or_1_out));  // open: preset, en
  D_Flip_Flop q2_2 (.clk(q1_2_qn), .D(q2_2_qn), .Q(q2_2_q), .Qn(q2_2_qn), .reset(or_2_out));  // open: preset, en
  T_Flip_Flop q3 (.clk(q2_qn), .T(1'b1), .Q(q3_q), .reset(or_1_out));  // open: Qn, preset, en
  D_Flip_Flop q3_2 (.clk(q2_2_qn), .D(q3_2_qn), .Q(q3_2_q), .Qn(q3_2_qn), .reset(or_2_out));  // open: preset, en
endmodule

module p8_3 (
);

  wire CLK_2_out, CLK_out, INIT_PRE_2_out, INIT_PRE_out, or_1_out, or_2_out, q0_2_q, q0_2_qn, q0_q, q1_2_q,
       q1_2_qn, q1_q, q2_2_q, q2_2_qn, q2_q, q2_qn, q3_2_qn, q3_prime_q2_prime_2_out, q3_prime_q2_prime_out,
       q3_qn;

  Clock CLK (.out(CLK_out));
  Button INIT_PRE (.out(INIT_PRE_out));
  or or_1 (or_1_out, INIT_PRE_out, q3_prime_q2_prime_2_out);
  Clock CLK_2 (.out(CLK_2_out));
  Button INIT_PRE_2 (.out(INIT_PRE_2_out));
  or or_2 (or_2_out, INIT_PRE_2_out, q3_prime_q2_prime_out);
  and q3_prime_q2_prime (q3_prime_q2_prime_out, q2_2_qn, q3_2_qn);
  T_Flip_Flop q0 (.clk(CLK_out), .T(1'b1), .Q(q0_q), .preset(or_1_out));  // open: Qn, reset, en
  and q3_prime_q2_prime_2 (q3_prime_q2_prime_2_out, q2_qn, q3_qn);
  D_Flip_Flop q0_2 (.clk(CLK_2_out), .D(q0_2_qn), .Q(q0_2_q), .Qn(q0_2_qn), .preset(or_2_out));  // open: en, reset
  T_Flip_Flop q1 (.clk(q0_q), .T(1'b1), .Q(q1_q), .preset(or_1_out));  // open: Qn, reset, en
  D_Flip_Flop q1_2 (.clk(q0_2_q), .D(q1_2_qn), .Q(q1_2_q), .Qn(q1_2_qn), .preset(or_2_out));  // open: en, reset
  T_Flip_Flop q2 (.clk(q1_q), .T(1'b1), .Q(q2_q), .Qn(q2_qn), .preset(or_1_out));  // open: reset, en
  D_Flip_Flop q2_2 (.clk(q1_2_q), .D(q2_2_qn), .Q(q2_2_q), .Qn(q2_2_qn), .preset(or_2_out));  // open: en, reset
  T_Flip_Flop q3 (.clk(q2_q), .T(1'b1), .Qn(q3_qn), .preset(or_1_out));  // open: Q, reset, en
  D_Flip_Flop q3_2 (.clk(q2_2_q), .D(q3_2_qn), .Qn(q3_2_qn), .preset(or_2_out));  // open: Q, en, reset
endmodule

module p8_4 (
);

  wire and_1_out, CLK_out, q0_qn, q2_qn;
  wire [3:0] q0_q;

  J_K_Flip_Flop #(.trigger("falling")) q0 (
    .J(1'b1), .clk(CLK_out), .K(1'b1), .Q(q0_q[0]), .Qn(q0_qn), .reset(and_1_out));  // open: preset, en
  Clock CLK (.out(CLK_out));
  J_K_Flip_Flop #(.trigger("falling")) q1 (
    .J(1'b1), .clk(q0_q[0]), .K(1'b1), .Q(q0_q[1]), .reset(and_1_out));  // open: Qn, preset, en
  and and_1 (and_1_out, q0_qn, q0_q[3], q2_qn, q0_q[1]);
  J_K_Flip_Flop #(.trigger("falling")) q2 (
    .J(1'b1), .clk(q0_q[1]), .K(1'b1), .Q(q0_q[2]), .Qn(q2_qn), .reset(and_1_out));  // open: preset, en
  J_K_Flip_Flop #(.trigger("falling")) q3 (
    .J(1'b1), .clk(q0_q[2]), .K(1'b1), .Q(q0_q[3]), .reset(and_1_out));  // open: Qn, preset, en
  Hex_Digit_Display hex_digit_display_1 (.value(q0_q));  // open: dp
endmodule

module p8_5 (
);

  wire CLK_out, q1_q, q2_q;

  Clock CLK (.out(CLK_out));
  J_K_Flip_Flop q2 (.J(1'b1), .clk(CLK_out), .K(1'b1), .Q(q2_q));  // open: Qn, preset, en, reset
  J_K_Flip_Flop q1 (.J(q2_q), .clk(CLK_out), .K(q2_q), .Q(q1_q));  // open: Qn, preset, en, reset
  J_K_Flip_Flop q0 (.J(q1_q), .clk(CLK_out), .K(q1_q));  // open: Q, Qn, preset, en, reset
endmodule

module p8_7 (
  input  EN
);

  wire CLK_out, INIT_CLR_out, q0_q, q0_qn, q1_q, q1_qn, q2_q, q2_qn;

  Clock CLK (.out(CLK_out));
  J_K_Flip_Flop q0 (
    .J(q2_q), .clk(CLK_out), .K(q2_qn), .Q(q0_q), .Qn(q0_qn), .en(EN), .reset(INIT_CLR_out));  // open: preset
  Button INIT_CLR (.out(INIT_CLR_out));
  J_K_Flip_Flop q1 (
    .J(q0_q), .clk(CLK_out), .K(q0_qn), .Q(q1_q), .Qn(q1_qn), .en(EN), .reset(INIT_CLR_out));  // open: preset
  J_K_Flip_Flop q2 (
    .J(q1_qn), .clk(CLK_out), .K(q1_q), .Q(q2_q), .Qn(q2_qn), .en(EN), .reset(INIT_CLR_out));  // open: preset
endmodule

module p8_8 (
  input  CTEN,
  input  INIT_CLR,
  output TC,
  output [3:0] CNT
);

  wire CLK_out, or_1_out, q1q0_out, q2q1q0_out, q3_prime_q0_out, q3_qn;

  J_K_Flip_Flop q0 (.J(1'b1), .clk(CLK_out), .K(1'b1), .Q(CNT[0]), .en(CTEN), .reset(INIT_CLR));  // open: Qn, preset
  Clock CLK (.out(CLK_out));
  and q3_prime_q0 (q3_prime_q0_out, CNT[0], q3_qn);
  J_K_Flip_Flop q1 (
    .J(q3_prime_q0_out), .clk(CLK_out), .K(q3_prime_q0_out), .Q(CNT[1]), .en(CTEN), .reset(INIT_CLR));  // open: Qn, preset
  and q1q0 (q1q0_out, CNT[0], CNT[1]);
  and q3q0 (TC, CNT[3], CNT[0]);
  and q2q1q0 (q2q1q0_out, q1q0_out, CNT[2]);
  J_K_Flip_Flop q2 (.J(q1q0_out), .clk(CLK_out), .K(q1q0_out), .Q(CNT[2]), .reset(INIT_CLR));  // open: Qn, preset, en
  or or_1 (or_1_out, TC, q2q1q0_out);
  J_K_Flip_Flop q3 (
    .J(or_1_out), .clk(CLK_out), .K(or_1_out), .Q(CNT[3]), .Qn(q3_qn), .en(CTEN), .reset(INIT_CLR));  // open: preset
endmodule

module p8_10 (
  input  EN
);

  wire CLK_out, decoder_1_out0, decoder_1_out1, decoder_1_out2, decoder_1_out3, INIT_CLR_out;
  wire [1:0] q0_q;

  Clock CLK (.out(CLK_out));
  Button INIT_CLR (.out(INIT_CLR_out));
  T_Flip_Flop q0 (.clk(CLK_out), .T(1'b1), .Q(q0_q[0]), .reset(INIT_CLR_out), .en(EN));  // open: Qn, preset
  Decoder #(.select(2), .enable("false")) decoder_1 (
    .out0(decoder_1_out0), .out1(decoder_1_out1), .out2(decoder_1_out2), .out3(decoder_1_out3), .sel(q0_q));
  T_Flip_Flop q1 (.clk(CLK_out), .T(q0_q[0]), .Q(q0_q[1]), .reset(INIT_CLR_out), .en(EN));  // open: Qn, preset
  LED En____Sistema_0 (.in(decoder_1_out0));
  LED En____Sistema_1 (.in(decoder_1_out1));
  LED En____Sistema_2 (.in(decoder_1_out2));
  LED En____Sistema_3 (.in(decoder_1_out3));
endmodule

module p8_10__cont (
  input  EN,
  input  EN_2
);

  wire CLK_2_out, CLK_out, INIT_2_out, INIT_out, q0_2_q, q0_2_qn, q0_q, q1_2_q, q1_2_qn, q1_q, q2_2_q,
       q2_2_qn, q2_q, q3_2_q, q3_2_qn, q3_q;

  Clock CLK (.out(CLK_out));
  D_Flip_Flop q0 (.clk(CLK_out), .D(q3_q), .Q(q0_q), .preset(INIT_out), .en(EN));  // open: Qn, reset
  Button INIT (.out(INIT_out));
  Clock CLK_2 (.out(CLK_2_out));
  Button INIT_2 (.out(INIT_2_out));
  D_Flip_Flop q1 (.clk(CLK_out), .D(q0_q), .Q(q1_q), .en(EN), .reset(INIT_out));  // open: Qn, preset
  J_K_Flip_Flop q1_2 (
    .J(q0_2_q), .clk(CLK_2_out), .K(q0_2_qn), .Q(q1_2_q), .Qn(q1_2_qn), .en(EN_2), .reset(INIT_2_out));  // open: preset
  J_K_Flip_Flop q0_2 (
    .J(q3_2_q), .clk(CLK_2_out), .K(q3_2_qn), .Q(q0_2_q), .Qn(q0_2_qn), .preset(INIT_2_out), .en(EN_2));  // open: reset
  D_Flip_Flop q2 (.clk(CLK_out), .D(q1_q), .Q(q2_q), .en(EN), .reset(INIT_out));  // open: Qn, preset
  J_K_Flip_Flop q2_2 (
    .J(q1_2_q), .clk(CLK_2_out), .K(q1_2_qn), .Q(q2_2_q), .Qn(q2_2_qn), .en(EN_2), .reset(INIT_2_out));  // open: preset
  D_Flip_Flop q3 (.clk(CLK_out), .D(q2_q), .Q(q3_q), .en(EN), .reset(INIT_out));  // open: Qn, preset
  J_K_Flip_Flop q3_2 (
    .J(q2_2_q), .clk(CLK_2_out), .K(q2_2_qn), .Q(q3_2_q), .Qn(q3_2_qn), .en(EN_2), .reset(INIT_2_out));  // open: preset
endmodule

module p8_11 (
  input  EN,
  input  EN_2
);

  wire CLK_2_out, CLK_out, INIT_CLR_2_out, INIT_CLR_out, q0_2_q, q0_q, q0_qn, q1_2_q, q1_q, q1_qn, q2_2_qn,
       q2_q, q2_qn;

  Clock CLK (.out(CLK_out));
  J_K_Flip_Flop q0 (
    .J(q2_qn), .clk(CLK_out), .K(q2_q), .Q(q0_q), .Qn(q0_qn), .en(EN), .reset(INIT_CLR_out));  // open: preset
  Button INIT_CLR (.out(INIT_CLR_out));
  D_Flip_Flop q0_2 (.clk(CLK_2_out), .D(q2_2_qn), .Q(q0_2_q), .en(EN_2), .reset(INIT_CLR_2_out));  // open: Qn, preset
  Clock CLK_2 (.out(CLK_2_out));
  Button INIT_CLR_2 (.out(INIT_CLR_2_out));
  J_K_Flip_Flop q1 (
    .J(q0_q), .clk(CLK_out), .K(q0_qn), .Q(q1_q), .Qn(q1_qn), .en(EN), .reset(INIT_CLR_out));  // open: preset
  D_Flip_Flop q1_2 (.clk(CLK_2_out), .D(q0_2_q), .Q(q1_2_q), .en(EN_2), .reset(INIT_CLR_2_out));  // open: Qn, preset
  J_K_Flip_Flop q2 (
    .J(q1_q), .clk(CLK_out), .K(q1_qn), .Q(q2_q), .Qn(q2_qn), .en(EN), .reset(INIT_CLR_out));  // open: preset
  D_Flip_Flop q2_2 (.clk(CLK_2_out), .D(q1_2_q), .Qn(q2_2_qn), .en(EN_2), .reset(INIT_CLR_2_out));  // open: Q, preset
endmodule

module p8_13 (
  input  H_prime_C,
  output q2,
  output q1,
  output q0
);

  wire CLK_out, INIT_CLR_out, q0_q, q1_q, q2_q;

  D_Flip_Flop u_q0 (.clk(CLK_out), .D(q2_q), .Q(q0_q), .preset(INIT_CLR_out));  // open: Qn, en, reset
  Clock CLK (.out(CLK_out));
  Button INIT_CLR (.out(INIT_CLR_out));
  D_Flip_Flop u_q1 (.clk(CLK_out), .D(q0_q), .Q(q1_q), .reset(INIT_CLR_out));  // open: Qn, preset, en
  D_Flip_Flop u_q2 (.clk(CLK_out), .D(q1_q), .Q(q2_q), .reset(INIT_CLR_out));  // open: Qn, preset, en
  xor xor_1 (q2, q2_q, H_prime_C);
  xor xor_2 (q1, q1_q, H_prime_C);
  xor xor_3 (q0, q0_q, H_prime_C);
endmodule
