// Logisim project Prob_Cap9.circ as structural Verilog: 30 circuits, main circuit p9.1
module p9_1 (
  input  X,
  input  INIT_CLR,
  output y
);

  wire CLK_out, q0_q, q1_q, q1_qn;

  Clock CLK (.out(CLK_out));
  D_Flip_Flop q1 (.clk(CLK_out), .D(X), .Q(q1_q), .Qn(q1_qn), .preset(INIT_CLR));  // open: en, reset
  D_Flip_Flop q0 (.clk(CLK_out), .D(q1_q), .Q(q0_q), .reset(INIT_CLR));  // open: Qn, preset, en
  and and_1 (y, q0_q, q1_qn);
endmodule

module p9_2 (
  input  X,
  output y
);

  wire and_1_out, and_2_out, CLK_out, not_1_out, or_1_out, q0_q, q0_qn;

  and and_1 (and_1_out, q0_q, not_1_out);
  not not_1 (not_1_out, X);
  and and_2 (and_2_out, X, q0_qn);
  or or_1 (or_1_out, and_1_out, and_2_out);
  Clock CLK (.out(CLK_out));
  J_K_Flip_Flop q0 (.J(or_1_out), .clk(CLK_out), .K(or_1_out), .Q(q0_q), .Qn(q0_qn));  // open: preset, en, reset
  and and_3 (y, q0_q, X);
endmodule

module p9_4 (
  input  X,
  output y
);

  wire CLK_out, INIT_CLR_out, nand_1_out, nand_2_out, not_1_out, q0_q, q1_qn;

  not not_1 (not_1_out, X);
  Clock CLK (.out(CLK_out));
  Button INIT_CLR (.out(INIT_CLR_out));
  J_K_Flip_Flop q1 (
    .J(nand_2_out), .clk(CLK_out), .K(not_1_out), .Qn(q1_qn), .reset(INIT_CLR_out));  // open: Q, preset, en
  J_K_Flip_Flop q0 (.J(X), .clk(CLK_out), .K(q0_q), .Q(q0_q), .reset(INIT_CLR_out));  // open: Qn, preset, en
  nor nor_1 (y, q1_qn, q0_q, not_1_out);
  nand nand_1 (nand_1_out, q1_qn, q0_q);
  nand nand_2 (nand_2_out, nand_1_out, X);
endmodule

module p9_5 (
  input  X,
  output y
);

  wire and_1_out, CLK_out, INIT_CLR_out, not_1_out, or_1_out, q0_q, q1_q;

  Clock CLK (.out(CLK_out));
  not not_1 (not_1_out, CLK_out);
  Button INIT_CLR (.out(INIT_CLR_out));
  D_Flip_Flop #(.trigger("falling")) q0 (
    .clk(not_1_out), .D(X), .Q(q0_q), .reset(INIT_CLR_out));  // open: Qn, preset, en
  and and_1 (and_1_out, or_1_out, X);
  D_Flip_Flop #(.trigger("falling")) q1 (
    .clk(not_1_out), .D(and_1_out), .Q(q1_q), .reset(INIT_CLR_out));  // open: Qn, preset, en
  or or_1 (or_1_out, q0_q, q1_q);
  and and_2 (y, q1_q, X);
endmodule

module p9_7 (
  input  X,
  output y
);

  wire CLK_out, nand_1_out, q0_q, q0_qn, q1_q, q1_qn, xor_1_out;

  Clock CLK (.out(CLK_out));
  D_Flip_Flop q1 (.clk(CLK_out), .D(X), .Q(q1_q), .Qn(q1_qn));  // open: preset, en, reset
  nand nand_1 (nand_1_out, X, q1_q);
  xor xor_1 (xor_1_out, q1_q, q0_qn);
  J_K_Flip_Flop q0 (.J(nand_1_out), .clk(CLK_out), .K(xor_1_out), .Q(q0_q), .Qn(q0_qn));  // open: preset, en, reset
  and and_1 (y, q0_q, q1_qn);
endmodule

module p9_8 (
  output q0,
  output [3:0] q3q2q1q0
);

  wire CLK_2_out, CLK_out, CLR_out, INIT_2_out, INIT_out, nor_1_out, nor_2_out, not_1_out, not_2_out,
       or_1_out, or_2_out, q0_q, q1_q, q2_q, q3_q, xor_1_out, xor_2_out;

  Clock CLK (.out(CLK_out));
  Button CLR (.out(CLR_out));
  not not_1 (not_1_out, CLK_2_out);
  Clock CLK_2 (.out(CLK_2_out));
  Button INIT (.out(INIT_out));
  or or_1 (or_1_out, xor_2_out, nor_2_out);
  Button INIT_2 (.out(INIT_2_out));
  Shift_Register #(.length(4)) shift_register_1 (
    .in(or_2_out), .clk(not_2_out), .out(q0), .load(INIT_2_out), .clr(CLR_out), .d0(1'b1), .q0(q3q2q1q0[3]),
    .d1(1'b1), .q1(q3q2q1q0[2]), .d2(1'b1), .q2(q3q2q1q0[1]), .d3(1'b0), .q3(q3q2q1q0[0]));  // open: shift
  not not_2 (not_2_out, CLK_out);
  xor xor_1 (xor_1_out, q3q2q1q0[2], q3q2q1q0[1]);
  or or_2 (or_2_out, xor_1_out, nor_1_out);
  nor nor_1 (nor_1_out, q3q2q1q0[2], q3q2q1q0[0]);
  D_Flip_Flop #(.trigger("falling")) q3 (
    .clk(not_1_out), .D(or_1_out), .Q(q3_q), .preset(INIT_out));  // open: Qn, en, reset
  xor xor_2 (xor_2_out, q2_q, q1_q);
  nor nor_2 (nor_2_out, q2_q, q0_q);
  D_Flip_Flop #(.trigger("falling")) q2 (
    .clk(not_1_out), .D(q3_q), .Q(q2_q), .preset(INIT_out));  // open: Qn, en, reset
  D_Flip_Flop #(.trigger("falling")) u_q0 (
    .clk(not_1_out), .D(q1_q), .Q(q0_q), .reset(INIT_out));  // open: Qn, preset, en
  D_Flip_Flop #(.trigger("falling")) q1 (
    .clk(not_1_out), .D(q2_q), .Q(q1_q), .preset(INIT_out));  // open: Qn, en, reset

  // Notes on the sheet:
  //   X
  //   X
endmodule

module P9_9 (
  input  CNT_prime_INIT,
  input  [2:0] INIT_Val
);

  wire CLK_out, multiplexer_1_out, multiplexer_2_out, multiplexer_3_out, q0_q, q0_qn, q1_q, q1q0_out, q2_q,
       xor_1_out, xor_2_out;

  Clock CLK (.out(CLK_out));
  Multiplexer #(.enable("false")) multiplexer_1 (
    .in0(q0_qn), .in1(INIT_Val[0]), .out(multiplexer_1_out), .sel(CNT_prime_INIT));
  D_Flip_Flop q0 (.clk(CLK_out), .D(multiplexer_1_out), .Q(q0_q), .Qn(q0_qn));  // open: preset, en, reset
  xor xor_1 (xor_1_out, q0_q, q1_q);
  Multiplexer #(.enable("false")) multiplexer_2 (
    .in0(xor_1_out), .in1(INIT_Val[1]), .out(multiplexer_2_out), .sel(CNT_prime_INIT));
  D_Flip_Flop q1 (.clk(CLK_out), .D(multiplexer_2_out), .Q(q1_q));  // open: Qn, preset, en, reset
  and q1q0 (q1q0_out, q1_q, q0_q);
  xor xor_2 (xor_2_out, q1q0_out, q2_q);
  Multiplexer #(.enable("false")) multiplexer_3 (
    .in0(xor_2_out), .in1(INIT_Val[2]), .out(multiplexer_3_out), .sel(CNT_prime_INIT));
  D_Flip_Flop q2 (.clk(CLK_out), .D(multiplexer_3_out), .Q(q2_q));  // open: Qn, preset, en, reset
endmodule

module p9_10 (
  input  X,
  input  X_2,
  input  X_3,
  output y,
  output y_2,
  output y_3
);

  wire CLK_2_out, CLK_3_out, CLK_out, decoder_1_out1, decoder_1_out2, decoder_1_out3, decoder_1_out5,
       decoder_2_out0, decoder_2_out1, decoder_2_out3, INIT_CLR_2_out, INIT_CLR_3_out, INIT_CLR_out,
       or_1_out, or_2_out, or_3_out, q0_3_q, q0_3_qn, q0_prime_X_out, q0_prime_X_prime_out, q0X_out, q1_3_q,
       q1_3_qn, q1_prime_q0_2_out, q1_prime_q0_out, q1_qn;
  wire [1:1] q0_2_q;
  wire [2:1] q0_q;

  Button INIT_CLR (.out(INIT_CLR_out));
  Decoder #(.select(3), .disabled(0), .enable("false")) decoder_1 (
    .out1(decoder_1_out1), .out2(decoder_1_out2), .out3(decoder_1_out3), .out4(y_2), .out5(decoder_1_out5),
    .sel({q0_q, X_2}));  // open: out0, out6, out7
  Button INIT_CLR_2 (.out(INIT_CLR_2_out));
  Decoder #(.select(2), .disabled(0), .enable("false")) decoder_2 (
    .out0(decoder_2_out0), .out1(decoder_2_out1), .out3(decoder_2_out3), .sel({q0_2_q[1], X_3}));  // open: out2
  Button INIT_CLR_3 (.out(INIT_CLR_3_out));
  Clock CLK (.out(CLK_out));
  and q0X (q0X_out, q0_3_q, X);
  and q0_prime_X_prime (q0_prime_X_prime_out, ~X, q0_3_qn);  // AND_Gate
  and q0_prime_X (q0_prime_X_out, q0_3_qn, X);
  Clock CLK_2 (.out(CLK_2_out));
  Clock CLK_3 (.out(CLK_3_out));
  and q1_prime_q0 (q1_prime_q0_out, q0_3_q, q1_qn);
  J_K_Flip_Flop q1 (
    .J(q0X_out), .clk(CLK_out), .K(q0_prime_X_prime_out), .Qn(q1_qn), .reset(INIT_CLR_out));  // open: Q, preset, en
  and q1q0_prime_X_prime (y, ~q1_qn, q0_prime_X_prime_out);  // AND_Gate
  J_K_Flip_Flop q1_2 (
    .J(decoder_1_out3), .clk(CLK_2_out), .K(y_2), .Q(q0_q[2]), .reset(INIT_CLR_2_out));  // open: Qn, preset, en
  or or_1 (or_1_out, decoder_1_out1, decoder_1_out2, decoder_1_out3, decoder_1_out5);
  J_K_Flip_Flop q1_3 (
    .J(decoder_2_out3), .clk(CLK_3_out), .K(decoder_2_out0), .Q(q1_3_q), .Qn(q1_3_qn), .reset(INIT_CLR_3_out));  // open: preset, en
  and q1_prime_q0_2 (q1_prime_q0_2_out, q1_3_qn, q0_2_q[1]);
  or or_2 (or_2_out, q1_prime_q0_out, q0_prime_X_out);
  T_Flip_Flop q0 (.clk(CLK_2_out), .T(or_1_out), .Q(q0_q[1]), .reset(INIT_CLR_2_out));  // open: Qn, preset, en
  T_Flip_Flop q0_2 (.clk(CLK_3_out), .T(or_3_out), .Q(q0_2_q[1]), .reset(INIT_CLR_3_out));  // open: Qn, preset, en
  or or_3 (or_3_out, q1_prime_q0_2_out, decoder_2_out1);
  T_Flip_Flop q0_3 (.clk(CLK_out), .T(or_2_out), .Q(q0_3_q), .Qn(q0_3_qn), .reset(INIT_CLR_out));  // open: preset, en
  and m0q1 (y_3, decoder_2_out0, q1_3_q);

  // Notes on the sheet:
  //   m(1,2,3,5)
endmodule

module p9_11_mod (
  input  X,
  output y
);

  wire and_1_out, and_2_out, CLK_out, decoder_1_out2, decoder_1_out3, decoder_1_out4, decoder_1_out5,
       decoder_1_out9, decoder_1_out11, multiplexer_1_out, nand_1_out, not_1_out, not_2_out, not_3_out,
       not_4_out, not_5_out, not_6_out, not_7_out, not_8_out, or_1_out, q0_qn, q1_prime_X_prime_out, q1_qn,
       q1q0_prime_out, q2X_prime_out;
  wire [3:1] q0_q;

  Decoder #(.select(4), .enable("false")) decoder_1 (
    .out2(decoder_1_out2), .out3(decoder_1_out3), .out4(decoder_1_out4), .out5(decoder_1_out5),
    .out9(decoder_1_out9), .out11(decoder_1_out11), .sel({q0_q, X}));  // open: out0, out1, out6, out7, out8, out10, out12, out13, out14, out15
  not not_1 (not_1_out, decoder_1_out2);
  not not_2 (not_2_out, decoder_1_out3);
  not not_3 (not_3_out, decoder_1_out4);
  not not_4 (not_4_out, decoder_1_out5);
  not not_5 (not_5_out, decoder_1_out9);
  not not_6 (not_6_out, decoder_1_out11);
  nand nand_1 (nand_1_out, not_1_out, not_3_out, not_6_out, not_5_out);
  and and_1 (and_1_out, not_4_out, not_5_out);
  and and_2 (and_2_out, not_2_out, not_6_out);
  not not_7 (not_7_out, X);
  or or_1 (or_1_out, q0_q[3], q1_prime_X_prime_out);
  and q1_prime_X_prime (q1_prime_X_prime_out, not_7_out, q1_qn);
  Clock CLK (.out(CLK_out));
  Multiplexer #(.enable("false")) multiplexer_1 (.in0(or_1_out), .in1(X), .out(multiplexer_1_out), .sel(q0_q[1]));
  not not_8 (not_8_out, X);
  T_Flip_Flop q2 (.clk(CLK_out), .T(multiplexer_1_out), .Q(q0_q[3]));  // open: Qn, preset, reset, en
  D_Flip_Flop q1 (.clk(CLK_out), .D(nand_1_out), .Q(q0_q[2]), .Qn(q1_qn));  // open: preset, en, reset
  J_K_Flip_Flop q0 (.J(and_1_out), .clk(CLK_out), .K(and_2_out), .Q(q0_q[1]), .Qn(q0_qn));  // open: preset, en, reset
  and q2X_prime (q2X_prime_out, not_8_out, q0_q[3]);
  or or_2 (y, q2X_prime_out, q1q0_prime_out);
  and q1q0_prime (q1q0_prime_out, q0_q[2], q0_qn);
endmodule

module p9_11_tunnels (
  input  X__Entrada,
  output y__salida
);

  wire CLK_out, D1, decoder_1_out2, decoder_1_out3, decoder_1_out4, decoder_1_out5, decoder_1_out9,
       decoder_1_out11, INIT_CLR_out, J0, K0, or_2_out, q0, q1, q1q0_prime_out, q2, q2X_prime_out, T2;

  Decoder #(.select(4), .enable("false")) decoder_1 (
    .out2(decoder_1_out2), .out3(decoder_1_out3), .out4(decoder_1_out4), .out5(decoder_1_out5),
    .out9(decoder_1_out9), .out11(decoder_1_out11), .sel({q2, q1, q0, X__Entrada}));  // open: out0, out1, out6, out7, out8, out10, out12, out13, out14, out15
  or or_1 (D1, decoder_1_out2, decoder_1_out4, decoder_1_out11, decoder_1_out9);
  nor nor_1 (J0, decoder_1_out5, decoder_1_out9);
  nor nor_2 (K0, decoder_1_out3, decoder_1_out11);
  or or_2 (or_2_out, ~q1, q2);  // OR_Gate
  Multiplexer #(.select(2), .enable("false")) multiplexer_1 (
    .in0(or_2_out), .in1(q2), .in2(1'b0), .in3(1'b1), .out(T2), .sel({q0, X__Entrada}));
  Clock CLK (.out(CLK_out));
  // Probe on {q2, q1, q0}
  T_Flip_Flop u_q2 (.clk(CLK_out), .T(T2), .Q(q2), .reset(INIT_CLR_out));  // open: Qn, preset, en
  D_Flip_Flop u_q1 (.clk(CLK_out), .D(D1), .Q(q1), .reset(INIT_CLR_out));  // open: Qn, preset, en
  J_K_Flip_Flop u_q0 (.J(J0), .clk(CLK_out), .K(K0), .Q(q0), .reset(INIT_CLR_out));  // open: Qn, preset, en
  Button INIT_CLR (.out(INIT_CLR_out));
  and q2X_prime (q2X_prime_out, q2, ~X__Entrada);  // AND_Gate
  or or_3 (y__salida, q2X_prime_out, q1q0_prime_out);
  and q1q0_prime (q1q0_prime_out, q1, ~q0);  // AND_Gate

  // Other names for the same wires on the sheet: X = X__Entrada
endmodule

module p9_12 (
  output y1,
  output y0,
  output y1_2,
  output y0_2,
  output y1_3,
  output y0_3
);

  wire CLK_2_out, CLK_3_out, CLK_4_out, CLK_5_out, CLK_out, CLR_out, decoder_1_out0, decoder_1_out2,
       decoder_1_out3, decoder_1_out5, decoder_1_out6, INIT_CLR_2_out, INIT_CLR_3_out, INIT_CLR_out,
       INIT_out, or_1_out, or_4_out, q0_2_q, q0_2_qn, q0_3_q, q1_2_q, q1_2_qn, q1_3_q, q1_3_qn, q1q0_2_out,
       q1q0_3_out, q1q0_out, q1q0_prime_out, q2_2_q, q2_2_qn, q2_3_q, q2_prime_q1_out, q2q1_prime_out,
       q2q1_prime_q0_out, xor_1_out;
  wire [1:0] rom_1_data, shift_register_1_out;
  wire [2:0] counter_1_q, q0_q;

  Clock CLK (.out(CLK_out));
  Button INIT_CLR (.out(INIT_CLR_out));
  Clock CLK_2 (.out(CLK_2_out));
  Button INIT_CLR_2 (.out(INIT_CLR_2_out));
  Clock CLK_3 (.out(CLK_3_out));
  Button INIT_CLR_3 (.out(INIT_CLR_3_out));
  Button INIT (.out(INIT_out));
  Shift_Register #(.width(2)) shift_register_1 (
    .in(shift_register_1_out), .clk(CLK_4_out), .out(shift_register_1_out), .load(INIT_out), .clr(CLR_out),
    .d0(2'b01), .d1(2'b10), .d2(2'b11), .d3(2'b01), .d4(2'b11), .d5(2'b10), .d6(2'b01), .d7(2'b00));  // open: shift, q0, q1, q2, q3, q4, q5, q6, q7
  Clock CLK_4 (.out(CLK_4_out));
  Button CLR (.out(CLR_out));
  T_Flip_Flop q0 (.clk(CLK_out), .T(1'b1), .Q(q0_q[0]), .reset(INIT_CLR_out));  // open: Qn, preset, en
  T_Flip_Flop q0_2 (.clk(CLK_2_out), .T(1'b1), .Q(q0_2_q), .Qn(q0_2_qn), .reset(INIT_CLR_2_out));  // open: preset, en
  T_Flip_Flop q0_3 (.clk(CLK_3_out), .T(1'b1), .Q(q0_3_q), .reset(INIT_CLR_3_out));  // open: Qn, preset, en
  and q1q0 (q1q0_out, q0_q[0], q0_q[1]);
  T_Flip_Flop q1 (.clk(CLK_out), .T(q0_q[0]), .Q(q0_q[1]), .reset(INIT_CLR_out));  // open: Qn, preset, en
  and q1q0_2 (q1q0_2_out, q0_2_q, q1_2_q);
  T_Flip_Flop q1_2 (.clk(CLK_2_out), .T(q0_2_q), .Q(q1_2_q), .Qn(q1_2_qn), .reset(INIT_CLR_2_out));  // open: preset, en
  and q1q0_3 (q1q0_3_out, q0_3_q, q1_3_q);
  T_Flip_Flop q1_3 (.clk(CLK_3_out), .T(q0_3_q), .Q(q1_3_q), .Qn(q1_3_qn), .reset(INIT_CLR_3_out));  // open: preset, en
  // Probe on shift_register_1_out
  Decoder #(.select(3), .enable("false")) decoder_1 (
    .out0(decoder_1_out0), .out2(decoder_1_out2), .out3(decoder_1_out3), .out5(decoder_1_out5),
    .out6(decoder_1_out6), .sel(q0_q));  // open: out1, out4, out7
  T_Flip_Flop q2 (.clk(CLK_out), .T(q1q0_out), .Q(q0_q[2]), .reset(INIT_CLR_out));  // open: Qn, preset, en
  T_Flip_Flop q2_2 (
    .clk(CLK_2_out), .T(q1q0_2_out), .Q(q2_2_q), .Qn(q2_2_qn), .reset(INIT_CLR_2_out));  // open: preset, en
  T_Flip_Flop q2_3 (.clk(CLK_3_out), .T(q1q0_3_out), .Q(q2_3_q), .reset(INIT_CLR_3_out));  // open: Qn, preset, en
  xor xor_1 (xor_1_out, q1_3_q, q0_3_q);
  or or_1 (or_1_out, q0_3_q, q1_3_qn);
  and q1q0_prime (q1q0_prime_out, q0_2_qn, q1_2_q);
  and q2_prime_q1 (q2_prime_q1_out, q1_2_q, q2_2_qn);
  and q2q1_prime_q0 (q2q1_prime_q0_out, q0_2_q, q2q1_prime_out);
  and q2q1_prime (q2q1_prime_out, q2_2_q, q1_2_qn);
  or or_2 (y0_2, q2q1_prime_out, q0_2_q);
  Multiplexer #(.enable("false")) multiplexer_1 (.in0(q1_3_q), .in1(xor_1_out), .out(y1_3), .sel(q2_3_q));
  Multiplexer #(.enable("false")) multiplexer_2 (.in0(q0_3_q), .in1(or_1_out), .out(y0_3), .sel(q2_3_q));
  // Probe on {y1_3, y0_3}
  Clock CLK_5 (.out(CLK_5_out));
  or or_3 (y1, decoder_1_out2, decoder_1_out3, decoder_1_out5, decoder_1_out6);
  nor nor_1 (y0, decoder_1_out6, decoder_1_out2, decoder_1_out0);
  // Probe on {y1, y0}
  or or_4 (or_4_out, q1q0_prime_out, q2_prime_q1_out);
  or or_5 (y1_2, or_4_out, q2q1_prime_q0_out);
  // Probe on {y1_2, y0_2}
  Counter #(.width(3), .max('h7)) counter_1 (
    .count(1'b1), .Q(counter_1_q), .clk(CLK_5_out));  // open: load, D, carry, clr
  ROM #(.addrWidth(3), .dataWidth(2)) rom_1 (.addr(counter_1_q), .data(rom_1_data));  // open: sel
  // Probe on rom_1_data
  // Probe on rom_1_data

  // Notes on the sheet:
  //   contents of rom_1 (hex, n*v repeats v):
  //   0 1 2 3 1 3 2 1
endmodule

module p9_13_Moore (
  input  X1,
  input  X0,
  output y
);

  wire and_1_out, and_2_out, and_3_out, CLK_out, or_1_out, or_2_out, or_3_out, q0_q, q1_q;

  Clock CLK (.out(CLK_out));
  and and_1 (and_1_out, X1, ~X0, q0_q);  // AND_Gate
  or or_1 (or_1_out, q0_q, ~X0, X1);  // OR_Gate
  and and_2 (and_2_out, ~X1, ~X0);  // AND_Gate
  J_K_Flip_Flop q1 (.J(and_1_out), .clk(CLK_out), .K(or_1_out), .Q(q1_q));  // open: Qn, preset, en, reset
  or or_2 (or_2_out, and_2_out, and_3_out);
  and and_3 (and_3_out, q1_q, ~X1);  // AND_Gate
  or or_3 (or_3_out, q1_q, X0, X1);
  J_K_Flip_Flop q0 (.J(or_2_out), .clk(CLK_out), .K(or_3_out), .Q(q0_q));  // open: Qn, preset, en, reset
  and and_4 (y, q1_q, q0_q);
endmodule

module p9_13_Mealy (
  input  X1,
  input  X0,
  output y
);

  wire and_1_out, and_2_out, CLK_out, or_1_out, q0_q, q1_q;

  Clock CLK (.out(CLK_out));
  and and_1 (and_1_out, X1, ~X0, q0_q);  // AND_Gate
  J_K_Flip_Flop q1 (.J(and_1_out), .clk(CLK_out), .K(1'b1), .Q(q1_q));  // open: Qn, preset, en, reset
  and and_2 (and_2_out, ~X1, ~X0);  // AND_Gate
  or or_1 (or_1_out, X0, X1);
  and and_3 (y, ~X1, X0, q1_q);  // AND_Gate
  J_K_Flip_Flop q0 (.J(and_2_out), .clk(CLK_out), .K(or_1_out), .Q(q0_q));  // open: Qn, preset, en, reset
endmodule

module p9_14 (
);

  wire CLK_2_out, CLK_out, not_1_out, or_1_out, or_2_out, q0_2_q, q0_q, q0X_prime_out, q1_2_q,
       q1_prime_q0_out, q1_prime_q0X_prime_out, q1_q, q1q0_prime_out, q1X_out, X_2_out, X_out, xor_1_out;

  Button X (.out(X_out));
  not not_1 (not_1_out, X_out);
  Clock CLK (.out(CLK_out));
  Button X_2 (.out(X_2_out));
  D_Flip_Flop q0 (.clk(CLK_2_out), .D(X_2_out), .Q(q0_q));  // open: Qn, preset, en, reset
  Clock CLK_2 (.out(CLK_2_out));
  J_K_Flip_Flop q0_2 (.J(X_out), .clk(CLK_out), .K(not_1_out), .Q(q0_2_q));  // open: Qn, preset, en, reset
  and q1q0_prime (q1q0_prime_out, q1_2_q, ~q0_q);  // AND_Gate
  and q1_prime_q0 (q1_prime_q0_out, ~q1_2_q, q0_q);  // AND_Gate
  and q0X_prime (q0X_prime_out, ~X_out, q0_2_q);  // AND_Gate
  and q1_prime_q0X_prime (q1_prime_q0X_prime_out, q1_prime_q0_out, ~X_2_out);  // AND_Gate
  and q1X (q1X_out, X_2_out, q1_2_q);
  xor xor_1 (xor_1_out, q0_2_q, q1_q);
  J_K_Flip_Flop q1 (.J(q0X_prime_out), .clk(CLK_out), .K(q0X_prime_out), .Q(q1_q));  // open: Qn, preset, en, reset
  or or_1 (or_1_out, q1q0_prime_out, q1_prime_q0_out);
  or or_2 (or_2_out, q1q0_prime_out, q1_prime_q0X_prime_out, q1X_out);
  LED y (.in(xor_1_out));
  LED y_2 (.in(or_1_out));
  D_Flip_Flop q1_2 (.clk(CLK_2_out), .D(or_2_out), .Q(q1_2_q));  // open: Qn, preset, en, reset
endmodule

module p9_15 (
  output y,
  output y_2
);

  wire CLK_2_out, CLK_out, INIT_CLR_2_out, INIT_CLR_out, not_1_out, not_2_out, q0_q, q0X_out, q0X_prime_out,
       q1_prime_X_out, q1_qn, X_2_out, X_out;
  wire [7:0] CNT_2_q, CNT_4_q;

  Button X (.out(X_out));
  Clock CLK (.out(CLK_out));
  Button X_2 (.out(X_2_out));
  Clock CLK_2 (.out(CLK_2_out));
  and q0X (q0X_out, y, X_out);
  J_K_Flip_Flop q1 (
    .J(q0X_out), .clk(CLK_out), .K(not_1_out), .Qn(q1_qn), .reset(INIT_CLR_out));  // open: Q, preset, en
  not not_1 (not_1_out, X_out);
  Button INIT_CLR (.out(INIT_CLR_out));
  and q0X_prime (q0X_prime_out, q0_q, ~X_2_out);  // AND_Gate
  J_K_Flip_Flop q1_2 (
    .J(q0X_prime_out), .clk(CLK_2_out), .K(1'b1), .Q(y_2), .reset(INIT_CLR_2_out));  // open: Qn, preset, en
  Button INIT_CLR_2 (.out(INIT_CLR_2_out));
  and q1_prime_X (q1_prime_X_out, X_out, q1_qn);
  J_K_Flip_Flop q0 (
    .J(X_2_out), .clk(CLK_2_out), .K(not_2_out), .Q(q0_q), .reset(INIT_CLR_2_out));  // open: Qn, preset, en
  not not_2 (not_2_out, X_2_out);
  // Probe on CNT_2_q
  Counter CNT_2 (.count(y), .Q(CNT_2_q), .clk(CLK_out), .clr(INIT_CLR_out));  // open: load, D, carry
  J_K_Flip_Flop q0_2 (
    .J(q1_prime_X_out), .clk(CLK_out), .K(1'b1), .Q(y), .reset(INIT_CLR_out));  // open: Qn, preset, en
  // Probe on CNT_4_q
  Counter CNT_4 (.count(y_2), .Q(CNT_4_q), .clk(CLK_2_out), .clr(INIT_CLR_2_out));  // open: load, D, carry

  // Notes on the sheet:
  //   Pulso cuando X pasa de 0->1
  //   Pulso cuando X pasa de 1->0
endmodule

module p9_16 (
  input  H,
  input  C,
  input  Detector_Pasillo,
  input  Caja_Fuerte,
  output p,
  output g,
  output Guarda_Seguridad,
  output Policia
);

  wire and_1_out, and_2_out, and_3_out, and_4_out, CLK_out, clock_1_out, D0_q, D0_qn, INIT_CLR_2_out,
       INIT_CLR_out, not_1_out, not_2_out, or_1_out, or_2_out, or_3_out, q0_prime_H_out, q0_qn,
       q0H_prime_out, q1_prime_C_prime_out, q1_q, q1_qn, T1_q, T1_qn;

  Clock CLK (.out(CLK_out));
  and q0H_prime (q0H_prime_out, g, ~H);  // AND_Gate
  Button INIT_CLR (.out(INIT_CLR_out));
  not not_1 (not_1_out, Caja_Fuerte);
  not not_2 (not_2_out, Detector_Pasillo);
  Button INIT_CLR_2 (.out(INIT_CLR_2_out));
  D_Flip_Flop q1 (.clk(CLK_out), .D(or_1_out), .Q(q1_q), .Qn(q1_qn), .reset(INIT_CLR_out));  // open: preset, en
  or or_1 (or_1_out, q0H_prime_out, ~q1_qn);  // OR_Gate
  and and_1 (and_1_out, not_1_out, D0_q, not_2_out);
  and and_2 (and_2_out, Detector_Pasillo, T1_qn);
  and and_3 (and_3_out, q0H_prime_out, q1_prime_C_prime_out);
  and q1_prime_C_prime (q1_prime_C_prime_out, q1_qn, ~C);  // AND_Gate
  and q0_prime_H (q0_prime_H_out, H, q0_qn);
  or or_2 (or_2_out, and_1_out, and_2_out);
  or or_3 (or_3_out, and_3_out, q0_prime_H_out);
  Clock clock_1 (.out(clock_1_out));
  and and_4 (and_4_out, not_2_out, D0_q, T1_qn);
  and q1q0 (p, q1_q, g);
  T_Flip_Flop q0 (.clk(CLK_out), .T(or_3_out), .Q(g), .Qn(q0_qn), .reset(INIT_CLR_out));  // open: preset, en
  D_Flip_Flop D0 (.clk(clock_1_out), .D(or_2_out), .Q(D0_q), .Qn(D0_qn), .reset(INIT_CLR_2_out));  // open: preset, en
  T_Flip_Flop T1 (.clk(clock_1_out), .T(and_4_out), .Q(T1_q), .Qn(T1_qn), .reset(INIT_CLR_2_out));  // open: preset, en
  xor xor_1 (Guarda_Seguridad, D0_q, T1_q);
  and and_5 (Policia, D0_qn, T1_q);
endmodule

module p9_17_4ff (
);

  wire CLK_out, INIT_CLR_out, q0, q1, q2, q2_prime_q0_prime_out, q2_prime_q1_out, q3,
       q3_prime_q1_prime_q0_out, q3_prime_q2q1_out, q3_prime_q2q1_prime_out, q3q0_prime_out, q3q1_out,
       q3q1_prime_q0_out, T0, T1, T2, T3;

  Clock CLK (.out(CLK_out));
  Button INIT_CLR (.out(INIT_CLR_out));
  and q3_prime_q2q1 (q3_prime_q2q1_out, ~q3, q2, q1);  // AND_Gate
  or or_1 (T3, q3_prime_q2q1_out, q3q0_prime_out);
  and q3q0_prime (q3q0_prime_out, q3, ~q0);  // AND_Gate
  and q3_prime_q1_prime_q0 (q3_prime_q1_prime_q0_out, ~q3, ~q1, q0);  // AND_Gate
  or or_2 (T1, q3_prime_q1_prime_q0_out, q3q1_out);
  and q3q1 (q3q1_out, q3, q1);
  T_Flip_Flop u_q3 (.clk(CLK_out), .T(T3), .Q(q3), .reset(INIT_CLR_out));  // open: Qn, preset, en
  T_Flip_Flop u_q2 (.clk(CLK_out), .T(T2), .Q(q2), .reset(INIT_CLR_out));  // open: Qn, preset, en
  or or_3 (T2, q3_prime_q2q1_prime_out, q2_prime_q1_out);
  or or_4 (T0, q3q1_prime_q0_out, q2_prime_q0_prime_out);
  T_Flip_Flop u_q1 (.clk(CLK_out), .T(T1), .Q(q1), .reset(INIT_CLR_out));  // open: Qn, preset, en
  and q3_prime_q2q1_prime (q3_prime_q2q1_prime_out, ~q3, q2, ~q1);  // AND_Gate
  and q2_prime_q1 (q2_prime_q1_out, ~q2, q1);  // AND_Gate
  and q3q1_prime_q0 (q3q1_prime_q0_out, q3, ~q1, q0);  // AND_Gate
  and q2_prime_q0_prime (q2_prime_q0_prime_out, ~q0, ~q2);  // AND_Gate
  T_Flip_Flop u_q0 (.clk(CLK_out), .T(T0), .Q(q0), .reset(INIT_CLR_out));  // open: Qn, preset, en
  LED led_1 (.in(q3));
  LED led_2 (.in(q3));
  LED led_3 (.in(q0));
  LED led_4 (.in(q0));
  LED led_5 (.in(q1));
  LED led_6 (.in(q1));
  LED led_7 (.in(q2));
  LED led_8 (.in(q2));
endmodule

module p9_17_gates (
);

  wire CLK_out, q0, q1, q1q0_2_out, q1q0_out, q2, q2_prime_q0_out, q2_prime_q1_out, q2q0_prime_out,
       q2q1_prime_out, q2q1_prime_q0_prime_out, xor_1_out, y0, y1, y2, y3;

  T_Flip_Flop u_q0 (.clk(CLK_out), .T(1'b1), .Q(q0));  // open: Qn, preset, reset, en
  Clock CLK (.out(CLK_out));
  xor xor_1 (xor_1_out, q2, q1);
  and q2_prime_q0 (q2_prime_q0_out, ~q2, q0);  // AND_Gate
  and q2_prime_q1 (q2_prime_q1_out, ~q2, q1);  // AND_Gate
  and q2q1_prime_q0_prime (q2q1_prime_q0_prime_out, q2, ~q1, ~q0);  // AND_Gate
  or u_y0 (y0, xor_1_out, q2_prime_q0_out);
  or u_y1 (y1, q2_prime_q1_out, q2q1_prime_q0_prime_out);
  and q1q0 (q1q0_out, q0, q1);
  T_Flip_Flop u_q1 (.clk(CLK_out), .T(q0), .Q(q1));  // open: Qn, preset, reset, en
  and q1q0_2 (q1q0_2_out, q1, q0);
  T_Flip_Flop u_q2 (.clk(CLK_out), .T(q1q0_out), .Q(q2));  // open: Qn, preset, reset, en
  or u_y2 (y2, q1q0_2_out, q2);
  and q2q1_prime (q2q1_prime_out, ~q1, q2);  // AND_Gate
  or u_y3 (y3, q2q1_prime_out, q2q0_prime_out);
  and q2q0_prime (q2q0_prime_out, q2, ~q0);  // AND_Gate
  LED led_1 (.in(y0));
  LED led_2 (.in(y3));
  LED led_3 (.in(y3));
  LED led_4 (.in(y2));
  LED led_5 (.in(y0));
  LED led_6 (.in(y1));
  LED led_7 (.in(y1));
  LED led_8 (.in(y2));
endmodule

module p9_17_DEC (
);

  wire CLK_out, decoder_1_out0, decoder_1_out1, decoder_1_out2, decoder_1_out3, decoder_1_out4,
       decoder_1_out5, decoder_1_out6, decoder_1_out7, INIT_CLR_out, y0_out, y1_out, y2_out, y3_out;
  wire [2:0] counter_1_q;

  Clock CLK (.out(CLK_out));
  Decoder #(.select(3), .enable("false")) decoder_1 (
    .out0(decoder_1_out0), .out1(decoder_1_out1), .out2(decoder_1_out2), .out3(decoder_1_out3),
    .out4(decoder_1_out4), .out5(decoder_1_out5), .out6(decoder_1_out6), .out7(decoder_1_out7),
    .sel(counter_1_q));
  Counter #(.width(3), .max('h7)) counter_1 (
    .count(1'b1), .Q(counter_1_q), .clk(CLK_out), .clr(INIT_CLR_out));  // open: load, D, carry
  Button INIT_CLR (.out(INIT_CLR_out));
  nor y2 (y2_out, decoder_1_out2, decoder_1_out1, decoder_1_out0);
  or y1 (y1_out, decoder_1_out2, decoder_1_out3, decoder_1_out4);
  nor y0 (y0_out, decoder_1_out6, decoder_1_out7, decoder_1_out0);
  LED led_1 (.in(y3_out));
  or y3 (y3_out, decoder_1_out4, decoder_1_out5, decoder_1_out6);
  LED led_2 (.in(y3_out));
  LED led_3 (.in(y0_out));
  LED led_4 (.in(y0_out));
  LED led_5 (.in(y1_out));
  LED led_6 (.in(y1_out));
  LED led_7 (.in(y2_out));
  LED led_8 (.in(y2_out));
endmodule

module p9_17_MUX (
);

  wire CLK_out, multiplexer_1_out, multiplexer_2_out, multiplexer_3_out, multiplexer_4_out, not_1_out,
       not_2_out, q0_q, q1_q, q1_q0_out, q1_qn, q1q0_out, q2_q;

  Clock CLK (.out(CLK_out));
  T_Flip_Flop q2 (.clk(CLK_out), .T(q1q0_out), .Q(q2_q));  // open: Qn, preset, reset, en
  T_Flip_Flop q1 (.clk(CLK_out), .T(q0_q), .Q(q1_q), .Qn(q1_qn));  // open: preset, reset, en
  T_Flip_Flop q0 (.clk(CLK_out), .T(1'b1), .Q(q0_q));  // open: Qn, preset, reset, en
  not not_1 (not_1_out, q1q0_out);
  and q1q0 (q1q0_out, q1_q, q0_q);
  not not_2 (not_2_out, q1_q0_out);
  or q1_q0 (q1_q0_out, q1_q, q0_q);
  Multiplexer #(.enable("false")) multiplexer_1 (.in0(1'b0), .in1(not_1_out), .out(multiplexer_1_out), .sel(q2_q));
  Multiplexer #(.enable("false")) multiplexer_2 (.in0(q1q0_out), .in1(1'b1), .out(multiplexer_2_out), .sel(q2_q));
  LED led_1 (.in(multiplexer_1_out));
  LED led_2 (.in(multiplexer_1_out));
  Multiplexer #(.enable("false")) multiplexer_3 (.in0(q1_q), .in1(not_2_out), .out(multiplexer_3_out), .sel(q2_q));
  Multiplexer #(.enable("false")) multiplexer_4 (.in0(q1_q0_out), .in1(q1_qn), .out(multiplexer_4_out), .sel(q2_q));
  LED led_3 (.in(multiplexer_4_out));
  LED led_4 (.in(multiplexer_4_out));
  LED led_5 (.in(multiplexer_3_out));
  LED led_6 (.in(multiplexer_3_out));
  LED led_7 (.in(multiplexer_2_out));
  LED led_8 (.in(multiplexer_2_out));

  // Notes on the sheet:
  //   y3
  //   y2
  //   y1
  //   y0
endmodule

module p9_17_reg (
);

  wire CLK_out, CLR_out, INIT_out;
  wire [3:0] shift_register_1_out;

  Button INIT (.out(INIT_out));
  Shift_Register #(.width(4)) shift_register_1 (
    .in(shift_register_1_out), .clk(CLK_out), .out(shift_register_1_out), .load(INIT_out), .clr(CLR_out),
    .d0(4'b0100), .d1(4'b1100), .d2(4'b1101), .d3(4'b1111), .d4(4'b0111), .d5(4'b0011), .d6(4'b0001),
    .d7(4'b0000));  // open: shift, q0, q1, q2, q3, q4, q5, q6, q7
  Clock CLK (.out(CLK_out));
  Button CLR (.out(CLR_out));
  LED led_1 (.in(shift_register_1_out[3]));
  LED led_2 (.in(shift_register_1_out[3]));
  LED led_3 (.in(shift_register_1_out[0]));
  LED led_4 (.in(shift_register_1_out[0]));
  LED led_5 (.in(shift_register_1_out[1]));
  LED led_6 (.in(shift_register_1_out[1]));
  LED led_7 (.in(shift_register_1_out[2]));
  LED led_8 (.in(shift_register_1_out[2]));
endmodule

module p9_17_ROM (
);

  wire CLK_out, INIT_CLR_out;
  wire [2:0] counter_1_q;
  wire [3:0] rom_1_data;

  Clock CLK (.out(CLK_out));
  Counter #(.width(3), .max('h7)) counter_1 (
    .count(1'b1), .Q(counter_1_q), .clk(CLK_out), .clr(INIT_CLR_out));  // open: load, D, carry
  Button INIT_CLR (.out(INIT_CLR_out));
  ROM #(.addrWidth(3), .dataWidth(4)) rom_1 (.addr(counter_1_q), .data(rom_1_data));  // open: sel
  LED led_1 (.in(rom_1_data[0]));
  LED led_2 (.in(rom_1_data[0]));
  LED led_3 (.in(rom_1_data[3]));
  LED led_4 (.in(rom_1_data[3]));
  LED led_5 (.in(rom_1_data[2]));
  LED led_6 (.in(rom_1_data[2]));
  LED led_7 (.in(rom_1_data[1]));
  LED led_8 (.in(rom_1_data[1]));

  // Notes on the sheet:
  //   contents of rom_1 (hex, n*v repeats v):
  //   0 1 3 7 f d c 4
endmodule

module p9_18_main (
);

  wire CLK_out, INIT_out;
  wire [2:0] counter_1_q;
  wire [3:0] p9_18_dec_rom_1_out_2, p9_18_dec_rom_1_out_3, p9_18_dec_rom_1_out_4, p9_18_dec_rom_1_out_5,
       p9_18_dec_rom_1_out_6, p9_18_dec_rom_1_out_7, rom_1_data;

  Clock CLK (.out(CLK_out));
  Button INIT (.out(INIT_out));
  Counter #(.width(3), .max('h7)) counter_1 (
    .count(1'b1), .Q(counter_1_q), .clk(CLK_out), .clr(INIT_out));  // open: load, D, carry
  DotMatrix #(.inputtype("row"), .matrixcols(4), .matrixrows(6), .dotshape("circle")) dotmatrix_1 (
    .row0(p9_18_dec_rom_1_out_2), .row1(p9_18_dec_rom_1_out_3), .row2(p9_18_dec_rom_1_out_4),
    .row3(p9_18_dec_rom_1_out_5), .row4(p9_18_dec_rom_1_out_6), .row5(p9_18_dec_rom_1_out_7));
  p9_18_DEC_ROM p9_18_dec_rom_1 (
    .in_1(rom_1_data), .out_2(p9_18_dec_rom_1_out_2), .out_3(p9_18_dec_rom_1_out_3),
    .out_4(p9_18_dec_rom_1_out_4), .out_5(p9_18_dec_rom_1_out_5), .out_6(p9_18_dec_rom_1_out_6),
    .out_7(p9_18_dec_rom_1_out_7));
  ROM #(.addrWidth(3), .dataWidth(4)) rom_1 (.addr(counter_1_q), .data(rom_1_data));  // open: sel

  // Notes on the sheet:
  //   CNT
  //   Secuencia generada
  //   Decod.
  //   contents of rom_1 (hex, n*v repeats v):
  //   1 3 6 2 0 2 2 e
endmodule

module p9_18_codigos (
  input  [3:0] in_1,
  input  [3:0] in_2,
  input  [3:0] in_3,
  input  [3:0] in_4,
  input  [3:0] in_5,
  input  [3:0] in_6
);

  DotMatrix #(.inputtype("row"), .matrixcols(4), .matrixrows(6), .dotshape("circle")) dotmatrix_1 (
    .row0(4'b0110), .row1(4'b1001), .row2(4'b1001), .row3(4'b1001), .row4(4'b1001), .row5(4'b0110));
  DotMatrix #(.inputtype("row"), .matrixcols(4), .matrixrows(6), .dotshape("circle")) dotmatrix_2 (
    .row0(4'b1001), .row1(4'b1001), .row2(4'b1001), .row3(4'b0111), .row4(4'b0001), .row5(4'b0001));
  DotMatrix #(.inputtype("row"), .matrixcols(4), .matrixrows(6), .dotshape("circle")) dotmatrix_3 (
    .row0(4'b0110), .row1(4'b1001), .row2(4'b1001), .row3(4'b0110), .row4(4'b1001), .row5(4'b0110));
  DotMatrix #(.inputtype("row"), .matrixcols(4), .matrixrows(6), .dotshape("circle")) dotmatrix_4 (
    .row0(4'b0111), .row1(4'b1000), .row2(4'b1000), .row3(4'b1000), .row4(4'b1000), .row5(4'b0111));
  DotMatrix #(.inputtype("row"), .matrixcols(4), .matrixrows(6), .dotshape("circle")) dotmatrix_5 (
    .row0(in_1), .row1(in_2), .row2(in_3), .row3(in_4), .row4(in_5), .row5(in_6));
  DotMatrix #(.inputtype("row"), .matrixcols(4), .matrixrows(6), .dotshape("circle")) dotmatrix_6 (
    .row0(4'b0010), .row1(4'b0110), .row2(4'b1010), .row3(4'b0010), .row4(4'b0010), .row5(4'b0111));
  DotMatrix #(.inputtype("row"), .matrixcols(4), .matrixrows(6), .dotshape("circle")) dotmatrix_7 (
    .row0(4'b1111), .row1(4'b1000), .row2(4'b1000), .row3(4'b0111), .row4(4'b0001), .row5(4'b0110));
  DotMatrix #(.inputtype("row"), .matrixcols(4), .matrixrows(6), .dotshape("circle")) dotmatrix_8 (
    .row0(4'b0110), .row1(4'b1001), .row2(4'b1001), .row3(4'b0111), .row4(4'b0001), .row5(4'b0001));
  DotMatrix #(.inputtype("row"), .matrixcols(4), .matrixrows(6), .dotshape("circle")) dotmatrix_9 (
    .row0(4'b1110), .row1(4'b1001), .row2(4'b1001), .row3(4'b1001), .row4(4'b1001), .row5(4'b1110));
  DotMatrix #(.inputtype("row"), .matrixcols(4), .matrixrows(6), .dotshape("circle")) dotmatrix_10 (
    .row0(4'b0110), .row1(4'b1001), .row2(4'b0001), .row3(4'b0010), .row4(4'b0100), .row5(4'b1111));
  DotMatrix #(.inputtype("row"), .matrixcols(4), .matrixrows(6), .dotshape("circle")) dotmatrix_11 (
    .row0(4'b0110), .row1(4'b1001), .row2(4'b1000), .row3(4'b1111), .row4(4'b1001), .row5(4'b0110));
  DotMatrix #(.inputtype("row"), .matrixcols(4), .matrixrows(6), .dotshape("circle")) dotmatrix_12 (
    .row0(4'b0110), .row1(4'b1001), .row2(4'b1001), .row3(4'b1111), .row4(4'b1001), .row5(4'b1001));
  DotMatrix #(.inputtype("row"), .matrixcols(4), .matrixrows(6), .dotshape("circle")) dotmatrix_13 (
    .row0(4'b1111), .row1(4'b1000), .row2(4'b1000), .row3(4'b1111), .row4(4'b1000), .row5(4'b1111));
  DotMatrix #(.inputtype("row"), .matrixcols(4), .matrixrows(6), .dotshape("circle")) dotmatrix_14 (
    .row0(4'b0110), .row1(4'b1001), .row2(4'b0001), .row3(4'b0110), .row4(4'b0001), .row5(4'b1111));
  DotMatrix #(.inputtype("row"), .matrixcols(4), .matrixrows(6), .dotshape("circle")) dotmatrix_15 (
    .row0(4'b1111), .row1(4'b0001), .row2(4'b0010), .row3(4'b0010), .row4(4'b0010), .row5(4'b0010));
  DotMatrix #(.inputtype("row"), .matrixcols(4), .matrixrows(6), .dotshape("circle")) dotmatrix_16 (
    .row0(4'b1110), .row1(4'b1001), .row2(4'b1001), .row3(4'b1110), .row4(4'b1001), .row5(4'b1110));
  DotMatrix #(.inputtype("row"), .matrixcols(4), .matrixrows(6), .dotshape("circle")) dotmatrix_17 (
    .row0(4'b1111), .row1(4'b1000), .row2(4'b1000), .row3(4'b1110), .row4(4'b1000), .row5(4'b1000));
endmodule

module p9_18_DEC_ROM (
  input  [3:0] in_1,
  output [3:0] out_2,
  output [3:0] out_3,
  output [3:0] out_4,
  output [3:0] out_5,
  output [3:0] out_6,
  output [3:0] out_7
);

  ROM #(.addrWidth(4), .dataWidth(4)) rom_1 (.addr(in_1), .data(out_2));  // open: sel
  ROM #(.addrWidth(4), .dataWidth(4)) rom_2 (.addr(in_1), .data(out_3));  // open: sel
  ROM #(.addrWidth(4), .dataWidth(4)) rom_3 (.addr(in_1), .data(out_4));  // open: sel
  ROM #(.addrWidth(4), .dataWidth(4)) rom_4 (.addr(in_1), .data(out_5));  // open: sel
  ROM #(.addrWidth(4), .dataWidth(4)) rom_5 (.addr(in_1), .data(out_6));  // open: sel
  ROM #(.addrWidth(4), .dataWidth(4)) rom_6 (.addr(in_1), .data(out_7));  // open: sel

  // Notes on the sheet:
  //   contents of rom_1 (hex, n*v repeats v):
  //   6 2 6 6 9 f 6 f 6 6 6 e 7 e f f
  //   contents of rom_2 (hex, n*v repeats v):
  //   9 6 9 9 9 8 9 1 4*9 8 9 8 8
  //   contents of rom_3 (hex, n*v repeats v):
  //   9 a 1 1 9 8 8 2 4*9 8 9 8 8
  //   contents of rom_4 (hex, n*v repeats v):
  //   9 2 2 6 7 7 f 2 6 7 f e 8 9 f e
  //   contents of rom_5 (hex, n*v repeats v):
  //   9 2 4 1 1 1 9 2 9 1 9 9 8 9 8 8
  //   contents of rom_6 (hex, n*v repeats v):
  //   6 7 f f 1 6 6 2 6 1 9 e 7 e f 8
endmodule

module p9_19 (
);

  wire and_1_out, and_2_out, and_3_out, and_4_out, and_5_out, and_6_out, CLK_out, INIT_CLR_out, or_1_out,
       or_2_out, Pulse_out, s_r_ff_1_q, s_r_ff_1_qn, T1_carry, T2_2_carry, T3_2_carry, T4_2_carry,
       T5_2_carry, xnor_1_out;
  wire [2:0] T1_q, T2_2_q, T3_2_q;
  wire [7:0] T4_2_q, T5_2_q;

  LED led_1 (.in(and_1_out));
  LED led_2 (.in(and_2_out));
  LED led_3 (.in(xnor_1_out));
  Button Pulse (.out(Pulse_out));
  LED led_4 (.in(and_3_out));
  LED led_5 (.in(or_1_out));
  or or_1 (or_1_out, and_4_out, and_6_out);
  LED led_6 (.in(and_5_out));
  and and_1 (and_1_out, ~T4_2_carry, T2_2_carry);  // AND_Gate
  and and_2 (and_2_out, ~T2_2_carry, T1_carry);  // AND_Gate
  xnor xnor_1 (xnor_1_out, T4_2_carry, T1_carry);
  S_R_Flip_Flop #(.trigger("high")) s_r_ff_1 (
    .S(Pulse_out), .clk(1'b1), .R(1'b0), .Q(s_r_ff_1_q), .Qn(s_r_ff_1_qn), .reset(or_2_out));  // open: preset, en
  and and_3 (and_3_out, s_r_ff_1_qn, ~T5_2_carry);  // AND_Gate
  and and_4 (and_4_out, s_r_ff_1_q, ~T3_2_carry);  // AND_Gate
  and and_5 (and_5_out, T3_2_carry, ~T4_2_carry);  // AND_Gate
  and and_6 (and_6_out, T4_2_carry, ~T5_2_carry);  // AND_Gate
  Counter #(.width(3), .max('h3), .ongoal("stay")) T1 (
    .count(s_r_ff_1_q), .Q(T1_q), .carry(T1_carry), .clk(CLK_out), .clr(or_2_out));  // open: load, D
  Clock CLK (.out(CLK_out));
  // Probe on T1_q
  // Probe on T2_2_q
  Counter #(.width(3), .max('h5), .ongoal("stay")) T2_2 (
    .count(T1_carry), .Q(T2_2_q), .carry(T2_2_carry), .clk(CLK_out), .clr(or_2_out));  // open: load, D
  // Probe on T3_2_q
  Counter #(.width(3), .max('h3), .ongoal("stay")) T3_2 (
    .count(T2_2_carry), .Q(T3_2_q), .carry(T3_2_carry), .clk(CLK_out), .clr(or_2_out));  // open: load, D
  // Probe on T4_2_q
  Counter #(.max('h12), .ongoal("stay")) T4_2 (
    .count(T3_2_carry), .Q(T4_2_q), .carry(T4_2_carry), .clk(CLK_out), .clr(or_2_out));  // open: load, D
  // Probe on T5_2_q
  Counter #(.max('h1e), .ongoal("stay")) T5_2 (
    .count(T4_2_carry), .Q(T5_2_q), .carry(T5_2_carry), .clk(CLK_out), .clr(or_2_out));  // open: load, D
  or or_2 (or_2_out, T5_2_carry, INIT_CLR_out);
  Button INIT_CLR (.out(INIT_CLR_out));

  // Notes on the sheet:
  //   Vehículos
  //   Espere
  //   Pase
  //   Peatones
endmodule

module p29 (
  input  X,
  input  X_2
);

  wire and_1_out, and_2_out, and_3_out, Ck_out, CLK_out, nand_1_out, nand_2_out, nand_3_out, nand_4_out,
       not_1_out, not_2_out, not_3_out, not_4_out, not_5_out, not_6_out, not_7_out, not_8_out, not_9_out,
       qA_q, qB_q, qC_q, qD_q, qE_q;
  wire [1:0] counter_1_q;
  wire [2:0] counter_2_q;

  Clock Ck (.out(Ck_out));
  Clock CLK (.out(CLK_out));
  Counter #(.width(2), .max('h3)) counter_1 (.Q(counter_1_q), .clk(X), .clr(not_1_out));  // open: load, D, count, carry
  not not_1 (not_1_out, nand_2_out);
  not not_2 (not_2_out, X);
  and and_1 (and_1_out, X, Ck_out);
  not not_3 (not_3_out, X_2);
  and and_2 (and_2_out, X_2, CLK_out);
  Counter #(.width(3), .max('h7)) counter_2 (
    .Q(counter_2_q), .clk(and_1_out), .clr(not_4_out));  // open: load, D, count, carry
  not not_4 (not_4_out, nand_1_out);
  nand nand_1 (nand_1_out, counter_2_q[0], counter_2_q[2]);
  nand nand_2 (nand_2_out, counter_1_q[1], not_2_out);
  T_Flip_Flop qB (.clk(X_2), .T(1'b1), .Q(qB_q), .reset(not_5_out));  // open: Qn, preset, en
  not not_5 (not_5_out, nand_3_out);
  nand nand_3 (nand_3_out, qA_q, not_3_out);
  T_Flip_Flop qE (.clk(and_2_out), .T(1'b1), .Q(qE_q), .reset(not_6_out));  // open: Qn, preset, en
  not not_6 (not_6_out, nand_4_out);
  nand nand_4 (nand_4_out, qE_q, qC_q);
  T_Flip_Flop qA (.clk(X_2), .T(qB_q), .Q(qA_q), .reset(not_7_out));  // open: Qn, preset, en
  not not_7 (not_7_out, nand_3_out);
  T_Flip_Flop qD (.clk(and_2_out), .T(qE_q), .Q(qD_q), .reset(not_8_out));  // open: Qn, preset, en
  not not_8 (not_8_out, nand_4_out);
  T_Flip_Flop qC (.clk(and_2_out), .T(and_3_out), .Q(qC_q), .reset(not_9_out));  // open: Qn, preset, en
  and and_3 (and_3_out, qD_q, qE_q);
  not not_9 (not_9_out, nand_4_out);

  // Notes on the sheet:
  //   qA,qB
  //   qC,qD,qE
endmodule

module p31 (
  input  X,
  output y
);

  wire and_1_out, and_2_out, CLK_out, decoder_1_out2, decoder_1_out3, decoder_1_out4, decoder_1_out5,
       decoder_1_out9, decoder_1_out11, multiplexer_1_out, nand_1_out, not_1_out, not_2_out, not_3_out,
       not_4_out, not_5_out, not_6_out, not_7_out, not_8_out, or_1_out, q0_qn, q1_prime_X_prime_out, q1_qn,
       q1q0_prime_out, q2X_prime_out;
  wire [3:1] q0_q;

  nand nand_1 (nand_1_out, not_2_out, not_4_out, not_6_out, not_7_out);
  and and_1 (and_1_out, not_5_out, not_6_out);
  and and_2 (and_2_out, not_3_out, not_7_out);
  not not_1 (not_1_out, X);
  or or_1 (or_1_out, q0_q[3], q1_prime_X_prime_out);
  and q1_prime_X_prime (q1_prime_X_prime_out, not_1_out, q1_qn);
  Multiplexer #(.enable("false")) multiplexer_1 (.in0(or_1_out), .in1(X), .out(multiplexer_1_out), .sel(q0_q[1]));
  Clock CLK (.out(CLK_out));
  not not_2 (not_2_out, decoder_1_out2);
  not not_3 (not_3_out, decoder_1_out3);
  not not_4 (not_4_out, decoder_1_out4);
  not not_5 (not_5_out, decoder_1_out5);
  not not_6 (not_6_out, decoder_1_out9);
  not not_7 (not_7_out, decoder_1_out11);
  Decoder #(.select(4), .enable("false")) decoder_1 (
    .out2(decoder_1_out2), .out3(decoder_1_out3), .out4(decoder_1_out4), .out5(decoder_1_out5),
    .out9(decoder_1_out9), .out11(decoder_1_out11), .sel({q0_q, X}));  // open: out0, out1, out6, out7, out8, out10, out12, out13, out14, out15
  not not_8 (not_8_out, X);
  T_Flip_Flop q2 (.clk(CLK_out), .T(multiplexer_1_out), .Q(q0_q[3]));  // open: Qn, preset, reset, en
  D_Flip_Flop q1 (.clk(CLK_out), .D(nand_1_out), .Q(q0_q[2]), .Qn(q1_qn));  // open: preset, en, reset
  J_K_Flip_Flop q0 (.J(and_1_out), .clk(CLK_out), .K(and_2_out), .Q(q0_q[1]), .Qn(q0_qn));  // open: preset, en, reset
  and q2X_prime (q2X_prime_out, not_8_out, q0_q[3]);
  and q1q0_prime (q1q0_prime_out, q0_q[2], q0_qn);
  or or_2 (y, q2X_prime_out, q1q0_prime_out);
endmodule

module p31_D1 (
  input  q2,
  input  q1,
  input  q0,
  input  X,
  output D1,
  output J0,
  output K0
);

  wire decoder_1_out2, decoder_1_out3, decoder_1_out4, decoder_1_out5, decoder_1_out9, decoder_1_out11,
       not_1_out, not_2_out, not_3_out, not_4_out, not_5_out, not_6_out;

  Decoder #(.select(4), .enable("false")) decoder_1 (
    .out2(decoder_1_out2), .out3(decoder_1_out3), .out4(decoder_1_out4), .out5(decoder_1_out5),
    .out9(decoder_1_out9), .out11(decoder_1_out11), .sel({q2, q1, q0, X}));  // open: out0, out1, out6, out7, out8, out10, out12, out13, out14, out15
  not not_1 (not_1_out, decoder_1_out2);
  not not_2 (not_2_out, decoder_1_out3);
  not not_3 (not_3_out, decoder_1_out4);
  not not_4 (not_4_out, decoder_1_out5);
  not not_5 (not_5_out, decoder_1_out9);
  not not_6 (not_6_out, decoder_1_out11);
  nand nand_1 (D1, not_1_out, not_3_out, not_6_out, not_5_out);
  and and_1 (J0, not_4_out, not_5_out);
  and and_2 (K0, not_2_out, not_6_out);
endmodule

module p32 (
);

  wire CLK_out, nor_1_out, q0_qn, q1_qn, q2_qn;

  Clock CLK (.out(CLK_out));
  T_Flip_Flop q0 (.clk(CLK_out), .T(1'b1), .Qn(q0_qn), .reset(nor_1_out));  // open: Q, preset, en
  T_Flip_Flop q1 (.clk(q0_qn), .T(1'b1), .Qn(q1_qn), .reset(nor_1_out));  // open: Q, preset, en
  T_Flip_Flop q2 (.clk(q1_qn), .T(1'b1), .Qn(q2_qn), .reset(nor_1_out));  // open: Q, preset, en
  nor nor_1 (nor_1_out, q2_qn, q1_qn, q0_qn);
endmodule
