// Logisim project Cap2.circ as structural Verilog: 1 circuit, main circuit main
module main (
  input  [2:0] Magnitud,
  input  [2:0] Magnitud_2,
  output [2:0] C2__complemento,
  output [2:0] C1__complemento,
  output [2:0] C2__complemento_2,
  output [2:0] C1__complemento_2
);

  // Probe on Magnitud
  assign C1__complemento = ~Magnitud;  // NOT_Gate not_1, 3 bits wide
  // Probe on Magnitud_2
  assign C1__complemento_2 = ~Magnitud_2;  // NOT_Gate not_2, 3 bits wide
  // Probe on C2__complemento
  Negator #(.width(3)) negator_1 (.in(Magnitud), .out(C2__complemento));
  // Probe on C2__complemento_2
  Adder #(.width(3)) adder_1 (.a(3'b001), .b(C1__complemento_2), .out(C2__complemento_2));  // open: cin, cout
endmodule
