// Logisim project Cap3_1_MOSgates.circ as structural Verilog: 14 circuits, main circuit NAND-cmos
module NOT_nmos (
  input  A,
  input  A_2,
  output A_prime,
  output A_prime_2
);

  Pull_Resistor #(.pull(1)) pull_resistor_1 (.node(A_prime));
  Transistor #(.\type ("n")) transistor_1 (.in(1'b0), .out(A_prime), .gate(A));
  not not_1 (A_prime_2, A_2);
endmodule

module AND_nmos (
  input  A,
  input  B,
  input  A_2,
  input  B_2,
  output AB,
  output AB_2
);

  wire transistor_1_out;

  Transistor #(.\type ("n")) transistor_1 (.in(1'b1), .out(transistor_1_out), .gate(A));
  Pull_Resistor pull_resistor_1 (.node(AB));
  Transistor #(.\type ("n")) transistor_2 (.in(transistor_1_out), .out(AB), .gate(B));
  and and_1 (AB_2, A_2, B_2);
endmodule

module OR_nmos (
  input  A,
  input  B,
  input  A_2,
  input  B_2,
  output A_B,
  output A_B_2
);

  Transistor #(.\type ("n")) transistor_1 (.in(1'b1), .out(A_B), .gate(A));
  Transistor #(.\type ("n")) transistor_2 (.in(1'b1), .out(A_B), .gate(B));
  Pull_Resistor pull_resistor_1 (.node(A_B));
  or or_1 (A_B_2, A_2, B_2);
endmodule

module NOT_pmos (
  input  A,
  input  A_2,
  output A_prime,
  output A_prime_2
);

  Transistor transistor_1 (.in(1'b1), .out(A_prime), .gate(A));
  Pull_Resistor pull_resistor_1 (.node(A_prime));
  not not_1 (A_prime_2, A_2);
endmodule

module AND_pmos (
  input  A,
  input  B,
  input  A_2,
  input  B_2,
  output AB,
  output AB_2
);

  Pull_Resistor #(.pull(1)) pull_resistor_1 (.node(AB));
  Transistor transistor_1 (.in(1'b0), .out(AB), .gate(A));
  Transistor transistor_2 (.in(1'b0), .out(AB), .gate(B));
  and and_1 (AB_2, A_2, B_2);
endmodule

module OR_pmos (
  input  A,
  input  B,
  input  A_2,
  input  B_2,
  output A_B,
  output A_B_2
);

  wire transistor_2_out;

  Transistor transistor_1 (.in(transistor_2_out), .out(A_B), .gate(A));
  Pull_Resistor #(.pull(1)) pull_resistor_1 (.node(A_B));
  Transistor transistor_2 (.in(1'b0), .out(transistor_2_out), .gate(B));
  or or_1 (A_B_2, A_2, B_2);
endmodule

module NOT_cmos (
  input  A,
  input  A_2,
  output A_prime,
  output A_prime_2
);

  Transistor transistor_1 (.in(1'b1), .out(A_prime), .gate(A));
  Transistor #(.\type ("n")) transistor_2 (.in(1'b0), .out(A_prime), .gate(A));
  not not_1 (A_prime_2, A_2);
endmodule

module NAND_cmos (
  input  A,
  input  B,
  input  A_2,
  input  B_2,
  output f,
  output f_2
);

  wire transistor_4_out;

  Transistor transistor_1 (.in(1'b1), .out(f), .gate(A));
  nand nand_1 (f_2, A_2, B_2);
  Transistor transistor_2 (.in(1'b1), .out(f), .gate(B));
  Transistor #(.\type ("n")) transistor_3 (.in(transistor_4_out), .out(f), .gate(A));
  Transistor #(.\type ("n")) transistor_4 (.in(1'b0), .out(transistor_4_out), .gate(B));

  // Notes on the sheet:
  //   Vdd
  //   T1
  //   T2
  //   T3
  //   T4
endmodule

module NOR_cmos (
  input  A,
  input  B,
  input  A_2,
  input  B_2,
  output f,
  output f_2
);

  wire transistor_1_out;

  Transistor transistor_1 (.in(1'b1), .out(transistor_1_out), .gate(A));
  Transistor transistor_2 (.in(transistor_1_out), .out(f), .gate(B));
  Transistor #(.\type ("n")) transistor_3 (.in(1'b0), .out(f), .gate(A));
  Transistor #(.\type ("n")) transistor_4 (.in(1'b0), .out(f), .gate(B));
  nor nor_1 (f_2, A_2, B_2);

  // Notes on the sheet:
  //   Vdd
  //   T1
  //   T2
  //   T3
  //   T4
endmodule

module AND_cmos (
  input  A,
  input  B,
  input  A_2,
  input  B_2,
  output AB,
  output AB_2
);

  wire transistor_1_out, transistor_4_out;

  Transistor transistor_1 (.in(1'b1), .out(transistor_1_out), .gate(B));
  Transistor transistor_2 (.in(1'b1), .out(transistor_1_out), .gate(A));
  Transistor #(.\type ("n")) transistor_3 (.in(transistor_4_out), .out(transistor_1_out), .gate(A));
  Transistor #(.\type ("n")) transistor_4 (.in(1'b0), .out(transistor_4_out), .gate(B));
  and and_1 (AB_2, A_2, B_2);
  Transistor transistor_5 (.in(1'b1), .out(AB), .gate(transistor_1_out));
  Transistor #(.\type ("n")) transistor_6 (.in(1'b0), .out(AB), .gate(transistor_1_out));
endmodule

module OR_cmos (
  input  A,
  input  B,
  input  A_2,
  input  B_2,
  output A_B,
  output A_B_2
);

  wire transistor_1_out, transistor_2_out;

  Transistor transistor_1 (.in(1'b1), .out(transistor_1_out), .gate(A));
  Transistor transistor_2 (.in(transistor_1_out), .out(transistor_2_out), .gate(B));
  Transistor #(.\type ("n")) transistor_3 (.in(1'b0), .out(transistor_2_out), .gate(B));
  Transistor #(.\type ("n")) transistor_4 (.in(1'b0), .out(transistor_2_out), .gate(A));
  Transistor transistor_5 (.in(1'b1), .out(A_B), .gate(transistor_2_out));
  Transistor #(.\type ("n")) transistor_6 (.in(1'b0), .out(A_B), .gate(transistor_2_out));
  or or_1 (A_B_2, A_2, B_2);
endmodule

module Buffer_cmos (
  input  A,
  input  A_2,
  output A_3,
  output A_4
);

  wire transistor_1_out;

  Transistor transistor_1 (.in(1'b1), .out(transistor_1_out), .gate(A));
  Transistor #(.\type ("n")) transistor_2 (.in(1'b0), .out(transistor_1_out), .gate(A));
  buf buffer_1 (A_4, A_2);
  Transistor transistor_3 (.in(1'b1), .out(A_3), .gate(transistor_1_out));
  Transistor #(.\type ("n")) transistor_4 (.in(1'b0), .out(A_3), .gate(transistor_1_out));
endmodule

module Puerta_de_transmision_cmos (
  input  A,
  input  S,
  input  A_2,
  input  S_2,
  output f,
  output f_2
);

  wire transistor_1_out, transistor_3_out;

  Transistor transistor_1 (.in(1'b1), .out(transistor_1_out), .gate(S));
  Transistor #(.\type ("n")) transistor_2 (.in(1'b0), .out(transistor_1_out), .gate(S));
  Transistor transistor_3 (.in(1'b1), .out(transistor_3_out), .gate(S_2));
  Transistor #(.\type ("n")) transistor_4 (.in(1'b0), .out(transistor_3_out), .gate(S_2));
  // Transmission_Gate transmission_1: pin names not known; wires that end beside it: A, transistor_1_out, S, transistor_3_out, f
  Transistor transistor_5 (.in(A_2), .out(f_2), .gate(transistor_3_out));
  Transistor #(.\type ("n"), .gate("br")) transistor_6 (.in(A_2), .out(f_2), .gate(S_2));
endmodule

module Buffer_triestado_cmos (
  input  A,
  input  S,
  input  A_2,
  input  S_2,
  output f,
  output f_2
);

  wire transistor_1_out, transistor_3_out, transistor_4_out;

  Transistor transistor_1 (.in(1'b1), .out(transistor_1_out), .gate(A));
  Transistor #(.\type ("n")) transistor_2 (.in(1'b0), .out(transistor_1_out), .gate(A));
  assign f_2 = S_2 ? A_2 : 1'bz;  // Controlled_Buffer controlled_buffer_1
  Transistor transistor_3 (.in(1'b1), .out(transistor_3_out), .gate(S));
  Transistor transistor_4 (.in(1'b1), .out(transistor_4_out), .gate(transistor_1_out));
  Transistor #(.\type ("n")) transistor_5 (.in(1'b0), .out(transistor_3_out), .gate(S));
  Transistor #(.\type ("n")) transistor_6 (.in(1'b0), .out(transistor_4_out), .gate(transistor_1_out));
  // Transmission_Gate transmission_1: pin names not known; wires that end beside it: transistor_4_out, transistor_3_out, S, f
endmodule
