// Logisim project Cap3_2_gates.circ as structural Verilog: 9 circuits, main circuit Alarma-cinturon
module complemento_1 (
  input  in_1,
  input  in_2,
  input  in_3,
  input  in_4,
  input  in_5,
  input  in_6,
  input  in_7,
  input  in_8,
  input  [7:0] in_9,
  output out_10,
  output out_11,
  output out_12,
  output out_13,
  output out_14,
  output out_15,
  output out_16,
  output out_17,
  output [7:0] out_18
);

  not not_1 (out_11, in_2);
  not not_2 (out_10, in_1);
  not not_3 (out_13, in_4);
  not not_4 (out_12, in_3);
  not not_5 (out_14, in_5);
  not not_6 (out_15, in_6);
  not not_7 (out_16, in_7);
  not not_8 (out_17, in_8);
  assign out_18 = ~in_9;  // NOT_Gate not_9, 8 bits wide
endmodule

module Alarma_cinturon (
  input  Arranque,
  input  \Cinturón ,
  output Alerta
);

  and and_1 (Alerta, Arranque, ~\Cinturón );  // AND_Gate
endmodule

module enable (
  output Salida,
  output Salida_2
);

  wire Enable_2_out, Enable_out, Entrada_2_out, Entrada_out;

  Clock Entrada (.out(Entrada_out));
  and and_1 (Salida, Entrada_out, Enable_out);
  Button Enable (.out(Enable_out));
  Clock Entrada_2 (.out(Entrada_2_out));
  Button Enable_2 (.out(Enable_2_out));
  and and_2 (Salida_2, Entrada_2_out, ~Enable_2_out);  // AND_Gate
endmodule

module Alarma_hogar (
  input  Ventanas,
  input  Puerta,
  input  Pasillo,
  output Alarma
);

  or or_1 (Alarma, Ventanas, Puerta, Pasillo);
endmodule

module complemento_2 (
  input  [2:0] in_1,
  input  signo,
  output [3:0] C2
);

  wire [2:0] xor_3_out;

  // Probe on in_1
  xor xor_1 (xor_3_out[2], signo, in_1[2]);
  xor xor_2 (xor_3_out[1], signo, in_1[1]);
  xor xor_3 (xor_3_out[0], signo, in_1[0]);
  Adder #(.width(3)) adder_1 (.a(xor_3_out), .b(3'b000), .out(C2[2:0]), .cin(signo));  // open: cout
  // Probe on {signo, C2[2:0]}

  assign C2[3] = signo;
endmodule

module gates (
  input  A,
  input  A_2,
  input  A_3,
  input  B,
  input  B_2,
  input  A_4,
  input  A_5,
  input  B_3,
  input  B_4,
  input  A_6,
  input  A_7,
  input  B_5,
  input  B_6,
  input  A_8,
  input  A_9,
  input  B_7,
  input  B_8,
  output f,
  output f_2,
  output f_3,
  output f_4,
  output f_5,
  output f_6,
  output f_7,
  output f_8,
  output f_9
);

  not NOT (f, A_3);
  and AND (f_2, A, B);
  nand NAND (f_4, A_4, B_3);
  nor NOR (f_6, A_6, B_5);
  xor XOR (f_8, A_8, B_7);
  or OR (f_3, A_2, B_2);
  or OR_2 (f_5, ~A_5, ~B_4);  // OR_Gate
  and AND_2 (f_7, ~A_7, ~B_6);  // AND_Gate
  xnor XNOR (f_9, A_9, B_8);
endmodule

module asociativa_AND (
  input  A,
  input  B,
  input  C,
  input  A_2,
  input  B_2,
  input  C_2,
  input  A_3,
  input  B_3,
  input  C_3,
  output f,
  output f_2,
  output f_3
);

  wire and_1_out, and_2_out;

  and and_1 (and_1_out, B, C);
  and and_2 (and_2_out, A_3, B_3);
  and and_3 (f, A, and_1_out);
  and and_4 (f_3, and_2_out, C_3);
  and and_5 (f_2, A_2, B_2, C_2);

  // Notes on the sheet:
  //   BC
  //   AB
  //   A(BC)
  //   (AB)C
  //   ABC
endmodule

module Universalidad_NAND_NOR (
  input  A,
  input  A_2,
  input  A_3,
  input  A_4,
  input  B,
  input  B_2,
  input  A_5,
  input  A_6,
  input  B_3,
  input  B_4,
  output A_prime,
  output A_prime_2,
  output A_prime_3,
  output A_prime_4,
  output AB,
  output AB_2,
  output AB_3,
  output AB_4,
  output A_B,
  output A_B_2,
  output A_B_3,
  output A_B_4
);

  wire nand_2_out, nand_3_out, nand_4_out, nor_2_out, nor_4_out, nor_6_out;

  not not_1 (A_prime, A);
  nand nand_1 (A_prime_3, A, A);
  and and_1 (AB, A_3, B);
  nand nand_2 (nand_2_out, A_3, B);
  or or_1 (A_B, A_5, B_3);
  nand nand_3 (nand_3_out, A_5, A_5);
  nand nand_4 (nand_4_out, B_3, B_3);
  nand nand_5 (AB_3, nand_2_out, nand_2_out);
  nand nand_6 (A_B_3, nand_3_out, nand_4_out);
  not not_2 (A_prime_2, A_2);
  and and_2 (AB_2, A_4, B_2);
  or or_2 (A_B_2, A_6, B_4);
  nor nor_1 (A_prime_4, A_2, A_2);
  nor nor_2 (nor_2_out, A_4, A_4);
  nor nor_3 (AB_4, nor_2_out, nor_4_out);
  nor nor_4 (nor_4_out, B_2, B_2);
  nor nor_5 (A_B_4, nor_6_out, nor_6_out);
  nor nor_6 (nor_6_out, A_6, B_4);

  // Notes on the sheet:
  //   (AA)'
  //   (AB)'
  //   A'
  //   B'
  //   (AB)''
  //   (A'B')'
  //   B'
  //   (A+B)'
  //   (A+A)'
  //   A'
  //   (A'+B')'
endmodule

module XOR_XNOR_con_elementales (
  input  A,
  input  B,
  input  A_2,
  input  A_3,
  input  B_2,
  input  B_3,
  input  A_4,
  input  B_4,
  input  A_5,
  input  A_6,
  input  B_5,
  input  B_6,
  output A_XOR_B,
  output A_XOR_B_2,
  output A_XOR_B_3,
  output A_XNOR_B,
  output A_XNOR_B_2,
  output A_XNOR_B_3
);

  wire A_B_out, A_B_prime_out, A_prime_B_2_out, A_prime_B_out, A_prime_B_prime_2_out, A_prime_B_prime_out,
       AB_out, AB_prime_out;

  and AB_prime (AB_prime_out, A_2, ~B_2);  // AND_Gate
  and A_prime_B (A_prime_B_out, B_2, ~A_2);  // AND_Gate
  and AB (AB_out, A_5, B_5);
  and A_prime_B_prime (A_prime_B_prime_out, ~B_5, ~A_5);  // AND_Gate
  or or_1 (A_XOR_B_2, AB_prime_out, A_prime_B_out);
  or or_2 (A_XNOR_B_2, AB_out, A_prime_B_prime_out);
  xor xor_1 (A_XOR_B, A, B);
  xnor xnor_1 (A_XNOR_B, A_4, B_4);
  or A_B (A_B_out, A_3, B_3);
  or A_prime_B_prime_2 (A_prime_B_prime_2_out, ~B_3, ~A_3);  // OR_Gate
  or A_B_prime (A_B_prime_out, A_6, ~B_6);  // OR_Gate
  or A_prime_B_2 (A_prime_B_2_out, B_6, ~A_6);  // OR_Gate
  and and_1 (A_XOR_B_3, A_B_out, A_prime_B_prime_2_out);
  and and_2 (A_XNOR_B_3, A_B_prime_out, A_prime_B_2_out);
endmodule
