// Logisim project Cap3_3_gatesBoole.circ as structural Verilog: 19 circuits, main circuit gates
module gates (
  input  A,
  input  A_2,
  input  A_3,
  input  A_4,
  input  B,
  input  B_2,
  input  B_3,
  input  A_5,
  input  A_6,
  input  A_7,
  input  B_4,
  input  B_5,
  input  B_6,
  input  A_8,
  input  A_9,
  input  B_7,
  input  B_8,
  input  A_10,
  input  B_9,
  output f,
  output f_2,
  output f_3,
  output f_4,
  output f_5,
  output f_6,
  output f_7,
  output f_8,
  output f_9,
  output f_10
);

  wire AND_2_out;

  not not_1 (f, A);
  and AND (f_2, A_2, B);
  or OR (f_5, A_5, B_4);
  xor XOR (f_8, A_8, B_7);
  and AND_2 (AND_2_out, A_10, B_9);
  not not_2 (f_10, AND_2_out);
  nand NAND (f_3, A_3, B_2);
  nor NOR (f_6, A_6, B_5);
  xnor XNOR (f_9, A_9, B_8);
  or OR_2 (f_4, ~A_4, ~B_3);  // OR_Gate
  and AND_3 (f_7, ~A_7, ~B_6);  // AND_Gate

  // Notes on the sheet:
  //   Equivalente a NAND
  //   Equivalente a NOR
endmodule

module Inversor (
  input  A,
  input  A_2,
  input  in_3,
  input  in_4,
  input  in_5,
  input  in_6,
  input  in_7,
  input  in_8,
  input  in_9,
  input  in_10,
  input  [7:0] in_11,
  output f,
  output f_2,
  output out_14,
  output out_15,
  output out_16,
  output out_17,
  output out_18,
  output out_19,
  output C1,
  output out_21,
  output [7:0] out_22
);

  not not_1 (out_15, in_4);
  not not_2 (out_14, in_3);
  not not_3 (f, A);
  not not_4 (f_2, A_2);
  not not_5 (out_16, in_5);
  not not_6 (out_19, in_8);
  not not_7 (out_17, in_6);
  not not_8 (out_18, in_7);
  not not_9 (out_21, in_10);
  not not_10 (C1, in_9);
  assign out_22 = ~in_11;  // NOT_Gate not_11, 8 bits wide
endmodule

module Apl_AND_I (
  input  A,
  output Salida,
  output Salida_2,
  output f
);

  wire Enable_2_out, Enable_out, Entrada_2_out, Entrada_out, not_1_out;

  Clock Entrada (.out(Entrada_out));
  and and_1 (Salida, Entrada_out, Enable_out);
  Button Enable (.out(Enable_out));
  not not_1 (not_1_out, A);
  and and_2 (f, A, not_1_out);
  Clock Entrada_2 (.out(Entrada_2_out));
  and and_3 (Salida_2, Entrada_2_out, ~Enable_2_out);  // AND_Gate
  Button Enable_2 (.out(Enable_2_out));

  // Notes on the sheet:
  //   Habilitación a nivel alto
  //   B
  //   Habilitación a nivel bajo
endmodule

module Apl_AND_II (
  input  Arranque,
  input  \Cinturón ,
  input  Alarma_previa,
  input  Arranque_2,
  input  \Cinturón_2 ,
  output Alarma
);

  wire and_1_out, and_3_out, CLK_out, not_1_out, or_1_out, Timer_carry;

  Clock CLK (.out(CLK_out));
  and and_1 (and_1_out, \Cinturón_2 , Arranque_2);
  or or_1 (or_1_out, and_1_out, ~Arranque_2);  // OR_Gate
  and and_2 (Alarma, Arranque, \Cinturón , ~Alarma_previa);  // AND_Gate
  Counter #(.width(4), .max('h6)) Timer (
    .count(Arranque_2), .carry(Timer_carry), .clk(CLK_out), .clr(or_1_out));  // open: load, D, Q
  not not_1 (not_1_out, \Cinturón_2 );
  LED led_1 (.in(and_3_out));
  and and_3 (and_3_out, Arranque_2, not_1_out, Timer_carry);

  // Notes on the sheet:
  //   Alarma
endmodule

module Apl_OR_I (
  input  Ventanas,
  input  Puerta,
  input  Pasillo,
  input  Ventanas_2,
  input  Puerta_2,
  input  Pasillo_2,
  input  [3:0] Clave,
  input  [3:0] \Código ,
  output Alarma,
  output out_10,
  output out_11
);

  wire and_1_out, CLK_out, comparator_1_eq, not_1_out, or_2_out, or_3_out, RESET_out, sonido_on_off_q,
       Timer_carry;
  wire [3:0] Timer_q;

  or or_1 (Alarma, Ventanas, Puerta, Pasillo);
  Comparator #(.width(4)) comparator_1 (.a(Clave), .b(\Código ), .eq(comparator_1_eq));  // open: gt, lt
  or or_2 (or_2_out, Ventanas_2, Puerta_2, Pasillo_2);
  Clock CLK (.out(CLK_out));
  Button RESET (.out(RESET_out));
  and and_1 (and_1_out, comparator_1_eq, RESET_out);
  J_K_Flip_Flop Memoria_sensor (
    .J(or_2_out), .clk(CLK_out), .K(1'b0), .Q(out_10), .reset(comparator_1_eq));  // open: Qn, preset, en
  or or_3 (or_3_out, comparator_1_eq, out_11);
  Hex_Digit_Display hex_digit_display_1 (.value(Timer_q));  // open: dp
  Counter #(.width(4), .max('h4)) Timer (
    .count(out_10), .Q(Timer_q), .carry(Timer_carry), .clk(CLK_out), .clr(or_3_out));  // open: load, D
  J_K_Flip_Flop Mem__alarma (
    .J(Timer_carry), .clk(CLK_out), .K(1'b0), .Q(out_11), .reset(and_1_out));  // open: Qn, preset, en
  T_Flip_Flop sonido_on_off (.clk(CLK_out), .T(1'b1), .Q(sonido_on_off_q), .reset(not_1_out));  // open: Qn, preset, en
  LED led_1 (.in(sonido_on_off_q));
  not not_1 (not_1_out, out_11);

  // Notes on the sheet:
  //   Comparador
  //   Piloto
endmodule

module Universal_gates (
  input  A,
  input  B,
  output f,
  output f_2,
  output f_3,
  output f_4
);

  or OR (f, ~A, ~B);  // OR_Gate
  and AND (f_3, ~A, ~B);  // AND_Gate
  nand NAND (f_2, A, B);
  nor NOR (f_4, A, B);

  // Notes on the sheet:
  //   Equivalente a NAND
  //   Equivalente a NOR
endmodule

module Equiv_XOR (
  input  A,
  input  B,
  output f,
  output g,
  output h
);

  wire A_B_out, A_prime_B_out, A_prime_B_prime_out, AB_prime_out, not_1_out, not_2_out, not_3_out, not_4_out;

  not not_1 (not_1_out, A);
  and A_prime_B (A_prime_B_out, not_1_out, B);
  and AB_prime (AB_prime_out, A, not_2_out);
  not not_2 (not_2_out, B);
  or A_B (A_B_out, A, B);
  not not_3 (not_3_out, A);
  or A_prime_B_prime (A_prime_B_prime_out, not_3_out, not_4_out);
  not not_4 (not_4_out, B);
  xor xor_1 (f, A, B);
  or A_prime_B_AB_prime (g, A_prime_B_out, AB_prime_out);
  and A_B__A_prime_B_prime (h, A_B_out, A_prime_B_prime_out);
endmodule

module Equiv_XNOR (
  input  A,
  input  B,
  output f,
  output f_2,
  output f_3
);

  wire not_1_out, not_2_out;

  xnor xnor_1 (f, A, B);
  not not_1 (not_1_out, A);
  xor xor_1 (f_2, not_1_out, B);
  xor xor_2 (f_3, A, not_2_out);
  not not_2 (not_2_out, B);
endmodule

module Apl_XOR (
  input  A,
  input  B,
  input  [3:0] Signo_magnitud,
  output A____B__suma_A_B,
  output [3:0] C2
);

  wire [2:0] xor_4_out;

  xor xor_1 (A____B__suma_A_B, A, B);
  xor xor_2 (xor_4_out[2], Signo_magnitud[3], Signo_magnitud[2]);
  xor xor_3 (xor_4_out[1], Signo_magnitud[3], Signo_magnitud[1]);
  xor xor_4 (xor_4_out[0], Signo_magnitud[3], Signo_magnitud[0]);
  Adder #(.width(3)) adder_1 (.a(xor_4_out), .b(3'b000), .out(C2[2:0]), .cin(Signo_magnitud[3]));  // open: cout
  // Probe on {Signo_magnitud[3], C2[2:0]}

  assign C2[3] = Signo_magnitud[3];
endmodule

module Prop_asociativa_AND (
  input  A,
  input  B,
  input  C,
  output f,
  output g,
  output h
);

  wire AB_out, BC_out;

  and AB (AB_out, A, B);
  and AB_C (f, AB_out, C);
  and BC (BC_out, B, C);
  and A_BC (g, BC_out, A);
  and ABC (h, C, B, A);

  // Notes on the sheet:
  //   La puerta AND cumple la propiedad asociativa
endmodule

module Prop_asociativa_OR (
  input  A,
  input  B,
  input  C,
  output f,
  output g,
  output h
);

  wire A_B_out, B_C_out;

  or A_B (A_B_out, A, B);
  or B_C (B_C_out, B, C);
  or A_B__C (f, A_B_out, C);
  or A__B_C (g, B_C_out, A);
  or A_B_C (h, B, C, A);

  // Notes on the sheet:
  //   La puerta OR cumple la propiedad asociativa
endmodule

module Prop_asociativa_NAND (
  input  A,
  input  B,
  input  C,
  output f,
  output g,
  output h
);

  wire AB__prime_out, BC__prime_out;

  nand AB__prime (AB__prime_out, A, B);
  nand BC__prime (BC__prime_out, B, C);
  nand AB__prime_C__prime (f, AB__prime_out, C);
  nand A_BC__prime__prime (g, BC__prime_out, A);
  nand ABC__prime (h, B, C, A);

  // Notes on the sheet:
  //   La puerta NAND NO CUMPLE la propiedad asociativa
endmodule

module Prop_asociativa_NOR (
  input  A,
  input  B,
  input  C,
  output f,
  output g,
  output h
);

  wire A_B__prime_out, B_C__prime_out;

  nor A_B__prime (A_B__prime_out, A, B);
  nor B_C__prime (B_C__prime_out, B, C);
  nor A_B__prime_C__prime (f, A_B__prime_out, C);
  nor A__B_C__prime__prime (g, B_C__prime_out, A);
  nor A_B_C__prime (h, B, C, A);

  // Notes on the sheet:
  //   La puerta NOR NO CUMPLE la propiedad asociativa
endmodule

module Prop_asociativa_XOR (
  input  A,
  input  B,
  input  C,
  output f,
  output f_2,
  output f_3
);

  wire xor_1_out, xor_2_out;

  xor xor_1 (xor_1_out, A, B);
  xor xor_2 (xor_2_out, B, C);
  xor xor_3 (f, xor_1_out, C);
  xor xor_4 (f_2, xor_2_out, A);
  xor xor_5 (f_3, B, C, A);

  // Notes on the sheet:
  //   La puerta XOR cumple la propiedad asociativa
  //   No hay equivalencia con puertas de múltiples entradas
endmodule

module Prop_asociativa_XNOR (
  input  A,
  input  B,
  input  C,
  output f,
  output f_2,
  output f_3
);

  wire xnor_1_out, xnor_2_out;

  xnor xnor_1 (xnor_1_out, A, B);
  xnor xnor_2 (xnor_2_out, B, C);
  xnor xnor_3 (f, xnor_1_out, C);
  xnor xnor_4 (f_2, xnor_2_out, A);
  xnor xnor_5 (f_3, B, C, A);

  // Notes on the sheet:
  //   La puerta XNOR cumple la propiedad asociativa
  //   No hay equivalencia con puertas de múltiples entradas
endmodule

module Prop_distributiva_I (
  input  A,
  input  B,
  input  C,
  output A_B_C,
  output AB_AC
);

  wire and_1_out, and_2_out, or_1_out;

  or or_1 (or_1_out, B, C);
  and and_1 (and_1_out, A, B);
  and and_2 (and_2_out, A, C);
  and and_3 (A_B_C, A, or_1_out);
  or or_2 (AB_AC, and_1_out, and_2_out);
endmodule

module Prop_distributiva_II (
  input  A,
  input  B,
  input  C,
  output A_BC,
  output A_B__A_C
);

  wire and_1_out, or_1_out, or_2_out;

  and and_1 (and_1_out, B, C);
  or or_1 (or_1_out, A, B);
  or or_2 (or_2_out, A, C);
  or or_3 (A_BC, A, and_1_out);
  and and_2 (A_B__A_C, or_1_out, or_2_out);
endmodule

module Teorema_absorcion_T6_T6 (
  input  A,
  input  B,
  output A_2,
  output A_AB,
  output A_A_B
);

  wire and_1_out, or_1_out;

  and and_1 (and_1_out, A, B);
  or or_1 (or_1_out, A, B);
  or or_2 (A_AB, A, and_1_out);
  and and_2 (A_A_B, A, or_1_out);

  assign A_2 = A;
endmodule

module Teorema_consenso_T8_T8 (
  input  A,
  input  B,
  output A_2,
  output AB_AB_prime,
  output A_B__A_B_prime
);

  wire and_1_out, and_2_out, or_1_out, or_2_out;

  and and_1 (and_1_out, A, B);
  and and_2 (and_2_out, A, ~B);  // AND_Gate
  or or_1 (or_1_out, A, B);
  or or_2 (or_2_out, A, ~B);  // OR_Gate
  or or_3 (AB_AB_prime, and_1_out, and_2_out);
  and and_3 (A_B__A_B_prime, or_1_out, or_2_out);

  assign A_2 = A;
endmodule
