// Logisim project Cap3_4_optim.circ as structural Verilog: 10 circuits, main circuit Redes AND/OR y OR/AND
module main (
  input  A,
  input  B,
  input  C,
  output f
);

  wire BC_out;

  and BC (BC_out, B, C);
  or A__BC (f, A, BC_out);
endmodule

module Redes_AND_OR_y_OR_AND (
  input  A,
  input  B,
  input  C,
  input  D,
  input  A_2,
  input  B_2,
  input  C_2,
  input  D_2,
  input  A_3,
  input  B_3,
  input  C_3,
  input  D_3,
  output f_AB_BCD_AC,
  output f__A_B__B_C_D__A_C,
  output F
);

  wire and_1_out, and_2_out, and_3_out, and_5_out, not_1_out, not_2_out, not_3_out, not_4_out, or_1_out,
       or_2_out, or_3_out, or_5_out, or_6_out, or_7_out;

  not not_1 (not_1_out, A_3);
  not not_2 (not_2_out, B_3);
  not not_3 (not_3_out, C_3);
  not not_4 (not_4_out, D_3);
  and and_1 (and_1_out, A, B);
  and and_2 (and_2_out, B, C, D);
  and and_3 (and_3_out, A, C);
  or or_1 (or_1_out, A_2, B_2);
  or or_2 (or_2_out, B_2, C_2, D_2);
  or or_3 (or_3_out, A_2, C_2);
  or or_4 (f_AB_BCD_AC, and_1_out, and_2_out, and_3_out);
  and and_4 (f__A_B__B_C_D__A_C, or_1_out, or_2_out, or_3_out);
  or or_5 (or_5_out, not_1_out, not_2_out);
  and and_5 (and_5_out, or_5_out, or_6_out, or_7_out);
  or or_6 (or_6_out, not_2_out, not_3_out, not_4_out);
  or or_7 (or_7_out, not_1_out, not_3_out);
  not not_5 (F, and_5_out);

  // Notes on the sheet:
  //   f=((A'+B')(B'+C'+D')(A'+C'))'
endmodule

module \Formas_canónicas  (
  input  A,
  input  A_2,
  input  B,
  input  B_2,
  input  C,
  input  C_2,
  input  A_3,
  input  B_3,
  input  C_3,
  output f,
  output f_2,
  output f_3
);

  wire A_B_C_out, A_B_C_prime_out, A_B_prime_C_out, A_B_prime_C_prime_out, A_prime_B_C_out,
       A_prime_B_C_prime_out, A_prime_B_prime_C_out, A_prime_B_prime_C_prime_2_out,
       A_prime_B_prime_C_prime_out, AB_prime_C_out, ABC_out, and_2_out, not_1_out, not_2_out, not_3_out,
       not_4_out, not_5_out, not_6_out, not_7_out, not_8_out, not_9_out;

  not not_1 (not_1_out, A);
  not not_2 (not_2_out, B);
  not not_3 (not_3_out, C);
  not not_4 (not_4_out, C_3);
  and A_prime_B_prime_C_prime (A_prime_B_prime_C_prime_out, not_1_out, not_2_out, not_3_out);
  and AB_prime_C (AB_prime_C_out, A, not_2_out, C);
  and ABC (ABC_out, A, C, C);
  or A_B_C_prime (A_B_C_prime_out, A_3, B_3, not_4_out);
  or A_B_prime_C (A_B_prime_C_out, A_3, not_5_out, C_3);
  not not_5 (not_5_out, B_3);
  or A_B_prime_C_prime (A_B_prime_C_prime_out, A_3, not_5_out, not_4_out);
  not not_6 (not_6_out, A_3);
  or A_prime_B_C (A_prime_B_C_out, not_6_out, B_3, C_3);
  or A_prime_B_prime_C (A_prime_B_prime_C_out, not_6_out, not_5_out, not_4_out);
  or or_1 (f, A_prime_B_prime_C_prime_out, AB_prime_C_out, ABC_out);
  and and_1 (f_3, A_B_C_prime_out, A_B_prime_C_out, A_B_prime_C_prime_out, A_prime_B_C_out, A_prime_B_prime_C_out);
  not not_7 (not_7_out, C_2);
  not not_8 (not_8_out, A_2);
  not not_9 (not_9_out, B_2);
  or A_B_C (A_B_C_out, A_2, B_2, C_2);
  and and_2 (and_2_out, A_B_C_out, A_prime_B_C_prime_out, A_prime_B_prime_C_prime_2_out);
  or A_prime_B_C_prime (A_prime_B_C_prime_out, not_8_out, not_9_out, not_7_out);
  or A_prime_B_prime_C_prime_2 (A_prime_B_prime_C_prime_2_out, not_8_out, not_9_out, not_7_out);
  not not_10 (f_2, and_2_out);
endmodule

module \Ej__Simplificación  (
  input  A,
  input  B,
  input  C,
  input  D,
  input  A_2,
  input  B_2,
  input  C_2,
  input  D_2,
  output f,
  output f_2
);

  wire A_B__prime_out, CD__prime_out, CD_out;

  nor A_B__prime (A_B__prime_out, A, B);
  nand CD__prime (CD__prime_out, C, D);
  and CD (CD_out, C_2, D_2);
  nand nand_1 (f, A_B__prime_out, CD__prime_out);
  or or_1 (f_2, A_2, B_2, CD_out);

  // Notes on the sheet:
  //   A+B+CD
  //   ((A+B)'(CD)')'
endmodule

module Ej__Circuitos_equivalentes (
  input  A,
  input  B,
  input  C,
  input  D,
  input  A_2,
  input  B_2,
  input  C_2,
  input  D_2,
  output f,
  output f_2
);

  wire A_B__prime_out, CD__prime_out, nand_1_out, nor_1_out;

  nor A_B__prime (A_B__prime_out, A, B);
  nand CD__prime (CD__prime_out, C, D);
  and A_prime_B_prime_CD_prime (f_2, ~A_2, ~B_2, C_2, ~D_2);  // AND_Gate
  nand nand_1 (nand_1_out, A_B__prime_out, C);
  nor nor_1 (nor_1_out, B, CD__prime_out);
  nor nor_2 (f, nand_1_out, nor_1_out);

  // Notes on the sheet:
  //   ((A+B)'C)'
  //   (((A+B)'C)'+((CD)'+B)')'
  //   ((CD)'+B)'
endmodule

module \Ej__Minimización  (
  input  A,
  input  B,
  input  C,
  input  D,
  output f
);

  wire A_prime_B__prime_out, BC_prime_out, C_D_out, nand_1_out, not_1_out, not_2_out, or_1_out;

  not not_1 (not_1_out, A);
  nor A_prime_B__prime (A_prime_B__prime_out, not_1_out, B);
  and BC_prime (BC_prime_out, B, not_2_out);
  not not_2 (not_2_out, C);
  or C_D (C_D_out, C, D);
  or or_1 (or_1_out, A_prime_B__prime_out, BC_prime_out);
  nand nand_1 (nand_1_out, A_prime_B__prime_out, C_D_out);
  or or_2 (f, or_1_out, nand_1_out);

  // Notes on the sheet:
  //   (A'+B)'+BC'
  //   ((A'+B)'(C+D))'
endmodule

module \Min__simultánea_f_y_g  (
  input  A,
  input  B,
  input  C,
  input  A_2,
  input  B_2,
  input  C_2,
  output f,
  output f_2,
  output g,
  output g_2
);

  wire A_B_out, A_C_prime_out, A_prime_B_prime_2_out, A_prime_B_prime_out, A_prime_C_out, B_C_2_out, B_C_out,
       B_prime_C_prime_2_out, B_prime_C_prime_out, not_1_out, not_2_out, not_3_out, not_4_out, not_5_out,
       not_6_out;

  not not_1 (not_1_out, B);
  not not_2 (not_2_out, A);
  not not_3 (not_3_out, C);
  and A_prime_B_prime (A_prime_B_prime_out, not_2_out, not_1_out);
  and B_C (B_C_out, B, C);
  and B_prime_C_prime (B_prime_C_prime_out, not_1_out, not_3_out);
  and A_prime_C (A_prime_C_out, not_2_out, C);
  and A_B (A_B_out, A, B);
  or or_1 (f, A_prime_B_prime_out, B_C_out, B_prime_C_prime_out);
  or or_2 (g, B_prime_C_prime_out, A_prime_C_out, A_B_out);
  not not_4 (not_4_out, A_2);
  not not_5 (not_5_out, B_2);
  not not_6 (not_6_out, C_2);
  and B_prime_C_prime_2 (B_prime_C_prime_2_out, not_6_out, not_5_out);
  and B_C_2 (B_C_2_out, C_2, B_2);
  and A_prime_B_prime_2 (A_prime_B_prime_2_out, not_5_out, not_4_out);
  and A_C_prime (A_C_prime_out, not_6_out, A_2);
  or or_3 (f_2, B_prime_C_prime_2_out, B_C_2_out, A_prime_B_prime_2_out);
  or or_4 (g_2, B_C_2_out, A_prime_B_prime_2_out, A_C_prime_out);
endmodule

module Don_t_care (
  input  A,
  input  B,
  input  C,
  input  D,
  output f
);

  wire and_1_out, and_2_out;

  and and_1 (and_1_out, B, C);
  and and_2 (and_2_out, and_1_out, D);
  or or_1 (f, and_2_out, A);
endmodule

module Min__SOP_con_don_t_care (
  input  D,
  input  C,
  input  B,
  input  A,
  output f
);

  wire and_1_out, and_2_out, not_1_out, not_2_out;

  not not_1 (not_1_out, C);
  and and_1 (and_1_out, not_1_out, not_2_out);
  not not_2 (not_2_out, A);
  and and_2 (and_2_out, C, A);
  or or_1 (f, and_1_out, B, and_2_out, D);
endmodule

module Retardos (
  output out_1,
  output out_2
);

  wire and_1_out, and_2_out, clock_1_out, clock_2_out, not_1_out;

  Clock clock_1 (.out(clock_1_out));
  Clock clock_2 (.out(clock_2_out));
  and and_1 (and_1_out, clock_1_out, not_1_out);
  not not_1 (not_1_out, clock_1_out);
  and and_2 (and_2_out, clock_2_out, ~clock_2_out);  // AND_Gate
  // Probe on and_1_out
  T_Flip_Flop t_ff_1 (.clk(and_1_out), .T(1'b1), .Q(out_1));  // open: Qn, preset, reset, en
  // Probe on and_2_out
  T_Flip_Flop t_ff_2 (.clk(and_2_out), .T(1'b1), .Q(out_2));  // open: Qn, preset, reset, en
endmodule
