// Logisim project Cap4_1_CircComb.circ as structural Verilog: 26 circuits, main circuit SOP->Red AND/OR m(0,5,7)
module m_5_6_7 (
  input  A,
  input  B,
  input  C,
  output f
);

  wire or_1_out;

  or or_1 (or_1_out, B, C);
  and and_1 (f, A, or_1_out);
endmodule

module M_0_1_2 (
  input  A,
  input  B,
  input  C,
  output f
);

  wire BC_out;

  and BC (BC_out, B, C);
  or A_BC (f, A, BC_out);
endmodule

module \Análisis_circ___con_etiquetas  (
  input  A,
  input  B,
  input  C,
  output f,
  output g
);

  wire A_B_out, AB_out, and_1_out, and_2_out, and_3_out, not_1_out, or_2_out;

  and AB (AB_out, A, B);
  or A_B (A_B_out, A, B);
  or or_1 (f, AB_out, and_1_out);
  and and_1 (and_1_out, A_B_out, C);
  or or_2 (or_2_out, A_B_out, C);
  and and_2 (and_2_out, AB_out, C);
  not not_1 (not_1_out, f);
  and and_3 (and_3_out, not_1_out, or_2_out);
  or or_3 (g, and_3_out, and_2_out);

  // Notes on the sheet:
  //   (A+B)C
  //   (A+B)+C
  //   (AB)C
  //   AB+(A+B)C
  //   (AB+(A+B)C)'(A+B+C)
endmodule

module \Análisis_circ___sin_etiquetas  (
  input  A,
  input  B,
  input  C,
  output f,
  output g
);

  wire and_1_out, and_2_out, and_3_out, and_4_out, not_1_out, or_1_out, or_3_out;

  and and_1 (and_1_out, A, B);
  or or_1 (or_1_out, A, B);
  or or_2 (f, and_1_out, and_2_out);
  and and_2 (and_2_out, or_1_out, C);
  or or_3 (or_3_out, or_1_out, C);
  and and_3 (and_3_out, and_1_out, C);
  not not_1 (not_1_out, f);
  and and_4 (and_4_out, not_1_out, or_3_out);
  or or_4 (g, and_4_out, and_3_out);
endmodule

module Cir__no_combinacional (
  input  A,
  input  B,
  input  A_2,
  input  B_2,
  input  C,
  output out_6,
  output f_A_B_C
);

  wire or_1_out, or_2_out;

  or or_1 (or_1_out, B, out_6);
  or or_2 (or_2_out, B_2, C);
  and and_1 (out_6, A, or_1_out);
  and and_2 (f_A_B_C, A_2, or_2_out);

  // Notes on the sheet:
  //   Circuito no combinacional
  //   Circuito combinacional
  //   Realimentación
endmodule

module Exp__SOP (
  input  A,
  input  B,
  input  C,
  input  D,
  output f_AB_BCD_AC
);

  wire and_1_out, and_2_out, and_3_out;

  and and_1 (and_1_out, A, B);
  and and_2 (and_2_out, B, C, D);
  or or_1 (f_AB_BCD_AC, and_1_out, and_2_out, and_3_out);
  and and_3 (and_3_out, A, C);
endmodule

module Exp__POS (
  input  A,
  input  B,
  input  C,
  input  D,
  output f__A_B__B_C_D__A_C
);

  wire or_1_out, or_2_out, or_3_out;

  or or_1 (or_1_out, A, B);
  or or_2 (or_2_out, B, C, D);
  or or_3 (or_3_out, A, C);
  and and_1 (f__A_B__B_C_D__A_C, or_1_out, or_2_out, or_3_out);
endmodule

module SOP__Red_AND_OR_m_0_5_7 (
  input  A,
  input  B,
  input  C,
  input  A_2,
  input  B_2,
  input  C_2,
  input  A_3,
  input  B_3,
  input  C_3,
  output f,
  output f_2,
  output f_3
);

  wire and_1_out, and_2_out, nand_1_out, nand_2_out, nand_3_out, nand_4_out, nand_5_out, nand_6_out,
       nand_7_out, nand_8_out, nand_9_out, nand_10_out, not_1_out, not_2_out, not_3_out, not_4_out,
       not_5_out, not_6_out;

  not not_1 (not_1_out, A);
  not not_2 (not_2_out, B);
  not not_3 (not_3_out, C);
  not not_4 (not_4_out, A_2);
  not not_5 (not_5_out, B_2);
  not not_6 (not_6_out, C_2);
  nand nand_1 (nand_1_out, A_3, A_3);
  nand nand_2 (nand_2_out, B_3, B_3);
  and and_1 (and_1_out, not_1_out, not_2_out, not_3_out);
  and and_2 (and_2_out, A, C);
  nand nand_3 (nand_3_out, not_4_out, not_5_out);
  nand nand_4 (nand_4_out, ~nand_3_out, not_6_out);  // NAND_Gate
  nand nand_5 (nand_5_out, A_2, C_2);
  nand nand_6 (nand_6_out, nand_1_out, nand_2_out);
  nand nand_7 (nand_7_out, C_3, C_3);
  or or_1 (f, and_1_out, and_2_out);
  or or_2 (f_2, ~nand_4_out, ~nand_5_out);  // OR_Gate
  nand nand_8 (nand_8_out, nand_6_out, nand_6_out);
  nand nand_9 (nand_9_out, nand_8_out, nand_7_out);
  nand nand_10 (nand_10_out, A_3, C_3);
  nand nand_11 (f_3, nand_9_out, nand_10_out);
endmodule

module POS__Red_OR_AND_M_1_2_3_4_6 (
  input  A,
  input  B,
  input  C,
  output f
);

  wire not_1_out, not_2_out, not_3_out, or_1_out, or_2_out, or_3_out;

  not not_1 (not_1_out, C);
  not not_2 (not_2_out, B);
  not not_3 (not_3_out, A);
  or or_1 (or_1_out, A, not_1_out);
  or or_2 (or_2_out, A, not_2_out);
  or or_3 (or_3_out, not_3_out, C);
  and and_1 (f, or_1_out, or_2_out, or_3_out);
endmodule

module Equiv__NAND_NOR (
  input  A,
  input  A_2,
  input  A_3,
  input  A_4,
  input  B,
  input  B_2,
  input  A_5,
  input  A_6,
  input  B_3,
  input  B_4,
  output A_prime,
  output A_prime_2,
  output A_prime_3,
  output A_prime_4,
  output AB,
  output AB_2,
  output AB_3,
  output AB_4,
  output A_B,
  output A_B_2,
  output A_B_3,
  output A_B_4
);

  wire nand_2_out, nand_3_out, nand_4_out, nor_2_out, nor_4_out, nor_5_out;

  not not_1 (A_prime, A);
  nand nand_1 (A_prime_3, A, A);
  and and_1 (AB, A_3, B);
  nand nand_2 (nand_2_out, A_3, B);
  or or_1 (A_B, A_5, B_3);
  nand nand_3 (nand_3_out, A_5, A_5);
  nand nand_4 (nand_4_out, B_3, B_3);
  nand nand_5 (AB_3, nand_2_out, nand_2_out);
  nand nand_6 (A_B_4, nand_3_out, nand_4_out);
  not not_2 (A_prime_2, A_2);
  and and_2 (AB_2, A_4, B_2);
  or or_2 (A_B_2, A_6, B_4);
  nor nor_1 (A_prime_4, A_2, A_2);
  nor nor_2 (nor_2_out, A_4, A_4);
  nor nor_3 (AB_4, nor_2_out, nor_4_out);
  nor nor_4 (nor_4_out, B_2, B_2);
  nor nor_5 (nor_5_out, A_6, B_4);
  nor nor_6 (A_B_3, nor_5_out, nor_5_out);

  // Notes on the sheet:
  //   (AA)'
  //   (AB)'
  //   A'
  //   B'
  //   (A'B')'
  //   B'
  //   (AA)'
  //   A'
  //   (A'+B')'
  //   (A+B)'
endmodule

module Redes_NAND_NOR (
);

  wire and_1_out, and_2_out, and_3_out, and_4_out, nand_1_out, nand_2_out, nand_3_out, nand_4_out,
       nand_5_out, nor_1_out, nor_2_out, nor_3_out, nor_4_out, nor_5_out, or_1_out, or_2_out, or_3_out,
       or_4_out, undriven, undriven_2, undriven_3, undriven_4, undriven_5, undriven_6, undriven_7,
       undriven_8, undriven_9, undriven_10, undriven_11, undriven_12, undriven_13, undriven_14, undriven_15,
       undriven_16, undriven_17, undriven_18, undriven_19, undriven_20, undriven_21, undriven_22,
       undriven_23, undriven_24, undriven_25, undriven_26, undriven_27, undriven_28, undriven_29,
       undriven_30, undriven_31, undriven_32, undriven_33, undriven_34, undriven_35, undriven_36;

  and and_1 (and_1_out, undriven, undriven_2, undriven_3);
  and and_2 (and_2_out, undriven_4, undriven_5, undriven_6);
  or or_1 (or_1_out, undriven_7, undriven_8, undriven_9);
  or or_2 (or_2_out, undriven_10, undriven_11, undriven_12);
  or or_3 (or_3_out, and_1_out, and_2_out);
  and and_3 (and_3_out, or_1_out, or_2_out);
  nand nand_1 (nand_1_out, undriven_13, undriven_14, undriven_15);
  nand nand_2 (nand_2_out, undriven_16, undriven_17, undriven_18);
  nor nor_1 (nor_1_out, undriven_19, undriven_20, undriven_21);
  nor nor_2 (nor_2_out, undriven_22, undriven_23, undriven_24);
  or or_4 (or_4_out, ~nand_1_out, ~nand_2_out);  // OR_Gate
  and and_4 (and_4_out, ~nor_1_out, ~nor_2_out);  // AND_Gate
  nand nand_3 (nand_3_out, undriven_25, undriven_26, undriven_27);
  nand nand_4 (nand_4_out, undriven_28, undriven_29, undriven_30);
  nor nor_3 (nor_3_out, undriven_31, undriven_32, undriven_33);
  nor nor_4 (nor_4_out, undriven_34, undriven_35, undriven_36);
  nand nand_5 (nand_5_out, nand_3_out, nand_4_out);
  nor nor_5 (nor_5_out, nor_3_out, nor_4_out);
endmodule

module Compose_NAND_NOR (
  input  A,
  input  B,
  input  C,
  input  A_2,
  input  A_3,
  input  A_4,
  input  A_5,
  input  B_2,
  input  B_3,
  input  B_4,
  input  B_5,
  input  C_2,
  input  C_3,
  input  C_4,
  input  C_5,
  input  A_6,
  input  B_6,
  input  C_6,
  input  A_7,
  input  A_8,
  input  A_9,
  input  A_10,
  input  B_7,
  input  B_8,
  input  B_9,
  input  B_10,
  input  C_7,
  input  C_8,
  input  C_9,
  input  C_10,
  output AB__prime_C__prime,
  output ABC__prime,
  output AB_C__prime,
  output AB__prime_prime_C__prime,
  output ABC__prime_2,
  output A_B__prime_C__prime,
  output A_B_C__prime,
  output A_B__C__prime,
  output A_B_C__prime_2,
  output A_B_C__prime_3
);

  wire and_1_out, nand_2_out, nand_5_out, nand_7_out, nand_8_out, nor_2_out, nor_5_out, nor_7_out, nor_8_out,
       or_1_out;

  nand nand_1 (ABC__prime, A_2, B_2, C_2);
  nor nor_1 (A_B_C__prime, A_7, B_7, C_7);
  nand nand_2 (nand_2_out, A, B);
  and and_1 (and_1_out, A_3, B_3);
  nor nor_2 (nor_2_out, A_6, B_6);
  or or_1 (or_1_out, A_8, B_8);
  nand nand_3 (AB__prime_C__prime, nand_2_out, C);
  nand nand_4 (AB_C__prime, and_1_out, C_3);
  nor nor_3 (A_B__prime_C__prime, nor_2_out, C_6);
  nor nor_4 (A_B__C__prime, or_1_out, C_8);
  nand nand_5 (nand_5_out, A_4, B_4);
  nor nor_5 (nor_5_out, A_9, B_9);
  nand nand_6 (AB__prime_prime_C__prime, ~nand_5_out, C_4);  // NAND_Gate
  nor nor_6 (A_B_C__prime_2, ~nor_5_out, C_9);  // NOR_Gate
  nand nand_7 (nand_7_out, A_5, B_5);
  nor nor_7 (nor_7_out, A_10, B_10);
  nand nand_8 (nand_8_out, nand_7_out, nand_7_out);
  nor nor_8 (nor_8_out, nor_7_out, nor_7_out);
  nand nand_9 (ABC__prime_2, nand_8_out, C_5);
  nor nor_9 (A_B_C__prime_3, nor_8_out, C_10);
endmodule

module SOP__NAND_m_0_5_7 (
  input  A,
  input  B,
  input  C,
  output f
);

  wire nand_1_out, nand_2_out, nand_3_out, nand_4_out, nand_6_out;

  nand nand_1 (nand_1_out, A, A);
  nand nand_2 (nand_2_out, B, B);
  nand nand_3 (nand_3_out, C, C);
  nand nand_4 (nand_4_out, nand_1_out, nand_2_out, nand_3_out);
  nand nand_5 (f, nand_4_out, nand_6_out);
  nand nand_6 (nand_6_out, A, C);
endmodule

module POS__NOR_M_1_2_3_4_6 (
  input  A,
  input  B,
  input  C,
  output f
);

  wire nor_1_out, nor_2_out, nor_3_out, nor_4_out, nor_5_out, nor_6_out;

  nor nor_1 (nor_1_out, A, A);
  nor nor_2 (nor_2_out, B, B);
  nor nor_3 (nor_3_out, C, C);
  nor nor_4 (nor_4_out, nor_1_out, C);
  nor nor_5 (nor_5_out, A, nor_2_out);
  nor nor_6 (nor_6_out, A, nor_3_out);
  nor nor_7 (f, nor_4_out, nor_5_out, nor_6_out);
endmodule

module NAND_m_0_1_4_5_8_9_10 (
  input  A,
  input  B,
  input  C,
  input  D,
  output f
);

  wire nand_1_out, nand_2_out, nand_3_out, nand_4_out, nand_5_out, nand_7_out, nand_8_out;

  nand nand_1 (nand_1_out, A, A);
  nand nand_2 (nand_2_out, B, B);
  nand nand_3 (nand_3_out, C, C);
  nand nand_4 (nand_4_out, D, D);
  nand nand_5 (nand_5_out, nand_1_out, nand_3_out);
  nand nand_6 (f, nand_5_out, nand_7_out, nand_8_out);
  nand nand_7 (nand_7_out, nand_2_out, nand_3_out);
  nand nand_8 (nand_8_out, A, nand_2_out, nand_4_out);
endmodule

module NOR_M_2_3_6_7_11_12_13_14_15 (
  input  A,
  input  B,
  input  C,
  input  D,
  output f
);

  wire nor_1_out, nor_2_out, nor_3_out, nor_4_out, nor_5_out, nor_6_out, nor_7_out;

  nor nor_1 (nor_1_out, A, A);
  nor nor_2 (nor_2_out, B, B);
  nor nor_3 (nor_3_out, C, C);
  nor nor_4 (nor_4_out, D, D);
  nor nor_5 (nor_5_out, nor_1_out, nor_2_out);
  nor nor_6 (nor_6_out, A, nor_3_out);
  nor nor_7 (nor_7_out, nor_3_out, nor_4_out);
  nor nor_8 (f, nor_5_out, nor_6_out, nor_7_out);
endmodule

module \mini_Maxi_téminos  (
  input  A,
  input  A_2,
  input  B,
  input  B_2,
  input  C,
  input  C_2,
  input  A_3,
  input  A_4,
  input  B_3,
  input  B_4,
  input  C_3,
  input  C_4,
  output AB_prime_C,
  output A_prime_B_C_prime,
  output A_prime_B_C_prime_2,
  output AB_prime_C_2
);

  wire not_1_out, not_2_out, not_3_out, not_4_out, not_5_out, not_6_out;

  not not_1 (not_1_out, B);
  not not_2 (not_2_out, A_3);
  not not_3 (not_3_out, C_3);
  and and_1 (AB_prime_C, A, not_1_out, C);
  or or_1 (A_prime_B_C_prime_2, not_2_out, B_3, not_3_out);
  not not_4 (not_4_out, B_2);
  not not_5 (not_5_out, A_4);
  not not_6 (not_6_out, C_4);
  nand nand_1 (A_prime_B_C_prime, A_2, not_4_out, C_2);
  nor nor_1 (AB_prime_C_2, not_5_out, B_4, not_6_out);
endmodule

module V1_f_M_2_5_6__g_M_2_5 (
  input  A,
  input  B,
  input  C,
  output f,
  output g
);

  wire A_prime_B_prime_out, A_prime_C_out, AB_out, B_prime_C_prime_out, BC_out, not_1_out, not_2_out,
       not_3_out;

  not not_1 (not_1_out, A);
  not not_2 (not_2_out, C);
  not not_3 (not_3_out, B);
  and A_prime_B_prime (A_prime_B_prime_out, not_3_out, not_1_out);
  and BC (BC_out, C, B);
  and B_prime_C_prime (B_prime_C_prime_out, not_2_out, not_3_out);
  and A_prime_C (A_prime_C_out, C, not_1_out);
  and AB (AB_out, B, A);
  or or_1 (f, A_prime_B_prime_out, BC_out, B_prime_C_prime_out);
  or or_2 (g, B_prime_C_prime_out, A_prime_C_out, AB_out);
endmodule

module V2_f_M_2_5_6__g_M_2_5 (
  input  A,
  input  B,
  input  C,
  output f,
  output g
);

  wire A_prime_B_prime_out, AC_prime_out, B_prime_C_prime_out, BC_out, not_1_out, not_2_out, not_3_out;

  not not_1 (not_1_out, A);
  not not_2 (not_2_out, C);
  not not_3 (not_3_out, B);
  and B_prime_C_prime (B_prime_C_prime_out, not_2_out, not_3_out);
  and BC (BC_out, C, B);
  and A_prime_B_prime (A_prime_B_prime_out, not_3_out, not_1_out);
  and AC_prime (AC_prime_out, not_2_out, A);
  or or_1 (f, B_prime_C_prime_out, BC_out, A_prime_B_prime_out);
  or or_2 (g, BC_out, A_prime_B_prime_out, AC_prime_out);
endmodule

module \Circuito_mayoría  (
  input  A,
  input  B,
  input  C,
  output f
);

  wire and_1_out, and_2_out, and_3_out, or_1_out;

  and and_1 (and_1_out, B, C);
  and and_2 (and_2_out, A, C);
  or or_1 (or_1_out, and_1_out, and_2_out);
  and and_3 (and_3_out, A, B);
  or or_2 (f, or_1_out, and_3_out);
endmodule

module \Aspectos_prácticos  (
  input  A,
  input  A_2,
  input  B,
  input  B_2,
  input  A_3,
  input  A_4,
  input  C,
  input  C_2,
  input  B_3,
  input  B_4,
  input  Control,
  output f,
  output f_2,
  output f_3,
  output f_4,
  output g
);

  wire and_4_out, not_1_out, or_4_out, undriven;

  buf and_1 (f, A);  // AND_Gate
  buf or_1 (f, B);  // OR_Gate
  and and_2 (f_3, A_3, C);
  or or_2 (g, C, B_3);
  and and_3 (f_2, A_2, undriven);
  or or_3 (f_2, undriven, B_2);
  and and_4 (and_4_out, A_4, C_2);
  not not_1 (not_1_out, Control);
  or or_4 (or_4_out, C_2, B_4);
  assign f_4 = not_1_out ? and_4_out : 1'bz;  // Controlled_Buffer controlled_buffer_1
  assign f_4 = Control ? or_4_out : 1'bz;  // Controlled_Buffer controlled_buffer_2
endmodule

module Buffer_controlado (
  input  in_1,
  input  in_2
);

  wire pull_resistor_1_node;

  Pull_Resistor pull_resistor_1 (.node(pull_resistor_1_node));
  assign pull_resistor_1_node = in_2 ? in_1 : 1'bz;  // Controlled_Buffer controlled_buffer_1
  // Probe on pull_resistor_1_node
endmodule

module buffers (
  input  A,
  input  [3:0] Entr__datos_1,
  input  Control,
  input  Control_2,
  input  A_2,
  input  [3:0] Entr__datos_2,
  input  Control_3,
  output out_8,
  output out_9
);

  wire not_1_out;
  wire [3:0] controlled_buffer_3_out;

  assign out_8 = Control ? A : 1'bz;  // Controlled_Buffer controlled_buffer_1
  assign out_9 = Control_3 ? A_2 : 1'bz;  // Controlled_Buffer controlled_buffer_2
  assign controlled_buffer_3_out = Control_2 ? Entr__datos_1 : 4'bz;  // Controlled_Buffer controlled_buffer_3
  not not_1 (not_1_out, Control_2);
  assign controlled_buffer_3_out = not_1_out ? Entr__datos_2 : 4'bz;  // Controlled_Buffer controlled_buffer_4
  // Probe on controlled_buffer_3_out

  // Notes on the sheet:
  //   Bus de conexión
endmodule

module buffer_triestado (
  input  A,
  input  A_2,
  input  A_3,
  input  A_4,
  input  E,
  input  E_2,
  input  A_5,
  input  A_6,
  input  A_7,
  input  A_8,
  input  E_3,
  input  E_4,
  output Y,
  output Y_2,
  output Y_3,
  output Y_4,
  output Y_5,
  output Y_6,
  output Y_7,
  output Y_8
);

  assign Y = E ? A : 1'bz;  // Controlled_Buffer controlled_buffer_1
  assign Y_3 = E ? A_3 : 1'bz;  // Controlled_Buffer controlled_buffer_2
  Pull_Resistor pull_resistor_1 (.node(Y_5));
  assign Y_5 = E_3 ? A_5 : 1'bz;  // Controlled_Buffer controlled_buffer_3
  assign Y_7 = E_3 ? A_7 : 1'bz;  // Controlled_Buffer controlled_buffer_4
  Pull_Resistor pull_resistor_2 (.node(Y_7));
  assign Y_2 = E_2 ? A_2 : 1'bz;  // Controlled_Buffer controlled_buffer_5
  assign Y_4 = E_2 ? A_4 : 1'bz;  // Controlled_Buffer controlled_buffer_6
  Pull_Resistor #(.pull(1)) pull_resistor_3 (.node(Y_6));
  assign Y_6 = E_4 ? A_6 : 1'bz;  // Controlled_Buffer controlled_buffer_7
  assign Y_8 = E_4 ? A_8 : 1'bz;  // Controlled_Buffer controlled_buffer_8
  Pull_Resistor #(.pull(1)) pull_resistor_4 (.node(Y_8));
endmodule

module multibit (
  input  [3:0] A3_A2_A1_A0,
  input  A,
  input  B,
  input  [3:0] B3_B2_B1_B0,
  input  C,
  input  D,
  input  [3:0] A3_A2_A1_A0_2,
  input  [2:0] B2_B1_B0,
  output p,
  output q,
  output r,
  output [3:0] f3_f2_f1_f0,
  output s,
  output [3:0] f3_f2_f1_f0_2
);

  wire [3:3] undriven;

  // Probe on A3_A2_A1_A0
  // Probe on B3_B2_B1_B0
  // Probe on A3_A2_A1_A0
  // Probe on f3_f2_f1_f0
  assign f3_f2_f1_f0 = A3_A2_A1_A0 & B3_B2_B1_B0;  // AND_Gate and_1, 4 bits wide
  // Probe on B3_B2_B1_B0
  assign f3_f2_f1_f0_2 = A3_A2_A1_A0_2 & {undriven[3], B2_B1_B0};  // AND_Gate and_2, 4 bits wide
  // Probe on f3_f2_f1_f0
  assign {p, q, r, s} = ~{A, B, C, D};  // NOT_Gate not_1, 4 bits wide
  // Pins of 3 and 4 bits meet at {undriven[3], B2_B1_B0}
endmodule

module XOR_w__tunnels (
  input  A,
  input  B,
  output \xor ,
  output f
);

  wire and_1_out, and_2_out;

  xor xor_1 (\xor , A, B);
  and and_1 (and_1_out, A, ~B);  // AND_Gate
  and and_2 (and_2_out, B, ~A);  // AND_Gate
  or or_1 (f, and_1_out, and_2_out);
endmodule
