// Logisim project Cap5_1_DEC.circ as structural Verilog: 16 circuits, main circuit 2 DEC 2x4
module DEC_binario (
  input  E,
  input  A,
  input  B,
  output y0__A_prime_B_prime_E,
  output y1__A_prime_B_E,
  output y2__AB_prime_E,
  output y3__AB_E
);

  Decoder #(.select(2), .disabled(0)) decoder_1 (
    .out0(y0__A_prime_B_prime_E), .out1(y1__A_prime_B_E), .out2(y2__AB_prime_E), .out3(y3__AB_E),
    .sel({A, B}), .en(E));
endmodule

module DEC__activo_con_0 (
  input  E,
  input  A,
  input  B,
  output y0__A_B__E,
  output y1__A_B_prime__E,
  output y2__A_prime_B__E,
  output y3__A_prime_B_prime__E
);

  wire decoder_1_out0, decoder_1_out1, decoder_1_out2, decoder_1_out3, not_5_out;

  not not_1 (y0__A_B__E, decoder_1_out0);
  not not_2 (y1__A_B_prime__E, decoder_1_out1);
  not not_3 (y2__A_prime_B__E, decoder_1_out2);
  not not_4 (y3__A_prime_B_prime__E, decoder_1_out3);
  not not_5 (not_5_out, E);
  Decoder #(.select(2), .disabled(0)) decoder_1 (
    .out0(decoder_1_out0), .out1(decoder_1_out1), .out2(decoder_1_out2), .out3(decoder_1_out3), .sel({A, B}),
    .en(not_5_out));
endmodule

module DEC_2x4 (
  input  A,
  input  B,
  input  E,
  output y0,
  output y1,
  output y2,
  output y3
);

  wire not_1_out, not_2_out;

  not not_1 (not_1_out, A);
  not not_2 (not_2_out, B);
  and A_prime_B_prime_E (y0, not_1_out, E, not_2_out);
  and A_prime_B_E (y1, B, E, not_1_out);
  and AB_prime_E (y2, not_2_out, E, A);
  and AB_E (y3, B, E, A);
endmodule

module DEC_2x4__nivel_bajo (
  input  A,
  input  B,
  input  E,
  output y0,
  output y1,
  output y2,
  output y3
);

  wire not_1_out, not_2_out, not_3_out;

  not not_1 (not_1_out, A);
  not not_2 (not_2_out, E);
  not not_3 (not_3_out, B);
  nand A_B__E (y0, not_1_out, not_2_out, not_3_out);
  nand A_B_prime__E (y1, B, not_2_out, not_1_out);
  nand A_prime_B__E (y2, not_3_out, not_2_out, A);
  nand A_prime_B_prime__E (y3, B, not_2_out, A);
endmodule

module Bus_multibit___Spliter (
  input  [3:0] A_3_0,
  input  A3,
  input  A2,
  input  A1,
  input  A0,
  input  [3:0] A_3_0_2,
  output [3:0] A_3_0_3,
  output A0_2,
  output A1_2,
  output A2_2,
  output A3_2,
  output [2:0] A_3_0_4
);

  // Probe on A_3_0_2
  // Probe on A_3_0_2
  // Probe on A_3_0
  // Probe on A_3_0
  // Probe on A_3_0
  // Probe on A_3_0
  // Probe on {A3, A2, A1, A0}
  // Probe on {A3, A2, A1, A0}
  // Probe on {A3, A2, A1, A0}
  // Probe on {A3, A2, A1, A0}
  // Probe on A_3_0_2
  // Probe on A_3_0_2
  // Pins of 3 and 4 bits meet at A_3_0_2

  assign A0_2 = A0;
  assign A1_2 = A1;
  assign A2_2 = A2;
  assign A3_2 = A3;
  assign A_3_0_3 = A_3_0;
  assign A_3_0_4 = A_3_0_2[2:0];
endmodule

module DEC_3x8 (
  input  [2:0] A_B_C,
  input  [2:0] A_B_C_2,
  output f,
  output f_2
);

  wire decoder_1_out0, decoder_1_out5, decoder_1_out7, decoder_2_out1, decoder_2_out2, decoder_2_out3,
       decoder_2_out4, decoder_2_out6;

  Decoder #(.select(3), .disabled(0), .enable("false")) decoder_1 (
    .out0(decoder_1_out0), .out5(decoder_1_out5), .out7(decoder_1_out7), .sel(A_B_C));  // open: out1, out2, out3, out4, out6
  Decoder #(.select(3), .disabled(0), .enable("false")) decoder_2 (
    .out1(decoder_2_out1), .out2(decoder_2_out2), .out3(decoder_2_out3), .out4(decoder_2_out4),
    .out6(decoder_2_out6), .sel(A_B_C_2));  // open: out0, out5, out7
  or or_1 (f, decoder_1_out0, decoder_1_out5, decoder_1_out7);
  nor nor_1 (f_2, decoder_2_out1, decoder_2_out2, decoder_2_out3, decoder_2_out4, decoder_2_out6);
endmodule

module m_0_5_7__con_DEC_3x8 (
  input  A,
  input  B,
  input  C,
  input  [2:0] A_B_C,
  input  [2:0] A_B_C_2,
  output f,
  output f_2
);

  wire decoder_1_out0, decoder_1_out5, decoder_1_out7, decoder_2_out1, decoder_2_out2, decoder_2_out3,
       decoder_2_out4, decoder_2_out6, nor_2_out, not_1_out, or_1_out, or_2_out, undriven, undriven_2,
       undriven_3, undriven_4, undriven_5, undriven_6, undriven_7, undriven_8, undriven_9;

  Decoder #(.select(3), .disabled(0), .enable("false")) decoder_1 (
    .out0(decoder_1_out0), .out5(decoder_1_out5), .out7(decoder_1_out7), .sel({A, B, C}));  // open: out1, out2, out3, out4, out6
  Decoder #(.select(3), .disabled(0), .enable("false")) decoder_2 (
    .out1(decoder_2_out1), .out2(decoder_2_out2), .out3(decoder_2_out3), .out4(decoder_2_out4),
    .out6(decoder_2_out6), .sel(A_B_C_2));  // open: out0, out5, out7
  or or_1 (or_1_out, undriven, undriven_2, undriven_3);
  or or_2 (or_2_out, undriven_4, undriven_5, undriven_6);
  not not_1 (not_1_out, or_2_out);
  or or_3 (f, decoder_1_out0, decoder_1_out5, decoder_1_out7);
  nor nor_1 (f_2, decoder_2_out1, decoder_2_out2, decoder_2_out3, decoder_2_out4, decoder_2_out6);
  nor nor_2 (nor_2_out, undriven_7, undriven_8, undriven_9);

  // Notes on the sheet:
  //   1's
  //   0's
  //   f'
  //   f
  //   f
  //   0's
  //   f
endmodule

module m_0_5_7__con__DEC_3x8__nivel_bajo (
  input  [2:0] A_B_C,
  input  [2:0] A_B_C_2,
  output f,
  output f_2
);

  wire and_1_out, decoder_1_out0, decoder_1_out1, decoder_1_out2, decoder_1_out3, decoder_1_out4,
       decoder_1_out5, decoder_1_out6, decoder_1_out7, decoder_2_out0, decoder_2_out1, decoder_2_out2,
       decoder_2_out3, decoder_2_out4, decoder_2_out5, decoder_2_out6, decoder_2_out7, nand_1_out,
       nand_3_out, not_2_out, not_3_out, not_4_out, not_5_out, not_7_out, not_9_out, not_14_out, not_16_out,
       not_17_out, undriven, undriven_2, undriven_3, undriven_4, undriven_5, undriven_6, undriven_7,
       undriven_8, undriven_9;

  Decoder #(.select(3), .disabled(0), .enable("false")) decoder_1 (
    .out0(decoder_1_out0), .out1(decoder_1_out1), .out2(decoder_1_out2), .out3(decoder_1_out3),
    .out4(decoder_1_out4), .out5(decoder_1_out5), .out6(decoder_1_out6), .out7(decoder_1_out7), .sel(A_B_C));
  Decoder #(.select(3), .disabled(0), .enable("false")) decoder_2 (
    .out0(decoder_2_out0), .out1(decoder_2_out1), .out2(decoder_2_out2), .out3(decoder_2_out3),
    .out4(decoder_2_out4), .out5(decoder_2_out5), .out6(decoder_2_out6), .out7(decoder_2_out7), .sel(A_B_C_2));
  // NOT_Gate not_1 has open pins: in=decoder_1_out0, out=open
  not not_2 (not_2_out, decoder_1_out1);
  not not_3 (not_3_out, decoder_1_out2);
  not not_4 (not_4_out, decoder_1_out3);
  not not_5 (not_5_out, decoder_1_out4);
  // NOT_Gate not_6 has open pins: in=decoder_1_out5, out=open
  not not_7 (not_7_out, decoder_1_out6);
  // NOT_Gate not_8 has open pins: in=decoder_1_out7, out=open
  not not_9 (not_9_out, decoder_2_out0);
  // NOT_Gate not_10 has open pins: in=decoder_2_out1, out=open
  // NOT_Gate not_11 has open pins: in=decoder_2_out2, out=open
  // NOT_Gate not_12 has open pins: in=decoder_2_out3, out=open
  // NOT_Gate not_13 has open pins: in=decoder_2_out4, out=open
  not not_14 (not_14_out, decoder_2_out5);
  // NOT_Gate not_15 has open pins: in=decoder_2_out6, out=open
  not not_16 (not_16_out, decoder_2_out7);
  and and_1 (and_1_out, undriven, undriven_2, undriven_3);
  nand nand_1 (nand_1_out, undriven_4, undriven_5, undriven_6);
  and and_2 (f, not_2_out, not_3_out, not_4_out, not_5_out, not_7_out);
  nand nand_2 (f_2, not_9_out, not_14_out, not_16_out);
  not not_17 (not_17_out, nand_1_out);
  nand nand_3 (nand_3_out, undriven_7, undriven_8, undriven_9);

  // Notes on the sheet:
  //   0's
  //   1's
  //   f
  //   f'
  //   f
  //   1's
  //   f
endmodule

module m_0_5_7__altern (
  input  A,
  input  B,
  input  C,
  output f
);

  wire decoder_1_out0, decoder_1_out5, decoder_1_out7;

  Decoder #(.select(3), .disabled(0), .enable("false")) decoder_1 (
    .out0(decoder_1_out0), .out5(decoder_1_out5), .out7(decoder_1_out7), .sel({A, B, C}));  // open: out1, out2, out3, out4, out6
  or or_1 (f, decoder_1_out0, decoder_1_out5, decoder_1_out7);
endmodule

module Entradas_comp (
  input  A,
  input  B,
  input  C,
  output f
);

  wire decoder_1_out0, decoder_1_out2, not_1_out;
  wire [0:0] and_1_out;

  not not_1 (not_1_out, B);
  Decoder #(.select(2), .enable("false")) decoder_1 (
    .out0(decoder_1_out0), .out2(decoder_1_out2), .sel({A, and_1_out[0]}));  // open: out1, out3
  and and_1 (and_1_out[0], not_1_out, C);
  or or_1 (f, decoder_1_out0, decoder_1_out2);
endmodule

module Entrads_comp__con_E (
  input  A,
  input  B,
  input  C,
  output f
);

  wire decoder_1_out0, decoder_1_out1, decoder_1_out2, decoder_1_out3, not_1_out, not_2_out, not_4_out;
  wire [0:0] B_prime_C_out;

  not not_1 (not_1_out, B);
  Decoder #(.select(2), .disabled(0)) decoder_1 (
    .out0(decoder_1_out0), .out1(decoder_1_out1), .out2(decoder_1_out2), .out3(decoder_1_out3),
    .sel({A, B_prime_C_out[0]}), .en(C));
  and B_prime_C (B_prime_C_out[0], not_1_out, C);
  not not_2 (not_2_out, decoder_1_out0);
  and and_1 (f, not_2_out, not_4_out);
  // NOT_Gate not_3 has open pins: in=decoder_1_out1, out=open
  not not_4 (not_4_out, decoder_1_out2);
  // NOT_Gate not_5 has open pins: in=decoder_1_out3, out=open
endmodule

module _2_DEC_2x4 (
  input  A,
  input  [1:0] B_C,
  output [3:0] y3__y0,
  output [3:0] y7__y4
);

  wire not_1_out;

  not not_1 (not_1_out, A);
  Decoder #(.select(2), .disabled(0)) decoder_1 (
    .out0(y3__y0[0]), .out1(y3__y0[1]), .out2(y3__y0[2]), .out3(y3__y0[3]), .sel(B_C), .en(not_1_out));
  Decoder #(.select(2), .disabled(0)) decoder_2 (
    .out0(y7__y4[0]), .out1(y7__y4[1]), .out2(y7__y4[2]), .out3(y7__y4[3]), .sel(B_C), .en(A));

  // Notes on the sheet:
  //   DEC 2x4
  //   DEC 2x4
endmodule

module _4_DEC_1x2 (
  input  [1:0] A_B,
  input  C,
  output [1:0] y1_y0,
  output [1:0] y3_y2,
  output [1:0] y5_y4,
  output [1:0] y7_y6
);

  wire decoder_1_out0, decoder_1_out1, decoder_1_out2, decoder_1_out3;

  Decoder #(.select(2), .disabled(0)) decoder_1 (
    .out0(decoder_1_out0), .out1(decoder_1_out1), .out2(decoder_1_out2), .out3(decoder_1_out3), .sel(A_B),
    .en(1'b1));
  Decoder #(.disabled(0)) decoder_2 (.out0(y1_y0[0]), .out1(y1_y0[1]), .sel(C), .en(decoder_1_out0));
  Decoder #(.disabled(0)) decoder_3 (.out0(y3_y2[0]), .out1(y3_y2[1]), .sel(C), .en(decoder_1_out1));
  Decoder #(.disabled(0)) decoder_4 (.out0(y5_y4[0]), .out1(y5_y4[1]), .sel(C), .en(decoder_1_out2));
  Decoder #(.disabled(0)) decoder_5 (.out0(y7_y6[0]), .out1(y7_y6[1]), .sel(C), .en(decoder_1_out3));
endmodule

module _5_DEC_2x4 (
  input  [1:0] A_B,
  input  [1:0] C_D,
  output [3:0] y3__y0,
  output [3:0] y7__y4,
  output [3:0] y11__y8,
  output [3:0] y15__y12
);

  wire decoder_1_out0, decoder_1_out1, decoder_1_out2, decoder_1_out3;

  Decoder #(.select(2), .disabled(0)) decoder_1 (
    .out0(decoder_1_out0), .out1(decoder_1_out1), .out2(decoder_1_out2), .out3(decoder_1_out3), .sel(A_B),
    .en(1'b1));
  Decoder #(.select(2), .disabled(0)) decoder_2 (
    .out0(y3__y0[0]), .out1(y3__y0[1]), .out2(y3__y0[2]), .out3(y3__y0[3]), .sel(C_D), .en(decoder_1_out0));
  Decoder #(.select(2), .disabled(0)) decoder_3 (
    .out0(y7__y4[0]), .out1(y7__y4[1]), .out2(y7__y4[2]), .out3(y7__y4[3]), .sel(C_D), .en(decoder_1_out1));
  Decoder #(.select(2), .disabled(0)) decoder_4 (
    .out0(y11__y8[0]), .out1(y11__y8[1]), .out2(y11__y8[2]), .out3(y11__y8[3]), .sel(C_D), .en(decoder_1_out2));
  Decoder #(.select(2), .disabled(0)) decoder_5 (
    .out0(y15__y12[0]), .out1(y15__y12[1]), .out2(y15__y12[2]), .out3(y15__y12[3]), .sel(C_D),
    .en(decoder_1_out3));
endmodule

module _7_DEC_1x2 (
  input  A,
  input  B,
  input  C,
  output [1:0] y1_y0,
  output [1:0] y3_y2,
  output [1:0] y5_y4,
  output [1:0] y7_y6
);

  wire decoder_1_out0, decoder_1_out1, decoder_2_out0, decoder_2_out1, decoder_3_out0, decoder_3_out1;

  Decoder #(.disabled(0)) decoder_1 (.out0(decoder_1_out0), .out1(decoder_1_out1), .sel(B), .en(decoder_2_out0));
  Decoder #(.disabled(0)) decoder_2 (.out0(decoder_2_out0), .out1(decoder_2_out1), .sel(A), .en(1'b1));
  Decoder #(.disabled(0)) decoder_3 (.out0(decoder_3_out0), .out1(decoder_3_out1), .sel(B), .en(decoder_2_out1));
  Decoder #(.disabled(0)) decoder_4 (.out0(y1_y0[0]), .out1(y1_y0[1]), .sel(C), .en(decoder_1_out0));
  Decoder #(.disabled(0)) decoder_5 (.out0(y3_y2[0]), .out1(y3_y2[1]), .sel(C), .en(decoder_1_out1));
  Decoder #(.disabled(0)) decoder_6 (.out0(y5_y4[0]), .out1(y5_y4[1]), .sel(C), .en(decoder_3_out0));
  Decoder #(.disabled(0)) decoder_7 (.out0(y7_y6[0]), .out1(y7_y6[1]), .sel(C), .en(decoder_3_out1));
endmodule

module fun_decs (
);

  wire and_1_out, and_2_out, nand_1_out, not_1_out, undriven, undriven_2, undriven_3, undriven_4, undriven_5,
       undriven_6, undriven_7, undriven_8, undriven_9;

  and and_1 (and_1_out, undriven, undriven_2, undriven_3);
  not not_1 (not_1_out, and_2_out);
  and and_2 (and_2_out, undriven_4, undriven_5, undriven_6);
  nand nand_1 (nand_1_out, undriven_7, undriven_8, undriven_9);

  // Notes on the sheet:
  //   0's
  //   1's
  //   f
  //   f
  //   f'
  //   1's
  //   f
endmodule
