// Logisim project Cap5_2_MUX.circ as structural Verilog: 20 circuits, main circuit Comparación
module MUX_4x1_gen (
  input  D0,
  input  D1,
  input  D2,
  input  D3,
  input  A,
  input  B,
  input  E,
  output y
);

  Multiplexer #(.select(2), .disabled(0)) multiplexer_1 (
    .in0(D0), .in1(D1), .in2(D2), .in3(D3), .out(y), .sel({A, B}), .en(E));
endmodule

module MUX_4x1 (
  input  A,
  input  B,
  input  D0,
  input  D1,
  input  D2,
  input  D3,
  input  E,
  output y
);

  wire A_prime_B__D1_E_out, A_prime_B_prime__D0_E_out, AB__D3_E_out, AB_prime__D2_E_out, not_1_out, not_2_out;

  not not_1 (not_1_out, A);
  not not_2 (not_2_out, B);
  and A_prime_B_prime__D0_E (A_prime_B_prime__D0_E_out, not_1_out, not_2_out, D0, E);
  and A_prime_B__D1_E (A_prime_B__D1_E_out, not_1_out, B, D1, E);
  and AB_prime__D2_E (AB_prime__D2_E_out, not_2_out, A, D2, E);
  and AB__D3_E (AB__D3_E_out, B, A, D3, E);
  or or_1 (y, A_prime_B_prime__D0_E_out, A_prime_B__D1_E_out, AB_prime__D2_E_out, AB__D3_E_out);
endmodule

module MUX_4x1_con_DEC_2x4 (
  input  E,
  input  [1:0] A_B,
  input  D0,
  input  D1,
  input  D2,
  input  D3,
  output y
);

  wire and_1_out, and_2_out, and_3_out, and_4_out, decoder_1_out0, decoder_1_out1, decoder_1_out2,
       decoder_1_out3;

  Decoder #(.select(2), .disabled(0)) decoder_1 (
    .out0(decoder_1_out0), .out1(decoder_1_out1), .out2(decoder_1_out2), .out3(decoder_1_out3), .sel(A_B),
    .en(E));
  and and_1 (and_1_out, decoder_1_out0, D0);
  and and_2 (and_2_out, decoder_1_out1, D1);
  and and_3 (and_3_out, decoder_1_out2, D2);
  and and_4 (and_4_out, decoder_1_out3, D3);
  or or_1 (y, and_1_out, and_2_out, and_3_out, and_4_out);
endmodule

module \Comparación  (
  input  [3:0] D3__D0,
  input  [1:0] S1_S0,
  input  E,
  output y,
  output y_2
);

  wire and_1_out, and_2_out, and_3_out, and_4_out, not_1_out, not_2_out, not_3_out, not_4_out, or_1_out;

  not not_1 (not_1_out, S1_S0[1]);
  not not_2 (not_2_out, S1_S0[0]);
  not not_3 (not_3_out, S1_S0[1]);
  not not_4 (not_4_out, S1_S0[0]);
  and and_1 (and_1_out, D3__D0[0], not_1_out, not_2_out);
  and and_2 (and_2_out, D3__D0[1], not_3_out, S1_S0[0]);
  and and_3 (and_3_out, D3__D0[2], S1_S0[1], not_4_out);
  and and_4 (and_4_out, D3__D0[3], S1_S0[1], S1_S0[0]);
  Multiplexer #(.select(2), .disabled(0)) multiplexer_1 (
    .in0(D3__D0[0]), .in1(D3__D0[1]), .in2(D3__D0[2]), .in3(D3__D0[3]), .out(y), .sel(S1_S0), .en(E));
  Pull_Resistor pull_resistor_1 (.node(y_2));
  assign y_2 = E ? or_1_out : 1'bz;  // Controlled_Buffer controlled_buffer_1
  or or_1 (or_1_out, and_1_out, and_2_out, and_3_out, and_4_out);
endmodule

module f_A_B_C__m_0_2_6_7 (
  input  [2:0] A_B_C,
  input  [2:0] A_B_C_2,
  input  C,
  input  [1:0] A_B,
  input  C_2,
  input  B,
  input  A,
  output f,
  output f_2,
  output f_3,
  output f_4
);

  wire not_1_out, not_2_out;

  Multiplexer #(.select(3), .disabled(0), .enable("false")) multiplexer_1 (
    .in0(1'b1), .in1(1'b0), .in2(1'b1), .in3(1'b0), .in4(1'b0), .in5(1'b0), .in6(1'b1), .in7(1'b1), .out(f),
    .sel(A_B_C));
  not not_1 (not_1_out, C);
  Multiplexer #(.select(2), .disabled(0), .enable("false")) multiplexer_2 (
    .in0(not_1_out), .in1(not_1_out), .in2(1'b0), .in3(1'b1), .out(f_3), .sel(A_B));
  not not_2 (not_2_out, C_2);
  Multiplexer #(.disabled(0), .enable("false")) multiplexer_3 (.in0(not_2_out), .in1(B), .out(f_4), .sel(A));
  Multiplexer #(.select(3), .disabled(0), .enable("false")) multiplexer_4 (
    .in0(1'b1), .in1(1'b0), .in2(1'b1), .in3(1'b0), .in4(1'b0), .in5(1'b0), .in6(1'b1), .in7(1'b1),
    .out(f_2), .sel(A_B_C_2));

  // Notes on the sheet:
  //   f=m0+m2+m6+m7
endmodule

module f_A_B_C__A_C__AB (
  input  C,
  input  A,
  input  B,
  output f
);

  wire not_1_out;

  not not_1 (not_1_out, C);
  Multiplexer #(.select(2), .disabled(0), .enable("false")) multiplexer_1 (
    .in0(not_1_out), .in1(not_1_out), .in2(1'b0), .in3(1'b1), .out(f), .sel({A, B}));
endmodule

module f_A_B_C__m_1_3_5_6 (
  input  A,
  input  B,
  input  C,
  output f,
  output g,
  output h,
  output j,
  output p
);

  wire A1_prime_A0_out, A2_prime_A0_out, A2A1A0_prime_out, not_1_out, not_2_out, not_3_out, not_4_out,
       xor_1_out;

  Multiplexer #(.select(3), .enable("false")) multiplexer_1 (
    .in0(1'b0), .in1(1'b1), .in2(1'b0), .in3(1'b1), .in4(1'b0), .in5(1'b1), .in6(1'b1), .in7(1'b0), .out(f),
    .sel({A, B, C}));
  Multiplexer #(.select(2), .enable("false")) multiplexer_2 (
    .in0(C), .in1(C), .in2(C), .in3(not_1_out), .out(h), .sel({A, B}));
  not not_1 (not_1_out, C);
  not not_2 (not_2_out, A);
  not not_3 (not_3_out, B);
  not not_4 (not_4_out, C);
  and A2_prime_A0 (A2_prime_A0_out, not_2_out, C);
  and A1_prime_A0 (A1_prime_A0_out, not_3_out, C);
  and A2A1A0_prime (A2A1A0_prime_out, A, B, not_4_out);
  xor xor_1 (xor_1_out, C, B);
  or or_1 (p, A2_prime_A0_out, A1_prime_A0_out, A2A1A0_prime_out);
  Multiplexer #(.select(3), .disabled(0), .enable("false")) multiplexer_3 (
    .in0(1'b0), .in1(1'b1), .in2(1'b0), .in3(1'b1), .in4(1'b0), .in5(1'b1), .in6(1'b1), .in7(1'b0), .out(g),
    .sel({A, B, C}));
  Multiplexer #(.enable("false")) multiplexer_4 (.in0(C), .in1(xor_1_out), .out(j), .sel(A));

  // Notes on the sheet:
  //   f=m1+m3+m5+m6
endmodule

module f_A_B_C_D__m_0_1_4_5_6_7_13_14_15 (
  input  D,
  input  [2:0] A_B_C,
  input  C,
  input  B,
  input  C_2,
  input  D_2,
  input  A,
  input  D_3,
  input  [1:0] A_B,
  input  A_2,
  input  A_3,
  input  D_4,
  input  D_5,
  input  B_2,
  input  [1:0] B_C,
  input  C_3,
  output f,
  output f_2,
  output f_3,
  output f_4,
  output f_5
);

  wire and_1_out, and_2_out, not_1_out, not_2_out, not_3_out, or_1_out, or_2_out, or_3_out, or_4_out,
       or_5_out;

  not not_1 (not_1_out, C_2);
  or or_1 (or_1_out, C_2, D_3);
  not not_2 (not_2_out, A_2);
  or or_2 (or_2_out, not_2_out, D_5);
  Multiplexer #(.select(3), .disabled(0), .enable("false")) multiplexer_1 (
    .in0(1'b1), .in1(1'b0), .in2(1'b1), .in3(1'b1), .in4(1'b0), .in5(1'b0), .in6(D), .in7(1'b1), .out(f),
    .sel(A_B_C));
  Multiplexer #(.select(2), .enable("false")) multiplexer_2 (
    .in0(not_1_out), .in1(1'b1), .in2(1'b0), .in3(or_1_out), .out(f_3), .sel(A_B));
  Multiplexer #(.select(2), .disabled(0), .enable("false")) multiplexer_3 (
    .in0(not_2_out), .in1(1'b0), .in2(or_2_out), .in3(1'b1), .out(f_4), .sel(B_C));
  or or_3 (or_3_out, ~C, B);  // OR_Gate
  or or_4 (or_4_out, C, D_2);
  not not_3 (not_3_out, A_3);
  and and_1 (and_1_out, D_4, B_2);
  and and_2 (and_2_out, B, or_4_out);
  or or_5 (or_5_out, not_3_out, and_1_out);
  Multiplexer #(.disabled(0), .enable("false")) multiplexer_4 (.in0(or_5_out), .in1(B_2), .out(f_5), .sel(C_3));
  Multiplexer #(.disabled(0), .enable("false")) multiplexer_5 (.in0(or_3_out), .in1(and_2_out), .out(f_2), .sel(A));

  // Notes on the sheet:
  //   f = m(0,1,4,5,6,7,13,14,15)=A'C'+BD+BC
endmodule

module f_A_B_C_D__m_1_5_9_10_11_13 (
  input  D,
  input  C,
  input  [2:0] A_B_C,
  input  D_2,
  input  [1:0] A_B,
  input  C_2,
  input  D_3,
  input  B,
  input  A,
  input  D_4,
  input  A_2,
  input  D_5,
  input  A_3,
  input  B_2,
  input  [1:0] B_C,
  input  C_3,
  output f,
  output f_2,
  output f_3,
  output f_4,
  output f_5
);

  wire and_1_out, and_2_out, and_3_out, and_4_out, not_1_out, not_2_out, not_3_out, or_1_out, or_2_out;

  not not_1 (not_1_out, C_2);
  and and_1 (and_1_out, not_1_out, D_3);
  and and_2 (and_2_out, C_2, not_2_out);
  not not_2 (not_2_out, B);
  Multiplexer #(.select(2), .disabled(0), .enable("false")) multiplexer_1 (
    .in0(D_4), .in1(A_2), .in2(D_4), .in3(1'b0), .out(f_4), .sel(B_C));
  Multiplexer #(.select(3), .disabled(0), .enable("false")) multiplexer_2 (
    .in0(D), .in1(1'b0), .in2(D), .in3(1'b0), .in4(D), .in5(1'b1), .in6(D), .in7(1'b0), .out(f), .sel(A_B_C));
  or or_1 (or_1_out, and_1_out, and_2_out);
  Multiplexer #(.disabled(0), .enable("false")) multiplexer_3 (.in0(and_1_out), .in1(or_1_out), .out(f_3), .sel(A));
  Multiplexer #(.disabled(0), .enable("false")) multiplexer_4 (.in0(D_5), .in1(and_3_out), .out(f_5), .sel(C_3));
  and and_3 (and_3_out, A_3, ~B_2);  // AND_Gate
  not not_3 (not_3_out, C);
  and and_4 (and_4_out, not_3_out, D_2);
  or or_2 (or_2_out, C, D_2);
  Multiplexer #(.select(2), .disabled(0), .enable("false")) multiplexer_5 (
    .in0(and_4_out), .in1(and_4_out), .in2(or_2_out), .in3(and_4_out), .out(f_2), .sel(A_B));

  // Notes on the sheet:
  //   f = m(1,5,9,10,11,13) = C'D+AB'C
endmodule

module f_A_B_C__m_1_3_4_7 (
  input  A,
  input  B,
  input  C,
  input  B_2,
  input  [1:0] A_C,
  output f,
  output f_2
);

  wire not_1_out;

  not not_1 (not_1_out, A);
  Multiplexer #(.disabled(0), .enable("false")) multiplexer_1 (.in0(not_1_out), .in1(B), .out(f), .sel(C));
  Multiplexer #(.select(2), .enable("false")) multiplexer_2 (
    .in0(1'b1), .in1(B_2), .in2(1'b0), .in3(B_2), .out(f_2), .sel(A_C));
endmodule

module f_A_B_C_D__m_0_1_6_8_9_12_13_14 (
  input  A,
  input  A_2,
  input  D,
  input  B,
  input  D_2,
  input  [1:0] B_C,
  input  C,
  output f,
  output f_2
);

  wire and_1_out, not_1_out, or_1_out;

  not not_1 (not_1_out, D);
  Multiplexer #(.select(2), .disabled(0), .enable("false")) multiplexer_1 (
    .in0(1'b1), .in1(1'b0), .in2(A_2), .in3(not_1_out), .out(f), .sel(B_C));
  or or_1 (or_1_out, A, ~B);  // OR_Gate
  Multiplexer #(.disabled(0), .enable("false")) multiplexer_2 (.in0(or_1_out), .in1(and_1_out), .out(f_2), .sel(C));
  and and_1 (and_1_out, B, ~D_2);  // AND_Gate
endmodule

module Puertas_con_MUX (
  input  A,
  input  B,
  input  B_2,
  input  B_3,
  input  A_2,
  input  A_3,
  input  A_4,
  input  B_4,
  input  B_5,
  input  B_6,
  input  A_5,
  input  A_6,
  input  A_7,
  output A_prime,
  output AB,
  output AB__prime,
  output A_XOR_B,
  output A_B,
  output A_B__prime,
  output A_XNOR_B
);

  wire not_1_out, not_2_out, not_3_out, not_4_out;

  Multiplexer #(.disabled(0), .enable("false")) multiplexer_1 (.in0(1'b1), .in1(1'b0), .out(A_prime), .sel(A));
  Multiplexer #(.disabled(0), .enable("false")) multiplexer_2 (.in0(1'b0), .in1(B_2), .out(AB), .sel(A_2));
  Multiplexer #(.disabled(0), .enable("false")) multiplexer_3 (.in0(B_4), .in1(1'b1), .out(A_B), .sel(A_5));
  not not_1 (not_1_out, B_3);
  not not_2 (not_2_out, B_5);
  Multiplexer #(.disabled(0), .enable("false")) multiplexer_4 (.in0(1'b1), .in1(not_1_out), .out(AB__prime), .sel(A_3));
  Multiplexer #(.disabled(0), .enable("false")) multiplexer_5 (
    .in0(not_2_out), .in1(1'b0), .out(A_B__prime), .sel(A_6));
  not not_3 (not_3_out, B);
  not not_4 (not_4_out, B_6);
  Multiplexer #(.disabled(0), .enable("false")) multiplexer_6 (.in0(B), .in1(not_3_out), .out(A_XOR_B), .sel(A_4));
  Multiplexer #(.disabled(0), .enable("false")) multiplexer_7 (.in0(not_4_out), .in1(B_6), .out(A_XNOR_B), .sel(A_7));
endmodule

module MUX_8x1__2MUX_4x1 (
  input  [3:0] D3__D0,
  input  [3:0] D7__D4,
  input  [1:0] B_C,
  input  A,
  output y
);

  wire multiplexer_1_out, multiplexer_2_out, not_1_out;

  Multiplexer #(.select(2), .disabled(0)) multiplexer_1 (
    .in0(D3__D0[0]), .in1(D3__D0[1]), .in2(D3__D0[2]), .in3(D3__D0[3]), .out(multiplexer_1_out), .sel(B_C),
    .en(not_1_out));
  Multiplexer #(.select(2), .disabled(0)) multiplexer_2 (
    .in0(D7__D4[0]), .in1(D7__D4[1]), .in2(D7__D4[2]), .in3(D7__D4[3]), .out(multiplexer_2_out), .sel(B_C),
    .en(A));
  not not_1 (not_1_out, A);
  or or_1 (y, multiplexer_1_out, multiplexer_2_out);
endmodule

module MUX_8x1__4_MUX_2x1___DEC_2x4 (
  input  D0,
  input  D1,
  input  D2,
  input  D3,
  input  D4,
  input  D5,
  input  D6,
  input  D7,
  input  C,
  input  A,
  input  B,
  output y
);

  wire decoder_1_out0, decoder_1_out1, decoder_1_out2, decoder_1_out3, multiplexer_1_out, multiplexer_2_out,
       multiplexer_3_out, multiplexer_4_out;

  Multiplexer #(.disabled(0)) multiplexer_1 (.in0(D0), .in1(D1), .out(multiplexer_1_out), .sel(C), .en(decoder_1_out0));
  Multiplexer #(.disabled(0)) multiplexer_2 (.in0(D2), .in1(D3), .out(multiplexer_2_out), .sel(C), .en(decoder_1_out1));
  Multiplexer #(.disabled(0)) multiplexer_3 (.in0(D4), .in1(D5), .out(multiplexer_3_out), .sel(C), .en(decoder_1_out2));
  Multiplexer #(.disabled(0)) multiplexer_4 (.in0(D6), .in1(D7), .out(multiplexer_4_out), .sel(C), .en(decoder_1_out3));
  Decoder #(.select(2), .disabled(0)) decoder_1 (
    .out0(decoder_1_out0), .out1(decoder_1_out1), .out2(decoder_1_out2), .out3(decoder_1_out3), .sel({A, B}),
    .en(1'b1));
  or or_1 (y, multiplexer_1_out, multiplexer_2_out, multiplexer_3_out, multiplexer_4_out);
endmodule

module MUX_8x1__2MUX_4x1___MUX_2x1 (
  input  [1:0] B_C,
  input  A,
  input  [3:0] D3__D0,
  input  [3:0] D7__D4,
  output y
);

  wire multiplexer_1_out, multiplexer_2_out;

  Multiplexer #(.select(2), .disabled(0), .enable("false")) multiplexer_1 (
    .in0(D3__D0[0]), .in1(D3__D0[1]), .in2(D3__D0[2]), .in3(D3__D0[3]), .out(multiplexer_1_out), .sel(B_C));
  Multiplexer #(.select(2), .disabled(0), .enable("false")) multiplexer_2 (
    .in0(D7__D4[0]), .in1(D7__D4[1]), .in2(D7__D4[2]), .in3(D7__D4[3]), .out(multiplexer_2_out), .sel(B_C));
  Multiplexer #(.disabled(0), .enable("false")) multiplexer_3 (
    .in0(multiplexer_1_out), .in1(multiplexer_2_out), .out(y), .sel(A));
endmodule

module MUX_8x1__4MUX_2x1___MUX_4x1 (
  input  C,
  input  B,
  input  A,
  input  D0,
  input  D1,
  input  D2,
  input  D3,
  input  D4,
  input  D5,
  input  D6,
  input  D7,
  output y
);

  wire multiplexer_1_out, multiplexer_2_out, multiplexer_3_out, multiplexer_4_out;

  Multiplexer #(.disabled(0), .enable("false")) multiplexer_1 (.in0(D0), .in1(D1), .out(multiplexer_1_out), .sel(C));
  Multiplexer #(.disabled(0), .enable("false")) multiplexer_2 (.in0(D2), .in1(D3), .out(multiplexer_2_out), .sel(C));
  Multiplexer #(.disabled(0), .enable("false")) multiplexer_3 (.in0(D4), .in1(D5), .out(multiplexer_3_out), .sel(C));
  Multiplexer #(.disabled(0), .enable("false")) multiplexer_4 (.in0(D6), .in1(D7), .out(multiplexer_4_out), .sel(C));
  Multiplexer #(.select(2), .disabled(0), .enable("false")) multiplexer_5 (
    .in0(multiplexer_1_out), .in1(multiplexer_2_out), .in2(multiplexer_3_out), .in3(multiplexer_4_out),
    .out(y), .sel({A, B}));
endmodule

module MUX_8x1__6MUX_2x1___MUX_2x1 (
  input  C,
  input  B,
  input  A,
  input  D0,
  input  D1,
  input  D2,
  input  D3,
  input  D4,
  input  D5,
  input  D6,
  input  D7,
  output y
);

  wire multiplexer_1_out, multiplexer_2_out, multiplexer_3_out, multiplexer_4_out, multiplexer_5_out,
       multiplexer_7_out;

  Multiplexer #(.disabled(0), .enable("false")) multiplexer_1 (.in0(D0), .in1(D1), .out(multiplexer_1_out), .sel(C));
  Multiplexer #(.disabled(0), .enable("false")) multiplexer_2 (.in0(D2), .in1(D3), .out(multiplexer_2_out), .sel(C));
  Multiplexer #(.disabled(0), .enable("false")) multiplexer_3 (.in0(D4), .in1(D5), .out(multiplexer_3_out), .sel(C));
  Multiplexer #(.disabled(0), .enable("false")) multiplexer_4 (.in0(D6), .in1(D7), .out(multiplexer_4_out), .sel(C));
  Multiplexer #(.disabled(0), .enable("false")) multiplexer_5 (
    .in0(multiplexer_1_out), .in1(multiplexer_2_out), .out(multiplexer_5_out), .sel(B));
  Multiplexer #(.disabled(0), .enable("false")) multiplexer_6 (
    .in0(multiplexer_5_out), .in1(multiplexer_7_out), .out(y), .sel(A));
  Multiplexer #(.disabled(0), .enable("false")) multiplexer_7 (
    .in0(multiplexer_3_out), .in1(multiplexer_4_out), .out(multiplexer_7_out), .sel(B));
endmodule

module LUT_2x3___4vars (
  input  D,
  input  C,
  input  B,
  input  A,
  output f
);

  wire multiplexer_1_out, multiplexer_2_out, multiplexer_3_out, multiplexer_4_out, multiplexer_5_out,
       multiplexer_6_out, multiplexer_7_out, multiplexer_8_out, multiplexer_9_out, multiplexer_10_out,
       multiplexer_11_out, multiplexer_12_out, multiplexer_13_out, multiplexer_14_out;

  Multiplexer #(.disabled(0), .enable("false")) multiplexer_1 (
    .in0(1'b1), .in1(1'b1), .out(multiplexer_1_out), .sel(D));
  Multiplexer #(.disabled(0), .enable("false")) multiplexer_2 (
    .in0(1'b0), .in1(1'b0), .out(multiplexer_2_out), .sel(D));
  Multiplexer #(.disabled(0), .enable("false")) multiplexer_3 (
    .in0(1'b1), .in1(1'b1), .out(multiplexer_3_out), .sel(D));
  Multiplexer #(.disabled(0), .enable("false")) multiplexer_4 (
    .in0(1'b1), .in1(1'b1), .out(multiplexer_4_out), .sel(D));
  Multiplexer #(.disabled(0), .enable("false")) multiplexer_5 (
    .in0(1'b0), .in1(1'b0), .out(multiplexer_5_out), .sel(D));
  Multiplexer #(.disabled(0), .enable("false")) multiplexer_6 (
    .in0(1'b0), .in1(1'b0), .out(multiplexer_6_out), .sel(D));
  Multiplexer #(.disabled(0), .enable("false")) multiplexer_7 (
    .in0(1'b0), .in1(1'b1), .out(multiplexer_7_out), .sel(D));
  Multiplexer #(.disabled(0), .enable("false")) multiplexer_8 (
    .in0(1'b1), .in1(1'b1), .out(multiplexer_8_out), .sel(D));
  Multiplexer #(.disabled(0), .enable("false")) multiplexer_9 (
    .in0(multiplexer_1_out), .in1(multiplexer_2_out), .out(multiplexer_9_out), .sel(C));
  Multiplexer #(.disabled(0), .enable("false")) multiplexer_10 (
    .in0(multiplexer_3_out), .in1(multiplexer_4_out), .out(multiplexer_10_out), .sel(C));
  Multiplexer #(.disabled(0), .enable("false")) multiplexer_11 (
    .in0(multiplexer_5_out), .in1(multiplexer_6_out), .out(multiplexer_11_out), .sel(C));
  Multiplexer #(.disabled(0), .enable("false")) multiplexer_12 (
    .in0(multiplexer_7_out), .in1(multiplexer_8_out), .out(multiplexer_12_out), .sel(C));
  Multiplexer #(.disabled(0), .enable("false")) multiplexer_13 (
    .in0(multiplexer_9_out), .in1(multiplexer_10_out), .out(multiplexer_13_out), .sel(B));
  Multiplexer #(.disabled(0), .enable("false")) multiplexer_14 (
    .in0(multiplexer_11_out), .in1(multiplexer_12_out), .out(multiplexer_14_out), .sel(B));
  Multiplexer #(.disabled(0), .enable("false")) multiplexer_15 (
    .in0(multiplexer_13_out), .in1(multiplexer_14_out), .out(f), .sel(A));
endmodule

module f_A_B_C__m_0_2_3_7 (
  input  C,
  input  A,
  input  B,
  input  C_2,
  input  [1:0] A_B,
  output f,
  output f_2
);

  wire not_1_out, not_2_out;

  not not_1 (not_1_out, C);
  Multiplexer #(.select(2), .disabled(0), .enable("false")) multiplexer_1 (
    .in0(not_1_out), .in1(1'b1), .in2(1'b0), .in3(C), .out(f_2), .sel(A_B));
  not not_2 (not_2_out, A);
  Multiplexer #(.disabled(0), .enable("false")) multiplexer_2 (.in0(not_2_out), .in1(B), .out(f), .sel(C_2));
endmodule

module MUX_neg (
  input  A,
  input  B,
  input  C,
  output f
);

  wire [2:0] not_1_out;

  Multiplexer #(.select(3), .enable("false")) multiplexer_1 (
    .in0(1'b1), .in1(1'b0), .in2(1'b0), .in3(1'b0), .in4(1'b0), .in5(1'b1), .in6(1'b0), .in7(1'b1), .out(f),
    .sel(not_1_out));
  assign not_1_out = ~{A, B, C};  // NOT_Gate not_1, 3 bits wide
endmodule
