// Logisim project Cap5_3_DEMUX.circ as structural Verilog: 4 circuits, main circuit Demux 1x4
module Demux_1x4 (
  input  Dato,
  input  E,
  input  A,
  input  B,
  output y0,
  output y1,
  output y2,
  output y3
);

  Demultiplexer #(.select(2), .disabled(0)) demultiplexer_1 (
    .out0(y0), .out1(y1), .out2(y2), .out3(y3), .in(Dato), .sel({A, B}), .en(E));
endmodule

module Demux_1x4__nivel_alto (
  input  A,
  input  B,
  input  E,
  input  D,
  output y0,
  output y1,
  output y2,
  output y3
);

  wire ED_out, not_1_out, not_2_out;

  and ED (ED_out, E, D);
  not not_1 (not_1_out, A);
  not not_2 (not_2_out, B);
  and A_prime_B_prime_ED (y0, not_1_out, not_2_out, ED_out);
  and A_prime_B_ED (y1, not_1_out, B, ED_out);
  and AB_prime_ED (y2, A, not_2_out, ED_out);
  and AB_ED (y3, A, B, ED_out);
endmodule

module Demux_1x4__nivel_bajo (
  input  A,
  input  B,
  input  E,
  input  D,
  output y0,
  output y1,
  output y2,
  output y3
);

  wire and_1_out, not_1_out, not_2_out;

  and and_1 (and_1_out, ~E, ~D);  // AND_Gate
  not not_1 (not_1_out, A);
  not not_2 (not_2_out, B);
  nand nand_1 (y0, not_1_out, not_2_out, and_1_out);
  nand nand_2 (y1, not_1_out, B, and_1_out);
  nand nand_3 (y2, A, not_2_out, and_1_out);
  nand nand_4 (y3, A, B, and_1_out);
endmodule

module Func_w__demux (
  input  A,
  input  B,
  input  C,
  output f,
  output f_2
);

  wire demultiplexer_1_out0, demultiplexer_1_out3, xnor_1_out;

  Demultiplexer #(.select(2), .enable("false")) demultiplexer_1 (
    .out0(demultiplexer_1_out0), .out3(demultiplexer_1_out3), .in(A), .sel({B, C}));  // open: out1, out2
  xnor xnor_1 (xnor_1_out, B, C);
  or or_1 (f, demultiplexer_1_out0, demultiplexer_1_out3);
  and and_1 (f_2, A, xnor_1_out);
endmodule
