// Logisim project Cap5_4_COD.circ as structural Verilog: 6 circuits, main circuit COD 8x3 (completo)
// COD 8x3
module COD_8x3__nivel_alto (
  input  D0,
  input  D1,
  input  D2,
  input  D3,
  input  D4,
  input  D5,
  input  D6,
  input  D7,
  output y2,
  output y1,
  output y0
);

  or or_1 (y2, D4, D5, D6, D7);
  or or_2 (y1, D2, D3, D6, D7);
  or or_3 (y0, D1, D3, D5, D7);

  // Notes on the sheet:
  //   E/S y E activadas con nivel alto
endmodule

module COD_8x3__nivel_bajo (
  input  D0,
  input  D1,
  input  D2,
  input  D3,
  input  D4,
  input  D5,
  input  D6,
  input  D7,
  output y2,
  output y1,
  output y0
);

  and and_1 (y2, D4, D5, D6, D7);
  and and_2 (y1, D2, D3, D6, D7);
  and and_3 (y0, D1, D3, D5, D7);

  // Notes on the sheet:
  //   E/S y E activadas con nivel bajo
endmodule

// Prior 8x3
module Circuito_de_Prioridad_8x3 (
  input  D0,
  input  D1,
  input  D2,
  input  D3,
  input  D4,
  input  D5,
  input  D6,
  input  D7,
  output D0_star,
  output D1_star,
  output D2_star,
  output D3_star,
  output D4_star,
  output D5_star,
  output D6_star,
  output D7_star
);

  wire not_1_out, not_2_out, not_3_out, not_4_out, not_5_out, not_6_out, not_7_out;

  not not_1 (not_1_out, D1);
  and and_1 (D0_star, D0, not_1_out, not_2_out, not_3_out, not_4_out, not_5_out, not_6_out, not_7_out);
  not not_2 (not_2_out, D2);
  and and_2 (D1_star, D1, not_2_out, not_3_out, not_4_out, not_5_out, not_6_out, not_7_out);
  not not_3 (not_3_out, D3);
  and and_3 (D2_star, D2, not_3_out, not_4_out, not_5_out, not_6_out, not_7_out);
  not not_4 (not_4_out, D4);
  and and_4 (D3_star, D3, not_4_out, not_5_out, not_6_out, not_7_out);
  not not_5 (not_5_out, D5);
  and and_5 (D4_star, D4, not_5_out, not_6_out, not_7_out);
  not not_6 (not_6_out, D6);
  not not_7 (not_7_out, D7);
  and and_6 (D6_star, D6, not_7_out);
  and and_7 (D5_star, D5, not_6_out, not_7_out);

  assign D7_star = D7;
endmodule

// COD 8x3
module COD_8x3__completo (
  input  D0,
  input  D1,
  input  D2,
  input  D3,
  input  D4,
  input  D5,
  input  D6,
  input  D7,
  input  Ei,
  output [2:0] A2_A0,
  output Gs,
  output Eo
);

  wire circuito_de_prioridad_8x3_1_d0_star, circuito_de_prioridad_8x3_1_d1_star,
       circuito_de_prioridad_8x3_1_d2_star, circuito_de_prioridad_8x3_1_d3_star,
       circuito_de_prioridad_8x3_1_d4_star, circuito_de_prioridad_8x3_1_d5_star,
       circuito_de_prioridad_8x3_1_d6_star, circuito_de_prioridad_8x3_1_d7_star, or_1_out;
  wire [2:0] cod_8x3_nivel_alto_1_y0;

  Circuito_de_Prioridad_8x3 circuito_de_prioridad_8x3_1 (
    .D0(D0), .D1(D1), .D2(D2), .D3(D3), .D4(D4), .D5(D5), .D6(D6), .D7(D7),
    .D0_star(circuito_de_prioridad_8x3_1_d0_star), .D1_star(circuito_de_prioridad_8x3_1_d1_star),
    .D2_star(circuito_de_prioridad_8x3_1_d2_star), .D3_star(circuito_de_prioridad_8x3_1_d3_star),
    .D4_star(circuito_de_prioridad_8x3_1_d4_star), .D5_star(circuito_de_prioridad_8x3_1_d5_star),
    .D6_star(circuito_de_prioridad_8x3_1_d6_star), .D7_star(circuito_de_prioridad_8x3_1_d7_star));
  COD_8x3__nivel_alto cod_8x3_nivel_alto_1 (
    .D0(circuito_de_prioridad_8x3_1_d0_star), .D1(circuito_de_prioridad_8x3_1_d1_star),
    .D2(circuito_de_prioridad_8x3_1_d2_star), .D3(circuito_de_prioridad_8x3_1_d3_star),
    .D4(circuito_de_prioridad_8x3_1_d4_star), .D5(circuito_de_prioridad_8x3_1_d5_star),
    .D6(circuito_de_prioridad_8x3_1_d6_star), .D7(circuito_de_prioridad_8x3_1_d7_star),
    .y2(cod_8x3_nivel_alto_1_y0[2]), .y1(cod_8x3_nivel_alto_1_y0[1]), .y0(cod_8x3_nivel_alto_1_y0[0]));
  or or_1 (or_1_out, circuito_de_prioridad_8x3_1_d7_star, circuito_de_prioridad_8x3_1_d6_star, circuito_de_prioridad_8x3_1_d5_star, circuito_de_prioridad_8x3_1_d4_star, circuito_de_prioridad_8x3_1_d3_star, circuito_de_prioridad_8x3_1_d2_star, circuito_de_prioridad_8x3_1_d1_star, circuito_de_prioridad_8x3_1_d0_star);
  assign A2_A0 = Gs ? cod_8x3_nivel_alto_1_y0 : 3'bz;  // Controlled_Buffer controlled_buffer_1
  and and_1 (Gs, or_1_out, Ei);
  and and_2 (Eo, ~or_1_out, Ei);  // AND_Gate
endmodule

module \Comparación  (
  input  [7:0] D7_D0,
  input  Ei,
  output [2:0] A2_A0,
  output Gs,
  output Eo,
  output [2:0] A2_A0_2,
  output Eo_2,
  output Gs_2
);

  COD_8x3__completo cod_8x3_completo_1 (
    .D0(D7_D0[0]), .D1(D7_D0[1]), .D2(D7_D0[2]), .D3(D7_D0[3]), .D4(D7_D0[4]), .D5(D7_D0[5]), .D6(D7_D0[6]),
    .D7(D7_D0[7]), .Ei(Ei), .A2_A0(A2_A0), .Gs(Gs), .Eo(Eo));
  Priority_Encoder priority_encoder_1 (
    .in0(D7_D0[0]), .in1(D7_D0[1]), .in2(D7_D0[2]), .in3(D7_D0[3]), .in4(D7_D0[4]), .in5(D7_D0[5]),
    .in6(D7_D0[6]), .in7(D7_D0[7]), .out(A2_A0_2), .en_in(Ei), .gs(Gs_2), .en_out(Eo_2));
endmodule

module _2_COD_8x3 (
  input  [15:0] in_1,
  output [2:0] out_2,
  output [3:0] out_3,
  output [2:0] out_4,
  output out_5,
  output out_6
);

  wire priority_encoder_2_en_out;

  Priority_Encoder priority_encoder_1 (
    .in0(in_1[0]), .in1(in_1[1]), .in2(in_1[2]), .in3(in_1[3]), .in4(in_1[4]), .in5(in_1[5]), .in6(in_1[6]),
    .in7(in_1[7]), .out(out_2), .en_in(priority_encoder_2_en_out), .gs(out_6));  // open: en_out
  Priority_Encoder #(.disabled(0)) priority_encoder_2 (
    .in0(in_1[8]), .in1(in_1[9]), .in2(in_1[10]), .in3(in_1[11]), .in4(in_1[12]), .in5(in_1[13]),
    .in6(in_1[14]), .in7(in_1[15]), .out(out_4), .en_in(1'b1), .gs(out_5), .en_out(priority_encoder_2_en_out));
  Pull_Resistor pull_resistor_1 (.node(out_2));
  not not_1 (out_3[3], priority_encoder_2_en_out);
  Pull_Resistor pull_resistor_2 (.node(out_4));
  assign out_3[2:0] = out_2 | out_4;  // OR_Gate or_1, 3 bits wide

  // Notes on the sheet:
  //   out_2: pull=down
  //   out_4: pull=down
endmodule
