// Logisim project Cap5_5_LogisimErrs.circ as structural Verilog: 4 circuits, main circuit Error 1
module Error_1 (
  input  A,
  input  B,
  output f
);

  wire and_1_out, and_2_out, undriven;

  and and_1 (and_1_out, A, B);
  and and_2 (and_2_out, B, undriven);
  or or_1 (f, and_1_out, and_2_out);
endmodule

module Error_2 (
  input  A,
  input  B,
  input  [1:0] AB,
  input  C,
  output f,
  output f_2,
  output g
);

  and and_1 (f_2, A, B);
  Multiplexer #(.select(2)) multiplexer_1 (.in0(1'b1), .in1(1'b1), .in2(1'b1), .out(f), .sel(AB));  // open: in3, en
endmodule

module Error_3 (
  input  A,
  input  B,
  output f
);

  and and_1 (f, A, B);
endmodule

module Error_4 (
  input  A,
  input  A_2,
  input  B,
  input  B_2,
  input  C,
  input  C_2,
  input  D,
  input  D_2,
  input  [1:0] AB,
  input  [1:0] AB_2,
  output f,
  output f_2,
  output f_3,
  output f_4
);

  wire and_1_out, and_3_out;

  and and_1 (and_1_out, A, C);
  or or_1 (f, C, D);
  Decoder #(.select(2), .enable("false")) decoder_1 (.out1(f_3), .out3(f_3), .sel(AB));  // open: out0, out2
  and and_2 (f, and_1_out, B);
  Decoder #(.select(2), .enable("false")) decoder_2 (.out1(f_4), .out3(f_4), .sel(AB_2));  // open: out0, out2
  and and_3 (and_3_out, A_2, C_2);
  or or_2 (f_2, C_2, D_2);
  and and_4 (f_2, and_3_out, B_2);
endmodule
