// Logisim project Cap5_74HC154-Aplic.circ as structural Verilog: 3 circuits, main circuit CPU
module CPU (
  input  [3:0] I_O_port_adress,
  input  I_O_request,
  output [7:0] Datos__Bus
);

  wire n74hc154_1_out_3, n74hc154_1_out_4, n74hc154_1_out_5, n74hc154_1_out_6;

  // Probe on Datos__Bus
  _74HC154 u_74hc154_1 (
    .Address(I_O_port_adress), .Enable(I_O_request), .out_3(n74hc154_1_out_3), .out_4(n74hc154_1_out_4),
    .out_5(n74hc154_1_out_5), .out_6(n74hc154_1_out_6));  // open: out_7, out_8, out_9, out_10, out_11, out_12, out_13, out_14, out_15, out_16, out_17, out_18
  Device Impresora (.in_2(n74hc154_1_out_3), .Out(Datos__Bus), .Data(8'hfa));
  Device Monitor (.in_2(n74hc154_1_out_4), .Out(Datos__Bus), .Data(8'hfb));
  Device Teclado (.in_2(n74hc154_1_out_5), .Out(Datos__Bus), .Data(8'hfc));
  Device Disco_ext (.in_2(n74hc154_1_out_6), .Out(Datos__Bus), .Data(8'hfd));

  // Notes on the sheet:
  //   Bus de datos
  //   Data
endmodule

module _74HC154 (
  input  [3:0] Address,
  input  Enable,
  output out_3,
  output out_4,
  output out_5,
  output out_6,
  output out_7,
  output out_8,
  output out_9,
  output out_10,
  output out_11,
  output out_12,
  output out_13,
  output out_14,
  output out_15,
  output out_16,
  output out_17,
  output out_18
);

  wire decoder_1_out0, decoder_1_out1, decoder_1_out2, decoder_1_out3, decoder_1_out4, decoder_1_out5,
       decoder_1_out6, decoder_1_out7, decoder_1_out8, decoder_1_out9, decoder_1_out10, decoder_1_out11,
       decoder_1_out12, decoder_1_out13, decoder_1_out14, decoder_1_out15, not_1_out;

  not not_1 (not_1_out, Enable);
  not not_2 (out_3, decoder_1_out0);
  not not_3 (out_4, decoder_1_out1);
  not not_4 (out_5, decoder_1_out2);
  not not_5 (out_6, decoder_1_out3);
  not not_6 (out_7, decoder_1_out4);
  not not_7 (out_8, decoder_1_out5);
  not not_8 (out_9, decoder_1_out6);
  not not_9 (out_10, decoder_1_out7);
  not not_10 (out_11, decoder_1_out8);
  not not_11 (out_12, decoder_1_out9);
  not not_12 (out_13, decoder_1_out10);
  not not_13 (out_14, decoder_1_out11);
  not not_14 (out_15, decoder_1_out12);
  not not_15 (out_16, decoder_1_out13);
  not not_16 (out_17, decoder_1_out14);
  not not_17 (out_18, decoder_1_out15);
  Decoder #(.select(4)) decoder_1 (
    .out0(decoder_1_out0), .out1(decoder_1_out1), .out2(decoder_1_out2), .out3(decoder_1_out3),
    .out4(decoder_1_out4), .out5(decoder_1_out5), .out6(decoder_1_out6), .out7(decoder_1_out7),
    .out8(decoder_1_out8), .out9(decoder_1_out9), .out10(decoder_1_out10), .out11(decoder_1_out11),
    .out12(decoder_1_out12), .out13(decoder_1_out13), .out14(decoder_1_out14), .out15(decoder_1_out15),
    .sel(Address), .en(not_1_out));
endmodule

module Device (
  input  [7:0] Data,
  input  in_2,
  output [7:0] Out
);

  wire not_1_out;

  assign Out = not_1_out ? Data : 8'bz;  // Controlled_Buffer controlled_buffer_1
  not not_1 (not_1_out, in_2);
endmodule
