// Logisim project Cap6_1_ModLogs.circ as structural Verilog: 17 circuits, main circuit Comp. 1 bit
module Conversor_Cod1 (
  input  A1,
  input  A0,
  input  A1_2,
  input  A0_2,
  input  A1_3,
  input  A0_3,
  output B1,
  output B0,
  output B1_2,
  output B1_3,
  output B0_2,
  output B0_3
);

  wire decoder_1_out0, decoder_1_out1, decoder_1_out2, decoder_2_out0, decoder_2_out1, decoder_2_out2,
       decoder_2_out3;

  xor xor_1 (B1_3, A1_2, A0_2);
  not not_1 (B0_3, A0_2);
  Decoder #(.select(2), .enable("false")) decoder_1 (
    .out0(decoder_1_out0), .out1(decoder_1_out1), .out2(decoder_1_out2), .sel({A1, A0}));  // open: out3
  Decoder #(.select(2), .enable("false")) decoder_2 (
    .out0(decoder_2_out0), .out1(decoder_2_out1), .out2(decoder_2_out2), .out3(decoder_2_out3),
    .sel({A1_3, A0_3}));
  or or_1 (B1, decoder_1_out1, decoder_1_out2);
  or or_2 (B0, decoder_1_out2, decoder_1_out0);
  Priority_Encoder #(.select(2)) priority_encoder_1 (
    .in0(decoder_2_out3), .in1(decoder_2_out0), .in2(decoder_2_out1), .in3(decoder_2_out2), .out({B1_2, B0_2}));  // open: gs, en_out, en_in
endmodule

module Conversor_Cod2 (
  input  A1,
  input  A0,
  input  A1_2,
  input  A0_2,
  input  A1_3,
  input  A0_3,
  output B3,
  output B2,
  output B3_2,
  output B2_2,
  output B1,
  output B1_2,
  output B0,
  output B1_3,
  output B3_3,
  output B2_3,
  output B1_4,
  output B0_2
);

  wire decoder_1_out0, decoder_1_out1, decoder_1_out2, decoder_1_out3, decoder_2_out0, decoder_2_out1,
       decoder_2_out2;

  not not_1 (B0, A0);
  Decoder #(.select(2), .enable("false")) decoder_1 (
    .out0(decoder_1_out0), .out1(decoder_1_out1), .out2(decoder_1_out2), .out3(decoder_1_out3),
    .sel({A1_3, A0_3}));
  and and_1 (B3_2, A1, A0);
  Priority_Encoder #(.select(4)) priority_encoder_1 (
    .in1(decoder_1_out0), .in2(decoder_1_out1), .in5(decoder_1_out2), .in14(decoder_1_out3),
    .out({B3_3, B2_3, B1_4, B0_2}));  // open: in0, in3, in4, in6, in7, in8, in9, in10, in11, in12, in13, in15, gs, en_out, en_in
  Decoder #(.select(2), .enable("false")) decoder_2 (
    .out0(decoder_2_out0), .out1(decoder_2_out1), .out2(decoder_2_out2), .out3(B3), .sel({A1_2, A0_2}));
  or or_1 (B2, decoder_2_out2, B3);
  or or_2 (B1, decoder_2_out1, B3);
  or or_3 (B1_3, decoder_2_out2, decoder_2_out0);

  assign B1_2 = A0;
  assign B2_2 = A1;
endmodule

module coders_rom (
  input  [1:0] in_1,
  input  [1:0] in_2,
  output [1:0] out_3,
  output [3:0] out_4
);

  // Probe on out_3
  ROM #(.addrWidth(2), .dataWidth(2)) rom_1 (.addr(in_1), .data(out_3));  // open: sel
  // Probe on out_4
  ROM #(.addrWidth(2), .dataWidth(4)) rom_2 (.addr(in_2), .data(out_4));  // open: sel

  // Notes on the sheet:
  //   contents of rom_1 (hex, n*v repeats v):
  //   1 2 3
  //   contents of rom_2 (hex, n*v repeats v):
  //   1 2 5 e
endmodule

module Cod2_rom (
  input  A1,
  input  A0,
  output B3,
  output B2,
  output B1,
  output B0
);

  // Probe on {B3, B2, B1, B0}
  ROM #(.addrWidth(2), .dataWidth(4)) rom_1 (.addr({A1, A0}), .data({B3, B2, B1, B0}));  // open: sel

  // Notes on the sheet:
  //   contents of rom_1 (hex, n*v repeats v):
  //   1 2 5 e
endmodule

module Comp__1_bit (
  input  A,
  input  B,
  output f1__A_B,
  output f2__A_B,
  output f3__A_B
);

  wire not_1_out, not_2_out;

  not not_1 (not_1_out, B);
  xnor xnor_1 (f2__A_B, A, B);
  not not_2 (not_2_out, A);
  and AB_prime (f1__A_B, A, not_1_out);
  and A_prime_B (f3__A_B, not_2_out, B);
endmodule

module Comp__1_bit_completo (
  input  A1,
  input  B1,
  input  A0_B0,
  input  A0_B0_2,
  input  A0_B0_3,
  output f1__A_B,
  output f2__A_B,
  output f3__A_B
);

  wire A1_B1_2_out, A1_B1_3_out, A1_B1_out, and_1_out, and_3_out, not_1_out, not_2_out;

  not not_1 (not_1_out, B1);
  not not_2 (not_2_out, A1);
  and A1_B1 (A1_B1_out, A1, not_1_out);
  xnor A1_B1_2 (A1_B1_2_out, A1, B1);
  and A1_B1_3 (A1_B1_3_out, not_2_out, B1);
  or or_1 (f1__A_B, A1_B1_out, and_1_out);
  and and_1 (and_1_out, A1_B1_2_out, A0_B0);
  and and_2 (f2__A_B, A1_B1_2_out, A0_B0_2);
  or or_2 (f3__A_B, A1_B1_3_out, and_3_out);
  and and_3 (and_3_out, A1_B1_2_out, A0_B0_3);
endmodule

module Comp__2_bits (
  input  A1,
  input  A0,
  input  B1,
  input  B0,
  output f1__A_B,
  output f2__A_B,
  output f3__A_B
);

  wire and_1_out, and_2_out, and_3_out, and_4_out, and_5_out, and_6_out, and_7_out, and_8_out, and_9_out,
       and_10_out, not_1_out, not_2_out, not_3_out, not_4_out;

  not not_1 (not_1_out, A1);
  not not_2 (not_2_out, B1);
  not not_3 (not_3_out, A0);
  not not_4 (not_4_out, B0);
  and and_1 (and_1_out, A0, not_2_out, not_4_out);
  and and_2 (and_2_out, A1, not_2_out);
  or or_1 (f1__A_B, and_1_out, and_2_out, and_3_out);
  and and_3 (and_3_out, A1, A0, not_4_out);
  and and_4 (and_4_out, not_1_out, not_3_out, not_2_out, not_4_out);
  and and_5 (and_5_out, not_1_out, A0, not_2_out, B0);
  and and_6 (and_6_out, A1, not_3_out, B1, not_4_out);
  and and_7 (and_7_out, A1, A0, B1, B0);
  and and_8 (and_8_out, not_1_out, not_3_out, B0);
  and and_9 (and_9_out, not_1_out, B1);
  or or_2 (f3__A_B, and_8_out, and_9_out, and_10_out);
  and and_10 (and_10_out, not_3_out, B1, B0);
  or or_3 (f2__A_B, and_4_out, and_5_out, and_6_out, and_7_out);
endmodule

module Comp__2_bits__1bitx2 (
  input  A1,
  input  B1,
  input  A0,
  input  B0,
  output f1__A_B,
  output f2__A_B,
  output f3__A_B
);

  wire and_1_out, and_2_out, comp_1_bit_1_f1__a_b, comp_1_bit_1_f2__a_b, comp_1_bit_1_f3__a_b,
       comp_1_bit_2_f1__a_b, comp_1_bit_2_f2__a_b, comp_1_bit_2_f3__a_b;

  Comp__1_bit comp_1_bit_1 (
    .A(A1), .B(B1), .f1__A_B(comp_1_bit_1_f1__a_b), .f2__A_B(comp_1_bit_1_f2__a_b),
    .f3__A_B(comp_1_bit_1_f3__a_b));
  Comp__1_bit comp_1_bit_2 (
    .A(A0), .B(B0), .f1__A_B(comp_1_bit_2_f1__a_b), .f2__A_B(comp_1_bit_2_f2__a_b),
    .f3__A_B(comp_1_bit_2_f3__a_b));
  and and_1 (and_1_out, comp_1_bit_1_f2__a_b, comp_1_bit_2_f1__a_b);
  and and_2 (and_2_out, comp_1_bit_1_f2__a_b, comp_1_bit_2_f3__a_b);
  or or_1 (f1__A_B, comp_1_bit_1_f1__a_b, and_1_out);
  and and_3 (f2__A_B, comp_1_bit_1_f2__a_b, comp_1_bit_2_f2__a_b);
  or or_2 (f3__A_B, comp_1_bit_1_f3__a_b, and_2_out);
endmodule

// CMP4
module Comp__4_bits__1bitx4 (
  input  A3,
  input  A2,
  input  A1,
  input  A0,
  input  A_B,
  input  A_B_2,
  input  A_B_3,
  input  B3,
  input  B2,
  input  B1,
  input  B0,
  output A_B_4,
  output A_B_5,
  output A_B_6
);

  wire comp_1_bit_completo_1_f1__a_b, comp_1_bit_completo_1_f2__a_b, comp_1_bit_completo_1_f3__a_b,
       comp_1_bit_completo_2_f1__a_b, comp_1_bit_completo_2_f2__a_b, comp_1_bit_completo_2_f3__a_b,
       comp_1_bit_completo_3_f1__a_b, comp_1_bit_completo_3_f2__a_b, comp_1_bit_completo_3_f3__a_b;

  Comp__1_bit_completo comp_1_bit_completo_1 (
    .A1(A0), .B1(B0), .A0_B0(A_B), .A0_B0_2(A_B_2), .A0_B0_3(A_B_3), .f1__A_B(comp_1_bit_completo_1_f1__a_b),
    .f2__A_B(comp_1_bit_completo_1_f2__a_b), .f3__A_B(comp_1_bit_completo_1_f3__a_b));
  Comp__1_bit_completo comp_1_bit_completo_2 (
    .A1(A1), .B1(B1), .A0_B0(comp_1_bit_completo_1_f1__a_b), .A0_B0_2(comp_1_bit_completo_1_f2__a_b),
    .A0_B0_3(comp_1_bit_completo_1_f3__a_b), .f1__A_B(comp_1_bit_completo_2_f1__a_b),
    .f2__A_B(comp_1_bit_completo_2_f2__a_b), .f3__A_B(comp_1_bit_completo_2_f3__a_b));
  Comp__1_bit_completo comp_1_bit_completo_3 (
    .A1(A2), .B1(B2), .A0_B0(comp_1_bit_completo_2_f1__a_b), .A0_B0_2(comp_1_bit_completo_2_f2__a_b),
    .A0_B0_3(comp_1_bit_completo_2_f3__a_b), .f1__A_B(comp_1_bit_completo_3_f1__a_b),
    .f2__A_B(comp_1_bit_completo_3_f2__a_b), .f3__A_B(comp_1_bit_completo_3_f3__a_b));
  Comp__1_bit_completo comp_1_bit_completo_4 (
    .A1(A3), .B1(B3), .A0_B0(comp_1_bit_completo_3_f1__a_b), .A0_B0_2(comp_1_bit_completo_3_f2__a_b),
    .A0_B0_3(comp_1_bit_completo_3_f3__a_b), .f1__A_B(A_B_4), .f2__A_B(A_B_5), .f3__A_B(A_B_6));
endmodule

module Comp__8_bits__4bitsx2 (
  input  [3:0] A3A2A1A0,
  input  [3:0] A7A6A5A4,
  input  [3:0] B3B2B1B0,
  input  [3:0] B7B6B5B4,
  input  [7:0] A7A6A5A4A3A2A1A0,
  input  [7:0] B7B6B5B4B3B2B1B0,
  output A_B,
  output A_B_2,
  output A_B_3,
  output A_B_4,
  output A_B_5,
  output A_B_6
);

  wire comp_4_bits_1bitx4_1_a_b_4, comp_4_bits_1bitx4_1_a_b_5, comp_4_bits_1bitx4_1_a_b_6;

  // Probe on 1'b1
  // Probe on 1'b0
  Comp__4_bits__1bitx4 comp_4_bits_1bitx4_1 (
    .A1(A3A2A1A0[1]), .A0(A3A2A1A0[0]), .A_B(1'b0), .A_B_2(1'b1), .A_B_3(1'b0), .B1(B3B2B1B0[1]),
    .B0(B3B2B1B0[0]), .A_B_4(comp_4_bits_1bitx4_1_a_b_4), .A_B_5(comp_4_bits_1bitx4_1_a_b_5),
    .A_B_6(comp_4_bits_1bitx4_1_a_b_6), .A3(A3A2A1A0[3]), .A2(A3A2A1A0[2]), .B3(B3B2B1B0[3]), .B2(B3B2B1B0[2]));
  Comparator #(.mode("unsigned")) comparator_1 (
    .a(A7A6A5A4A3A2A1A0), .b(B7B6B5B4B3B2B1B0), .gt(A_B_4), .eq(A_B_5), .lt(A_B_6));
  Comp__4_bits__1bitx4 comp_4_bits_1bitx4_2 (
    .A1(A7A6A5A4[1]), .A0(A7A6A5A4[0]), .A_B(comp_4_bits_1bitx4_1_a_b_4), .A_B_2(comp_4_bits_1bitx4_1_a_b_5),
    .A_B_3(comp_4_bits_1bitx4_1_a_b_6), .B1(B7B6B5B4[1]), .B0(B7B6B5B4[0]), .A_B_4(A_B), .A_B_5(A_B_2),
    .A_B_6(A_B_3), .A3(A7A6A5A4[3]), .A2(A7A6A5A4[2]), .B3(B7B6B5B4[3]), .B2(B7B6B5B4[2]));

  // Notes on the sheet:
  //   LSB
  //   MSB
endmodule

module Comp__4_bits__C2 (
  input  [3:0] A,
  input  [3:0] B,
  input  [3:0] A_2,
  input  [3:0] B_2,
  output A_B,
  output A_B_2,
  output A_B_3,
  output A_B_4,
  output A_B_5,
  output A_B_6
);

  wire and_1_out, and_2_out, and_3_out, and_4_out, comparator_1_gt, comparator_1_lt, not_1_out, not_2_out,
       not_3_out, not_4_out, not_5_out, not_6_out, signo_1_signo, signo_2_signo, xnor_1_out;

  signo signo_1 (.Dato(A), .signo(signo_1_signo));
  not not_1 (not_1_out, signo_1_signo);
  not not_2 (not_2_out, signo_2_signo);
  signo signo_2 (.Dato(B), .signo(signo_2_signo));
  not not_3 (not_3_out, A_2[3]);
  Comp__4_bits__1bitx4 comp_4_bits_1bitx4_1 (
    .A1(A_2[1]), .A0(A_2[0]), .A_B(1'b0), .A_B_2(1'b1), .A_B_3(1'b0), .B1(B_2[1]), .B0(B_2[0]),
    .A_B_4(A_B_4), .A_B_5(A_B_5), .A_B_6(A_B_6), .A3(not_3_out), .A2(A_2[2]), .B3(not_4_out), .B2(B_2[2]));
  not not_4 (not_4_out, B_2[3]);
  and and_1 (and_1_out, not_1_out, not_5_out);
  not not_5 (not_5_out, not_2_out);
  xnor xnor_1 (xnor_1_out, not_1_out, not_2_out);
  not not_6 (not_6_out, not_1_out);
  and and_2 (and_2_out, not_6_out, not_2_out);
  Comparator #(.width(4), .mode("unsigned")) comparator_1 (
    .a(A), .b(B), .gt(comparator_1_gt), .eq(A_B_2), .lt(comparator_1_lt));
  and and_3 (and_3_out, xnor_1_out, comparator_1_gt);
  and and_4 (and_4_out, xnor_1_out, comparator_1_lt);
  or or_1 (A_B, and_1_out, and_3_out);
  or or_2 (A_B_3, and_2_out, and_4_out);

  // Notes on the sheet:
  //   COMP
  //   4 bits
  //   A>0 y B<0
  //   A<0 y B>0
endmodule

module signo (
  input  [3:0] Dato,
  output signo
);


  assign signo = Dato[3];
endmodule

module Comp__4_bits__C2_alt (
  input  A3,
  input  A2,
  input  A1,
  input  A0,
  input  B3,
  input  B2,
  input  B1,
  input  B0,
  output A_B,
  output A_B_2,
  output A_B_3
);

  wire comp_1_bit_completo_1_f1__a_b, comp_1_bit_completo_1_f2__a_b, comp_1_bit_completo_1_f3__a_b,
       comp_1_bit_completo_2_f1__a_b, comp_1_bit_completo_2_f2__a_b, comp_1_bit_completo_2_f3__a_b,
       comp_1_bit_completo_3_f1__a_b, comp_1_bit_completo_3_f2__a_b, comp_1_bit_completo_3_f3__a_b,
       not_1_out, not_2_out;

  not not_1 (not_1_out, A3);
  not not_2 (not_2_out, B3);
  Comp__1_bit_completo comp_1_bit_completo_1 (
    .A1(A0), .B1(B0), .A0_B0(1'b0), .A0_B0_2(1'b1), .A0_B0_3(1'b0), .f1__A_B(comp_1_bit_completo_1_f1__a_b),
    .f2__A_B(comp_1_bit_completo_1_f2__a_b), .f3__A_B(comp_1_bit_completo_1_f3__a_b));
  Comp__1_bit_completo comp_1_bit_completo_2 (
    .A1(A1), .B1(B1), .A0_B0(comp_1_bit_completo_1_f1__a_b), .A0_B0_2(comp_1_bit_completo_1_f2__a_b),
    .A0_B0_3(comp_1_bit_completo_1_f3__a_b), .f1__A_B(comp_1_bit_completo_2_f1__a_b),
    .f2__A_B(comp_1_bit_completo_2_f2__a_b), .f3__A_B(comp_1_bit_completo_2_f3__a_b));
  Comp__1_bit_completo comp_1_bit_completo_3 (
    .A1(A2), .B1(B2), .A0_B0(comp_1_bit_completo_2_f1__a_b), .A0_B0_2(comp_1_bit_completo_2_f2__a_b),
    .A0_B0_3(comp_1_bit_completo_2_f3__a_b), .f1__A_B(comp_1_bit_completo_3_f1__a_b),
    .f2__A_B(comp_1_bit_completo_3_f2__a_b), .f3__A_B(comp_1_bit_completo_3_f3__a_b));
  Comp__1_bit_completo comp_1_bit_completo_4 (
    .A1(not_1_out), .B1(not_2_out), .A0_B0(comp_1_bit_completo_3_f1__a_b),
    .A0_B0_2(comp_1_bit_completo_3_f2__a_b), .A0_B0_3(comp_1_bit_completo_3_f3__a_b), .f1__A_B(A_B),
    .f2__A_B(A_B_2), .f3__A_B(A_B_3));
endmodule

module Comp__8_bits__C2 (
  input  [3:0] A3A2A1A0,
  input  [3:0] A7A6A5A4,
  input  [3:0] B3B2B1B0,
  input  [3:0] B7B6B5B4,
  input  [7:0] A7A6A5A4A3A2A1A0,
  input  [7:0] B7B6B5B4B3B2B1B0,
  output A_B,
  output A_B_2,
  output A_B_3,
  output A_B_4,
  output A_B_5,
  output A_B_6
);

  wire comp_4_bits_1bitx4_1_a_b_4, comp_4_bits_1bitx4_1_a_b_5, comp_4_bits_1bitx4_1_a_b_6, not_1_out,
       not_2_out;

  Comp__4_bits__1bitx4 comp_4_bits_1bitx4_1 (
    .A1(A3A2A1A0[1]), .A0(A3A2A1A0[0]), .A_B(1'b0), .A_B_2(1'b1), .A_B_3(1'b0), .B1(B3B2B1B0[1]),
    .B0(B3B2B1B0[0]), .A_B_4(comp_4_bits_1bitx4_1_a_b_4), .A_B_5(comp_4_bits_1bitx4_1_a_b_5),
    .A_B_6(comp_4_bits_1bitx4_1_a_b_6), .A3(A3A2A1A0[3]), .A2(A3A2A1A0[2]), .B3(B3B2B1B0[3]), .B2(B3B2B1B0[2]));
  not not_1 (not_1_out, A7A6A5A4[3]);
  not not_2 (not_2_out, B7B6B5B4[3]);
  Comparator comparator_1 (.a(A7A6A5A4A3A2A1A0), .b(B7B6B5B4B3B2B1B0), .gt(A_B_4), .eq(A_B_5), .lt(A_B_6));
  Comp__4_bits__1bitx4 comp_4_bits_1bitx4_2 (
    .A1(A7A6A5A4[1]), .A0(A7A6A5A4[0]), .A_B(comp_4_bits_1bitx4_1_a_b_4), .A_B_2(comp_4_bits_1bitx4_1_a_b_5),
    .A_B_3(comp_4_bits_1bitx4_1_a_b_6), .B1(B7B6B5B4[1]), .B0(B7B6B5B4[0]), .A_B_4(A_B), .A_B_5(A_B_2),
    .A_B_6(A_B_3), .A3(not_1_out), .A2(A7A6A5A4[2]), .B3(not_2_out), .B2(B7B6B5B4[2]));

  // Notes on the sheet:
  //   LSB
  //   MSB
endmodule

module Gen__Paridad_7_bits__1 (
  input  D7,
  input  D6,
  input  D5,
  input  D4,
  input  D3,
  input  D2,
  input  D1,
  input  D0,
  output P__par,
  output P__impar
);

  wire xor_1_out, xor_2_out, xor_3_out, xor_4_out, xor_5_out, xor_6_out;

  xor xor_1 (xor_1_out, D7, D6);
  xor xor_2 (xor_2_out, D5, D4);
  xor xor_3 (xor_3_out, D3, D2);
  xor xor_4 (xor_4_out, D1, D0);
  xor xor_5 (xor_5_out, xor_1_out, xor_2_out);
  xor xor_6 (xor_6_out, xor_3_out, xor_4_out);
  xor xor_7 (P__par, xor_5_out, xor_6_out);
  not not_1 (P__impar, P__par);
endmodule

// 74HC180
module Gen__Paridad_74180 (
  input  D7,
  input  D6,
  input  D5,
  input  D4,
  input  D3,
  input  D2,
  input  D1,
  input  D0,
  input  Tp,
  input  Ti,
  output check,
  output set
);

  wire and_1_out, and_2_out, and_3_out, and_4_out, xor_1_out, xor_2_out, xor_3_out, xor_4_out, xor_5_out,
       xor_6_out, xor_7_out;

  xor xor_1 (xor_1_out, D7, D6);
  xor xor_2 (xor_2_out, D5, D4);
  xor xor_3 (xor_3_out, D3, D2);
  xor xor_4 (xor_4_out, D1, D0);
  xor xor_5 (xor_5_out, xor_1_out, xor_2_out);
  xor xor_6 (xor_6_out, xor_3_out, xor_4_out);
  xor xor_7 (xor_7_out, xor_5_out, xor_6_out);
  and and_1 (and_1_out, xor_7_out, Tp);
  and and_2 (and_2_out, ~xor_7_out, Ti);  // AND_Gate
  and and_3 (and_3_out, xor_7_out, Ti);
  and and_4 (and_4_out, ~xor_7_out, Tp);  // AND_Gate
  and and_5 (check, ~and_1_out, ~and_2_out);  // AND_Gate
  and and_6 (set, ~and_3_out, ~and_4_out);  // AND_Gate
endmodule

module Gen__par_16_bits__w_74180 (
  input  [7:0] D15_D8,
  input  [7:0] D0_D7,
  input  Tp,
  output check,
  output set
);

  wire gen_paridad_74180_1_check, gen_paridad_74180_1_set, not_1_out;

  Gen__Paridad_74180 gen_paridad_74180_1 (
    .D7(D0_D7[7]), .D6(D0_D7[6]), .D5(D0_D7[5]), .D4(D0_D7[4]), .D3(D0_D7[3]), .D2(D0_D7[2]), .D1(D0_D7[1]),
    .D0(D0_D7[0]), .Tp(Tp), .Ti(not_1_out), .check(gen_paridad_74180_1_check), .set(gen_paridad_74180_1_set));
  not not_1 (not_1_out, Tp);
  Gen__Paridad_74180 gen_paridad_74180_2 (
    .D7(D15_D8[7]), .D6(D15_D8[6]), .D5(D15_D8[5]), .D4(D15_D8[4]), .D3(D15_D8[3]), .D2(D15_D8[2]),
    .D1(D15_D8[1]), .D0(D15_D8[0]), .Tp(gen_paridad_74180_1_check), .Ti(gen_paridad_74180_1_set),
    .check(check), .set(set));
endmodule
