// Logisim project Cap6_2_ModAritm.circ as structural Verilog: 24 circuits, main circuit Sumador paralelo 4bits (acarreo serie)
module Half_adder (
  input  A,
  input  B,
  output Suma,
  output Cout
);

  xor xor_1 (Suma, A, B);
  and and_1 (Cout, A, B);

  // Notes on the sheet:
  //   A XOR B
endmodule

// FA
module Full_Adder__puertas (
  input  A,
  input  B,
  input  Cin,
  output Suma,
  output Cout
);

  wire A_B_out, and_1_out, xor_1_out;

  xor xor_1 (xor_1_out, A, B);
  xor xor_2 (Suma, xor_1_out, Cin);
  and and_1 (and_1_out, xor_1_out, Cin);
  and A_B (A_B_out, A, B);
  or or_1 (Cout, and_1_out, A_B_out);

  // Notes on the sheet:
  //   A XOR B
  //   (A XOR B) XOR Cin
  //   (A XOR B)Cin
endmodule

module Full_adder__con_semisumadores (
  input  A,
  input  B,
  input  Cin,
  input  A_2,
  input  B_2,
  input  Cin_2,
  output Suma,
  output Cout,
  output Suma_2,
  output Cout_2
);

  wire AB_out, and_1_out, half_adder_1_cout, half_adder_1_suma, half_adder_2_cout, xor_1_out;

  Half_adder half_adder_1 (.A(A), .B(B), .Suma(half_adder_1_suma), .Cout(half_adder_1_cout));
  xor xor_1 (xor_1_out, A_2, B_2);
  and AB (AB_out, A_2, B_2);
  Half_adder half_adder_2 (.A(half_adder_1_suma), .B(Cin), .Suma(Suma), .Cout(half_adder_2_cout));
  or or_1 (Cout, half_adder_2_cout, half_adder_1_cout);
  xor xor_2 (Suma_2, xor_1_out, Cin_2);
  and and_1 (and_1_out, xor_1_out, Cin_2);
  or or_2 (Cout_2, and_1_out, AB_out);

  // Notes on the sheet:
  //   A XOR B
  //   A XOR B
  //   (A XOR B) Cin
  //   AB
  //   (A XOR B) XOR Cin
  //   (A XOR B) Cin
  //   (A XOR B) XOR Cin
  //   AB + (A XOR B) Cin
endmodule

module FA_3bits (
  input  A0,
  input  A1,
  input  A2,
  input  B0,
  input  B1,
  input  B2,
  input  Cin,
  output S0,
  output S1,
  output S2,
  output Cout
);

  wire and_1_out, and_2_out, and_3_out, and_4_out, and_5_out, and_6_out, or_1_out, or_2_out, xor_1_out,
       xor_3_out, xor_5_out;

  xor xor_1 (xor_1_out, A0, B0);
  xor xor_2 (S0, xor_1_out, Cin);
  and and_1 (and_1_out, xor_1_out, Cin);
  and and_2 (and_2_out, A0, B0);
  or or_1 (or_1_out, and_1_out, and_2_out);
  xor xor_3 (xor_3_out, A1, B1);
  xor xor_4 (S1, xor_3_out, or_1_out);
  and and_3 (and_3_out, xor_3_out, or_1_out);
  and and_4 (and_4_out, A1, B1);
  or or_2 (or_2_out, and_3_out, and_4_out);
  xor xor_5 (xor_5_out, A2, B2);
  xor xor_6 (S2, xor_5_out, or_2_out);
  and and_5 (and_5_out, xor_5_out, or_2_out);
  or or_3 (Cout, and_5_out, and_6_out);
  and and_6 (and_6_out, A2, B2);
endmodule

module FA_4bits_ripple_carry (
  input  A3,
  input  B3,
  input  A2,
  input  B2,
  input  A1,
  input  B1,
  input  A0,
  input  B0,
  input  Cin,
  output Cout,
  output S3,
  output S2,
  output S1,
  output S0
);

  wire full_adder_puertas_2_cout, full_adder_puertas_3_cout, full_adder_puertas_4_cout;

  Full_Adder__puertas full_adder_puertas_1 (.A(B3), .B(A3), .Cin(full_adder_puertas_2_cout), .Suma(S3), .Cout(Cout));
  Full_Adder__puertas full_adder_puertas_2 (
    .A(B2), .B(A2), .Cin(full_adder_puertas_3_cout), .Suma(S2), .Cout(full_adder_puertas_2_cout));
  Full_Adder__puertas full_adder_puertas_3 (
    .A(B1), .B(A1), .Cin(full_adder_puertas_4_cout), .Suma(S1), .Cout(full_adder_puertas_3_cout));
  Full_Adder__puertas full_adder_puertas_4 (.A(B0), .B(A0), .Cin(Cin), .Suma(S0), .Cout(full_adder_puertas_4_cout));
endmodule

// FA 4b
module Sumador_paralelo_4bits__acarreo_serie (
  input  [3:0] A,
  input  [3:0] B,
  input  Cin,
  output [3:0] S,
  output Overflow,
  output Cout
);

  wire full_adder_puertas_2_cout, full_adder_puertas_3_cout, full_adder_puertas_4_cout;

  // Probe on A
  xor xor_1 (Overflow, full_adder_puertas_2_cout, Cout);
  Full_Adder__puertas full_adder_puertas_1 (
    .A(B[3]), .B(A[3]), .Cin(full_adder_puertas_2_cout), .Suma(S[3]), .Cout(Cout));
  // Probe on B
  Full_Adder__puertas full_adder_puertas_2 (
    .A(B[2]), .B(A[2]), .Cin(full_adder_puertas_3_cout), .Suma(S[2]), .Cout(full_adder_puertas_2_cout));
  Full_Adder__puertas full_adder_puertas_3 (
    .A(B[1]), .B(A[1]), .Cin(full_adder_puertas_4_cout), .Suma(S[1]), .Cout(full_adder_puertas_3_cout));
  // Probe on S
  Full_Adder__puertas full_adder_puertas_4 (
    .A(B[0]), .B(A[0]), .Cin(Cin), .Suma(S[0]), .Cout(full_adder_puertas_4_cout));

  // Notes on the sheet:
  //   B3
  //   C3
  //   A3
  //   C4
  //   C2
  //   B2
  //   A2
  //   B1
  //   A1
  //   C1
  //   B0
  //   A0
  //   C0
endmodule

module FA_4bits_look_ahead_carry__1 (
  input  A3,
  input  B3,
  input  A2,
  input  B2,
  input  A1,
  input  B1,
  input  A0,
  input  B0,
  input  Cin,
  output Cout,
  output S3,
  output S2,
  output S1,
  output S0
);

  wire and_1_out, and_2_out, and_3_out, and_4_out, and_5_out, and_6_out, C1_out, C2_out, C3_out, G0_2_out,
       G0_out, G1_out, G2_out, G3_out, P0_out, P1_out, P2_out, P3_out;

  and G3 (G3_out, A3, B3);
  and and_1 (and_1_out, P3_out, G2_out);
  or or_1 (Cout, G3_out, and_1_out, and_3_out, and_2_out);
  xor P3 (P3_out, A3, B3);
  and and_2 (and_2_out, P3_out, P2_out, P1_out, C1_out);
  and and_3 (and_3_out, P3_out, P2_out, G1_out);
  and G2 (G2_out, A2, B2);
  and and_4 (and_4_out, P2_out, P1_out, C1_out);
  or C3 (C3_out, G2_out, and_4_out, and_5_out);
  xor xor_1 (S3, P3_out, C3_out);
  xor P2 (P2_out, A2, B2);
  and and_5 (and_5_out, P2_out, G1_out);
  and G1 (G1_out, A1, B1);
  xor P1 (P1_out, A1, B1);
  and and_6 (and_6_out, P1_out, C1_out);
  or C2 (C2_out, G1_out, and_6_out);
  xor xor_2 (S2, P2_out, C2_out);
  xor P0 (P0_out, A0, B0);
  and G0 (G0_out, A0, B0);
  or C1 (C1_out, G0_out, G0_2_out);
  xor xor_3 (S1, P1_out, C1_out);
  and G0_2 (G0_2_out, P0_out, Cin);
  xor xor_4 (S0, P0_out, Cin);
endmodule

module FA_4bits_look_ahead_carry__2 (
  input  Cin,
  input  A0,
  input  B0,
  input  A1,
  input  B1,
  input  A2,
  input  B2,
  input  A3,
  input  B3,
  output S0,
  output S1,
  output S2,
  output S2_2,
  output Cout
);

  wire and_1_out, and_2_out, and_3_out, and_4_out, and_5_out, and_6_out, and_7_out, and_8_out, and_9_out,
       and_10_out, C1_out, C2_out, C3_out, G0_out, G1_out, G2_out, G3_out, P0_out, P1_out, P2_out, P3_out;

  xor P0 (P0_out, B0, A0);
  and G0 (G0_out, A0, B0);
  xor P1 (P1_out, B1, A1);
  and G1 (G1_out, A1, B1);
  xor P2 (P2_out, B2, A2);
  and G2 (G2_out, A2, B2);
  xor P3 (P3_out, B3, A3);
  and G3 (G3_out, A3, B3);
  xor xor_1 (S0, Cin, P0_out);
  xor xor_2 (S1, C1_out, P1_out);
  xor xor_3 (S2, C2_out, P2_out);
  xor xor_4 (S2_2, C3_out, P3_out);
  or C1 (C1_out, G0_out, and_1_out);
  or C2 (C2_out, G1_out, and_2_out, and_3_out);
  or C3 (C3_out, G2_out, and_4_out, and_5_out, and_6_out);
  or or_1 (Cout, G3_out, and_7_out, and_8_out, and_9_out, and_10_out);
  and and_1 (and_1_out, P0_out, Cin);
  and and_2 (and_2_out, P1_out, G0_out);
  and and_3 (and_3_out, P1_out, P0_out, Cin);
  and and_4 (and_4_out, P2_out, G1_out);
  and and_5 (and_5_out, P2_out, P1_out, G0_out);
  and and_6 (and_6_out, P2_out, P1_out, P0_out, Cin);
  and and_7 (and_7_out, P3_out, G2_out);
  and and_8 (and_8_out, P3_out, P2_out, G1_out);
  and and_9 (and_9_out, P3_out, P2_out, P1_out, G0_out);
  and and_10 (and_10_out, P3_out, P2_out, P1_out, P0_out, Cin);
endmodule

// LAi
module FA___w__Pi_Gi_carries (
  input  Ai,
  input  Bi,
  input  Ci,
  output Pi,
  output Si,
  output Gi
);

  xor xor_1 (Pi, Ai, Bi);
  xor xor_2 (Si, Pi, Ci);
  and and_1 (Gi, Ai, Bi);
endmodule

// 4b LA
module _4bit_carry_LA (
  input  [3:0] A,
  input  [3:0] B,
  input  C0,
  output [3:0] S,
  output C4,
  output PG,
  output GG
);

  wire and_1_out, and_2_out, and_3_out, and_4_out, and_5_out, and_6_out, and_7_out, and_8_out, and_9_out, G0,
       G1, G2, G3, LA0_pi, LA1_pi, LA2_pi, LA3_pi, or_2_out, or_3_out, or_4_out;

  // Probe on A
  or or_1 (C4, G3, and_1_out);
  and and_1 (and_1_out, LA3_pi, or_2_out);
  FA___w__Pi_Gi_carries LA3 (.Ai(A[3]), .Bi(B[3]), .Ci(or_2_out), .Pi(LA3_pi), .Si(S[3]), .Gi(G3));
  or or_2 (or_2_out, G2, and_2_out);
  // Probe on B
  and and_2 (and_2_out, LA2_pi, or_3_out);
  FA___w__Pi_Gi_carries LA2 (.Ai(A[2]), .Bi(B[2]), .Ci(or_3_out), .Pi(LA2_pi), .Si(S[2]), .Gi(G2));
  or or_3 (or_3_out, G1, and_5_out);
  and and_3 (and_3_out, LA2_pi, LA3_pi);
  and and_4 (and_4_out, LA3_pi, G2);
  FA___w__Pi_Gi_carries LA1 (.Ai(A[1]), .Bi(B[1]), .Ci(or_4_out), .Pi(LA1_pi), .Si(S[1]), .Gi(G1));
  and and_5 (and_5_out, LA1_pi, or_4_out);
  and and_6 (and_6_out, and_3_out, G1);
  // Probe on S
  or or_4 (or_4_out, G0, and_7_out);
  and and_7 (and_7_out, LA0_pi, C0);
  and and_8 (and_8_out, LA1_pi, and_3_out);
  and and_9 (and_9_out, and_8_out, G0);
  FA___w__Pi_Gi_carries LA0 (.Ai(A[0]), .Bi(B[0]), .Ci(C0), .Pi(LA0_pi), .Si(S[0]), .Gi(G0));
  and and_10 (PG, LA0_pi, and_8_out);
  or or_5 (GG, and_9_out, and_6_out, and_4_out, G3);
endmodule

module test_sumador (
  input  [7:0] in_1,
  input  [7:0] in_2,
  input  in_3,
  output [7:0] out_4
);

  wire and_1_out, n4bit_carry_la_2_gg, n4bit_carry_la_2_pg, or_1_out;

  // Probe on in_1
  _4bit_carry_LA u_4bit_carry_la_1 (.C0(or_1_out), .A(in_1[7:4]), .B(in_2[7:4]), .S(out_4[7:4]));  // open: C4, PG, GG
  or or_1 (or_1_out, n4bit_carry_la_2_gg, and_1_out);
  and and_1 (and_1_out, n4bit_carry_la_2_pg, in_3);
  _4bit_carry_LA u_4bit_carry_la_2 (
    .C0(in_3), .PG(n4bit_carry_la_2_pg), .GG(n4bit_carry_la_2_gg), .A(in_1[3:0]), .B(in_2[3:0]),
    .S(out_4[3:0]));  // open: C4
  // Probe on in_2
  // Probe on out_4

  // Other names for the same wires on the sheet: A0[3:0] = in_1[3:0]; A1[3:0] = in_1[7:4]; B0[3:0] = in_2[3:0];
  //   B1[3:0] = in_2[7:4]; S0[3:0] = out_4[3:0]; S1[3:0] = out_4[7:4]
endmodule

module Sumador_serie (
  input  [3:0] A,
  input  [3:0] B,
  input  LD_prime_ADD,
  input  CLR
);

  wire and_1_out, CLK_out, counter_1_carry, d_ff_1_q, full_adder_puertas_1_cout, full_adder_puertas_1_suma,
       not_1_out, shift_register_1_out, shift_register_2_out;
  wire [3:0] shift_register_1_q3, shift_register_2_q3;

  // Probe on A
  // Probe on B
  Clock CLK (.out(CLK_out));
  not not_1 (not_1_out, LD_prime_ADD);
  Counter #(.width(3), .max('h4), .ongoal("stay")) counter_1 (
    .count(LD_prime_ADD), .carry(counter_1_carry), .clk(CLK_out), .clr(CLR));  // open: load, D, Q
  and and_1 (and_1_out, LD_prime_ADD, ~counter_1_carry);  // AND_Gate
  Shift_Register #(.length(4)) shift_register_1 (
    .shift(and_1_out), .in(full_adder_puertas_1_suma), .clk(CLK_out), .out(shift_register_1_out),
    .load(not_1_out), .clr(CLR), .d0(A[3]), .q0(shift_register_1_q3[3]), .d1(A[2]),
    .q1(shift_register_1_q3[2]), .d2(A[1]), .q2(shift_register_1_q3[1]), .d3(A[0]),
    .q3(shift_register_1_q3[0]));
  Shift_Register #(.length(4)) shift_register_2 (
    .shift(and_1_out), .in(1'b0), .clk(CLK_out), .out(shift_register_2_out), .load(not_1_out), .clr(CLR),
    .d0(B[3]), .q0(shift_register_2_q3[3]), .d1(B[2]), .q1(shift_register_2_q3[2]), .d2(B[1]),
    .q2(shift_register_2_q3[1]), .d3(B[0]), .q3(shift_register_2_q3[0]));
  // Probe on shift_register_1_q3
  // Probe on shift_register_2_q3
  Full_Adder__puertas full_adder_puertas_1 (
    .A(shift_register_1_out), .B(shift_register_2_out), .Cin(d_ff_1_q), .Suma(full_adder_puertas_1_suma),
    .Cout(full_adder_puertas_1_cout));
  D_Flip_Flop d_ff_1 (
    .clk(CLK_out), .D(full_adder_puertas_1_cout), .Q(d_ff_1_q), .en(and_1_out), .reset(CLR));  // open: Qn, preset

  // Notes on the sheet:
  //   Control de habilitación
  //   Registro A
  //   Registro B
  //   Suma bit a bit
  //   Propag. acarreo
endmodule

module Sumador_Restador_4_bits__completo (
  input  A3,
  input  A2,
  input  A1,
  input  A0,
  input  B3,
  input  B2,
  input  B1,
  input  B0,
  input  Suma_prime_Resta,
  output Overflow,
  output S4,
  output S3,
  output S2,
  output S1,
  output S0
);

  wire [3:0] xor_4_out;

  xor xor_1 (xor_4_out[3], B3, Suma_prime_Resta);
  xor xor_2 (xor_4_out[2], B2, Suma_prime_Resta);
  xor xor_3 (xor_4_out[1], B1, Suma_prime_Resta);
  Sumador_paralelo_4bits__acarreo_serie sumador_paralelo_4bits_acarreo_serie_1 (
    .Cin(Suma_prime_Resta), .Cout(S4), .Overflow(Overflow), .A({A3, A2, A1, A0}), .B(xor_4_out),
    .S({S3, S2, S1, S0}));
  xor xor_4 (xor_4_out[0], B0, Suma_prime_Resta);

  // Notes on the sheet:
  //   C0 (acarreo de entrada)
  //   +/-
endmodule

module Sum_Rest_4_bits__con_sondas (
  input  A3,
  input  A2,
  input  A1,
  input  A0,
  input  B3,
  input  B2,
  input  B1,
  input  B0,
  input  Suma_prime_Resta,
  output Overflow,
  output S4,
  output S3,
  output S2,
  output S1,
  output S0
);

  wire [3:0] xor_4_out;

  xor xor_1 (xor_4_out[3], B3, Suma_prime_Resta);
  xor xor_2 (xor_4_out[2], B2, Suma_prime_Resta);
  xor xor_3 (xor_4_out[1], B1, Suma_prime_Resta);
  Sumador_paralelo_4bits__acarreo_serie sumador_paralelo_4bits_acarreo_serie_1 (
    .Cin(Suma_prime_Resta), .Cout(S4), .Overflow(Overflow), .A({A3, A2, A1, A0}), .B(xor_4_out),
    .S({S3, S2, S1, S0}));
  // Probe on {S3, S2, S1, S0}
  xor xor_4 (xor_4_out[0], B0, Suma_prime_Resta);

  // Notes on the sheet:
  //   C0 (acarreo de entrada)
  //   +/-
endmodule

module Sum_Rest_4_bits__con_display (
  input  A3,
  input  A2,
  input  A1,
  input  A0,
  input  B3,
  input  B2,
  input  B1,
  input  B0,
  input  Suma_prime_Resta,
  output Overflow,
  output S4,
  output S3,
  output S2,
  output S1,
  output S0
);

  wire [3:0] c2_disp_1_mo, c2_disp_2_mo, c2_disp_3_mo, xor_3_out;

  Hex_Digit_Display hex_digit_display_1 (.value(c2_disp_1_mo), .dp(A3));
  C2_disp c2_disp_1 (.Mi({A2, A1, A0}), .Sig(A3), .Mo(c2_disp_1_mo));
  // Probe on {A3, A2, A1, A0}
  xor xor_1 (xor_3_out[2], B2, Suma_prime_Resta);
  xor xor_2 (xor_3_out[3], B3, Suma_prime_Resta);
  // Probe on xor_3_out
  Sumador_paralelo_4bits__acarreo_serie sumador_paralelo_4bits_acarreo_serie_1 (
    .Cin(Suma_prime_Resta), .Cout(S4), .Overflow(Overflow), .A({A3, A2, A1, A0}), .B(xor_3_out),
    .S({S3, S2, S1, S0}));
  // Probe on {S3, S2, S1, S0}
  xor xor_3 (xor_3_out[0], B0, Suma_prime_Resta);
  xor xor_4 (xor_3_out[1], B1, Suma_prime_Resta);
  Hex_Digit_Display hex_digit_display_2 (.value(c2_disp_2_mo), .dp(B3));
  C2_disp c2_disp_2 (.Mi({B2, B1, B0}), .Sig(B3), .Mo(c2_disp_2_mo));
  C2_disp c2_disp_3 (.Mi({S2, S1, S0}), .Sig(S3), .Mo(c2_disp_3_mo));
  Hex_Digit_Display hex_digit_display_3 (.value(c2_disp_3_mo), .dp(S3));

  // Notes on the sheet:
  //   C0 (acarreo de entrada)
  //   +/-
  //   =
endmodule

// C2d
module C2_disp (
  input  [2:0] Mi,
  input  Sig,
  output [3:0] Mo
);

  wire [2:0] adder_1_out, bit_extender_1_out, xor_1_out;

  assign xor_1_out = Mi ^ bit_extender_1_out;  // XOR_Gate xor_1, 3 bits wide
  assign bit_extender_1_out = {{2{Sig}}, Sig};  // Bit_Extender bit_extender_1
  Adder #(.width(3)) adder_1 (.a(xor_1_out), .b(3'b000), .out(adder_1_out), .cin(Sig));  // open: cout
  assign Mo = {{1{1'b0}}, adder_1_out};  // Bit_Extender bit_extender_2
endmodule

module Sumador_BCD (
  input  [3:0] A,
  input  [3:0] B,
  input  C0,
  output C1,
  output [3:0] Suma
);

  wire sumador_paralelo_4bits_acarreo_serie_1_cout;
  wire [3:0] sumador_paralelo_4bits_acarreo_serie_1_s;

  Hex_Digit_Display hex_digit_display_1 (.value(A));  // open: dp
  Hex_Digit_Display hex_digit_display_2 (.value(B));  // open: dp
  Hex_Digit_Display hex_digit_display_3 (.value({3'b000, C1}));  // open: dp
  Hex_Digit_Display hex_digit_display_4 (.value(Suma));  // open: dp
  \Corrección_BCD  \corrección_bcd_1  (
    .C1(sumador_paralelo_4bits_acarreo_serie_1_cout), .P3(sumador_paralelo_4bits_acarreo_serie_1_s[3]),
    .P2(sumador_paralelo_4bits_acarreo_serie_1_s[2]), .P1(sumador_paralelo_4bits_acarreo_serie_1_s[1]),
    .P0(sumador_paralelo_4bits_acarreo_serie_1_s[0]), .Corregir(C1));
  Sumador_paralelo_4bits__acarreo_serie sumador_paralelo_4bits_acarreo_serie_1 (
    .Cin(C0), .Cout(sumador_paralelo_4bits_acarreo_serie_1_cout), .A(A), .B(B),
    .S(sumador_paralelo_4bits_acarreo_serie_1_s));  // open: Overflow
  Sumador_paralelo_4bits__acarreo_serie sumador_paralelo_4bits_acarreo_serie_2 (
    .Cin(1'b0), .A(sumador_paralelo_4bits_acarreo_serie_1_s), .B({1'b0, {2{C1}}, 1'b0}), .S(Suma));  // open: Cout, Overflow

  // Notes on the sheet:
  //   =
  //   +
endmodule

// Suma>9
module \Corrección_BCD  (
  input  C1,
  input  P3,
  input  P2,
  input  P1,
  input  P0,
  output Corregir
);

  wire and_1_out, and_2_out, or_1_out;

  and and_1 (and_1_out, P3, P1);
  and and_2 (and_2_out, P3, P2);
  or or_1 (or_1_out, and_1_out, and_2_out);
  or or_2 (Corregir, or_1_out, C1);
endmodule

module Multiplicador_3x3 (
  input  A0,
  input  B0,
  input  A1,
  input  B1,
  input  A2,
  input  B2,
  output R5,
  output R4,
  output R3,
  output R2,
  output R1,
  output R0
);

  wire and_1_out, and_2_out, and_3_out, and_4_out, and_5_out, and_6_out, and_7_out, and_9_out,
       full_adder_puertas_2_cout, full_adder_puertas_2_suma, full_adder_puertas_3_cout,
       full_adder_puertas_4_cout, full_adder_puertas_4_suma, full_adder_puertas_5_cout,
       full_adder_puertas_6_cout;

  and and_1 (and_1_out, A2, B2);
  Full_Adder__puertas full_adder_puertas_1 (
    .A(and_1_out), .B(full_adder_puertas_2_cout), .Cin(full_adder_puertas_3_cout), .Suma(R4), .Cout(R5));
  and and_2 (and_2_out, A1, B2);
  Full_Adder__puertas full_adder_puertas_2 (
    .A(and_2_out), .B(1'b0), .Cin(full_adder_puertas_4_cout), .Suma(full_adder_puertas_2_suma),
    .Cout(full_adder_puertas_2_cout));
  and and_3 (and_3_out, A2, B1);
  Full_Adder__puertas full_adder_puertas_3 (
    .A(and_3_out), .B(full_adder_puertas_2_suma), .Cin(full_adder_puertas_5_cout), .Suma(R3),
    .Cout(full_adder_puertas_3_cout));
  and and_4 (and_4_out, A0, B2);
  and and_5 (and_5_out, A1, B1);
  Full_Adder__puertas full_adder_puertas_4 (
    .A(and_5_out), .B(and_4_out), .Cin(full_adder_puertas_6_cout), .Suma(full_adder_puertas_4_suma),
    .Cout(full_adder_puertas_4_cout));
  and and_6 (and_6_out, A2, B0);
  Full_Adder__puertas full_adder_puertas_5 (
    .A(and_6_out), .B(full_adder_puertas_4_suma), .Cin(1'b0), .Suma(R2), .Cout(full_adder_puertas_5_cout));
  and and_7 (and_7_out, A0, B1);
  and and_8 (R0, A0, B0);
  and and_9 (and_9_out, A1, B0);
  Full_Adder__puertas full_adder_puertas_6 (
    .A(and_9_out), .B(and_7_out), .Cin(1'b0), .Suma(R1), .Cout(full_adder_puertas_6_cout));
  // Probe on {1'b0, A2, A1, A0}
  // Probe on {1'b0, B2, B1, B0}
  // Probe on {R5, R4, R3, R2, R1, R0}

  // Notes on the sheet:
  //   X
endmodule

module Suma_1s (
  input  [6:0] E6_E0,
  input  [6:0] E6_E0_2,
  input  [6:0] E6_E0_3,
  input  [7:0] E7_E0,
  input  [6:0] E6_E0_4
);

  wire adder_4_cout, adder_4_out, adder_5_cout, adder_5_out, adder_8_cout, full_adder_puertas_1_cout,
       full_adder_puertas_1_suma, full_adder_puertas_2_cout, full_adder_puertas_2_suma,
       full_adder_puertas_3_cout;
  wire [1:0] adder_1_out, adder_2_out, adder_3_out, adder_6_out, adder_7_out, adder_10_out;
  wire [2:0] adder_8_out, adder_11_out, bitadder_1_out, full_adder_puertas_3_suma;
  wire [2:2] adder_3_cout, adder_10_cout;
  wire [3:3] adder_11_cout;

  Full_Adder__puertas full_adder_puertas_1 (
    .A(E6_E0[2]), .B(E6_E0[3]), .Cin(E6_E0[1]), .Suma(full_adder_puertas_1_suma),
    .Cout(full_adder_puertas_1_cout));
  Full_Adder__puertas full_adder_puertas_2 (
    .A(E6_E0[5]), .B(E6_E0[6]), .Cin(E6_E0[4]), .Suma(full_adder_puertas_2_suma),
    .Cout(full_adder_puertas_2_cout));
  Adder #(.width(1)) adder_1 (
    .a(E6_E0_3[2]), .b(E6_E0_3[3]), .out(adder_1_out[0]), .cin(E6_E0_3[1]), .cout(adder_1_out[1]));
  Adder #(.width(1)) adder_2 (
    .a(E6_E0_3[5]), .b(E6_E0_3[6]), .out(adder_2_out[0]), .cin(E6_E0_3[4]), .cout(adder_2_out[1]));
  Full_Adder__puertas full_adder_puertas_3 (
    .A(full_adder_puertas_1_suma), .B(full_adder_puertas_2_suma), .Cin(E6_E0[0]),
    .Suma(full_adder_puertas_3_suma[0]), .Cout(full_adder_puertas_3_cout));
  Full_Adder__puertas full_adder_puertas_4 (
    .A(full_adder_puertas_1_cout), .B(full_adder_puertas_2_cout), .Cin(full_adder_puertas_3_cout),
    .Suma(full_adder_puertas_3_suma[1]), .Cout(full_adder_puertas_3_suma[2]));
  Adder #(.width(2)) adder_3 (
    .a(adder_1_out), .b(adder_2_out), .out(adder_3_out), .cin(E6_E0_3[0]), .cout(adder_3_cout[2]));
  BitAdder #(.width(7)) bitadder_1 (.in0(E6_E0_4), .out(bitadder_1_out));
  // Probe on bitadder_1_out
  // Probe on {1'b0, full_adder_puertas_3_suma}
  // Probe on {1'b0, adder_3_cout[2], adder_3_out}
  Adder #(.width(1)) adder_4 (.a(E6_E0_2[2]), .b(E6_E0_2[3]), .out(adder_4_out), .cin(E6_E0_2[1]), .cout(adder_4_cout));
  Adder #(.width(1)) adder_5 (.a(E6_E0_2[5]), .b(E6_E0_2[6]), .out(adder_5_out), .cin(E6_E0_2[4]), .cout(adder_5_cout));
  Adder #(.width(1)) adder_6 (.a(E7_E0[3]), .b(E7_E0[4]), .out(adder_6_out[0]), .cin(E7_E0[2]), .cout(adder_6_out[1]));
  Adder #(.width(1)) adder_7 (.a(E7_E0[6]), .b(E7_E0[7]), .out(adder_7_out[0]), .cin(E7_E0[5]), .cout(adder_7_out[1]));
  Adder #(.width(1)) adder_8 (
    .a(adder_4_out), .b(adder_5_out), .out(adder_8_out[0]), .cin(E6_E0_2[0]), .cout(adder_8_cout));
  Adder #(.width(1)) adder_9 (
    .a(adder_4_cout), .b(adder_5_cout), .out(adder_8_out[1]), .cin(adder_8_cout), .cout(adder_8_out[2]));
  Adder #(.width(2)) adder_10 (
    .a(adder_6_out), .b(adder_7_out), .out(adder_10_out), .cin(E7_E0[1]), .cout(adder_10_cout[2]));
  // Probe on {1'b0, adder_8_out}
  Adder #(.width(3)) adder_11 (
    .a({adder_10_cout[2], adder_10_out}), .b(3'b000), .out(adder_11_out), .cin(E7_E0[0]),
    .cout(adder_11_cout[3]));
  // Probe on {adder_11_cout[3], adder_11_out}

  // Notes on the sheet:
  //   2 bits
  //   2 bits
  //   3 bits
endmodule

module ALU_Elemental (
  input  [3:0] A,
  input  [3:0] B,
  input  S3,
  input  S2,
  input  S1,
  input  S0,
  output [3:0] f,
  output Cout
);

  wire [3:0] \bloque_aritmético_1_f , \bloque_lógico_1_f ;

  \Bloque_Lógico  \bloque_lógico_1  (.A(A), .B(B), .f(\bloque_lógico_1_f ), .S2_S1({S2, S1}));
  \Bloque_Aritmético  \bloque_aritmético_1  (
    .Cout(Cout), .S2_S1({S2, S1}), .S0(S0), .A(A), .B(B), .f(\bloque_aritmético_1_f ));
  Multiplexer #(.width(4), .enable("false")) multiplexer_1 (
    .in0(\bloque_lógico_1_f ), .in1(\bloque_aritmético_1_f ), .out(f), .sel(S3));

  // Notes on the sheet:
  //   (Operandos)
  //   (Acarreo)
  //   (Señales de control)
  //   (Resultado)
endmodule

// B. Lógico
module \Bloque_Lógico  (
  input  [3:0] A,
  input  [3:0] B,
  input  [1:0] S2_S1,
  output [3:0] f
);

  wire [3:0] and_1_out, not_1_out, or_1_out, xor_1_out;

  assign and_1_out = A & B;  // AND_Gate and_1, 4 bits wide
  assign or_1_out = A | B;  // OR_Gate or_1, 4 bits wide
  assign not_1_out = ~A;  // NOT_Gate not_1, 4 bits wide
  Multiplexer #(.select(2), .width(4), .enable("false")) multiplexer_1 (
    .in0(and_1_out), .in1(or_1_out), .in2(not_1_out), .in3(xor_1_out), .out(f), .sel(S2_S1));
  assign xor_1_out = A ^ B;  // XOR_Gate xor_1, 4 bits wide
endmodule

// B. Aritmético
module \Bloque_Aritmético  (
  input  [3:0] A,
  input  [3:0] B,
  input  [1:0] S2_S1,
  input  S0,
  output Cout,
  output [3:0] f
);

  wire [3:0] bloque_b_d_1_d;

  Bloque_B__D bloque_b_d_1 (.S2_S1(S2_S1), .B(B), .D(bloque_b_d_1_d));
  Sumador_paralelo_4bits__acarreo_serie sumador_paralelo_4bits_acarreo_serie_1 (
    .Cin(S0), .Cout(Cout), .A(A), .B(bloque_b_d_1_d), .S(f));  // open: Overflow

  // Notes on the sheet:
  //   D
endmodule

// B->D
module Bloque_B__D (
  input  [3:0] B,
  input  [1:0] S2_S1,
  output [3:0] D
);

  wire [3:0] and_1_out, and_2_out, bit_extender_1_out, bit_extender_2_out, not_1_out, not_2_out;

  assign bit_extender_1_out = {{3{S2_S1[1]}}, S2_S1[1]};  // Bit_Extender bit_extender_1
  assign not_1_out = ~bit_extender_1_out;  // NOT_Gate not_1, 4 bits wide
  assign bit_extender_2_out = {{3{S2_S1[0]}}, S2_S1[0]};  // Bit_Extender bit_extender_2
  assign not_2_out = ~B;  // NOT_Gate not_2, 4 bits wide
  assign and_1_out = bit_extender_2_out & not_2_out;  // AND_Gate and_1, 4 bits wide
  assign and_2_out = B & not_1_out;  // AND_Gate and_2, 4 bits wide
  assign D = and_1_out | and_2_out;  // OR_Gate or_1, 4 bits wide
endmodule
