// Logisim project Cap7_Biestables.circ as structural Verilog
module Alarma (
  input  Enable,
  input  Enable_2,
  input  Enable_3,
  input  Enable_4,
  input  Enable_5,
  input  Enable_6
);

  wire and_1_out, and_2_out, and_3_out, and_4_out, and_5_out, CLK_2_out, CLK_out, d_ff_1_q, Detector_2_out,
       Detector_3_out, Detector_4_out, Detector_5_out, Detector_6_out, Detector_out, gated_latch_2_q,
       gated_latch_3_q, gated_latch_q, j_k_ff_1_q, or_1_out, or_2_out, or_3_out, Reset_2_out, Reset_3_out,
       Reset_4_out, Reset_5_out, Reset_out;

  Button Detector (.out(Detector_out));
  Button Reset (.out(Reset_out));
  or or_1 (or_1_out, gated_latch_2_q, Detector_2_out);
  Button Detector_2 (.out(Detector_2_out));
  Button Reset_2 (.out(Reset_2_out));
  Button Detector_3 (.out(Detector_3_out));
  Button Reset_3 (.out(Reset_3_out));
  Button Detector_4 (.out(Detector_4_out));
  and and_1 (and_1_out, Detector_out, ~Reset_out);  // AND_Gate
  and and_2 (and_2_out, or_1_out, ~Reset_2_out);  // AND_Gate
  and and_3 (and_3_out, Detector_3_out, ~Reset_3_out);  // AND_Gate
  Clock CLK (.out(CLK_out));
  and and_4 (and_4_out, Detector_4_out, Enable);
  LED Alarma (.in(gated_latch_q));
  S_R_Flip_Flop #(.trigger("high")) gated_latch (
    .S(and_1_out), .clk(Enable_3), .R(Reset_out), .Q(gated_latch_q));  // open: Qn, preset, reset, en
  LED Alarma_2 (.in(gated_latch_2_q));
  D_Flip_Flop #(.trigger("high")) gated_latch_2 (
    .clk(Enable_4), .D(and_2_out), .Q(gated_latch_2_q));  // open: Qn, preset, en, reset
  LED Alarma_3 (.in(j_k_ff_1_q));
  J_K_Flip_Flop j_k_ff_1 (
    .J(and_3_out), .clk(CLK_out), .K(Reset_3_out), .Q(j_k_ff_1_q), .en(Enable_5));  // open: Qn, preset, reset
  LED Alarma_4 (.in(and_4_out));
  Button Detector_5 (.out(Detector_5_out));
  Button Detector_6 (.out(Detector_6_out));
  Button Reset_4 (.out(Reset_4_out));
  or or_2 (or_2_out, gated_latch_3_q, Detector_5_out);
  Button Reset_5 (.out(Reset_5_out));
  or or_3 (or_3_out, d_ff_1_q, Detector_6_out);
  and and_5 (and_5_out, or_3_out, ~Reset_4_out);  // AND_Gate
  LED Alarma_5 (.in(gated_latch_3_q));
  D_Flip_Flop #(.trigger("high")) gated_latch_3 (
    .clk(Enable_2), .D(or_2_out), .Q(gated_latch_3_q), .reset(Reset_5_out));  // open: Qn, preset, en
  Clock CLK_2 (.out(CLK_2_out));
  D_Flip_Flop d_ff_1 (.clk(CLK_2_out), .D(and_5_out), .Q(d_ff_1_q), .en(Enable_6));  // open: Qn, preset, reset
  LED Alarma_6 (.in(d_ff_1_q));
endmodule

module Biestable_S_R (
  input  S,
  input  R,
  output out_3
);

  wire and_1_out, and_2_out, CLK_out;

  and and_1 (and_1_out, S, ~R);  // AND_Gate
  Clock CLK (.out(CLK_out));
  and and_2 (and_2_out, ~S, R);  // AND_Gate
  J_K_Flip_Flop j_k_ff_1 (.J(and_1_out), .clk(CLK_out), .K(and_2_out), .Q(out_3));  // open: Qn, preset, en, reset
endmodule

module Reloj_vs__tick (
  output A,
  output B,
  output C,
  output [2:0] N
);

  Clock #(.highDuration(4), .lowDuration(4)) CLK_3 (.out(A));
  Clock #(.highDuration(2), .lowDuration(2)) CLK_2 (.out(B));
  Clock CLK_1 (.out(C));
  // Probe on {A, B, C}

  assign N = {A, B, C};

  // Notes on the sheet:
  //   4+ 4-
  //   2+ 2-
endmodule

module Biestable_J_K__con_otros_biestables (
  input  J,
  input  K,
  input  J_2,
  input  K_2,
  input  J_3,
  input  K_3,
  output out_7,
  output out_8,
  output out_9
);

  wire and_1_out, and_2_out, and_3_out, and_4_out, and_5_out, and_6_out, CLK_2_out, CLK_3_out, CLK_out,
       d_ff_1_qn, or_1_out, or_2_out, s_r_ff_1_qn, t_ff_1_qn;

  Clock CLK (.out(CLK_out));
  and and_1 (and_1_out, d_ff_1_qn, J);
  or or_1 (or_1_out, and_1_out, and_2_out);
  and and_2 (and_2_out, ~K, out_7);  // AND_Gate
  Clock CLK_2 (.out(CLK_2_out));
  and and_3 (and_3_out, s_r_ff_1_qn, J_2);
  and and_4 (and_4_out, K_2, out_8);
  Clock CLK_3 (.out(CLK_3_out));
  and and_5 (and_5_out, t_ff_1_qn, J_3);
  or or_2 (or_2_out, and_5_out, and_6_out);
  and and_6 (and_6_out, K_3, out_9);
  D_Flip_Flop d_ff_1 (.clk(CLK_out), .D(or_1_out), .Q(out_7), .Qn(d_ff_1_qn));  // open: preset, en, reset
  S_R_Flip_Flop s_r_ff_1 (
    .S(and_3_out), .clk(CLK_2_out), .R(and_4_out), .Q(out_8), .Qn(s_r_ff_1_qn));  // open: preset, reset, en
  T_Flip_Flop t_ff_1 (.clk(CLK_3_out), .T(or_2_out), .Q(out_9), .Qn(t_ff_1_qn));  // open: preset, reset, en

  // Notes on the sheet:
  //   Biestable J-K (con D)
  //   Biestable J-K (con SR)
  //   Biestable J-K (con T)
endmodule

module Biestable_D__con_otros_biestables (
  input  D,
  input  D_2,
  input  D_3,
  output out_4,
  output out_5,
  output out_6
);

  wire CLK_2_out, CLK_3_out, CLK_out, not_1_out, not_2_out, xor_1_out;

  not not_1 (not_1_out, D);
  Clock CLK (.out(CLK_out));
  S_R_Flip_Flop s_r_ff_1 (.S(D), .clk(CLK_out), .R(not_1_out), .Q(out_4));  // open: Qn, preset, reset, en
  not not_2 (not_2_out, D_2);
  Clock CLK_2 (.out(CLK_2_out));
  J_K_Flip_Flop j_k_ff_1 (.J(D_2), .clk(CLK_2_out), .K(not_2_out), .Q(out_5));  // open: Qn, preset, en, reset
  xor xor_1 (xor_1_out, out_6, D_3);
  Clock CLK_3 (.out(CLK_3_out));
  T_Flip_Flop t_ff_1 (.clk(CLK_3_out), .T(xor_1_out), .Q(out_6));  // open: Qn, preset, reset, en

  // Notes on the sheet:
  //   Biestable D (con SR)
  //   Biestable D (con JK)
  //   Biestable D (con T)
endmodule

module Biestable_T__con_otros_biestables (
  input  T,
  input  T_2,
  input  T_3,
  input  T_4,
  output out_5,
  output out_6,
  output out_7,
  output out_8
);

  wire and_1_out, and_2_out, and_3_out, and_4_out, CLK_2_out, CLK_3_out, CLK_4_out, CLK_out, d_ff_1_qn,
       not_1_out, or_1_out, s_r_ff_1_qn, xor_1_out;

  Clock CLK (.out(CLK_out));
  J_K_Flip_Flop j_k_ff_1 (.J(T), .clk(CLK_out), .K(T), .Q(out_5));  // open: Qn, preset, en, reset
  and and_1 (and_1_out, out_7, not_1_out);
  not not_1 (not_1_out, T_3);
  and and_2 (and_2_out, T_3, d_ff_1_qn);
  Clock CLK_2 (.out(CLK_2_out));
  or or_1 (or_1_out, and_1_out, and_2_out);
  xor xor_1 (xor_1_out, out_6, T_2);
  Clock CLK_3 (.out(CLK_3_out));
  D_Flip_Flop d_ff_1 (.clk(CLK_2_out), .D(or_1_out), .Q(out_7), .Qn(d_ff_1_qn));  // open: preset, en, reset
  D_Flip_Flop d_ff_2 (.clk(CLK_3_out), .D(xor_1_out), .Q(out_6));  // open: Qn, preset, en, reset
  and and_3 (and_3_out, s_r_ff_1_qn, T_4);
  and and_4 (and_4_out, T_4, out_8);
  Clock CLK_4 (.out(CLK_4_out));
  S_R_Flip_Flop s_r_ff_1 (
    .S(and_3_out), .clk(CLK_4_out), .R(and_4_out), .Q(out_8), .Qn(s_r_ff_1_qn));  // open: preset, reset, en

  // Notes on the sheet:
  //   Biestable T (con JK)
  //   Biestable T (con D)
  //   Biestable T (con D)
  //   Biestable T (con SR)
endmodule

module Divisor_de_frecuencia (
);

  wire CLK_2_out, CLK_3_out, CLK_4_out, CLK_out, d_ff_1_q, d_ff_2_qn, d_ff_3_q, d_ff_4_qn;

  Clock CLK (.out(CLK_out));
  D_Flip_Flop d_ff_1 (.clk(CLK_out), .D(d_ff_1_q), .Q(d_ff_1_q));  // open: Qn, preset, en, reset
  Clock CLK_2 (.out(CLK_2_out));
  D_Flip_Flop d_ff_2 (.clk(CLK_2_out), .D(d_ff_2_qn), .Qn(d_ff_2_qn));  // open: Q, preset, en, reset
  D_Flip_Flop d_ff_3 (.clk(d_ff_3_q), .D(CLK_3_out), .Q(d_ff_3_q));  // open: Qn, preset, en, reset
  Clock CLK_3 (.out(CLK_3_out));
  Clock CLK_4 (.out(CLK_4_out));
  D_Flip_Flop d_ff_4 (.clk(d_ff_4_qn), .D(CLK_4_out), .Qn(d_ff_4_qn));  // open: Q, preset, en, reset

  // Notes on the sheet:
  //   (A)
  //   (B)
  //   (C)
  //   (D)
endmodule

module slide (
  input  A
);

  wire CLK_out, or_1_out, Q_q;

  Clock CLK (.out(CLK_out));
  or or_1 (or_1_out, A, Q_q);
  T_Flip_Flop Q (.clk(CLK_out), .T(or_1_out), .Q(Q_q));  // open: Qn, preset, reset, en
endmodule
