// Logisim project Cap8_1_Registros.circ as structural Verilog: 9 circuits, main circuit Reg. paralelo/paralelo
module Reg__paralelo_paralelo (
  input  D3,
  input  D2,
  input  D1,
  input  D0,
  input  EN,
  input  CLR_prime,
  output q3,
  output q2,
  output q1,
  output q0
);

  wire CLK_out, not_1_out;

  Clock CLK (.out(CLK_out));
  D_Flip_Flop u_q3 (.clk(CLK_out), .D(D3), .Q(q3), .en(EN), .reset(not_1_out));  // open: Qn, preset
  not not_1 (not_1_out, CLR_prime);
  D_Flip_Flop u_q2 (.clk(CLK_out), .D(D2), .Q(q2), .en(EN), .reset(not_1_out));  // open: Qn, preset
  D_Flip_Flop u_q1 (.clk(CLK_out), .D(D1), .Q(q1), .en(EN), .reset(not_1_out));  // open: Qn, preset
  D_Flip_Flop u_q0 (.clk(CLK_out), .D(D0), .Q(q0), .en(EN), .reset(not_1_out));  // open: Qn, preset
endmodule

module Reg__serie_serie (
  input  Entrada,
  input  EN,
  input  CLR_prime,
  output Salida
);

  wire CLK_out, not_1_out, q1_q, q2_q, q3_q;

  Clock CLK (.out(CLK_out));
  not not_1 (not_1_out, CLR_prime);
  D_Flip_Flop q3 (.clk(CLK_out), .D(Entrada), .Q(q3_q), .en(EN), .reset(not_1_out));  // open: Qn, preset
  D_Flip_Flop q2 (.clk(CLK_out), .D(q3_q), .Q(q2_q), .en(EN), .reset(not_1_out));  // open: Qn, preset
  D_Flip_Flop q1 (.clk(CLK_out), .D(q2_q), .Q(q1_q), .en(EN), .reset(not_1_out));  // open: Qn, preset
  D_Flip_Flop q0 (.clk(CLK_out), .D(q1_q), .Q(Salida), .en(EN), .reset(not_1_out));  // open: Qn, preset
endmodule

module Reg__SIPO (
  input  Entrada,
  input  EN,
  input  CLR_prime,
  output q3,
  output q2,
  output q1,
  output q0__Salida
);

  wire CLK_out, not_1_out;

  Clock CLK (.out(CLK_out));
  not not_1 (not_1_out, CLR_prime);
  D_Flip_Flop u_q2 (.clk(CLK_out), .D(q3), .Q(q2), .en(EN), .reset(not_1_out));  // open: Qn, preset
  D_Flip_Flop u_q3 (.clk(CLK_out), .D(Entrada), .Q(q3), .en(EN), .reset(not_1_out));  // open: Qn, preset
  D_Flip_Flop u_q1 (.clk(CLK_out), .D(q2), .Q(q1), .en(EN), .reset(not_1_out));  // open: Qn, preset
  D_Flip_Flop q0 (.clk(CLK_out), .D(q1), .Q(q0__Salida), .en(EN), .reset(not_1_out));  // open: Qn, preset
endmodule

module Reg__PISO_3b (
  input  D2,
  input  D1,
  input  D0,
  input  LOAD_prime_SHIFT,
  input  EN,
  input  CLR_prime,
  output q2,
  output q1,
  output q0
);

  wire CLK_out, multiplexer_1_out, multiplexer_2_out, multiplexer_3_out, not_1_out;

  Multiplexer #(.disabled(0), .enable("false")) multiplexer_1 (
    .in0(D2), .in1(1'b0), .out(multiplexer_1_out), .sel(LOAD_prime_SHIFT));
  Clock CLK (.out(CLK_out));
  not not_1 (not_1_out, CLR_prime);
  D_Flip_Flop u_q2 (.clk(CLK_out), .D(multiplexer_1_out), .Q(q2), .en(EN), .reset(not_1_out));  // open: Qn, preset
  Multiplexer #(.disabled(0), .enable("false")) multiplexer_2 (
    .in0(D1), .in1(q2), .out(multiplexer_2_out), .sel(LOAD_prime_SHIFT));
  Multiplexer #(.disabled(0), .enable("false")) multiplexer_3 (
    .in0(D0), .in1(q1), .out(multiplexer_3_out), .sel(LOAD_prime_SHIFT));
  D_Flip_Flop u_q1 (.clk(CLK_out), .D(multiplexer_2_out), .Q(q1), .en(EN), .reset(not_1_out));  // open: Qn, preset
  D_Flip_Flop u_q0 (.clk(CLK_out), .D(multiplexer_3_out), .Q(q0), .en(EN), .reset(not_1_out));  // open: Qn, preset
endmodule

module Reg__PISO_4b (
  input  D3,
  input  D2,
  input  D1,
  input  D0,
  input  LOAD_prime_SHIFT,
  input  Entrada,
  input  EN,
  input  CLR_prime,
  output q3,
  output q2,
  output q1,
  output q0
);

  wire CLK_out, multiplexer_1_out, multiplexer_2_out, multiplexer_3_out, multiplexer_4_out, not_1_out;

  Clock CLK (.out(CLK_out));
  Multiplexer #(.disabled(0), .enable("false")) multiplexer_1 (
    .in0(D3), .in1(Entrada), .out(multiplexer_1_out), .sel(LOAD_prime_SHIFT));
  not not_1 (not_1_out, CLR_prime);
  Multiplexer #(.disabled(0), .enable("false")) multiplexer_2 (
    .in0(D2), .in1(q3), .out(multiplexer_2_out), .sel(LOAD_prime_SHIFT));
  D_Flip_Flop u_q3 (.clk(CLK_out), .D(multiplexer_1_out), .Q(q3), .en(EN), .reset(not_1_out));  // open: Qn, preset
  D_Flip_Flop u_q2 (.clk(CLK_out), .D(multiplexer_2_out), .Q(q2), .en(EN), .reset(not_1_out));  // open: Qn, preset
  Multiplexer #(.disabled(0), .enable("false")) multiplexer_3 (
    .in0(D1), .in1(q2), .out(multiplexer_3_out), .sel(LOAD_prime_SHIFT));
  Multiplexer #(.disabled(0), .enable("false")) multiplexer_4 (
    .in0(D0), .in1(q1), .out(multiplexer_4_out), .sel(LOAD_prime_SHIFT));
  D_Flip_Flop u_q1 (.clk(CLK_out), .D(multiplexer_3_out), .Q(q1), .en(EN), .reset(not_1_out));  // open: Qn, preset
  D_Flip_Flop u_q0 (.clk(CLK_out), .D(multiplexer_4_out), .Q(q0), .en(EN), .reset(not_1_out));  // open: Qn, preset
endmodule

module Reg__PISO__2 (
  input  EN,
  input  CLR_prime,
  input  LOAD_prime_SHIFT,
  input  D3,
  input  D2,
  input  D1,
  input  D0,
  output Salida
);

  wire and_1_out, and_2_out, and_3_out, and_4_out, and_5_out, and_6_out, and_7_out, CLK_out, not_1_out,
       not_2_out, or_1_out, or_2_out, or_3_out, q1_q, q2_q, q3_q;

  Clock CLK (.out(CLK_out));
  not not_1 (not_1_out, CLR_prime);
  and and_1 (and_1_out, not_2_out, D3);
  not not_2 (not_2_out, LOAD_prime_SHIFT);
  D_Flip_Flop q3 (.clk(CLK_out), .D(and_1_out), .Q(q3_q), .en(EN), .reset(not_1_out));  // open: Qn, preset
  or or_1 (or_1_out, and_2_out, and_4_out);
  and and_2 (and_2_out, q3_q, LOAD_prime_SHIFT);
  D_Flip_Flop q2 (.clk(CLK_out), .D(or_1_out), .Q(q2_q), .en(EN), .reset(not_1_out));  // open: Qn, preset
  and and_3 (and_3_out, q2_q, LOAD_prime_SHIFT);
  and and_4 (and_4_out, not_2_out, D2);
  D_Flip_Flop q1 (.clk(CLK_out), .D(or_2_out), .Q(q1_q), .en(EN), .reset(not_1_out));  // open: Qn, preset
  or or_2 (or_2_out, and_3_out, and_6_out);
  and and_5 (and_5_out, q1_q, LOAD_prime_SHIFT);
  and and_6 (and_6_out, not_2_out, D1);
  D_Flip_Flop q0 (.clk(CLK_out), .D(or_3_out), .Q(Salida), .en(EN), .reset(not_1_out));  // open: Qn, preset
  or or_3 (or_3_out, and_5_out, and_7_out);
  and and_7 (and_7_out, not_2_out, D0);
endmodule

module Reg__Bidireccional (
  input  EN,
  input  CLR_prime,
  input  LEFT_prime_RIGHT,
  input  Entrada,
  output q3,
  output q0
);

  wire and_1_out, and_2_out, and_3_out, and_4_out, and_5_out, and_6_out, and_7_out, and_8_out, CLK_out,
       not_1_out, not_2_out, or_1_out, or_2_out, or_3_out, or_4_out, q1_q, q2_q;

  Clock CLK (.out(CLK_out));
  not not_1 (not_1_out, CLR_prime);
  and and_1 (and_1_out, Entrada, LEFT_prime_RIGHT);
  not not_2 (not_2_out, LEFT_prime_RIGHT);
  D_Flip_Flop u_q3 (.clk(CLK_out), .D(or_1_out), .Q(q3), .en(EN), .reset(not_1_out));  // open: Qn, preset
  or or_1 (or_1_out, and_1_out, and_2_out);
  and and_2 (and_2_out, not_2_out, q2_q);
  D_Flip_Flop q2 (.clk(CLK_out), .D(or_2_out), .Q(q2_q), .en(EN), .reset(not_1_out));  // open: Qn, preset
  or or_2 (or_2_out, and_4_out, and_3_out);
  and and_3 (and_3_out, not_2_out, q1_q);
  and and_4 (and_4_out, q3, LEFT_prime_RIGHT);
  or or_3 (or_3_out, and_6_out, and_5_out);
  and and_5 (and_5_out, not_2_out, q0);
  and and_6 (and_6_out, q2_q, LEFT_prime_RIGHT);
  D_Flip_Flop q1 (.clk(CLK_out), .D(or_3_out), .Q(q1_q), .en(EN), .reset(not_1_out));  // open: Qn, preset
  or or_4 (or_4_out, and_7_out, and_8_out);
  and and_7 (and_7_out, q1_q, LEFT_prime_RIGHT);
  and and_8 (and_8_out, not_2_out, Entrada);
  D_Flip_Flop u_q0 (.clk(CLK_out), .D(or_4_out), .Q(q0), .en(EN), .reset(not_1_out));  // open: Qn, preset
endmodule

module Reg__universal (
  input  [1:0] \m__operación ,
  input  INIT_CLR,
  input  D3,
  input  D2,
  input  D1,
  input  D0,
  output q3,
  output q0
);

  wire CLK_out, multiplexer_1_out, multiplexer_2_out, multiplexer_3_out, multiplexer_4_out, q1_q, q2_q;

  Clock CLK (.out(CLK_out));
  Multiplexer #(.select(2), .disabled(0), .enable("false")) multiplexer_1 (
    .in0(D3), .in1(D3), .in2(q3), .in3(q2_q), .out(multiplexer_1_out), .sel(\m__operación ));
  // Probe on \m__operación 
  D_Flip_Flop u_q3 (.clk(CLK_out), .D(multiplexer_1_out), .Q(q3), .reset(INIT_CLR));  // open: Qn, preset, en
  D_Flip_Flop q2 (.clk(CLK_out), .D(multiplexer_2_out), .Q(q2_q), .reset(INIT_CLR));  // open: Qn, preset, en
  Multiplexer #(.select(2), .disabled(0), .enable("false")) multiplexer_2 (
    .in0(q3), .in1(D2), .in2(q2_q), .in3(q1_q), .out(multiplexer_2_out), .sel(\m__operación ));
  Multiplexer #(.select(2), .disabled(0), .enable("false")) multiplexer_3 (
    .in0(q2_q), .in1(D1), .in2(q1_q), .in3(q0), .out(multiplexer_3_out), .sel(\m__operación ));
  D_Flip_Flop q1 (.clk(CLK_out), .D(multiplexer_3_out), .Q(q1_q), .reset(INIT_CLR));  // open: Qn, preset, en
  Multiplexer #(.select(2), .disabled(0), .enable("false")) multiplexer_4 (
    .in0(q1_q), .in1(D0), .in2(q0), .in3(D0), .out(multiplexer_4_out), .sel(\m__operación ));
  D_Flip_Flop u_q0 (.clk(CLK_out), .D(multiplexer_4_out), .Q(q0), .reset(INIT_CLR));  // open: Qn, preset, en

  // Notes on the sheet:
  //   m=00 (shift right)
  //   m=01 (load)
  //   m=10 (enable)
  //   m=11 (shift left)
endmodule

module Registro_multibit (
  input  [1:0] D3,
  input  [1:0] D2,
  input  [1:0] D1,
  input  [1:0] D0,
  input  LOAD,
  input  EN,
  input  [1:0] Dato__Serie,
  input  CLR,
  input  D3_1,
  input  D2_1,
  input  D1_1,
  input  D0_1,
  input  D3_0,
  input  D2_0,
  input  D1_0,
  input  D0_0,
  input  LOAD_prime_SHIFT,
  input  [1:0] Entrada,
  input  CLR_2,
  input  EN_2,
  output [1:0] Salida,
  output [1:0] Salida_2,
  output q3_1,
  output q2_1,
  output q1_1,
  output q0_1,
  output q3_0,
  output q2_0,
  output q1_0,
  output q0_0
);

  wire CLK_2_out, CLK_out, multiplexer_1_out, multiplexer_2_out, multiplexer_3_out, multiplexer_4_out,
       multiplexer_5_out, multiplexer_6_out, multiplexer_7_out, multiplexer_8_out;

  Clock CLK (.out(CLK_out));
  Shift_Register #(.width(2), .length(4)) shift_register_1 (
    .shift(EN), .in(Dato__Serie), .clk(CLK_2_out), .out(Salida), .load(LOAD), .clr(CLR), .d0(D3), .d1(D2),
    .d2(D1), .d3(D0));  // open: q0, q1, q2, q3
  Clock CLK_2 (.out(CLK_2_out));
  Multiplexer #(.disabled(0), .enable("false")) multiplexer_1 (
    .in0(D3_1), .in1(Entrada[1]), .out(multiplexer_1_out), .sel(LOAD_prime_SHIFT));
  Multiplexer #(.disabled(0), .enable("false")) multiplexer_2 (
    .in0(D3_0), .in1(Entrada[0]), .out(multiplexer_2_out), .sel(LOAD_prime_SHIFT));
  // Probe on Salida
  D_Flip_Flop q3 (.clk(CLK_out), .D(multiplexer_1_out), .Q(q3_1), .en(EN_2), .reset(CLR_2));  // open: Qn, preset
  D_Flip_Flop q3_2 (.clk(CLK_out), .D(multiplexer_2_out), .Q(q3_0), .en(EN_2), .reset(CLR_2));  // open: Qn, preset
  Multiplexer #(.disabled(0), .enable("false")) multiplexer_3 (
    .in0(D2_1), .in1(q3_1), .out(multiplexer_3_out), .sel(LOAD_prime_SHIFT));
  Multiplexer #(.disabled(0), .enable("false")) multiplexer_4 (
    .in0(D2_0), .in1(q3_0), .out(multiplexer_4_out), .sel(LOAD_prime_SHIFT));
  Multiplexer #(.disabled(0), .enable("false")) multiplexer_5 (
    .in0(D1_1), .in1(q2_1), .out(multiplexer_5_out), .sel(LOAD_prime_SHIFT));
  D_Flip_Flop q2 (.clk(CLK_out), .D(multiplexer_3_out), .Q(q2_1), .en(EN_2), .reset(CLR_2));  // open: Qn, preset
  Multiplexer #(.disabled(0), .enable("false")) multiplexer_6 (
    .in0(D1_0), .in1(q2_0), .out(multiplexer_6_out), .sel(LOAD_prime_SHIFT));
  D_Flip_Flop q2_2 (.clk(CLK_out), .D(multiplexer_4_out), .Q(q2_0), .en(EN_2), .reset(CLR_2));  // open: Qn, preset
  D_Flip_Flop q1 (.clk(CLK_out), .D(multiplexer_5_out), .Q(q1_1), .en(EN_2), .reset(CLR_2));  // open: Qn, preset
  D_Flip_Flop q1_2 (.clk(CLK_out), .D(multiplexer_6_out), .Q(q1_0), .en(EN_2), .reset(CLR_2));  // open: Qn, preset
  Multiplexer #(.disabled(0), .enable("false")) multiplexer_7 (
    .in0(D0_1), .in1(q1_1), .out(multiplexer_7_out), .sel(LOAD_prime_SHIFT));
  Multiplexer #(.disabled(0), .enable("false")) multiplexer_8 (
    .in0(D0_0), .in1(q1_0), .out(multiplexer_8_out), .sel(LOAD_prime_SHIFT));
  // Probe on {q0_1, q0_0}
  D_Flip_Flop q0 (.clk(CLK_out), .D(multiplexer_7_out), .Q(q0_1), .en(EN_2), .reset(CLR_2));  // open: Qn, preset
  D_Flip_Flop q0_2 (.clk(CLK_out), .D(multiplexer_8_out), .Q(q0_0), .en(EN_2), .reset(CLR_2));  // open: Qn, preset

  assign Salida_2 = {q0_1, q0_0};
endmodule
