// Logisim project Cap8_2_CntAsinc.circ as structural Verilog: 5 circuits, main circuit CNTAsincUpMod8
module CNTAsincUpMod8 (
  input  EN,
  input  INIT_CLR,
  input  EN_2,
  input  INIT_CLR_2,
  output [2:0] CNT__up,
  output [2:0] CNT__down,
  output [2:0] CNT
);

  wire CLK_2_out, CLK_out, q0_qn, q1_qn;

  Clock CLK (.out(CLK_out));
  Clock CLK_2 (.out(CLK_2_out));
  T_Flip_Flop q0 (.clk(CLK_out), .T(1'b1), .Q(CNT__up[0]), .Qn(q0_qn), .reset(INIT_CLR), .en(EN));  // open: preset
  T_Flip_Flop #(.trigger("falling")) q0_2 (
    .clk(CLK_2_out), .T(1'b1), .Q(CNT[0]), .reset(INIT_CLR_2), .en(EN_2));  // open: Qn, preset
  T_Flip_Flop q1 (.clk(q0_qn), .T(1'b1), .Q(CNT__up[1]), .Qn(q1_qn), .reset(INIT_CLR), .en(EN));  // open: preset
  T_Flip_Flop #(.trigger("falling")) q1_2 (
    .clk(CNT[0]), .T(1'b1), .Q(CNT[1]), .reset(INIT_CLR_2), .en(EN_2));  // open: Qn, preset
  // Probe on CNT__up
  assign CNT__down = ~CNT__up;  // NOT_Gate not_1, 3 bits wide
  // Probe on CNT__down
  T_Flip_Flop q2 (.clk(q1_qn), .T(1'b1), .Q(CNT__up[2]), .reset(INIT_CLR), .en(EN));  // open: Qn, preset
  // Probe on CNT
  T_Flip_Flop #(.trigger("falling")) q2_2 (
    .clk(CNT[1]), .T(1'b1), .Q(CNT[2]), .reset(INIT_CLR_2), .en(EN_2));  // open: Qn, preset
endmodule

module CNTAsinDownMod8 (
  input  EN,
  input  INIT_CLR,
  input  EN_2,
  input  INIT_CLR_2,
  output [2:0] CNT,
  output [2:0] CNT_2
);

  wire CLK_2_out, CLK_out, q0_2_qn, q1_2_qn;
  wire [2:0] not_1_out;

  Clock CLK (.out(CLK_out));
  T_Flip_Flop q0 (.clk(CLK_out), .T(1'b1), .Q(CNT[0]), .preset(INIT_CLR), .en(EN));  // open: Qn, reset
  Clock CLK_2 (.out(CLK_2_out));
  T_Flip_Flop #(.trigger("falling")) q0_2 (
    .clk(CLK_2_out), .T(1'b1), .Q(CNT_2[0]), .Qn(q0_2_qn), .preset(INIT_CLR_2), .en(EN_2));  // open: reset
  T_Flip_Flop q1 (.clk(CNT[0]), .T(1'b1), .Q(CNT[1]), .preset(INIT_CLR), .en(EN));  // open: Qn, reset
  T_Flip_Flop #(.trigger("falling")) q1_2 (
    .clk(q0_2_qn), .T(1'b1), .Q(CNT_2[1]), .Qn(q1_2_qn), .preset(INIT_CLR_2), .en(EN_2));  // open: reset
  T_Flip_Flop q2 (.clk(CNT[1]), .T(1'b1), .Q(CNT[2]), .preset(INIT_CLR), .en(EN));  // open: Qn, reset
  T_Flip_Flop #(.trigger("falling")) q2_2 (
    .clk(q1_2_qn), .T(1'b1), .Q(CNT_2[2]), .preset(INIT_CLR_2), .en(EN_2));  // open: Qn, reset
  // Probe on CNT
  // Probe on not_1_out
  assign not_1_out = ~CNT;  // NOT_Gate not_1, 3 bits wide
  // Probe on CNT_2
endmodule

module CNTAsinUpDecadas_BCD (
  input  EN,
  output [3:0] CNT
);

  wire CLK_out, INIT_CLR_out, or_1_out, q0_qn, q1_qn, q2_qn, q3q1_out;

  Clock CLK (.out(CLK_out));
  T_Flip_Flop q0 (.clk(CLK_out), .T(1'b1), .Q(CNT[0]), .Qn(q0_qn), .reset(or_1_out), .en(EN));  // open: preset
  Button INIT_CLR (.out(INIT_CLR_out));
  or or_1 (or_1_out, INIT_CLR_out, q3q1_out);
  T_Flip_Flop q1 (.clk(q0_qn), .T(1'b1), .Q(CNT[1]), .Qn(q1_qn), .reset(or_1_out), .en(EN));  // open: preset
  T_Flip_Flop q2 (.clk(q1_qn), .T(1'b1), .Q(CNT[2]), .Qn(q2_qn), .reset(or_1_out), .en(EN));  // open: preset
  T_Flip_Flop q3 (.clk(q2_qn), .T(1'b1), .Q(CNT[3]), .reset(or_1_out), .en(EN));  // open: Qn, preset
  and q3q1 (q3q1_out, CNT[1], CNT[3]);
  // Probe on CNT

  // Notes on the sheet:
  //   1 si la salida del contador es 10
endmodule

module CNTAsinUpMod5 (
  input  EN,
  output [3:0] CNT
);

  wire CLK_out, INIT_CLR_out, or_1_out, q0_qn, q1_qn, q2q0_out;
  wire [2:0] q0_q;

  Clock CLK (.out(CLK_out));
  Button INIT_CLR (.out(INIT_CLR_out));
  or or_1 (or_1_out, INIT_CLR_out, q2q0_out);
  T_Flip_Flop q0 (.clk(CLK_out), .T(1'b1), .Q(q0_q[0]), .Qn(q0_qn), .reset(or_1_out), .en(EN));  // open: preset
  and q2q0 (q2q0_out, q0_q[0], q0_q[2]);
  T_Flip_Flop q1 (.clk(q0_qn), .T(1'b1), .Q(q0_q[1]), .Qn(q1_qn), .reset(or_1_out), .en(EN));  // open: preset
  // Probe on q0_q
  T_Flip_Flop q2 (.clk(q1_qn), .T(1'b1), .Q(q0_q[2]), .reset(or_1_out), .en(EN));  // open: Qn, preset
  Hex_Digit_Display hex_digit_display_1 (.value(CNT));  // open: dp
  assign CNT = {{1{1'b0}}, q0_q};  // Bit_Extender bit_extender_1
endmodule

module CNT_BCD__w__strobing (
  input  EN,
  output [3:0] CNT
);

  wire and_1_out, CLK_out, INIT_CLR_out, or_1_out, q0_qn, q1_qn, q2_qn, q3q0_out;

  Clock CLK (.out(CLK_out));
  Button INIT_CLR (.out(INIT_CLR_out));
  and and_1 (and_1_out, ~CLK_out, q3q0_out);  // AND_Gate
  T_Flip_Flop q0 (.clk(CLK_out), .T(1'b1), .Q(CNT[0]), .Qn(q0_qn), .reset(or_1_out), .en(EN));  // open: preset
  or or_1 (or_1_out, INIT_CLR_out, and_1_out);
  T_Flip_Flop q1 (.clk(q0_qn), .T(1'b1), .Q(CNT[1]), .Qn(q1_qn), .reset(or_1_out), .en(EN));  // open: preset
  T_Flip_Flop q2 (.clk(q1_qn), .T(1'b1), .Q(CNT[2]), .Qn(q2_qn), .reset(or_1_out), .en(EN));  // open: preset
  T_Flip_Flop q3 (.clk(q2_qn), .T(1'b1), .Q(CNT[3]), .reset(or_1_out), .en(EN));  // open: Qn, preset
  and q3q0 (q3q0_out, CNT[0], CNT[3]);
  // Probe on CNT

  // Notes on the sheet:
  //   1 si la salida del contador es 9
endmodule
