// Logisim project Cap8_3_CntSinc.circ as structural Verilog: 35 circuits, main circuit CNTSincUpMod8
module CNTSincUpMod8 (
  input  EN,
  output [2:0] CNT
);

  wire CLK_out, INIT_CLR_out, q1q0_out;

  Clock CLK (.out(CLK_out));
  Button INIT_CLR (.out(INIT_CLR_out));
  T_Flip_Flop q0 (.clk(CLK_out), .T(1'b1), .Q(CNT[0]), .reset(INIT_CLR_out), .en(EN));  // open: Qn, preset
  and q1q0 (q1q0_out, CNT[0], CNT[1]);
  T_Flip_Flop q1 (.clk(CLK_out), .T(CNT[0]), .Q(CNT[1]), .reset(INIT_CLR_out), .en(EN));  // open: Qn, preset
  T_Flip_Flop q2 (.clk(CLK_out), .T(q1q0_out), .Q(CNT[2]), .reset(INIT_CLR_out), .en(EN));  // open: Qn, preset
  // Probe on CNT
endmodule

module CNTSincDownMod8 (
  input  EN,
  output [2:0] CNT
);

  wire CLK_out, INIT_PRE_out, q0_qn, q1_prime_q0_prime_out, q1_qn;

  Clock CLK (.out(CLK_out));
  Button INIT_PRE (.out(INIT_PRE_out));
  T_Flip_Flop q0 (.clk(CLK_out), .T(1'b1), .Q(CNT[0]), .Qn(q0_qn), .preset(INIT_PRE_out), .en(EN));  // open: reset
  T_Flip_Flop q1 (.clk(CLK_out), .T(q0_qn), .Q(CNT[1]), .Qn(q1_qn), .preset(INIT_PRE_out), .en(EN));  // open: reset
  T_Flip_Flop q2 (
    .clk(CLK_out), .T(q1_prime_q0_prime_out), .Q(CNT[2]), .preset(INIT_PRE_out), .en(EN));  // open: Qn, reset
  and q1_prime_q0_prime (q1_prime_q0_prime_out, q1_qn, q0_qn);
  // Probe on CNT
endmodule

module CNTSincUpMod16 (
  input  EN,
  output [3:0] CNT
);

  wire CLK_out, INIT_CLR_out, q1q0_out, q2q1q0_out;

  Clock CLK (.out(CLK_out));
  Button INIT_CLR (.out(INIT_CLR_out));
  T_Flip_Flop q1 (.clk(CLK_out), .T(CNT[0]), .Q(CNT[1]), .reset(INIT_CLR_out), .en(EN));  // open: Qn, preset
  T_Flip_Flop q0 (.clk(CLK_out), .T(1'b1), .Q(CNT[0]), .reset(INIT_CLR_out), .en(EN));  // open: Qn, preset
  and q1q0 (q1q0_out, CNT[0], CNT[1]);
  T_Flip_Flop q2 (.clk(CLK_out), .T(q1q0_out), .Q(CNT[2]), .reset(INIT_CLR_out), .en(EN));  // open: Qn, preset
  and q2q1q0 (q2q1q0_out, q1q0_out, CNT[2]);
  T_Flip_Flop q3 (.clk(CLK_out), .T(q2q1q0_out), .Q(CNT[3]), .reset(INIT_CLR_out), .en(EN));  // open: Qn, preset
  // Probe on CNT
endmodule

module CNTSincDownMod16 (
  input  EN,
  output [3:0] CNT
);

  wire CLK_out, INIT_PRE_out, q0_qn, q1_prime_q0_prime_out, q1_qn, q2_prime_q1_prime_q0_prime_out, q2_qn;

  T_Flip_Flop q0 (.clk(CLK_out), .T(1'b1), .Q(CNT[0]), .Qn(q0_qn), .preset(INIT_PRE_out), .en(EN));  // open: reset
  Clock CLK (.out(CLK_out));
  Button INIT_PRE (.out(INIT_PRE_out));
  T_Flip_Flop q1 (.clk(CLK_out), .T(q0_qn), .Q(CNT[1]), .Qn(q1_qn), .preset(INIT_PRE_out), .en(EN));  // open: reset
  and q1_prime_q0_prime (q1_prime_q0_prime_out, q1_qn, q0_qn);
  T_Flip_Flop q2 (
    .clk(CLK_out), .T(q1_prime_q0_prime_out), .Q(CNT[2]), .Qn(q2_qn), .preset(INIT_PRE_out), .en(EN));  // open: reset
  and q2_prime_q1_prime_q0_prime (q2_prime_q1_prime_q0_prime_out, q2_qn, q1_prime_q0_prime_out);
  // Probe on CNT
  T_Flip_Flop q3 (
    .clk(CLK_out), .T(q2_prime_q1_prime_q0_prime_out), .Q(CNT[3]), .preset(INIT_PRE_out), .en(EN));  // open: Qn, reset
endmodule

module CNT_DIV_10_CLRAsinc (
  input  EN,
  input  EN_2,
  output [3:0] CNT,
  output [3:0] CNT_2
);

  wire CLK_2_out, CLK_out, INIT_CLR_2_out, INIT_CLR_out, or_1_out, or_2_out, q1q0_2_out, q1q0_out,
       q2q1q0_2_out, q2q1q0_out, q3q0_out, q3q1_out;

  Clock CLK (.out(CLK_out));
  Button INIT_CLR (.out(INIT_CLR_out));
  or or_1 (or_1_out, INIT_CLR_out, q3q1_out);
  and q3q1 (q3q1_out, CNT[1], CNT[3]);
  Clock CLK_2 (.out(CLK_2_out));
  Button INIT_CLR_2 (.out(INIT_CLR_2_out));
  or or_2 (or_2_out, INIT_CLR_2_out, q3q0_out);
  and q3q0 (q3q0_out, CNT_2[0], ~CLK_2_out, CNT_2[3]);  // AND_Gate
  J_K_Flip_Flop q0 (.J(1'b1), .clk(CLK_out), .K(1'b1), .Q(CNT[0]), .en(EN), .reset(or_1_out));  // open: Qn, preset
  J_K_Flip_Flop q0_2 (
    .J(1'b1), .clk(CLK_2_out), .K(1'b1), .Q(CNT_2[0]), .en(EN_2), .reset(or_2_out));  // open: Qn, preset
  and q1q0 (q1q0_out, CNT[0], CNT[1]);
  J_K_Flip_Flop q1 (.J(CNT[0]), .clk(CLK_out), .K(CNT[0]), .Q(CNT[1]), .en(EN), .reset(or_1_out));  // open: Qn, preset
  and q1q0_2 (q1q0_2_out, CNT_2[0], CNT_2[1]);
  J_K_Flip_Flop q1_2 (
    .J(CNT_2[0]), .clk(CLK_2_out), .K(CNT_2[0]), .Q(CNT_2[1]), .en(EN_2), .reset(or_2_out));  // open: Qn, preset
  J_K_Flip_Flop q2 (
    .J(q1q0_out), .clk(CLK_out), .K(q1q0_out), .Q(CNT[2]), .en(EN), .reset(or_1_out));  // open: Qn, preset
  J_K_Flip_Flop q2_2 (
    .J(q1q0_2_out), .clk(CLK_2_out), .K(q1q0_2_out), .Q(CNT_2[2]), .en(EN_2), .reset(or_2_out));  // open: Qn, preset
  and q2q1q0 (q2q1q0_out, q1q0_out, CNT[2]);
  J_K_Flip_Flop q3 (
    .J(q2q1q0_out), .clk(CLK_out), .K(q2q1q0_out), .Q(CNT[3]), .en(EN), .reset(or_1_out));  // open: Qn, preset
  and q2q1q0_2 (q2q1q0_2_out, q1q0_2_out, CNT_2[2]);
  J_K_Flip_Flop q3_2 (
    .J(q2q1q0_2_out), .clk(CLK_2_out), .K(q2q1q0_2_out), .Q(CNT_2[3]), .en(EN_2), .reset(or_2_out));  // open: Qn, preset
  // Probe on CNT
  // Probe on CNT_2
endmodule

// CNT DIV 10
module CNT_DIV_10_CLRSinc (
  input  CLK,
  input  CTEN,
  input  INIT_CLR,
  output TC,
  output [3:0] CNT
);

  wire or_1_out, q1q0_out, q2q1q0_out, q3_prime_q0_out, q3_qn;

  and q3_prime_q0 (q3_prime_q0_out, CNT[0], q3_qn);
  J_K_Flip_Flop q0 (.J(1'b1), .clk(CLK), .K(1'b1), .Q(CNT[0]), .en(CTEN), .reset(INIT_CLR));  // open: Qn, preset
  J_K_Flip_Flop q1 (
    .J(q3_prime_q0_out), .clk(CLK), .K(q3_prime_q0_out), .Q(CNT[1]), .en(CTEN), .reset(INIT_CLR));  // open: Qn, preset
  and q1q0 (q1q0_out, CNT[0], CNT[1]);
  and q3q0 (TC, CNT[3], CNT[0]);
  J_K_Flip_Flop q2 (
    .J(q1q0_out), .clk(CLK), .K(q1q0_out), .Q(CNT[2]), .en(CTEN), .reset(INIT_CLR));  // open: Qn, preset
  and q2q1q0 (q2q1q0_out, q1q0_out, CNT[2]);
  or or_1 (or_1_out, TC, q2q1q0_out);
  J_K_Flip_Flop q3 (
    .J(or_1_out), .clk(CLK), .K(or_1_out), .Q(CNT[3]), .Qn(q3_qn), .en(CTEN), .reset(INIT_CLR));  // open: preset
  // Probe on CNT
endmodule

module CNT_MOD_16__w_LD (
  input  CLK,
  input  LD,
  input  [3:0] Data,
  input  INIT_CLR,
  input  EN,
  output [3:0] CNT
);

  wire multiplexer_1_out, multiplexer_2_out, multiplexer_3_out, multiplexer_4_out, q1q0_out, q2q1q0_out,
       xor_1_out, xor_2_out, xor_3_out, xor_4_out;

  xor xor_1 (xor_1_out, CNT[0], 1'b1);
  Multiplexer #(.enable("false")) multiplexer_1 (.in0(xor_1_out), .in1(Data[0]), .out(multiplexer_1_out), .sel(LD));
  D_Flip_Flop q0 (.clk(CLK), .D(multiplexer_1_out), .Q(CNT[0]), .en(EN), .reset(INIT_CLR));  // open: Qn, preset
  xor xor_2 (xor_2_out, CNT[1], CNT[0]);
  Multiplexer #(.enable("false")) multiplexer_2 (.in0(xor_2_out), .in1(Data[1]), .out(multiplexer_2_out), .sel(LD));
  D_Flip_Flop q1 (.clk(CLK), .D(multiplexer_2_out), .Q(CNT[1]), .en(EN), .reset(INIT_CLR));  // open: Qn, preset
  and q1q0 (q1q0_out, CNT[0], CNT[1]);
  xor xor_3 (xor_3_out, CNT[2], q1q0_out);
  Multiplexer #(.enable("false")) multiplexer_3 (.in0(xor_3_out), .in1(Data[2]), .out(multiplexer_3_out), .sel(LD));
  D_Flip_Flop q2 (.clk(CLK), .D(multiplexer_3_out), .Q(CNT[2]), .en(EN), .reset(INIT_CLR));  // open: Qn, preset
  xor xor_4 (xor_4_out, CNT[3], q2q1q0_out);
  and q2q1q0 (q2q1q0_out, q1q0_out, CNT[2]);
  D_Flip_Flop q3 (.clk(CLK), .D(multiplexer_4_out), .Q(CNT[3]), .en(EN), .reset(INIT_CLR));  // open: Qn, preset
  Multiplexer #(.enable("false")) multiplexer_4 (.in0(xor_4_out), .in1(Data[3]), .out(multiplexer_4_out), .sel(LD));
  // Probe on CNT
endmodule

module CNT_DIV_10_CLRSinc__w_LD (
  input  [3:0] Data,
  input  EN,
  output [3:0] out_3
);

  wire CLK_out, INIT_CLR_out, q3q0_out;

  Clock CLK (.out(CLK_out));
  Button INIT_CLR (.out(INIT_CLR_out));
  and q3q0 (q3q0_out, out_3[0], out_3[3]);
  // Probe on out_3
  CNT_MOD_16__w_LD cnt_mod_16_w_ld_1 (
    .CLK(CLK_out), .LD(q3q0_out), .Data(Data), .INIT_CLR(INIT_CLR_out), .EN(EN), .CNT(out_3));
endmodule

module CNT_Div_100 (
);

  wire and_1_out, CLK_out, cnt_div_10_clrsinc_1_tc, cnt_div_10_clrsinc_2_tc, INIT_CLR_out;
  wire [3:0] cnt_div_10_clrsinc_1_cnt, cnt_div_10_clrsinc_2_cnt;

  Clock CLK (.out(CLK_out));
  Button INIT_CLR (.out(INIT_CLR_out));
  CNT_DIV_10_CLRSinc cnt_div_10_clrsinc_1 (
    .CTEN(1'b1), .TC(cnt_div_10_clrsinc_1_tc), .CNT(cnt_div_10_clrsinc_1_cnt), .CLK(CLK_out),
    .INIT_CLR(INIT_CLR_out));
  CNT_DIV_10_CLRSinc cnt_div_10_clrsinc_2 (
    .CTEN(cnt_div_10_clrsinc_1_tc), .TC(cnt_div_10_clrsinc_2_tc), .CNT(cnt_div_10_clrsinc_2_cnt),
    .CLK(CLK_out), .INIT_CLR(INIT_CLR_out));
  // Probe on cnt_div_10_clrsinc_2_cnt
  and and_1 (and_1_out, cnt_div_10_clrsinc_1_tc, cnt_div_10_clrsinc_2_tc);
  LED led_1 (.in(and_1_out));
  // Probe on cnt_div_10_clrsinc_2_cnt
  // Probe on cnt_div_10_clrsinc_1_cnt
  // Probe on cnt_div_10_clrsinc_1_cnt

  // Notes on the sheet:
  //   f_in
  //   f_in/10
  //   f_in/100
  //   Decenas
  //   Unidades
endmodule

module CNTSincUpBCD_CLRSinc (
  input  EN,
  output [3:0] CNT
);

  wire CLK_out, INIT_CLR_out, or_1_out, q1q0_out, q2q1q0_out, q3_prime_q0_out, q3_qn, q3q0_out;

  Clock CLK (.out(CLK_out));
  T_Flip_Flop q0 (.clk(CLK_out), .T(1'b1), .Q(CNT[0]), .reset(INIT_CLR_out), .en(EN));  // open: Qn, preset
  Button INIT_CLR (.out(INIT_CLR_out));
  and q3_prime_q0 (q3_prime_q0_out, CNT[0], q3_qn);
  T_Flip_Flop q1 (.clk(CLK_out), .T(q3_prime_q0_out), .Q(CNT[1]), .reset(INIT_CLR_out), .en(EN));  // open: Qn, preset
  T_Flip_Flop q2 (.clk(CLK_out), .T(q1q0_out), .Q(CNT[2]), .reset(INIT_CLR_out), .en(EN));  // open: Qn, preset
  and q1q0 (q1q0_out, CNT[1], q3_prime_q0_out);
  and q3q0 (q3q0_out, CNT[3], CNT[0]);
  and q2q1q0 (q2q1q0_out, CNT[2], q1q0_out);
  or or_1 (or_1_out, q3q0_out, q2q1q0_out);
  T_Flip_Flop q3 (.clk(CLK_out), .T(or_1_out), .Q(CNT[3]), .Qn(q3_qn), .reset(INIT_CLR_out), .en(EN));  // open: preset
  // Probe on CNT
endmodule

module CNTSincBidMod8__w_MUX (
  input  EN,
  input  UP_prime_DOWN,
  input  UP_prime_DOWN_2,
  output [2:0] CNT
);

  wire and_1_out, and_2_out, and_3_out, and_4_out, CLK_out, decoder_1_out0, decoder_1_out1, INIT_2_out,
       INIT_out, multiplexer_1_out, multiplexer_2_out, not_1_out, not_2_out, q0_qn, q1_qn;

  Clock CLK (.out(CLK_out));
  Button INIT (.out(INIT_out));
  not not_1 (not_1_out, UP_prime_DOWN);
  Decoder #(.disabled(0)) decoder_1 (.out0(decoder_1_out0), .out1(decoder_1_out1), .sel(not_1_out), .en(INIT_out));
  J_K_Flip_Flop q0 (
    .J(1'b1), .clk(CLK_out), .K(1'b1), .Q(CNT[0]), .Qn(q0_qn), .preset(decoder_1_out0), .en(EN),
    .reset(decoder_1_out1));
  not not_2 (not_2_out, UP_prime_DOWN_2);
  Button INIT_2 (.out(INIT_2_out));
  J_K_Flip_Flop q1 (
    .J(multiplexer_1_out), .clk(CLK_out), .K(multiplexer_1_out), .Q(CNT[1]), .Qn(q1_qn),
    .preset(decoder_1_out0), .en(EN), .reset(decoder_1_out1));
  Multiplexer #(.disabled(0), .enable("false")) multiplexer_1 (
    .in0(CNT[0]), .in1(q0_qn), .out(multiplexer_1_out), .sel(UP_prime_DOWN));
  and and_1 (and_1_out, UP_prime_DOWN_2, INIT_2_out);
  and and_2 (and_2_out, INIT_2_out, not_2_out);
  and and_3 (and_3_out, multiplexer_1_out, CNT[1]);
  and and_4 (and_4_out, q1_qn, multiplexer_1_out);
  Multiplexer #(.disabled(0), .enable("false")) multiplexer_2 (
    .in0(and_3_out), .in1(and_4_out), .out(multiplexer_2_out), .sel(UP_prime_DOWN));
  // Probe on CNT
  J_K_Flip_Flop q2 (
    .J(multiplexer_2_out), .clk(CLK_out), .K(multiplexer_2_out), .Q(CNT[2]), .preset(decoder_1_out0),
    .en(EN), .reset(decoder_1_out1));  // open: Qn
endmodule

module CNTSincBidMod8__w_XOR (
  input  EN,
  input  UP_prime_DOWN,
  output [2:0] CNT
);

  wire CLK_out, INIT_out, q0_q, q1_q, q1q0_out, q2_q;

  Clock CLK (.out(CLK_out));
  Button INIT (.out(INIT_out));
  J_K_Flip_Flop q0 (.J(1'b1), .clk(CLK_out), .K(1'b1), .Q(q0_q), .en(EN), .reset(INIT_out));  // open: Qn, preset
  J_K_Flip_Flop q1 (.J(q0_q), .clk(CLK_out), .K(q0_q), .Q(q1_q), .en(EN), .reset(INIT_out));  // open: Qn, preset
  and q1q0 (q1q0_out, q0_q, q1_q);
  J_K_Flip_Flop q2 (
    .J(q1q0_out), .clk(CLK_out), .K(q1q0_out), .Q(q2_q), .en(EN), .reset(INIT_out));  // open: Qn, preset
  xor xor_1 (CNT[0], q0_q, UP_prime_DOWN);
  xor xor_2 (CNT[1], q1_q, UP_prime_DOWN);
  xor xor_3 (CNT[2], q2_q, UP_prime_DOWN);
  // Probe on CNT
endmodule

module CNTSincBidMod8__w_gates (
  input  EN,
  input  UP_prime_DOWN,
  output [2:0] CNT
);

  wire and_1_out, and_2_out, and_3_out, and_4_out, and_5_out, and_6_out, CLK_out, INIT_out, or_1_out,
       or_2_out, q0_qn, q1_qn;

  Clock CLK (.out(CLK_out));
  Button INIT (.out(INIT_out));
  T_Flip_Flop q0 (.clk(CLK_out), .T(1'b1), .Q(CNT[0]), .Qn(q0_qn), .preset(and_1_out), .reset(and_2_out), .en(EN));
  and and_1 (and_1_out, UP_prime_DOWN, INIT_out);
  and and_2 (and_2_out, INIT_out, ~UP_prime_DOWN);  // AND_Gate
  and and_3 (and_3_out, ~UP_prime_DOWN, CNT[0]);  // AND_Gate
  and and_4 (and_4_out, q0_qn, UP_prime_DOWN);
  or or_1 (or_1_out, and_3_out, and_4_out);
  and and_5 (and_5_out, and_3_out, CNT[1]);
  T_Flip_Flop q1 (.clk(CLK_out), .T(or_1_out), .Q(CNT[1]), .Qn(q1_qn), .preset(and_1_out), .reset(and_2_out), .en(EN));
  and and_6 (and_6_out, q1_qn, and_4_out);
  or or_2 (or_2_out, and_5_out, and_6_out);
  // Probe on CNT
  T_Flip_Flop q2 (.clk(CLK_out), .T(or_2_out), .Q(CNT[2]), .preset(and_1_out), .reset(and_2_out), .en(EN));  // open: Qn
endmodule

module Puerto_E_S (
  input  [7:0] Data,
  input  En,
  output [7:0] Output
);

  assign Output = En ? Data : 8'bz;  // Controlled_Buffer controlled_buffer_1
endmodule

module \Aplicación_CNT_Deco  (
  input  [3:0] Data,
  input  EN,
  output [7:0] Datos_para_CPU
);

  wire CLK_out, decoder_1_out0, decoder_1_out1, decoder_1_out2, decoder_1_out3, decoder_1_out4,
       decoder_1_out5, decoder_1_out6, INIT_CLR_out, q2q1_out;
  wire [3:0] cnt_mod_16_w_ld_1_cnt;

  and q2q1 (q2q1_out, cnt_mod_16_w_ld_1_cnt[1], cnt_mod_16_w_ld_1_cnt[2]);
  Clock CLK (.out(CLK_out));
  CNT_MOD_16__w_LD cnt_mod_16_w_ld_1 (
    .CLK(CLK_out), .LD(q2q1_out), .Data(Data), .INIT_CLR(INIT_CLR_out), .EN(EN), .CNT(cnt_mod_16_w_ld_1_cnt));
  Button INIT_CLR (.out(INIT_CLR_out));
  // Probe on cnt_mod_16_w_ld_1_cnt
  // Probe on Datos_para_CPU
  Decoder #(.select(4), .disabled(0)) decoder_1 (
    .out0(decoder_1_out0), .out1(decoder_1_out1), .out2(decoder_1_out2), .out3(decoder_1_out3),
    .out4(decoder_1_out4), .out5(decoder_1_out5), .out6(decoder_1_out6), .sel(cnt_mod_16_w_ld_1_cnt), .en(EN));  // open: out7, out8, out9, out10, out11, out12, out13, out14, out15
  Puerto_E_S puerto_e_s_1 (.Data(8'h10), .En(decoder_1_out0), .Output(Datos_para_CPU));
  Puerto_E_S puerto_e_s_2 (.Data(8'h20), .En(decoder_1_out1), .Output(Datos_para_CPU));
  Puerto_E_S puerto_e_s_3 (.Data(8'h30), .En(decoder_1_out2), .Output(Datos_para_CPU));
  Puerto_E_S puerto_e_s_4 (.Data(8'h40), .En(decoder_1_out3), .Output(Datos_para_CPU));
  Puerto_E_S puerto_e_s_5 (.Data(8'h50), .En(decoder_1_out4), .Output(Datos_para_CPU));
  Puerto_E_S puerto_e_s_6 (.Data(8'h60), .En(decoder_1_out5), .Output(Datos_para_CPU));
  Puerto_E_S puerto_e_s_7 (.Data(8'h70), .En(decoder_1_out6), .Output(Datos_para_CPU));

  // Notes on the sheet:
  //   Generación dirección puerto
  //   Bus de datos
  //   Deco dirección puerto
  //   Puertos E/S
endmodule

module CNT_Anillo (
  input  EN,
  input  EN_2,
  input  EN_3,
  input  EN_4,
  output [3:0] Cuenta__decodificada
);

  wire CLK_2_out, CLK_3_out, CLK_4_out, CLK_out, INIT_2_out, INIT_3_out, INIT_CLR_out, INIT_out, q0_q, q1_q,
       q2_q, q3_q, shift_register_1_out, shift_register_1_q0, shift_register_1_q1, shift_register_1_q2,
       shift_register_1_q3, shift_register_2_out;
  wire [1:0] q0_2_q;

  Clock CLK (.out(CLK_out));
  Button INIT (.out(INIT_out));
  Button INIT_CLR (.out(INIT_CLR_out));
  D_Flip_Flop q0 (.clk(CLK_out), .D(q3_q), .Q(q0_q), .preset(INIT_out), .en(EN_2));  // open: Qn, reset
  LED ENABLE_SISTEMA_0 (.in(q0_q));
  Clock CLK_2 (.out(CLK_2_out));
  T_Flip_Flop q0_2 (.clk(CLK_2_out), .T(1'b1), .Q(q0_2_q[0]), .reset(INIT_CLR_out), .en(EN_4));  // open: Qn, preset
  D_Flip_Flop q1 (.clk(CLK_out), .D(q0_q), .Q(q1_q), .en(EN_2), .reset(INIT_out));  // open: Qn, preset
  D_Flip_Flop q2 (.clk(CLK_out), .D(q1_q), .Q(q2_q), .en(EN_2), .reset(INIT_out));  // open: Qn, preset
  LED ENABLE_SISTEMA_1 (.in(q1_q));
  T_Flip_Flop q1_2 (
    .clk(CLK_2_out), .T(q0_2_q[0]), .Q(q0_2_q[1]), .reset(INIT_CLR_out), .en(EN_4));  // open: Qn, preset
  D_Flip_Flop q3 (.clk(CLK_out), .D(q2_q), .Q(q3_q), .en(EN_2), .reset(INIT_out));  // open: Qn, preset
  LED ENABLE_SISTEMA_2 (.in(q2_q));
  LED ENABLE_SISTEMA_3 (.in(q3_q));
  Decoder #(.select(2), .disabled(0), .enable("false")) decoder_1 (
    .out0(Cuenta__decodificada[0]), .out1(Cuenta__decodificada[1]), .out2(Cuenta__decodificada[2]),
    .out3(Cuenta__decodificada[3]), .sel(q0_2_q));
  Button INIT_2 (.out(INIT_2_out));
  Shift_Register #(.length(4)) shift_register_1 (
    .shift(EN), .in(shift_register_1_out), .clk(CLK_3_out), .out(shift_register_1_out), .load(INIT_2_out),
    .d0(1'b1), .q0(shift_register_1_q0), .d1(1'b0), .q1(shift_register_1_q1), .d2(1'b0),
    .q2(shift_register_1_q2), .d3(1'b0), .q3(shift_register_1_q3));  // open: clr
  Clock CLK_3 (.out(CLK_3_out));
  LED led_1 (.in(shift_register_1_q0));
  Button INIT_3 (.out(INIT_3_out));
  Clock CLK_4 (.out(CLK_4_out));
  LED led_2 (.in(shift_register_1_q3));
  LED led_3 (.in(shift_register_1_q2));
  LED led_4 (.in(shift_register_1_q1));
  Shift_Register #(.length(4)) shift_register_2 (
    .shift(EN_3), .in(shift_register_2_out), .clk(CLK_4_out), .out(shift_register_2_out), .load(INIT_3_out),
    .d0(1'b1), .d1(1'b0), .d2(1'b0), .d3(1'b0));  // open: clr, q0, q1, q2, q3
  Shift_Register #(.length(4)) shift_register_3 ();  // open: shift, in, clk, out, load, clr, d0, q0, d1, q1, d2, q2, d3, q3

  // Notes on the sheet:
  //   Cuenta
endmodule

module CNT_Anillo__w__J_K (
  input  EN
);

  wire CLK_out, INIT_CLR_out, q0_q, q0_qn, q1_q, q1_qn, q2_q, q2_qn;

  Clock CLK (.out(CLK_out));
  Button INIT_CLR (.out(INIT_CLR_out));
  J_K_Flip_Flop q0 (
    .J(q2_q), .clk(CLK_out), .K(q2_qn), .Q(q0_q), .Qn(q0_qn), .preset(INIT_CLR_out), .en(EN));  // open: reset
  J_K_Flip_Flop q2 (
    .J(q1_q), .clk(CLK_out), .K(q1_qn), .Q(q2_q), .Qn(q2_qn), .en(EN), .reset(INIT_CLR_out));  // open: preset
  J_K_Flip_Flop q1 (
    .J(q0_q), .clk(CLK_out), .K(q0_qn), .Q(q1_q), .Qn(q1_qn), .en(EN), .reset(INIT_CLR_out));  // open: preset
endmodule

module CNT_Anillo__MOD7 (
  input  CLK,
  input  EN,
  input  INIT,
  output out_4,
  output out_5,
  output out_6,
  output out_7,
  output out_8,
  output out_9,
  output out_10
);

  D_Flip_Flop q0 (.clk(CLK), .D(out_10), .Q(out_4), .preset(INIT), .en(EN));  // open: Qn, reset
  D_Flip_Flop q2 (.clk(CLK), .D(out_5), .Q(out_6), .en(EN), .reset(INIT));  // open: Qn, preset
  D_Flip_Flop q1 (.clk(CLK), .D(out_4), .Q(out_5), .en(EN), .reset(INIT));  // open: Qn, preset
  D_Flip_Flop q3 (.clk(CLK), .D(out_6), .Q(out_7), .en(EN), .reset(INIT));  // open: Qn, preset
  D_Flip_Flop q4 (.clk(CLK), .D(out_7), .Q(out_8), .en(EN), .reset(INIT));  // open: Qn, preset
  D_Flip_Flop q5 (.clk(CLK), .D(out_8), .Q(out_9), .en(EN), .reset(INIT));  // open: Qn, preset
  D_Flip_Flop q6 (.clk(CLK), .D(out_9), .Q(out_10), .en(EN), .reset(INIT));  // open: Qn, preset
endmodule

module \Aplicación_CNT_Anillo  (
  input  EN,
  output [7:0] Datos_para_CPU
);

  wire CLK_out, cnt_anillo_mod7_1_out_4, cnt_anillo_mod7_1_out_5, cnt_anillo_mod7_1_out_6,
       cnt_anillo_mod7_1_out_7, cnt_anillo_mod7_1_out_8, cnt_anillo_mod7_1_out_9, cnt_anillo_mod7_1_out_10,
       INIT_CLR_out;

  Clock CLK (.out(CLK_out));
  Button INIT_CLR (.out(INIT_CLR_out));
  CNT_Anillo__MOD7 cnt_anillo_mod7_1 (
    .CLK(CLK_out), .EN(EN), .INIT(INIT_CLR_out), .out_4(cnt_anillo_mod7_1_out_4),
    .out_5(cnt_anillo_mod7_1_out_5), .out_6(cnt_anillo_mod7_1_out_6), .out_7(cnt_anillo_mod7_1_out_7),
    .out_8(cnt_anillo_mod7_1_out_8), .out_9(cnt_anillo_mod7_1_out_9), .out_10(cnt_anillo_mod7_1_out_10));
  // Probe on Datos_para_CPU
  Puerto_E_S puerto_e_s_1 (.Data(8'h10), .En(cnt_anillo_mod7_1_out_4), .Output(Datos_para_CPU));
  Puerto_E_S puerto_e_s_2 (.Data(8'h20), .En(cnt_anillo_mod7_1_out_5), .Output(Datos_para_CPU));
  Puerto_E_S puerto_e_s_3 (.Data(8'h30), .En(cnt_anillo_mod7_1_out_6), .Output(Datos_para_CPU));
  Puerto_E_S puerto_e_s_4 (.Data(8'h40), .En(cnt_anillo_mod7_1_out_7), .Output(Datos_para_CPU));
  Puerto_E_S puerto_e_s_5 (.Data(8'h50), .En(cnt_anillo_mod7_1_out_8), .Output(Datos_para_CPU));
  Puerto_E_S puerto_e_s_6 (.Data(8'h60), .En(cnt_anillo_mod7_1_out_9), .Output(Datos_para_CPU));
  Puerto_E_S puerto_e_s_7 (.Data(8'h70), .En(cnt_anillo_mod7_1_out_10), .Output(Datos_para_CPU));

  // Notes on the sheet:
  //   Generación dirección puerto
  //   Deco dirección puerto
  //   Bus de datos
  //   Puertos E/S
endmodule

module CNT_Johnson (
  input  EN,
  input  EN_2
);

  wire CLK_2_out, CLK_out, INIT_CLR_out, INIT_out, not_1_out, q0_q, q1_q, q2_q, q3_qn, shift_register_1_out;

  D_Flip_Flop q0 (.clk(CLK_out), .D(q3_qn), .Q(q0_q), .en(EN), .reset(INIT_CLR_out));  // open: Qn, preset
  Clock CLK (.out(CLK_out));
  Button INIT_CLR (.out(INIT_CLR_out));
  D_Flip_Flop q1 (.clk(CLK_out), .D(q0_q), .Q(q1_q), .en(EN), .reset(INIT_CLR_out));  // open: Qn, preset
  Shift_Register #(.length(4)) shift_register_1 (
    .shift(EN_2), .in(not_1_out), .clk(CLK_2_out), .out(shift_register_1_out), .clr(INIT_out));  // open: load, d0, q0, d1, q1, d2, q2, d3, q3
  Clock CLK_2 (.out(CLK_2_out));
  Button INIT (.out(INIT_out));
  D_Flip_Flop q2 (.clk(CLK_out), .D(q1_q), .Q(q2_q), .en(EN), .reset(INIT_CLR_out));  // open: Qn, preset
  not not_1 (not_1_out, shift_register_1_out);
  D_Flip_Flop q3 (.clk(CLK_out), .D(q2_q), .Qn(q3_qn), .en(EN), .reset(INIT_CLR_out));  // open: Q, preset
endmodule

module CNT_Johnson__w__J_K (
  input  EN
);

  wire CLK_out, INIT_CLR_out, q0_q, q0_qn, q1_q, q1_qn, q2_2_q, q2_2_qn, q2_q, q2_qn;

  Clock CLK (.out(CLK_out));
  Button INIT_CLR (.out(INIT_CLR_out));
  J_K_Flip_Flop q0 (
    .J(q2_2_qn), .clk(CLK_out), .K(q2_2_q), .Q(q0_q), .Qn(q0_qn), .en(EN), .reset(INIT_CLR_out));  // open: preset
  J_K_Flip_Flop q1 (
    .J(q0_q), .clk(CLK_out), .K(q0_qn), .Q(q1_q), .Qn(q1_qn), .en(EN), .reset(INIT_CLR_out));  // open: preset
  J_K_Flip_Flop q2 (
    .J(q1_q), .clk(CLK_out), .K(q1_qn), .Q(q2_q), .Qn(q2_qn), .en(EN), .reset(INIT_CLR_out));  // open: preset
  J_K_Flip_Flop q2_2 (
    .J(q2_q), .clk(CLK_out), .K(q2_qn), .Q(q2_2_q), .Qn(q2_2_qn), .en(EN), .reset(INIT_CLR_out));  // open: preset
endmodule

module CNT_Jonhson__w__deco (
  input  EN,
  output G4,
  output G5,
  output G6,
  output G7,
  output G0,
  output G1,
  output G2,
  output G3
);

  wire CLK_out, INIT_CLR_out, q0_q, q1_q, q2_q, q3_q, q3_qn;

  Clock CLK (.out(CLK_out));
  Button INIT_CLR (.out(INIT_CLR_out));
  and q0q3 (G4, q0_q, q3_q);
  and q0_prime_q1 (G5, ~q0_q, q1_q);  // AND_Gate
  D_Flip_Flop q0 (.clk(CLK_out), .D(q3_qn), .Q(q0_q), .en(EN), .reset(INIT_CLR_out));  // open: Qn, preset
  and q0_prime_q3_prime (G0, ~q0_q, q3_qn);  // AND_Gate
  and q0q1_prime (G1, q0_q, ~q1_q);  // AND_Gate
  and q1_prime_q2 (G6, ~q1_q, q2_q);  // AND_Gate
  D_Flip_Flop q1 (.clk(CLK_out), .D(q0_q), .Q(q1_q), .en(EN), .reset(INIT_CLR_out));  // open: Qn, preset
  and q1q2_prime (G2, q1_q, ~q2_q);  // AND_Gate
  and q2_prime_q3 (G7, ~q2_q, q3_q);  // AND_Gate
  D_Flip_Flop q2 (.clk(CLK_out), .D(q1_q), .Q(q2_q), .en(EN), .reset(INIT_CLR_out));  // open: Qn, preset
  and q2q3_prime (G3, q2_q, q3_qn);
  D_Flip_Flop q3 (.clk(CLK_out), .D(q2_q), .Q(q3_q), .Qn(q3_qn), .en(EN), .reset(INIT_CLR_out));  // open: preset
endmodule

module CNT_Johnson_autocorregido (
  input  EN,
  input  EN_2
);

  wire CLK_2_out, CLK_out, INIT_CLR_2_out, INIT_CLR_out, nor_1_out, nor_2_out, q0_2_q, q0_q, q0_qn, q1_2_qn,
       q1_q, q1_qn, q2_2_q, q2_q, q2_qn, q3_2_qn, q3_q, q3_qn, q3q2_out;

  J_K_Flip_Flop q0 (
    .J(q3_qn), .clk(CLK_out), .K(q3q2_out), .Q(q0_q), .Qn(q0_qn), .en(EN), .reset(INIT_CLR_out));  // open: preset
  Clock CLK (.out(CLK_out));
  and q3q2 (q3q2_out, q2_q, q3_q);
  Button INIT_CLR (.out(INIT_CLR_out));
  Clock CLK_2 (.out(CLK_2_out));
  D_Flip_Flop q0_2 (.clk(CLK_2_out), .D(q3_2_qn), .Q(q0_2_q), .en(EN_2), .reset(INIT_CLR_2_out));  // open: Qn, preset
  Button INIT_CLR_2 (.out(INIT_CLR_2_out));
  J_K_Flip_Flop q1 (
    .J(q0_q), .clk(CLK_out), .K(q0_qn), .Q(q1_q), .Qn(q1_qn), .en(EN), .reset(INIT_CLR_out));  // open: preset
  D_Flip_Flop q1_2 (.clk(CLK_2_out), .D(q0_2_q), .Qn(q1_2_qn), .en(EN_2), .reset(INIT_CLR_2_out));  // open: Q, preset
  nor nor_1 (nor_1_out, q1_2_qn, q0_2_q, q2_2_q);
  J_K_Flip_Flop q2 (
    .J(q1_q), .clk(CLK_out), .K(q1_qn), .Q(q2_q), .Qn(q2_qn), .en(EN), .reset(INIT_CLR_out));  // open: preset
  D_Flip_Flop q2_2 (.clk(CLK_2_out), .D(nor_2_out), .Q(q2_2_q), .en(EN_2), .reset(INIT_CLR_2_out));  // open: Qn, preset
  nor nor_2 (nor_2_out, q1_2_qn, nor_1_out);
  J_K_Flip_Flop q3 (
    .J(q2_q), .clk(CLK_out), .K(q2_qn), .Q(q3_q), .Qn(q3_qn), .en(EN), .reset(INIT_CLR_out));  // open: preset
  D_Flip_Flop q3_2 (.clk(CLK_2_out), .D(q2_2_q), .Qn(q3_2_qn), .en(EN_2), .reset(INIT_CLR_2_out));  // open: Q, preset
endmodule

module CntEvent__w__ev2clk (
  input  EN,
  input  EN_2,
  input  EN_3
);

  wire and_1_out, and_2_out, CLK_2_out, CLK_3_out, CLK_out, Evento_2_out, Evento_3_out, Evento_out,
       INIT_CLR_2_out, INIT_CLR_3_out, INIT_CLR_out, q0_2_qn, q1_2_qn, q2_2_qn;
  wire [3:0] counter_1_q, q0_2_q, q0_q, register_1_q, register_2_q, register_3_q;

  Button Evento (.out(Evento_out));
  Button INIT_CLR (.out(INIT_CLR_out));
  Button Evento_2 (.out(Evento_2_out));
  Button INIT_CLR_2 (.out(INIT_CLR_2_out));
  T_Flip_Flop q1 (.clk(Evento_out), .T(q0_q[0]), .Q(q0_q[1]), .reset(INIT_CLR_out), .en(EN_2));  // open: Qn, preset
  T_Flip_Flop q0 (.clk(Evento_out), .T(1'b1), .Q(q0_q[0]), .reset(INIT_CLR_out), .en(EN_2));  // open: Qn, preset
  T_Flip_Flop q0_2 (
    .clk(Evento_2_out), .T(1'b1), .Q(q0_2_q[0]), .Qn(q0_2_qn), .reset(INIT_CLR_2_out), .en(EN_3));  // open: preset
  and and_1 (and_1_out, q0_q[1], q0_q[0]);
  T_Flip_Flop q1_2 (
    .clk(q0_2_qn), .T(1'b1), .Q(q0_2_q[1]), .Qn(q1_2_qn), .reset(INIT_CLR_2_out), .en(EN_3));  // open: preset
  T_Flip_Flop q2 (.clk(Evento_out), .T(and_1_out), .Q(q0_q[2]), .reset(INIT_CLR_out), .en(EN_2));  // open: Qn, preset
  and and_2 (and_2_out, q0_q[2], and_1_out);
  T_Flip_Flop q2_2 (
    .clk(q1_2_qn), .T(1'b1), .Q(q0_2_q[2]), .Qn(q2_2_qn), .reset(INIT_CLR_2_out), .en(EN_3));  // open: preset
  T_Flip_Flop q3 (.clk(Evento_out), .T(and_2_out), .Q(q0_q[3]), .reset(INIT_CLR_out), .en(EN_2));  // open: Qn, preset
  T_Flip_Flop q3_2 (.clk(q2_2_qn), .T(1'b1), .Q(q0_2_q[3]), .reset(INIT_CLR_2_out), .en(EN_3));  // open: Qn, preset
  Hex_Digit_Display hex_digit_display_1 (.value(q0_q));  // open: dp
  Clock CLK (.out(CLK_out));
  Hex_Digit_Display hex_digit_display_2 (.value(q0_2_q));  // open: dp
  Register #(.width(4)) register_1 (.D(q0_2_q), .Q(register_1_q), .clk(CLK_2_out), .clr(INIT_CLR_2_out));  // open: en
  Clock CLK_2 (.out(CLK_2_out));
  Hex_Digit_Display hex_digit_display_3 (.value(register_2_q));  // open: dp
  Register #(.width(4)) register_2 (.D(q0_q), .Q(register_2_q), .clk(CLK_out), .clr(INIT_CLR_out));  // open: en
  Hex_Digit_Display hex_digit_display_4 (.value(register_1_q));  // open: dp
  Button Evento_3 (.out(Evento_3_out));
  // Probe on register_3_q
  // Probe on counter_1_q
  Register #(.width(4)) register_3 (
    .D(counter_1_q), .Q(register_3_q), .clk(CLK_3_out), .clr(INIT_CLR_3_out));  // open: en
  Counter #(.width(4), .max('hf)) counter_1 (
    .count(EN), .Q(counter_1_q), .clk(Evento_3_out), .clr(INIT_CLR_3_out));  // open: load, D, carry
  Clock CLK_3 (.out(CLK_3_out));
  Button INIT_CLR_3 (.out(INIT_CLR_3_out));

  // Notes on the sheet:
  //   Asinc.
  //   Asinc.
  //   Sinc.
  //   Sinc.
endmodule

module CntEventAut_Mealy (
  input  EN
);

  wire and_1_out, and_2_out, and_3_out, and_4_out, and_5_out, CLK_2_out, CLK_3_out, CLK_out, d_ff_1_qn,
       d_ff_2_qn, Evento_2_out, Evento_3_out, Evento_out, INIT_CLR_2_out, INIT_CLR_3_out, INIT_CLR_out;
  wire [3:0] counter_1_q, counter_2_q, q0_q, register_1_q;

  Clock CLK (.out(CLK_out));
  Button Evento (.out(Evento_out));
  Button INIT_CLR (.out(INIT_CLR_out));
  Button Evento_2 (.out(Evento_2_out));
  Clock CLK_2 (.out(CLK_2_out));
  Button INIT_CLR_2 (.out(INIT_CLR_2_out));
  D_Flip_Flop d_ff_1 (.clk(CLK_out), .D(Evento_out), .Qn(d_ff_1_qn), .reset(INIT_CLR_out));  // open: Q, preset, en
  and and_1 (and_1_out, d_ff_1_qn, Evento_out);
  // Probe on counter_1_q
  Counter #(.width(4), .max('hf)) counter_1 (
    .count(1'b1), .Q(counter_1_q), .clk(Evento_2_out), .clr(INIT_CLR_2_out));  // open: load, D, carry
  Register #(.width(4)) register_1 (
    .D(counter_1_q), .Q(register_1_q), .clk(CLK_2_out), .clr(INIT_CLR_2_out));  // open: en
  T_Flip_Flop q0 (.clk(CLK_out), .T(and_1_out), .Q(q0_q[0]), .reset(INIT_CLR_out), .en(EN));  // open: Qn, preset
  // Probe on register_1_q
  and and_2 (and_2_out, q0_q[0], and_1_out);
  Button Evento_3 (.out(Evento_3_out));
  Clock CLK_3 (.out(CLK_3_out));
  Button INIT_CLR_3 (.out(INIT_CLR_3_out));
  T_Flip_Flop q1 (.clk(CLK_out), .T(and_2_out), .Q(q0_q[1]), .reset(INIT_CLR_out), .en(EN));  // open: Qn, preset
  and and_3 (and_3_out, q0_q[1], and_2_out);
  D_Flip_Flop d_ff_2 (
    .clk(CLK_3_out), .D(Evento_3_out), .Qn(d_ff_2_qn), .reset(INIT_CLR_3_out));  // open: Q, preset, en
  and and_4 (and_4_out, d_ff_2_qn, Evento_3_out);
  T_Flip_Flop q2 (.clk(CLK_out), .T(and_3_out), .Q(q0_q[2]), .reset(INIT_CLR_out), .en(EN));  // open: Qn, preset
  // Probe on counter_2_q
  Counter #(.width(4), .max('hf)) counter_2 (
    .count(and_4_out), .Q(counter_2_q), .clk(CLK_3_out), .clr(INIT_CLR_3_out));  // open: load, D, carry
  and and_5 (and_5_out, q0_q[2], and_3_out);
  // Probe on q0_q
  T_Flip_Flop q3 (.clk(CLK_out), .T(and_5_out), .Q(q0_q[3]), .reset(INIT_CLR_out), .en(EN));  // open: Qn, preset

  // Notes on the sheet:
  //   CNT
  //   Reg. D
  //   EvEN
  //   CNT
endmodule

module CntEventAut_Moore (
  input  EN
);

  wire and_1_out, and_2_out, and_3_out, and_4_out, and_5_out, and_6_out, and_7_out, CLK_2_out, CLK_out,
       Evento_2_out, Evento_out, INIT_CLR_2_out, INIT_CLR_out, j_k_ff_1_q, j_k_ff_2_q, j_k_ff_3_qn,
       j_k_ff_4_qn, not_1_out, not_2_out;
  wire [3:0] counter_1_q, q0_q;

  Clock CLK (.out(CLK_out));
  Button Evento (.out(Evento_out));
  Button INIT_CLR (.out(INIT_CLR_out));
  Button Evento_2 (.out(Evento_2_out));
  Clock CLK_2 (.out(CLK_2_out));
  Button INIT_CLR_2 (.out(INIT_CLR_2_out));
  J_K_Flip_Flop j_k_ff_1 (
    .J(and_1_out), .clk(CLK_out), .K(1'b1), .Q(j_k_ff_1_q), .en(EN), .reset(INIT_CLR_out));  // open: Qn, preset
  and and_1 (and_1_out, Evento_out, j_k_ff_3_qn);
  and and_2 (and_2_out, Evento_2_out, j_k_ff_4_qn);
  and and_3 (and_3_out, Evento_out, j_k_ff_1_q);
  not not_1 (not_1_out, Evento_out);
  and and_4 (and_4_out, Evento_2_out, j_k_ff_2_q);
  J_K_Flip_Flop j_k_ff_2 (
    .J(and_2_out), .clk(CLK_2_out), .K(1'b1), .Q(j_k_ff_2_q), .reset(INIT_CLR_2_out));  // open: Qn, preset, en
  not not_2 (not_2_out, Evento_2_out);
  J_K_Flip_Flop j_k_ff_3 (
    .J(and_3_out), .clk(CLK_out), .K(not_1_out), .Qn(j_k_ff_3_qn), .en(EN), .reset(INIT_CLR_out));  // open: Q, preset
  J_K_Flip_Flop j_k_ff_4 (
    .J(and_4_out), .clk(CLK_2_out), .K(not_2_out), .Qn(j_k_ff_4_qn), .reset(INIT_CLR_2_out));  // open: Q, preset, en
  T_Flip_Flop q0 (.clk(CLK_out), .T(j_k_ff_1_q), .Q(q0_q[0]), .reset(INIT_CLR_out), .en(EN));  // open: Qn, preset
  // Probe on counter_1_q
  Counter #(.width(4), .max('hf)) counter_1 (
    .count(j_k_ff_2_q), .Q(counter_1_q), .clk(CLK_2_out), .clr(INIT_CLR_2_out));  // open: load, D, carry
  and and_5 (and_5_out, q0_q[0], j_k_ff_1_q);
  T_Flip_Flop q1 (.clk(CLK_out), .T(and_5_out), .Q(q0_q[1]), .reset(INIT_CLR_out), .en(EN));  // open: Qn, preset
  and and_6 (and_6_out, q0_q[1], and_5_out);
  T_Flip_Flop q2 (.clk(CLK_out), .T(and_6_out), .Q(q0_q[2]), .reset(INIT_CLR_out), .en(EN));  // open: Qn, preset
  T_Flip_Flop q3 (.clk(CLK_out), .T(and_7_out), .Q(q0_q[3]), .reset(INIT_CLR_out), .en(EN));  // open: Qn, preset
  and and_7 (and_7_out, q0_q[2], and_6_out);
  Hex_Digit_Display hex_digit_display_1 (.value(q0_q));  // open: dp

  // Notes on the sheet:
  //   EvEN
  //   CNT
endmodule

module Temporizador (
  input  CTEN,
  input  CTEN_2
);

  wire and_1_out, and_2_out, CLK_2_out, CLK_out, CLR_2_out, CLR_out, counter_1_carry, counter_2_carry;

  Counter #(.width(4), .max('h6), .ongoal("stay")) counter_1 (
    .count(CTEN), .carry(counter_1_carry), .clk(CLK_out), .clr(CLR_out));  // open: load, D, Q
  Clock CLK (.out(CLK_out));
  and and_1 (and_1_out, CTEN, ~counter_1_carry);  // AND_Gate
  LED \Acción  (.in(and_1_out));
  Button CLR (.out(CLR_out));
  Counter #(.width(4), .max('h6), .ongoal("stay")) counter_2 (
    .count(CTEN_2), .carry(counter_2_carry), .clk(CLK_2_out), .clr(CLR_2_out));  // open: load, D, Q
  Clock CLK_2 (.out(CLK_2_out));
  LED \Acción_2  (.in(and_2_out));
  and and_2 (and_2_out, CTEN_2, counter_2_carry);
  Button CLR_2 (.out(CLR_2_out));

  // Notes on the sheet:
  //   t (s)
  //   (1 Hz)
  //   Timer (desactivación retardada)
  //   CTEN*TC'
  //   t (s)
  //   (1 Hz)
  //   Timer (activación retardada)
  //   CTEN*TC
endmodule

module Temporizador_full (
  input  CTEN,
  output TC,
  output [3:0] CNT
);

  wire and_1_out, CLK_out, INIT_CLR_out, or_1_out, q1q0_out, q2q1q0_out, q3_prime_q0_out, q3_qn;

  Button INIT_CLR (.out(INIT_CLR_out));
  Clock CLK (.out(CLK_out));
  and and_1 (and_1_out, ~TC, CTEN);  // AND_Gate
  and q3_prime_q0 (q3_prime_q0_out, CNT[0], q3_qn);
  J_K_Flip_Flop q0 (
    .J(1'b1), .clk(CLK_out), .K(1'b1), .Q(CNT[0]), .en(and_1_out), .reset(INIT_CLR_out));  // open: Qn, preset
  J_K_Flip_Flop q1 (
    .J(q3_prime_q0_out), .clk(CLK_out), .K(q3_prime_q0_out), .Q(CNT[1]), .en(and_1_out), .reset(INIT_CLR_out));  // open: Qn, preset
  and q1q0 (q1q0_out, CNT[0], CNT[1]);
  and q3q0 (TC, CNT[3], CNT[0]);
  J_K_Flip_Flop q2 (
    .J(q1q0_out), .clk(CLK_out), .K(q1q0_out), .Q(CNT[2]), .en(and_1_out), .reset(INIT_CLR_out));  // open: Qn, preset
  and q2q1q0 (q2q1q0_out, q1q0_out, CNT[2]);
  or or_1 (or_1_out, TC, q2q1q0_out);
  J_K_Flip_Flop q3 (
    .J(or_1_out), .clk(CLK_out), .K(or_1_out), .Q(CNT[3]), .Qn(q3_qn), .en(and_1_out), .reset(INIT_CLR_out));  // open: preset
  // Probe on CNT
endmodule

module CNTSincGrayMod8 (
  input  EN,
  output [2:0] CNT_Gray
);

  wire and_1_out, and_2_out, and_3_out, and_4_out, CLK_out, INIT_CLR_out, q0_qn, q1_qn, q2_qn, xnor_1_out,
       xor_1_out;

  xnor xnor_1 (xnor_1_out, CNT_Gray[1], CNT_Gray[2]);
  xor xor_1 (xor_1_out, CNT_Gray[1], CNT_Gray[2]);
  Clock CLK (.out(CLK_out));
  Button INIT_CLR (.out(INIT_CLR_out));
  J_K_Flip_Flop q0 (
    .J(xnor_1_out), .clk(CLK_out), .K(xor_1_out), .Q(CNT_Gray[0]), .Qn(q0_qn), .en(EN), .reset(INIT_CLR_out));  // open: preset
  and and_1 (and_1_out, CNT_Gray[0], q2_qn);
  and and_2 (and_2_out, CNT_Gray[0], CNT_Gray[2]);
  J_K_Flip_Flop q1 (
    .J(and_1_out), .clk(CLK_out), .K(and_2_out), .Q(CNT_Gray[1]), .Qn(q1_qn), .en(EN), .reset(INIT_CLR_out));  // open: preset
  and and_3 (and_3_out, CNT_Gray[1], q0_qn);
  and and_4 (and_4_out, q1_qn, q0_qn);
  J_K_Flip_Flop q2 (
    .J(and_3_out), .clk(CLK_out), .K(and_4_out), .Q(CNT_Gray[2]), .Qn(q2_qn), .en(EN), .reset(INIT_CLR_out));  // open: preset
endmodule

module CNTSincGray_from_bin (
  input  EN,
  output [2:0] CNT_bin,
  output [2:0] CNT_Gray
);

  wire CLK_out, INIT_CLR_out, q1q0_out;

  Clock CLK (.out(CLK_out));
  Button INIT_CLR (.out(INIT_CLR_out));
  T_Flip_Flop q0 (.clk(CLK_out), .T(1'b1), .Q(CNT_bin[0]), .reset(INIT_CLR_out), .en(EN));  // open: Qn, preset
  and q1q0 (q1q0_out, CNT_bin[0], CNT_bin[1]);
  T_Flip_Flop q1 (.clk(CLK_out), .T(CNT_bin[0]), .Q(CNT_bin[1]), .reset(INIT_CLR_out), .en(EN));  // open: Qn, preset
  T_Flip_Flop q2 (.clk(CLK_out), .T(q1q0_out), .Q(CNT_bin[2]), .reset(INIT_CLR_out), .en(EN));  // open: Qn, preset
  // Probe on CNT_bin
  // Probe on {CNT_bin[2], CNT_Gray[1:0]}
  xor xor_1 (CNT_Gray[1], CNT_bin[2], CNT_bin[1]);
  xor xor_2 (CNT_Gray[0], CNT_bin[1], CNT_bin[0]);

  assign CNT_Gray[2] = CNT_bin[2];
endmodule

module CNTSincGrayMod8__w__DEC (
  output [2:0] out_1
);

  wire CLK_out, decoder_1_out0, decoder_1_out1, decoder_1_out2, decoder_1_out3, decoder_1_out4,
       decoder_1_out5, decoder_1_out6, decoder_1_out7, INIT_CLR_out, or_1_out, or_2_out;

  Decoder #(.select(3), .disabled(0), .enable("false")) decoder_1 (
    .out0(decoder_1_out0), .out1(decoder_1_out1), .out2(decoder_1_out2), .out3(decoder_1_out3),
    .out4(decoder_1_out4), .out5(decoder_1_out5), .out6(decoder_1_out6), .out7(decoder_1_out7), .sel(out_1));
  Clock CLK (.out(CLK_out));
  or or_1 (or_1_out, decoder_1_out0, decoder_1_out6);
  or or_2 (or_2_out, decoder_1_out3, decoder_1_out5);
  J_K_Flip_Flop q2 (
    .J(decoder_1_out2), .clk(CLK_out), .K(decoder_1_out4), .Q(out_1[2]), .reset(INIT_CLR_out));  // open: Qn, preset, en
  J_K_Flip_Flop q1 (
    .J(decoder_1_out1), .clk(CLK_out), .K(decoder_1_out7), .Q(out_1[1]), .reset(INIT_CLR_out));  // open: Qn, preset, en
  J_K_Flip_Flop q0 (
    .J(or_1_out), .clk(CLK_out), .K(or_2_out), .Q(out_1[0]), .reset(INIT_CLR_out));  // open: Qn, preset, en
  Button INIT_CLR (.out(INIT_CLR_out));
endmodule

module CNTSincGrayMod8__w__MUX (
  output [2:0] out_1
);

  wire CLK_out, INIT_CLR_out;
  wire [5:0] multiplexer_1_out;

  Multiplexer #(.select(3), .width(6), .disabled(0), .enable("false")) multiplexer_1 (
    .in0(6'b000010), .in1(6'b001000), .in2(6'b100000), .in3(6'b000001), .in4(6'b010000), .in5(6'b000001),
    .in6(6'b000010), .in7(6'b000100), .out(multiplexer_1_out), .sel(out_1));
  Clock CLK (.out(CLK_out));
  J_K_Flip_Flop q2 (
    .J(multiplexer_1_out[5]), .clk(CLK_out), .K(multiplexer_1_out[4]), .Q(out_1[2]), .reset(INIT_CLR_out));  // open: Qn, preset, en
  J_K_Flip_Flop q1 (
    .J(multiplexer_1_out[3]), .clk(CLK_out), .K(multiplexer_1_out[2]), .Q(out_1[1]), .reset(INIT_CLR_out));  // open: Qn, preset, en
  J_K_Flip_Flop q0 (
    .J(multiplexer_1_out[1]), .clk(CLK_out), .K(multiplexer_1_out[0]), .Q(out_1[0]), .reset(INIT_CLR_out));  // open: Qn, preset, en
  Button INIT_CLR (.out(INIT_CLR_out));
endmodule

module CNTSincIncomp___INIT_0 (
  input  EN
);

  wire and_1_out, CLK_out, INIT_CLR_out, q0_qn, q1_q, q1_qn, q2_qn;

  Clock CLK (.out(CLK_out));
  D_Flip_Flop q2 (.clk(CLK_out), .D(and_1_out), .Qn(q2_qn), .en(EN), .reset(INIT_CLR_out));  // open: Q, preset
  Button INIT_CLR (.out(INIT_CLR_out));
  and and_1 (and_1_out, q1_q, q0_qn);
  T_Flip_Flop q1 (.clk(CLK_out), .T(q2_qn), .Q(q1_q), .Qn(q1_qn), .reset(INIT_CLR_out), .en(EN));  // open: preset
  J_K_Flip_Flop q0 (.J(1'b1), .clk(CLK_out), .K(q1_qn), .Qn(q0_qn), .en(EN), .reset(INIT_CLR_out));  // open: Q, preset
endmodule

module CNTSinc__w__START (
  input  EN
);

  wire and_1_out, CLK_out, INIT_out, or_1_out, q0_qn, q1_q, q1_qn, q2_qn, START_qn;

  Clock CLK (.out(CLK_out));
  D_Flip_Flop START (.clk(CLK_out), .D(1'b1), .Qn(START_qn));  // open: Q, preset, en, reset
  Button INIT (.out(INIT_out));
  or or_1 (or_1_out, START_qn, INIT_out);
  D_Flip_Flop q2 (.clk(CLK_out), .D(and_1_out), .Qn(q2_qn), .en(EN), .reset(or_1_out));  // open: Q, preset
  T_Flip_Flop q1 (.clk(CLK_out), .T(q2_qn), .Q(q1_q), .Qn(q1_qn), .preset(or_1_out), .en(EN));  // open: reset
  and and_1 (and_1_out, q1_q, q0_qn);
  J_K_Flip_Flop q0 (.J(1'b1), .clk(CLK_out), .K(q1_qn), .Qn(q0_qn), .preset(or_1_out), .en(EN));  // open: Q, reset
endmodule

module CNTSinc__w__START_Forzado (
  input  EN
);

  wire and_1_out, and_2_out, CLK_out, INIT_out, or_1_out, or_2_out, q0_qn, q1_q, q1_qn, q2_qn, START_qn;

  Clock CLK (.out(CLK_out));
  D_Flip_Flop START (.clk(CLK_out), .D(1'b1), .Qn(START_qn));  // open: Q, preset, en, reset
  Button INIT (.out(INIT_out));
  or or_1 (or_1_out, START_qn, INIT_out);
  and and_1 (and_1_out, q2_qn, q1_q, q0_qn);
  D_Flip_Flop q2 (.clk(CLK_out), .D(and_1_out), .Qn(q2_qn), .en(EN), .reset(or_1_out));  // open: Q, preset
  or or_2 (or_2_out, q2_qn, and_2_out);
  and and_2 (and_2_out, q1_qn, q0_qn);
  T_Flip_Flop q1 (.clk(CLK_out), .T(or_2_out), .Q(q1_q), .Qn(q1_qn), .preset(or_1_out), .en(EN));  // open: reset
  J_K_Flip_Flop q0 (.J(1'b1), .clk(CLK_out), .K(q1_qn), .Qn(q0_qn), .preset(or_1_out), .en(EN));  // open: Q, reset
endmodule
