// Logisim project Cap9_1_Autómatas.circ as structural Verilog: 7 circuits, main circuit Análisis Automáta Moore
module \Análisis_Automáta_Moore  (
  input  X1,
  input  X0,
  output y
);

  wire and_1_out, and_2_out, CLK_out, INIT_CLEAR_out, not_1_out, not_2_out, not_3_out, q1_q, xor_1_out,
       xor_2_out;

  Clock CLK (.out(CLK_out));
  Button INIT_CLEAR (.out(INIT_CLEAR_out));
  and and_1 (and_1_out, X1, X0);
  not not_1 (not_1_out, X0);
  and and_2 (and_2_out, not_1_out, not_2_out);
  not not_2 (not_2_out, X1);
  xor xor_1 (xor_1_out, X1, X0);
  J_K_Flip_Flop q1 (
    .J(and_1_out), .clk(CLK_out), .K(and_2_out), .Q(q1_q), .reset(INIT_CLEAR_out));  // open: Qn, preset, en
  xor xor_2 (xor_2_out, xor_1_out, q1_q);
  not not_3 (not_3_out, xor_2_out);
  J_K_Flip_Flop q0 (
    .J(xor_2_out), .clk(CLK_out), .K(not_3_out), .Q(y), .reset(INIT_CLEAR_out));  // open: Qn, preset, en
endmodule

module RecSec_Moore_____111 (
  input  X,
  input  EN,
  output y
);

  wire CLK_out, INIT_CLR_out, not_1_out, q0_q, q0X_out, q1_prime_X_prime_out, q1_q, q1_qn;

  and q0X (q0X_out, q0_q, X);
  not not_1 (not_1_out, X);
  Clock CLK (.out(CLK_out));
  Button INIT_CLR (.out(INIT_CLR_out));
  J_K_Flip_Flop q1 (
    .J(q0X_out), .clk(CLK_out), .K(not_1_out), .Q(q1_q), .Qn(q1_qn), .en(EN), .reset(INIT_CLR_out));  // open: preset
  or q1_prime_X_prime (q1_prime_X_prime_out, q1_qn, not_1_out);
  J_K_Flip_Flop q0 (
    .J(X), .clk(CLK_out), .K(q1_prime_X_prime_out), .Q(q0_q), .en(EN), .reset(INIT_CLR_out));  // open: Qn, preset
  and q1q0 (y, q1_q, q0_q);
endmodule

module RecSec_111_Moore_w_reg (
  input  EN,
  output y
);

  wire CLK_out, INIT, not_1_out, q0_q, q0X_out, q1_prime_X_prime_out, q1_q, q1_qn, shift_register_1_out;

  Button INIT_CLR (.out(INIT));
  Shift_Register shift_register_1 (
    .in(1'b0), .clk(CLK_out), .out(shift_register_1_out), .load(INIT), .d0(1'b0), .d1(1'b0), .d2(1'b1),
    .d3(1'b1), .d4(1'b1), .d5(1'b1), .d6(1'b0), .d7(1'b0));  // open: shift, clr, q0, q1, q2, q3, q4, q5, q6, q7
  Clock CLK (.out(CLK_out));
  // Probe on shift_register_1_out
  and q0X (q0X_out, q0_q, shift_register_1_out);
  not not_1 (not_1_out, shift_register_1_out);
  J_K_Flip_Flop q1 (
    .J(q0X_out), .clk(CLK_out), .K(not_1_out), .Q(q1_q), .Qn(q1_qn), .en(EN), .reset(INIT));  // open: preset
  or q1_prime_X_prime (q1_prime_X_prime_out, q1_qn, not_1_out);
  J_K_Flip_Flop q0 (
    .J(shift_register_1_out), .clk(CLK_out), .K(q1_prime_X_prime_out), .Q(q0_q), .en(EN), .reset(INIT));  // open: Qn, preset
  and q1q0 (y, q1_q, q0_q);
endmodule

module RecSec_11_Mealy_w_reg (
  output S
);

  wire button_1_out, clock_1_out, nand_1_out, or_1_out, q0_q, q0E_out, q1_q, shift_register_1_out, xor_1_out;
  wire [3:0] counter_1_q;

  Clock clock_1 (.out(clock_1_out));
  Button button_1 (.out(button_1_out));
  Shift_Register shift_register_1 (
    .in(1'b0), .clk(or_1_out), .out(shift_register_1_out), .load(button_1_out), .d0(1'b1), .d1(1'b1),
    .d2(1'b0), .d3(1'b1), .d4(1'b1), .d5(1'b0), .d6(1'b1), .d7(1'b0));  // open: shift, clr, q0, q1, q2, q3, q4, q5, q6, q7
  or or_1 (or_1_out, clock_1_out, button_1_out);
  xor xor_1 (xor_1_out, q1_q, shift_register_1_out);
  nand nand_1 (nand_1_out, q1_q, shift_register_1_out);
  J_K_Flip_Flop q0 (
    .J(xor_1_out), .clk(clock_1_out), .K(nand_1_out), .Q(q0_q), .reset(button_1_out));  // open: Qn, preset, en
  and q0E (q0E_out, shift_register_1_out, q0_q);
  and q1q0E (S, q0E_out, q1_q);
  J_K_Flip_Flop q1 (.J(q0E_out), .clk(clock_1_out), .K(q0_q), .Q(q1_q), .reset(button_1_out));  // open: Qn, preset, en
  Hex_Digit_Display hex_digit_display_1 (.value(counter_1_q));  // open: dp
  Counter #(.width(4), .max('hf)) counter_1 (
    .Q(counter_1_q), .clk(S), .clr(button_1_out));  // open: load, D, count, carry
endmodule

module RecSec_Mealy_____111 (
  input  X,
  input  EN,
  output y
);

  wire CLK_out, INIT_CLR_out, not_1_out, q0_q, q0X_out, q1_prime_X_out, q1_q, q1_qn;

  Clock CLK (.out(CLK_out));
  Button INIT_CLR (.out(INIT_CLR_out));
  and q0X (q0X_out, q0_q, X);
  J_K_Flip_Flop q1 (
    .J(q0X_out), .clk(CLK_out), .K(not_1_out), .Q(q1_q), .Qn(q1_qn), .en(EN), .reset(INIT_CLR_out));  // open: preset
  not not_1 (not_1_out, X);
  and q1X (y, X, q1_q);
  and q1_prime_X (q1_prime_X_out, X, q1_qn);
  J_K_Flip_Flop q0 (
    .J(q1_prime_X_out), .clk(CLK_out), .K(1'b1), .Q(q0_q), .en(EN), .reset(INIT_CLR_out));  // open: Qn, preset
endmodule

module RecSec_Mealy_____111_____sinc (
  input  X,
  input  EN,
  output y,
  output y_star
);

  wire CLK_out, INIT_CLR_out, not_1_out, q0_q, q0X_out, q1_prime_X_out, q1_q, q1_qn;

  Clock CLK (.out(CLK_out));
  Button INIT_CLR (.out(INIT_CLR_out));
  and q0X (q0X_out, q0_q, X);
  J_K_Flip_Flop q1 (
    .J(q0X_out), .clk(CLK_out), .K(not_1_out), .Q(q1_q), .Qn(q1_qn), .en(EN), .reset(INIT_CLR_out));  // open: preset
  not not_1 (not_1_out, X);
  and q1X (y, X, q1_q);
  and q1_prime_X (q1_prime_X_out, X, q1_qn);
  J_K_Flip_Flop q0 (
    .J(q1_prime_X_out), .clk(CLK_out), .K(1'b1), .Q(q0_q), .en(EN), .reset(INIT_CLR_out));  // open: Qn, preset
  D_Flip_Flop d_ff_1 (.clk(CLK_out), .D(y), .Q(y_star));  // open: Qn, preset, en, reset

  // Notes on the sheet:
  //   Asinc.
  //   Sinc.
endmodule

module ReconSec__1101 (
  input  E
);

  wire and_1_out, and_2_out, Q0_q, Q1_q, REC_out, xor_1_out;

  Button REC (.out(REC_out));
  and and_1 (and_1_out, E, Q0_q);
  xor xor_1 (xor_1_out, Q1_q, E);
  J_K_Flip_Flop Q1 (.J(and_1_out), .clk(xor_1_out), .K(Q0_q), .Q(Q1_q));  // open: Qn, preset, en, reset
  J_K_Flip_Flop Q0 (.J(xor_1_out), .clk(REC_out), .K(1'b1), .Q(Q0_q));  // open: Qn, preset, en, reset
  and and_2 (and_2_out, E, Q1_q, Q0_q);
  LED led_1 (.in(and_2_out));

  // Notes on the sheet:
  //   (Sec: 1101)
endmodule
