// Logisim project Cap9_2_SisTemporizados.circ as structural Verilog: 24 circuits, main circuit Semáforo Completo (1 Hz)
module Sec___0_3_2_1_2_1_3___w__trunc_DEC (
  input  En,
  output [1:0] y
);

  wire CLK_out, decoder_1_out0, decoder_1_out2, decoder_1_out3, decoder_1_out4, decoder_1_out5, INIT_CLR_out,
       or_1_out, q1q0_out, q2q1q0_out;
  wire [2:0] q0_q;

  Clock CLK (.out(CLK_out));
  Button INIT_CLR (.out(INIT_CLR_out));
  or or_1 (or_1_out, INIT_CLR_out, q2q1q0_out);
  and q2q1q0 (q2q1q0_out, q0_q[0], q0_q[1], q0_q[2]);
  T_Flip_Flop q0 (.clk(CLK_out), .T(1'b1), .Q(q0_q[0]), .reset(or_1_out), .en(En));  // open: Qn, preset
  and q1q0 (q1q0_out, q0_q[0], q0_q[1]);
  T_Flip_Flop q1 (.clk(CLK_out), .T(q0_q[0]), .Q(q0_q[1]), .reset(or_1_out), .en(En));  // open: Qn, preset
  T_Flip_Flop q2 (.clk(CLK_out), .T(q1q0_out), .Q(q0_q[2]), .reset(or_1_out), .en(En));  // open: Qn, preset
  Decoder #(.select(3), .enable("false")) decoder_1 (
    .out0(decoder_1_out0), .out2(decoder_1_out2), .out3(decoder_1_out3), .out4(decoder_1_out4),
    .out5(decoder_1_out5), .sel(q0_q));  // open: out1, out6, out7
  // Probe on y
  nor nor_1 (y[1], decoder_1_out0, decoder_1_out3, decoder_1_out5);
  nor nor_2 (y[0], decoder_1_out0, decoder_1_out2, decoder_1_out4);
endmodule

module Sec___0_3_2_1_2_1_3___w__trunc_asincr (
  output [1:0] y
);

  wire CLK_out, INIT_CLR_out, or_1_out, q0_q, q0_qn, q1_q, q1_qn, q1q0_out, q1q0_prime_out,
       q2_prime_q1_prime_q0_out, q2_q, q2_qn, q2q0_prime_out, q2q1_out, q2q1q0_out;

  Clock CLK (.out(CLK_out));
  Button INIT_CLR (.out(INIT_CLR_out));
  or or_1 (or_1_out, INIT_CLR_out, q2q1q0_out);
  and q2q1q0 (q2q1q0_out, q0_q, q1_q, q2_q);
  T_Flip_Flop q0 (.clk(CLK_out), .T(1'b1), .Q(q0_q), .Qn(q0_qn), .reset(or_1_out));  // open: preset, en
  and q1q0 (q1q0_out, q0_q, q1_q);
  T_Flip_Flop q1 (.clk(CLK_out), .T(q0_q), .Q(q1_q), .Qn(q1_qn), .reset(or_1_out));  // open: preset, en
  T_Flip_Flop q2 (.clk(CLK_out), .T(q1q0_out), .Q(q2_q), .Qn(q2_qn), .reset(or_1_out));  // open: preset, en
  and q2_prime_q1_prime_q0 (q2_prime_q1_prime_q0_out, q0_q, q2_qn, q1_qn);
  and q2q0_prime (q2q0_prime_out, q2_q, q0_qn);
  and q1q0_prime (q1q0_prime_out, q0_qn, q1_q);
  and q2q1 (q2q1_out, q1_q, q2_q);
  // Probe on y
  or or_2 (y[1], q2_prime_q1_prime_q0_out, q2q0_prime_out, q1q0_prime_out);
  or or_3 (y[0], q2q1_out, q0_q);
endmodule

module Sec___0_3_2_1_2_1_3___w__recodific (
  output [1:0] y
);

  wire CLK_out, INIT_CLR_out, q0_qn, q1_prime_q0_out, q1_qn, q1q0_out, q2_prime_q1_out, q2_q,
       q2_q0_prime_out, q2_qn;

  Clock CLK (.out(CLK_out));
  or q2_prime_q1 (q2_prime_q1_out, q2_qn, y[1]);
  Button INIT_CLR (.out(INIT_CLR_out));
  J_K_Flip_Flop q0 (
    .J(1'b1), .clk(CLK_out), .K(q2_prime_q1_out), .Q(y[0]), .Qn(q0_qn), .reset(INIT_CLR_out));  // open: preset, en
  J_K_Flip_Flop q1 (
    .J(1'b1), .clk(CLK_out), .K(q2_q0_prime_out), .Q(y[1]), .Qn(q1_qn), .reset(INIT_CLR_out));  // open: preset, en
  or q2_q0_prime (q2_q0_prime_out, q0_qn, q2_q);
  and q1_prime_q0 (q1_prime_q0_out, y[0], q1_qn);
  and q1q0 (q1q0_out, y[1], y[0]);
  // Probe on y
  J_K_Flip_Flop q2 (
    .J(q1_prime_q0_out), .clk(CLK_out), .K(q1q0_out), .Q(q2_q), .Qn(q2_qn), .reset(INIT_CLR_out));  // open: preset, en
endmodule

module Sec___0_3_2_1_2_1_3___w__recodific__DEC (
  output [1:0] y
);

  wire CLK_out, decoder_1_out1, decoder_1_out3, decoder_1_out5, decoder_1_out7, INIT_CLR_out, not_1_out,
       not_2_out;
  wire [2:2] q2_q;

  Decoder #(.select(3), .enable("false")) decoder_1 (
    .out1(decoder_1_out1), .out3(decoder_1_out3), .out5(decoder_1_out5), .out7(decoder_1_out7),
    .sel({q2_q[2], y}));  // open: out0, out2, out4, out6
  not not_1 (not_1_out, decoder_1_out3);
  not not_2 (not_2_out, decoder_1_out5);
  Clock CLK (.out(CLK_out));
  J_K_Flip_Flop q2 (
    .J(decoder_1_out1), .clk(CLK_out), .K(decoder_1_out7), .Q(q2_q[2]), .reset(INIT_CLR_out));  // open: Qn, preset, en
  J_K_Flip_Flop q1 (.J(1'b1), .clk(CLK_out), .K(not_1_out), .Q(y[1]), .reset(INIT_CLR_out));  // open: Qn, preset, en
  J_K_Flip_Flop q0 (.J(1'b1), .clk(CLK_out), .K(not_2_out), .Q(y[0]), .reset(INIT_CLR_out));  // open: Qn, preset, en
  // Probe on y
  Button INIT_CLR (.out(INIT_CLR_out));
endmodule

module Sec___0_3_2_1_2_1_3___w__trunc_asincr_y_MUX (
  input  INIT_CLR,
  output [1:0] y
);

  wire CLK_out, or_1_out, q0_q, q0_qn, q1_q, q1q0_out, q2_q, q2q1q0_out, xor_1_out;

  Clock CLK (.out(CLK_out));
  and q2q1q0 (q2q1q0_out, q0_q, q1_q, q2_q);
  T_Flip_Flop q0 (.clk(CLK_out), .T(1'b1), .Q(q0_q), .Qn(q0_qn), .reset(or_1_out));  // open: preset, en
  or or_1 (or_1_out, INIT_CLR, q2q1q0_out);
  T_Flip_Flop q1 (.clk(CLK_out), .T(q0_q), .Q(q1_q), .reset(or_1_out));  // open: Qn, preset, en
  and q1q0 (q1q0_out, q0_q, q1_q);
  xor xor_1 (xor_1_out, q1_q, q0_q);
  T_Flip_Flop q2 (.clk(CLK_out), .T(q1q0_out), .Q(q2_q), .reset(or_1_out));  // open: Qn, preset, en
  Multiplexer #(.enable("false")) multiplexer_1 (.in0(xor_1_out), .in1(q0_qn), .out(y[1]), .sel(q2_q));
  Multiplexer #(.enable("false")) multiplexer_2 (.in0(q0_q), .in1(xor_1_out), .out(y[0]), .sel(q2_q));
  // Probe on y
endmodule

module Sec___0_3_2_1_2_1_3___w__trunc_sincr_y_MUX (
  output [1:0] y
);

  wire CLK_out, or_1_out, or_2_out, or_3_out, q0_q, q0_qn, q1_q, q1_qn, q1q0_out, q2_q, q2_qn, q2q1_out,
       xor_1_out;

  or or_1 (or_1_out, q2_qn, q1_qn);
  Clock CLK (.out(CLK_out));
  T_Flip_Flop q0 (.clk(CLK_out), .T(or_1_out), .Q(q0_q), .Qn(q0_qn));  // open: preset, reset, en
  or or_2 (or_2_out, q2q1_out, q0_q);
  and q2q1 (q2q1_out, q2_q, q1_q);
  and q1q0 (q1q0_out, q0_q, q1_q);
  T_Flip_Flop q1 (.clk(CLK_out), .T(or_2_out), .Q(q1_q), .Qn(q1_qn));  // open: preset, reset, en
  xor xor_1 (xor_1_out, q1_q, q0_q);
  or or_3 (or_3_out, q2q1_out, q1q0_out);
  T_Flip_Flop q2 (.clk(CLK_out), .T(or_3_out), .Q(q2_q), .Qn(q2_qn));  // open: preset, reset, en
  Multiplexer #(.enable("false")) multiplexer_1 (.in0(xor_1_out), .in1(q0_qn), .out(y[1]), .sel(q2_q));
  Multiplexer #(.enable("false")) multiplexer_2 (.in0(q0_q), .in1(xor_1_out), .out(y[0]), .sel(q2_q));
  // Probe on y
endmodule

module Sec___0_3_2_1_2_1_3___w__MUX_v3 (
  output [1:0] y,
  output [1:0] y_2
);

  wire CLK_out, INIT_CLR_out;
  wire [2:0] CNT_MOD7_q;

  Counter #(.width(3), .max('h6)) CNT_MOD7 (
    .Q(CNT_MOD7_q), .clk(CLK_out), .clr(INIT_CLR_out));  // open: load, D, count, carry
  Clock CLK (.out(CLK_out));
  Button INIT_CLR (.out(INIT_CLR_out));
  Multiplexer #(.select(3), .width(2), .enable("false")) multiplexer_1 (
    .in0(2'b00), .in1(2'b11), .in2(2'b10), .in3(2'b01), .in4(2'b10), .in5(2'b01), .in6(2'b11), .out(y),
    .sel(CNT_MOD7_q));  // open: in7
  // Probe on CNT_MOD7_q
  // Probe on y
  // Probe on y_2
  ROM #(.addrWidth(3), .dataWidth(2)) rom_1 (.addr(CNT_MOD7_q), .data(y_2));  // open: sel

  // Notes on the sheet:
  //   ROM (con datos precargados)
  //   contents of rom_1 (hex, n*v repeats v):
  //   0 3 2 1 2 1 3
endmodule

module Sec___0_3_2_1_2_1_3___w__ROM (
  output [1:0] y
);

  wire CLK_out, INIT_CLR_out;
  wire [2:0] CNT_MOD7_q;

  Counter #(.width(3), .max('h6)) CNT_MOD7 (
    .Q(CNT_MOD7_q), .clk(CLK_out), .clr(INIT_CLR_out));  // open: load, D, count, carry
  Clock CLK (.out(CLK_out));
  Button INIT_CLR (.out(INIT_CLR_out));
  // Probe on CNT_MOD7_q
  // Probe on y
  ROM #(.addrWidth(3), .dataWidth(2)) rom_1 (.addr(CNT_MOD7_q), .data(y));  // open: sel

  // Notes on the sheet:
  //   ROM (con datos precargados)
  //   contents of rom_1 (hex, n*v repeats v):
  //   0 3 2 1 2 1 3
endmodule

module Sec___0_3_2_1_2_1_3___w__registro (
  output [1:0] y
);

  wire CLK_out, INIT_LD_out;

  Button INIT_LD (.out(INIT_LD_out));
  Shift_Register #(.width(2), .length(7)) shift_register_1 (
    .in(y), .clk(CLK_out), .out(y), .load(INIT_LD_out), .clr(1'b0), .d0(2'b11), .d1(2'b01), .d2(2'b10),
    .d3(2'b01), .d4(2'b10), .d5(2'b11), .d6(2'b00));  // open: shift, q0, q1, q2, q3, q4, q5, q6
  Clock CLK (.out(CLK_out));
  // Probe on y
endmodule

module Sec___0_1_2_3_1_3_2_1___w__MUX (
  output [1:0] y
);

  wire and_1_out, CLK_out, INIT_CLR_out;
  wire [2:0] q0_q;

  Clock CLK (.out(CLK_out));
  Button INIT_CLR (.out(INIT_CLR_out));
  T_Flip_Flop q0 (.clk(CLK_out), .T(1'b1), .Q(q0_q[0]), .reset(INIT_CLR_out));  // open: Qn, preset, en
  T_Flip_Flop q1 (.clk(CLK_out), .T(q0_q[0]), .Q(q0_q[1]), .reset(INIT_CLR_out));  // open: Qn, preset, en
  and and_1 (and_1_out, q0_q[0], q0_q[1]);
  T_Flip_Flop q2 (.clk(CLK_out), .T(and_1_out), .Q(q0_q[2]), .reset(INIT_CLR_out));  // open: Qn, preset, en
  // Probe on y
  Multiplexer #(.select(3), .width(2), .disabled(0), .enable("false")) multiplexer_1 (
    .in0(2'b00), .in1(2'b01), .in2(2'b10), .in3(2'b11), .in4(2'b01), .in5(2'b11), .in6(2'b10), .in7(2'b01),
    .out(y), .sel(q0_q));
endmodule

module Sec___0_1_2_3_1_3_2_1___w__gates (
  output [1:0] y
);

  wire and_1_out, CLK_out, INIT_CLR_out, or_1_out, q0_q, q0_qn, q1_q, q1_qn, q1q0_prime_out, q2_prime_q1_out,
       q2_q, q2_qn, q2q1_prime_out, q2q1_prime_q0_out;

  T_Flip_Flop q0 (.clk(CLK_out), .T(1'b1), .Q(q0_q), .Qn(q0_qn), .reset(INIT_CLR_out));  // open: preset, en
  Clock CLK (.out(CLK_out));
  Button INIT_CLR (.out(INIT_CLR_out));
  and and_1 (and_1_out, q0_q, q1_q);
  T_Flip_Flop q1 (.clk(CLK_out), .T(q0_q), .Q(q1_q), .Qn(q1_qn), .reset(INIT_CLR_out));  // open: preset, en
  T_Flip_Flop q2 (.clk(CLK_out), .T(and_1_out), .Q(q2_q), .Qn(q2_qn), .reset(INIT_CLR_out));  // open: preset, en
  and q1q0_prime (q1q0_prime_out, q0_qn, q1_q);
  and q2_prime_q1 (q2_prime_q1_out, q1_q, q2_qn);
  and q2q1_prime (q2q1_prime_out, q2_q, q1_qn);
  or or_1 (or_1_out, q1q0_prime_out, q2_prime_q1_out);
  or or_2 (y[1], or_1_out, q2q1_prime_q0_out);
  and q2q1_prime_q0 (q2q1_prime_q0_out, q0_q, q2q1_prime_out);
  or or_3 (y[0], q2q1_prime_out, q0_q);
  // Probe on y
endmodule

module Sec___0_1_2_3_1_3_2_1___w__DEC (
  output y1,
  output y0,
  output [1:0] y
);

  wire and_1_out, CLK_out, decoder_1_out0, decoder_1_out2, decoder_1_out3, decoder_1_out5, decoder_1_out6,
       INIT_out;
  wire [2:0] q0_q;

  Clock CLK (.out(CLK_out));
  Button INIT (.out(INIT_out));
  T_Flip_Flop q0 (.clk(CLK_out), .T(1'b1), .Q(q0_q[0]), .reset(INIT_out));  // open: Qn, preset, en
  T_Flip_Flop q1 (.clk(CLK_out), .T(q0_q[0]), .Q(q0_q[1]), .reset(INIT_out));  // open: Qn, preset, en
  and and_1 (and_1_out, q0_q[0], q0_q[1]);
  Decoder #(.select(3), .enable("false")) decoder_1 (
    .out0(decoder_1_out0), .out2(decoder_1_out2), .out3(decoder_1_out3), .out5(decoder_1_out5),
    .out6(decoder_1_out6), .sel(q0_q));  // open: out1, out4, out7
  T_Flip_Flop q2 (.clk(CLK_out), .T(and_1_out), .Q(q0_q[2]), .reset(INIT_out));  // open: Qn, preset, en
  // Probe on y
  or or_1 (y[1], decoder_1_out2, decoder_1_out3, decoder_1_out5, decoder_1_out6);
  nor nor_1 (y[0], decoder_1_out6, decoder_1_out2, decoder_1_out0);

  assign y0 = y[0];
  assign y1 = y[1];
endmodule

module Sec___0_1_2_3_1_3_2_1___w__recodific (
  output [1:0] y
);

  wire and_1_out, and_2_out, and_3_out, CLK_out, q0_q, q0_qn, q1_qn, q2_q, q2_qn, xnor_1_out, xor_1_out;

  Clock CLK (.out(CLK_out));
  xnor xnor_1 (xnor_1_out, y[1], q2_q);
  J_K_Flip_Flop q0 (.J(q2_qn), .clk(CLK_out), .K(xnor_1_out), .Q(q0_q), .Qn(q0_qn));  // open: preset, en, reset
  xor xor_1 (xor_1_out, q0_q, q2_q);
  and and_1 (and_1_out, q0_q, y[1]);
  J_K_Flip_Flop q1 (.J(q0_q), .clk(CLK_out), .K(xor_1_out), .Q(y[1]), .Qn(q1_qn));  // open: preset, en, reset
  and and_2 (and_2_out, q1_qn, q0_qn);
  J_K_Flip_Flop q2 (.J(and_1_out), .clk(CLK_out), .K(and_2_out), .Q(q2_q), .Qn(q2_qn));  // open: preset, en, reset
  or or_1 (y[0], q0_q, and_3_out);
  and and_3 (and_3_out, q2_q, q1_qn);
  // Probe on y
endmodule

module Sec___0_1_2_3_1_3_2_1___w__DEC4all (
  output [1:0] y
);

  wire CLK_out, decoder_1_out0, decoder_1_out1, decoder_1_out2, decoder_1_out3, decoder_1_out4,
       decoder_1_out5, decoder_1_out6, decoder_1_out7, or_1_out, or_2_out, or_3_out, or_4_out;
  wire [2:0] q0_q;

  Clock CLK (.out(CLK_out));
  Decoder #(.select(3), .enable("false")) decoder_1 (
    .out0(decoder_1_out0), .out1(decoder_1_out1), .out2(decoder_1_out2), .out3(decoder_1_out3),
    .out4(decoder_1_out4), .out5(decoder_1_out5), .out6(decoder_1_out6), .out7(decoder_1_out7), .sel(q0_q));
  or or_1 (or_1_out, decoder_1_out0, decoder_1_out2);
  or or_2 (or_2_out, decoder_1_out1, decoder_1_out7);
  or or_3 (or_3_out, decoder_1_out1, decoder_1_out5);
  or or_4 (or_4_out, decoder_1_out3, decoder_1_out6);
  nor nor_1 (y[0], decoder_1_out0, decoder_1_out2, decoder_1_out6);
  or or_5 (y[1], decoder_1_out6, decoder_1_out7, decoder_1_out2, decoder_1_out3);
  J_K_Flip_Flop q0 (.J(or_1_out), .clk(CLK_out), .K(or_2_out), .Q(q0_q[0]));  // open: Qn, preset, en, reset
  J_K_Flip_Flop q1 (.J(or_3_out), .clk(CLK_out), .K(or_4_out), .Q(q0_q[1]));  // open: Qn, preset, en, reset
  J_K_Flip_Flop q2 (.J(decoder_1_out3), .clk(CLK_out), .K(decoder_1_out4), .Q(q0_q[2]));  // open: Qn, preset, en, reset
  // Probe on y
endmodule

module Sec___0_1_2_3_1_3_2_1___w__MUX_v2 (
  output [1:0] y
);

  wire and_1_out, CLK_out, INIT_CLR_out, or_1_out, q0_q, q1_q, q1_qn, q2_q, xor_1_out;

  T_Flip_Flop q0 (.clk(CLK_out), .T(1'b1), .Q(q0_q), .reset(INIT_CLR_out));  // open: Qn, preset, en
  Clock CLK (.out(CLK_out));
  Button INIT_CLR (.out(INIT_CLR_out));
  and and_1 (and_1_out, q0_q, q1_q);
  T_Flip_Flop q1 (.clk(CLK_out), .T(q0_q), .Q(q1_q), .Qn(q1_qn), .reset(INIT_CLR_out));  // open: preset, en
  T_Flip_Flop q2 (.clk(CLK_out), .T(and_1_out), .Q(q2_q), .reset(INIT_CLR_out));  // open: Qn, preset, en
  xor xor_1 (xor_1_out, q1_q, q0_q);
  or or_1 (or_1_out, q0_q, q1_qn);
  Multiplexer #(.enable("false")) multiplexer_1 (.in0(q1_q), .in1(xor_1_out), .out(y[1]), .sel(q2_q));
  // Probe on y
  Multiplexer #(.enable("false")) multiplexer_2 (.in0(q0_q), .in1(or_1_out), .out(y[0]), .sel(q2_q));
endmodule

module \Semáforo_Completo__1_Hz  (
);

  wire and_1_out, CLK_out, INIT_CLR_out, or_1_out, q0_q, q1_q, q1_qn, q1q0_out, q2_q, q2_qn, q2q1_out,
       q2q1_prime_out, q3_prime_q1q0_out, q3_prime_q2_prime_out, q3_q, q3_q2_out, q3_qn;

  Clock CLK (.out(CLK_out));
  Button INIT_CLR (.out(INIT_CLR_out));
  T_Flip_Flop q0 (.clk(CLK_out), .T(1'b1), .Q(q0_q), .reset(INIT_CLR_out));  // open: Qn, preset, en
  T_Flip_Flop q1 (.clk(CLK_out), .T(q0_q), .Q(q1_q), .Qn(q1_qn), .reset(INIT_CLR_out));  // open: preset, en
  and q1q0 (q1q0_out, q1_q, q0_q);
  and q3_prime_q1q0 (q3_prime_q1q0_out, q1q0_out, q3_qn);
  and q2q1_prime (q2q1_prime_out, q1_qn, q2_q);
  and q2q1 (q2q1_out, q1_q, q2_q);
  T_Flip_Flop q2 (
    .clk(CLK_out), .T(q3_prime_q1q0_out), .Q(q2_q), .Qn(q2_qn), .reset(INIT_CLR_out));  // open: preset, en
  and and_1 (and_1_out, q1q0_out, q3_q2_out);
  and q3_prime_q2_prime (q3_prime_q2_prime_out, q2_qn, q3_qn);
  LED \u_Ámbar  (.in(q2q1_prime_out));
  or or_1 (or_1_out, q2q1_out, q3_q);
  LED Rojo (.in(or_1_out));
  T_Flip_Flop q3 (.clk(CLK_out), .T(and_1_out), .Q(q3_q), .Qn(q3_qn), .reset(INIT_CLR_out));  // open: preset, en
  or q3_q2 (q3_q2_out, q3_q, q2_q);
  LED Verde (.in(q3_prime_q2_prime_out));
endmodule

module \Semáforo__trunc__asinc___1_Hz  (
);

  wire CLK_out, INIT_CLR_out, or_1_out, or_2_out, q0_q, q1_q, q1q0_out, q2_q, q2_qn, q2q1_out,
       q2q1_prime_out, q2q1q0_out, q3_prime_q2_prime_out, q3_q, q3_qn, q3q2_out;

  Clock CLK (.out(CLK_out));
  Button INIT_CLR (.out(INIT_CLR_out));
  and q3q2 (q3q2_out, q2_q, q3_q);
  T_Flip_Flop q0 (.clk(CLK_out), .T(1'b1), .Q(q0_q), .reset(or_1_out));  // open: Qn, preset, en
  or or_1 (or_1_out, INIT_CLR_out, q3q2_out);
  T_Flip_Flop q1 (.clk(CLK_out), .T(q0_q), .Q(q1_q), .reset(or_1_out));  // open: Qn, preset, en
  T_Flip_Flop q2 (.clk(CLK_out), .T(q1q0_out), .Q(q2_q), .Qn(q2_qn), .reset(or_1_out));  // open: preset, en
  and q1q0 (q1q0_out, q1_q, q0_q);
  and q2q1q0 (q2q1q0_out, q2_q, q1q0_out);
  and q3_prime_q2_prime (q3_prime_q2_prime_out, q2_qn, q3_qn);
  and q2q1_prime (q2q1_prime_out, q1_q, q2_q);
  and q2q1 (q2q1_out, q1_q, q2_q);
  T_Flip_Flop q3 (.clk(CLK_out), .T(q2q1q0_out), .Q(q3_q), .Qn(q3_qn), .reset(or_1_out));  // open: preset, en
  LED Verde (.in(q3_prime_q2_prime_out));
  LED \u_Ámbar  (.in(q2q1_prime_out));
  or or_2 (or_2_out, q2q1_out, q3_q);
  LED Rojo (.in(or_2_out));
endmodule

module \Semáforo_Simplificado__0_5_Hz  (
);

  wire CLK_out, INIT_CLR_out, or_1_out, or_2_out, q0_q, q0_qn, q1_q, q1_qn, q1q0_2_out, q1q0_out,
       q1q0_prime_out, q2_prime_q0_out, q2_prime_q1_prime_out, q2_q, q2_qn, q2q0_out;

  Clock #(.highDuration(2), .lowDuration(2)) CLK (.out(CLK_out));
  Button INIT_CLR (.out(INIT_CLR_out));
  T_Flip_Flop q0 (.clk(CLK_out), .T(1'b1), .Q(q0_q), .Qn(q0_qn), .reset(INIT_CLR_out));  // open: preset, en
  T_Flip_Flop q1 (.clk(CLK_out), .T(q2_prime_q0_out), .Q(q1_q), .Qn(q1_qn), .reset(INIT_CLR_out));  // open: preset, en
  and q2_prime_q0 (q2_prime_q0_out, q0_q, q2_qn);
  and q1q0 (q1q0_out, q1_q, q0_q);
  and q2q0 (q2q0_out, q0_q, q2_q);
  T_Flip_Flop q2 (.clk(CLK_out), .T(or_1_out), .Q(q2_q), .Qn(q2_qn), .reset(INIT_CLR_out));  // open: preset, en
  or or_1 (or_1_out, q1q0_out, q2q0_out);
  and q2_prime_q1_prime (q2_prime_q1_prime_out, q1_qn, q2_qn);
  and q1q0_prime (q1q0_prime_out, q0_qn, q1_q);
  and q1q0_2 (q1q0_2_out, q0_q, q1_q);
  LED Verde (.in(q2_prime_q1_prime_out));
  LED \u_Ámbar  (.in(q1q0_prime_out));
  LED Rojo (.in(or_2_out));
  or or_2 (or_2_out, q1q0_2_out, q2_q);
endmodule

module \Semáforo_Simplificado_trunc__asinc___0_5_Hz  (
);

  wire CLK_out, INIT_CLR_out, or_1_out, or_2_out, q0_q, q0_qn, q1_q, q1_qn, q1q0_2_out, q1q0_out,
       q1q0_prime_out, q2_prime_q1_prime_out, q2_q, q2_qn, q2q1_out;

  Clock #(.highDuration(2), .lowDuration(2)) CLK (.out(CLK_out));
  Button INIT_CLR (.out(INIT_CLR_out));
  and q2q1 (q2q1_out, q1_q, q2_q);
  T_Flip_Flop q0 (.clk(CLK_out), .T(1'b1), .Q(q0_q), .Qn(q0_qn), .reset(or_1_out));  // open: preset, en
  or or_1 (or_1_out, INIT_CLR_out, q2q1_out);
  T_Flip_Flop q1 (.clk(CLK_out), .T(q0_q), .Q(q1_q), .Qn(q1_qn), .reset(or_1_out));  // open: preset, en
  T_Flip_Flop q2 (.clk(CLK_out), .T(q1q0_out), .Q(q2_q), .Qn(q2_qn), .reset(or_1_out));  // open: preset, en
  and q1q0 (q1q0_out, q1_q, q0_q);
  and q2_prime_q1_prime (q2_prime_q1_prime_out, q1_qn, q2_qn);
  and q1q0_prime (q1q0_prime_out, q0_qn, q1_q);
  and q1q0_2 (q1q0_2_out, q0_q, q1_q);
  LED Verde (.in(q2_prime_q1_prime_out));
  LED \u_Ámbar  (.in(q1q0_prime_out));
  LED Rojo (.in(or_2_out));
  or or_2 (or_2_out, q1q0_2_out, q2_q);
endmodule

module \Semáforo_Simplificado_w_MUX__0_5_Hz  (
);

  wire and_1_out, and_2_out, CLK_out, INIT_CLR_out, or_1_out;
  wire [2:0] multiplexer_1_out, q0_q;

  Clock #(.highDuration(2), .lowDuration(2)) CLK (.out(CLK_out));
  Button INIT_CLR (.out(INIT_CLR_out));
  T_Flip_Flop q0 (.clk(CLK_out), .T(1'b1), .Q(q0_q[0]), .reset(or_1_out));  // open: Qn, preset, en
  or or_1 (or_1_out, INIT_CLR_out, and_1_out);
  and and_1 (and_1_out, q0_q[1], q0_q[2]);
  T_Flip_Flop q1 (.clk(CLK_out), .T(q0_q[0]), .Q(q0_q[1]), .reset(or_1_out));  // open: Qn, preset, en
  and and_2 (and_2_out, q0_q[1], q0_q[0]);
  T_Flip_Flop q2 (.clk(CLK_out), .T(and_2_out), .Q(q0_q[2]), .reset(or_1_out));  // open: Qn, preset, en
  Multiplexer #(.select(3), .width(3), .enable("false")) multiplexer_1 (
    .in0(3'b100), .in1(3'b100), .in2(3'b010), .in3(3'b001), .in4(3'b001), .in5(3'b001), .in6(3'b001),
    .in7(3'b001), .out(multiplexer_1_out), .sel(q0_q));
  LED Verde (.in(multiplexer_1_out[2]));
  LED \u_Ámbar  (.in(multiplexer_1_out[1]));
  LED Rojo (.in(multiplexer_1_out[0]));
endmodule

module \Semáforo_Simplificado_w_MUX_corto__0_5_Hz  (
);

  wire CLK_out, INIT_CLR_out, multiplexer_1_out, multiplexer_2_out, multiplexer_3_out, or_1_out, q0_q, q0_qn,
       q1_q, q1_qn, q1q0_out, q1q0_prime_out, q2_q, q2q1_out;

  Clock #(.highDuration(2), .lowDuration(2)) CLK (.out(CLK_out));
  Button INIT_CLR (.out(INIT_CLR_out));
  or or_1 (or_1_out, INIT_CLR_out, q2q1_out);
  T_Flip_Flop q0 (.clk(CLK_out), .T(1'b1), .Q(q0_q), .Qn(q0_qn), .reset(or_1_out));  // open: preset, en
  and q2q1 (q2q1_out, q1_q, q2_q);
  T_Flip_Flop q1 (.clk(CLK_out), .T(q0_q), .Q(q1_q), .Qn(q1_qn), .reset(or_1_out));  // open: preset, en
  and q1q0 (q1q0_out, q1_q, q0_q);
  and q1q0_prime (q1q0_prime_out, q0_qn, q1_q);
  T_Flip_Flop q2 (.clk(CLK_out), .T(q1q0_out), .Q(q2_q), .reset(or_1_out));  // open: Qn, preset, en
  Multiplexer #(.enable("false")) multiplexer_1 (.in0(q1_qn), .in1(1'b0), .out(multiplexer_1_out), .sel(q2_q));
  LED Verde (.in(multiplexer_1_out));
  LED \u_Ámbar  (.in(multiplexer_2_out));
  Multiplexer #(.enable("false")) multiplexer_2 (.in0(q1q0_prime_out), .in1(1'b0), .out(multiplexer_2_out), .sel(q2_q));
  Multiplexer #(.enable("false")) multiplexer_3 (.in0(q1q0_out), .in1(1'b1), .out(multiplexer_3_out), .sel(q2_q));
  LED Rojo (.in(multiplexer_3_out));
endmodule

module \Semáforo_secuenciador__1  (
);

  wire CLK_out, CLR_out, INIT_out;
  wire [2:0] shift_register_1_out;

  Button INIT (.out(INIT_out));
  Shift_Register #(.width(3), .length(12)) shift_register_1 (
    .in(shift_register_1_out), .clk(CLK_out), .out(shift_register_1_out), .load(INIT_out), .clr(CLR_out),
    .d0(3'b100), .d1(3'b100), .d2(3'b100), .d3(3'b100), .d4(3'b100), .d5(3'b100), .d6(3'b010), .d7(3'b010),
    .d8(3'b001), .d9(3'b001), .d10(3'b001), .d11(3'b001));  // open: shift, q0, q1, q2, q3, q4, q5, q6, q7, q8, q9, q10, q11
  Clock CLK (.out(CLK_out));
  Button CLR (.out(CLR_out));
  LED Verde (.in(shift_register_1_out[0]));
  LED \u_Ámbar  (.in(shift_register_1_out[1]));
  LED Rojo (.in(shift_register_1_out[2]));
endmodule

module \Semáforo_secuenciador__2  (
);

  wire CLK_out, CLR_out, INIT_out;
  wire [2:0] shift_register_1_out;

  Button INIT (.out(INIT_out));
  Shift_Register #(.width(3), .length(6)) shift_register_1 (
    .in(shift_register_1_out), .clk(CLK_out), .out(shift_register_1_out), .load(INIT_out), .clr(CLR_out),
    .d0(3'b100), .d1(3'b100), .d2(3'b100), .d3(3'b010), .d4(3'b001), .d5(3'b001));  // open: shift, q0, q1, q2, q3, q4, q5
  Clock CLK (.out(CLK_out));
  Button CLR (.out(CLR_out));
  LED Verde (.in(shift_register_1_out[0]));
  LED \u_Ámbar  (.in(shift_register_1_out[1]));
  LED Rojo (.in(shift_register_1_out[2]));
endmodule

module \Semáforo_etapas  (
);

  wire and_1_out, and_2_out, and_3_out, CLK_out, INIT_CLR_out, or_1_out, T1_carry, T2_carry, T3_carry;

  Clock CLK (.out(CLK_out));
  Counter #(.width(3), .max('h4), .ongoal("stay")) T1 (
    .count(1'b1), .carry(T1_carry), .clk(CLK_out), .clr(or_1_out));  // open: load, D, Q
  Counter #(.width(3), .max('h2), .ongoal("stay")) T2 (
    .count(T1_carry), .carry(T2_carry), .clk(CLK_out), .clr(or_1_out));  // open: load, D, Q
  LED Verde (.in(and_1_out));
  and and_1 (and_1_out, 1'b1, ~T1_carry);  // AND_Gate
  and and_2 (and_2_out, T1_carry, ~T2_carry);  // AND_Gate
  LED \u_Ámbar  (.in(and_2_out));
  LED Rojo (.in(and_3_out));
  and and_3 (and_3_out, T2_carry, ~T3_carry);  // AND_Gate
  Counter #(.width(3), .max('h6), .ongoal("stay")) T3 (
    .count(T2_carry), .carry(T3_carry), .clk(CLK_out), .clr(or_1_out));  // open: load, D, Q
  or or_1 (or_1_out, T3_carry, INIT_CLR_out);
  Button INIT_CLR (.out(INIT_CLR_out));
endmodule
